// Logisim project scott.circ as structural Verilog: 23 circuits, main circuit CPU
module Enabler8 (
  input  enable,
  input  in0,
  input  in1,
  input  in2,
  input  in3,
  input  in4,
  input  in5,
  input  in6,
  input  in7,
  output out0,
  output out1,
  output out2,
  output out3,
  output out4,
  output out6,
  output out6_2,
  output out7
);

  assign out0 = enable ? in0 : 1'bz;  // Controlled_Buffer controlled_buffer_1
  assign out1 = enable ? in1 : 1'bz;  // Controlled_Buffer controlled_buffer_2
  assign out2 = enable ? in2 : 1'bz;  // Controlled_Buffer controlled_buffer_3
  assign out3 = enable ? in3 : 1'bz;  // Controlled_Buffer controlled_buffer_4
  assign out4 = enable ? in4 : 1'bz;  // Controlled_Buffer controlled_buffer_5
  assign out6 = enable ? in5 : 1'bz;  // Controlled_Buffer controlled_buffer_6
  assign out6_2 = enable ? in6 : 1'bz;  // Controlled_Buffer controlled_buffer_7
  assign out7 = enable ? in7 : 1'bz;  // Controlled_Buffer controlled_buffer_8
endmodule

module DLatch (
  input  data,
  input  write,
  input  reset,
  output out
);

  wire nand_1_out, nand_2_out, nand_3_out, nand_4_out, nand_6_out;

  nand nand_1 (nand_1_out, data, data);
  nand nand_2 (nand_2_out, data, write);
  nand nand_3 (nand_3_out, write, nand_1_out);
  nand nand_4 (nand_4_out, reset, reset);
  nand nand_5 (out, nand_2_out, nand_6_out);
  nand nand_6 (nand_6_out, out, nand_3_out, nand_4_out);
endmodule

module Reg4 (
  input  in0,
  input  in1,
  input  in2,
  input  in3,
  input  read,
  input  write,
  input  reset,
  output out0,
  output out1,
  output out2,
  output out3
);

  wire dlatch_1_out, dlatch_2_out, dlatch_3_out, dlatch_4_out;

  assign out0 = read ? dlatch_1_out : 1'bz;  // Controlled_Buffer controlled_buffer_1
  DLatch dlatch_1 (.data(in0), .write(write), .out(dlatch_1_out), .reset(reset));
  assign out1 = read ? dlatch_2_out : 1'bz;  // Controlled_Buffer controlled_buffer_2
  DLatch dlatch_2 (.data(in1), .write(write), .out(dlatch_2_out), .reset(reset));
  DLatch dlatch_3 (.data(in2), .write(write), .out(dlatch_3_out), .reset(reset));
  assign out2 = read ? dlatch_3_out : 1'bz;  // Controlled_Buffer controlled_buffer_3
  DLatch dlatch_4 (.data(in3), .write(write), .out(dlatch_4_out), .reset(reset));
  assign out3 = read ? dlatch_4_out : 1'bz;  // Controlled_Buffer controlled_buffer_4
endmodule

module Reg8 (
  input  read,
  input  write,
  input  reset,
  input  in0,
  input  in1,
  input  in2,
  input  in3,
  input  in4,
  input  in5,
  input  in6,
  input  in7,
  output out0,
  output out1,
  output out2,
  output out3,
  output out4,
  output out5,
  output out6,
  output out7
);

  Reg4 reg4_1 (
    .in0(in0), .in1(in1), .in2(in2), .in3(in3), .read(read), .write(write), .out0(out0), .out1(out1),
    .out2(out2), .out3(out3), .reset(reset));
  Reg4 reg4_2 (
    .in0(in4), .in1(in5), .in2(in6), .in3(in7), .read(read), .write(write), .out0(out4), .out1(out5),
    .out2(out6), .out3(out7), .reset(reset));
endmodule

module Ram256 (
  input  addr0,
  input  addr1,
  input  addr2,
  input  addr3,
  input  addr4,
  input  addr5,
  input  addr6,
  input  addr7,
  input  marw,
  input  read,
  input  write,
  input  clk,
  input  reset,
  input  in0,
  input  in1,
  input  in2,
  input  in3,
  input  in4,
  input  in5,
  input  in6,
  input  in7,
  output out0,
  output out1,
  output out2,
  output out3,
  output out4,
  output out5,
  output out6,
  output out7
);

  wire delayer_1_out, or_1_out;
  wire [7:0] MAR_out0;

  Reg8 MAR (
    .in0(addr0), .in1(addr1), .in2(addr2), .in3(addr3), .in4(addr4), .in5(addr5), .in6(addr6), .in7(addr7),
    .read(1'b1), .write(marw), .reset(reset), .out0(MAR_out0[0]), .out1(MAR_out0[1]), .out2(MAR_out0[2]),
    .out3(MAR_out0[3]), .out4(MAR_out0[4]), .out5(MAR_out0[5]), .out6(MAR_out0[6]), .out7(MAR_out0[7]));
  Delayer delayer_1 (.in(clk), .out(delayer_1_out));
  or or_1 (or_1_out, read, write);
  RAM #(.bus("separate")) ram_1 (
    .addr(MAR_out0), .din({in7, in6, in5, in4, in3, in2, in1, in0}),
    .data({out7, out6, out5, out4, out3, out2, out1, out0}), .str(write), .sel(or_1_out),
    .clk(delayer_1_out), .ld(read), .clr(reset));
endmodule

module Ram64KB (
  input  addr0,
  input  addr1,
  input  addr2,
  input  addr3,
  input  addr4,
  input  addr5,
  input  addr6,
  input  addr7,
  input  low,
  input  hiw,
  input  read,
  input  write,
  input  reset,
  input  in0,
  input  in1,
  input  in2,
  input  in3,
  input  in4,
  input  in5,
  input  in6,
  input  in7,
  output out0,
  output out1,
  output out2,
  output out3,
  output out4,
  output out5,
  output out6,
  output out7
);

  wire or_1_out;
  wire [7:0] HIGH_out0, LOW_out0;

  Reg8 u_LOW (
    .in0(addr0), .in1(addr1), .in2(addr2), .in3(addr3), .in4(addr4), .in5(addr5), .in6(addr6), .in7(addr7),
    .read(1'b1), .write(low), .reset(reset), .out0(LOW_out0[0]), .out1(LOW_out0[1]), .out2(LOW_out0[2]),
    .out3(LOW_out0[3]), .out4(LOW_out0[4]), .out5(LOW_out0[5]), .out6(LOW_out0[6]), .out7(LOW_out0[7]));
  Reg8 HIGH (
    .in0(addr0), .in1(addr1), .in2(addr2), .in3(addr3), .in4(addr4), .in5(addr5), .in6(addr6), .in7(addr7),
    .read(1'b1), .write(hiw), .reset(reset), .out0(HIGH_out0[0]), .out1(HIGH_out0[1]), .out2(HIGH_out0[2]),
    .out3(HIGH_out0[3]), .out4(HIGH_out0[4]), .out5(HIGH_out0[5]), .out6(HIGH_out0[6]), .out7(HIGH_out0[7]));
  assign out0 = write ? in0 : 1'bz;  // Controlled_Buffer controlled_buffer_1
  assign out1 = write ? in1 : 1'bz;  // Controlled_Buffer controlled_buffer_2
  assign out2 = write ? in2 : 1'bz;  // Controlled_Buffer controlled_buffer_3
  or or_1 (or_1_out, read, write);
  assign out3 = write ? in3 : 1'bz;  // Controlled_Buffer controlled_buffer_4
  assign out4 = write ? in4 : 1'bz;  // Controlled_Buffer controlled_buffer_5
  assign out5 = write ? in5 : 1'bz;  // Controlled_Buffer controlled_buffer_6
  assign out6 = write ? in6 : 1'bz;  // Controlled_Buffer controlled_buffer_7
  RAM #(.addrWidth(16)) ram_1 (
    .addr({HIGH_out0, LOW_out0}), .data({out7, out6, out5, out4, out3, out2, out1, out0}), .sel(or_1_out),
    .clk(or_1_out), .ld(read), .clr(reset));
  assign out7 = write ? in7 : 1'bz;  // Controlled_Buffer controlled_buffer_8
endmodule

module LeftShifter8 (
  input  cin,
  input  in0,
  input  in1,
  input  in2,
  input  in3,
  input  in4,
  input  in5,
  input  in6,
  input  in7,
  output out0,
  output out1,
  output out2,
  output out3,
  output out4,
  output out6,
  output out6_2,
  output out7,
  output cout
);


  assign cout = in7;
  assign out0 = cin;
  assign out1 = in0;
  assign out2 = in1;
  assign out3 = in2;
  assign out4 = in3;
  assign out6 = in4;
  assign out6_2 = in5;
  assign out7 = in6;
endmodule

module RightShifter8 (
  input  in0,
  input  in1,
  input  in2,
  input  in3,
  input  in4,
  input  in5,
  input  in6,
  input  in7,
  input  cin,
  output cout,
  output out0,
  output out1,
  output out2,
  output out3,
  output out4,
  output out6,
  output out6_2,
  output out7
);


  assign cout = in0;
  assign out0 = in1;
  assign out1 = in2;
  assign out2 = in3;
  assign out3 = in4;
  assign out4 = in5;
  assign out6 = in6;
  assign out6_2 = in7;
  assign out7 = cin;
endmodule

module Notter8 (
  input  in0,
  input  in1,
  input  in2,
  input  in3,
  input  in4,
  input  in5,
  input  in6,
  input  in7,
  output out0,
  output out1,
  output out2,
  output out3,
  output out4,
  output out6,
  output out6_2,
  output out7
);

  not not_1 (out0, in0);
  not not_2 (out1, in1);
  not not_3 (out2, in2);
  not not_4 (out3, in3);
  not not_5 (out4, in4);
  not not_6 (out6, in5);
  not not_7 (out6_2, in6);
  not not_8 (out7, in7);
endmodule

module Ander8 (
  input  a0,
  input  b0,
  input  a1,
  input  b1,
  input  a2,
  input  b2,
  input  a3,
  input  b3,
  input  a4,
  input  b4,
  input  a5,
  input  b5,
  input  a6,
  input  b6,
  input  a7,
  input  b7,
  output out0,
  output out1,
  output out2,
  output out3,
  output out4,
  output out5,
  output out6,
  output out7
);

  and and_1 (out0, a0, b0);
  and and_2 (out1, a1, b1);
  and and_3 (out2, a2, b2);
  and and_4 (out3, a3, b3);
  and and_5 (out4, a4, b4);
  and and_6 (out5, a5, b5);
  and and_7 (out6, a6, b6);
  and and_8 (out7, a7, b7);
endmodule

module Orer8 (
  input  a0,
  input  b0,
  input  a1,
  input  b1,
  input  a2,
  input  b2,
  input  a3,
  input  b3,
  input  a4,
  input  b4,
  input  a5,
  input  b5,
  input  a6,
  input  b6,
  input  a7,
  input  b7,
  output out0,
  output out1,
  output out2,
  output out3,
  output out4,
  output out5,
  output out6,
  output out7
);

  or or_1 (out0, a0, b0);
  or or_2 (out1, a1, b1);
  or or_3 (out2, a2, b2);
  or or_4 (out3, a3, b3);
  or or_5 (out4, a4, b4);
  or or_6 (out5, a5, b5);
  or or_7 (out6, a6, b6);
  or or_8 (out7, a7, b7);
endmodule

module Xorer8 (
  input  a0,
  input  b0,
  input  a1,
  input  b1,
  input  a2,
  input  b2,
  input  a3,
  input  b3,
  input  a4,
  input  b4,
  input  a5,
  input  b5,
  input  a6,
  input  b6,
  input  a7,
  input  b7,
  output out0,
  output out1,
  output out2,
  output out3,
  output out4,
  output out5,
  output out6,
  output out7
);

  xor xor_1 (out0, a0, b0);
  xor xor_2 (out1, a1, b1);
  xor xor_3 (out2, a2, b2);
  xor xor_4 (out3, a3, b3);
  xor xor_5 (out4, a4, b4);
  xor xor_6 (out5, a5, b5);
  xor xor_7 (out6, a6, b6);
  xor xor_8 (out7, a7, b7);
endmodule

module FullAdder (
  input  a,
  input  b,
  input  cin,
  output sum,
  output cout
);

  wire and_1_out, and_2_out, xor_1_out;

  xor xor_1 (xor_1_out, a, b);
  xor xor_2 (sum, xor_1_out, cin);
  and and_1 (and_1_out, xor_1_out, cin);
  and and_2 (and_2_out, a, b);
  or or_1 (cout, and_1_out, and_2_out);
endmodule

module Adder8 (
  input  cin,
  input  a0,
  input  b0,
  input  a1,
  input  b1,
  input  a2,
  input  b2,
  input  a3,
  input  b3,
  input  a4,
  input  b4,
  input  a5,
  input  b5,
  input  a6,
  input  b6,
  input  a7,
  input  b7,
  output out0,
  output out1,
  output out2,
  output out3,
  output out4,
  output out5,
  output out6,
  output out7,
  output ovcarry,
  output cout
);

  wire fulladder_1_cout, fulladder_2_cout, fulladder_3_cout, fulladder_4_cout, fulladder_5_cout,
       fulladder_6_cout;

  FullAdder fulladder_1 (.a(a0), .b(b0), .cin(cin), .sum(out0), .cout(fulladder_1_cout));
  FullAdder fulladder_2 (.a(a1), .b(b1), .cin(fulladder_1_cout), .sum(out1), .cout(fulladder_2_cout));
  FullAdder fulladder_3 (.a(a2), .b(b2), .cin(fulladder_2_cout), .sum(out2), .cout(fulladder_3_cout));
  FullAdder fulladder_4 (.a(a3), .b(b3), .cin(fulladder_3_cout), .sum(out3), .cout(fulladder_4_cout));
  FullAdder fulladder_5 (.a(a4), .b(b4), .cin(fulladder_4_cout), .sum(out4), .cout(fulladder_5_cout));
  FullAdder fulladder_6 (.a(a5), .b(b5), .cin(fulladder_5_cout), .sum(out5), .cout(fulladder_6_cout));
  FullAdder fulladder_7 (.a(a6), .b(b6), .cin(fulladder_6_cout), .sum(out6), .cout(ovcarry));
  FullAdder fulladder_8 (.a(a7), .b(b7), .cin(ovcarry), .sum(out7), .cout(cout));
endmodule

module AddSub8 (
  input  sub,
  input  a0,
  input  b0,
  input  a1,
  input  b1,
  input  a2,
  input  b2,
  input  a3,
  input  b3,
  input  a4,
  input  b4,
  input  a5,
  input  b5,
  input  a6,
  input  b6,
  input  a7,
  input  b7,
  input  cin,
  output carry,
  output overflow,
  output out7,
  output out6,
  output out5,
  output out4,
  output out3,
  output out2,
  output out1,
  output out0
);

  wire adder8_1_cout, adder8_1_ovcarry, xor_3_out, xor_4_out, xor_5_out, xor_6_out, xor_7_out, xor_8_out,
       xor_9_out, xor_10_out, xor_11_out;

  xor xor_1 (carry, sub, adder8_1_cout);
  xor xor_2 (overflow, adder8_1_ovcarry, adder8_1_cout);
  xor xor_3 (xor_3_out, sub, b0);
  xor xor_4 (xor_4_out, sub, b1);
  xor xor_5 (xor_5_out, sub, b2);
  xor xor_6 (xor_6_out, sub, b3);
  xor xor_7 (xor_7_out, sub, b4);
  xor xor_8 (xor_8_out, sub, b5);
  xor xor_9 (xor_9_out, sub, b6);
  xor xor_10 (xor_10_out, sub, b7);
  Adder8 adder8_1 (
    .cin(xor_11_out), .a0(a0), .b0(xor_3_out), .a1(a1), .b1(xor_4_out), .a2(a2), .b2(xor_5_out), .a3(a3),
    .b3(xor_6_out), .a4(a4), .b4(xor_7_out), .a5(a5), .b5(xor_8_out), .a6(a6), .b6(xor_9_out), .a7(a7),
    .b7(xor_10_out), .out0(out0), .out1(out1), .out2(out2), .out3(out3), .out4(out4), .out5(out5),
    .out6(out6), .out7(out7), .ovcarry(adder8_1_ovcarry), .cout(adder8_1_cout));
  xor xor_11 (xor_11_out, sub, cin);
endmodule

module Comparator (
  input  ineq,
  input  ingt,
  input  a,
  input  b,
  output outeq,
  output outgt
);

  wire and_2_out, not_1_out, xor_1_out;

  xor xor_1 (xor_1_out, a, b);
  not not_1 (not_1_out, xor_1_out);
  and and_1 (outeq, not_1_out, ineq);
  and and_2 (and_2_out, ineq, a, xor_1_out);
  or or_1 (outgt, and_2_out, ingt);
endmodule

module Comparator8 (
  input  a0,
  input  b0,
  input  a1,
  input  b1,
  input  a2,
  input  b2,
  input  a3,
  input  b3,
  input  a4,
  input  b4,
  input  a5,
  input  b5,
  input  a6,
  input  b6,
  input  a7,
  input  b7,
  output eq,
  output gt
);

  wire comparator_2_outeq, comparator_2_outgt, comparator_3_outeq, comparator_3_outgt, comparator_4_outeq,
       comparator_4_outgt, comparator_5_outeq, comparator_5_outgt, comparator_6_outeq, comparator_6_outgt,
       comparator_7_outeq, comparator_7_outgt, comparator_8_outeq, comparator_8_outgt;

  Comparator comparator_1 (
    .a(a0), .b(b0), .ineq(comparator_2_outeq), .ingt(comparator_2_outgt), .outeq(eq), .outgt(gt));
  Comparator comparator_2 (
    .a(a1), .b(b1), .ineq(comparator_3_outeq), .ingt(comparator_3_outgt), .outeq(comparator_2_outeq),
    .outgt(comparator_2_outgt));
  Comparator comparator_3 (
    .a(a2), .b(b2), .ineq(comparator_4_outeq), .ingt(comparator_4_outgt), .outeq(comparator_3_outeq),
    .outgt(comparator_3_outgt));
  Comparator comparator_4 (
    .a(a3), .b(b3), .ineq(comparator_5_outeq), .ingt(comparator_5_outgt), .outeq(comparator_4_outeq),
    .outgt(comparator_4_outgt));
  Comparator comparator_5 (
    .a(a4), .b(b4), .ineq(comparator_6_outeq), .ingt(comparator_6_outgt), .outeq(comparator_5_outeq),
    .outgt(comparator_5_outgt));
  Comparator comparator_6 (
    .a(a5), .b(b5), .ineq(comparator_7_outeq), .ingt(comparator_7_outgt), .outeq(comparator_6_outeq),
    .outgt(comparator_6_outgt));
  Comparator comparator_7 (
    .a(a6), .b(b6), .ineq(comparator_8_outeq), .ingt(comparator_8_outgt), .outeq(comparator_7_outeq),
    .outgt(comparator_7_outgt));
  Comparator comparator_8 (
    .a(a7), .b(b7), .ineq(1'b1), .ingt(1'b0), .outeq(comparator_8_outeq), .outgt(comparator_8_outgt));
endmodule

module Bus0Gate (
  input  in7,
  input  in6,
  input  in5,
  input  in4,
  input  in3,
  input  in2,
  input  in1,
  input  in0,
  input  bus_0,
  output out7,
  output out6,
  output out5,
  output out4,
  output out3,
  output out2,
  output out1,
  output out0
);

  wire not_1_out;

  and and_1 (out7, in7, not_1_out);
  and and_2 (out6, in6, not_1_out);
  and and_3 (out4, in4, not_1_out);
  and and_4 (out5, in5, not_1_out);
  and and_5 (out1, in1, not_1_out);
  and and_6 (out2, in2, not_1_out);
  and and_7 (out3, in3, not_1_out);
  not not_1 (not_1_out, bus_0);
  and and_8 (out0, in0, not_1_out);
endmodule

module ALU (
  input  a7,
  input  a6,
  input  a5,
  input  a4,
  input  a3,
  input  a2,
  input  a1,
  input  a0,
  input  b7,
  input  b6,
  input  b5,
  input  b4,
  input  b3,
  input  b2,
  input  b1,
  input  b0,
  input  op2,
  input  op1,
  input  op0,
  input  cin,
  output out0,
  output out1,
  output out2,
  output out3,
  output out4,
  output out5,
  output out6,
  output out7,
  output overflow,
  output carry,
  output sign,
  output zero
);

  wire addsub8_1_carry, addsub8_1_out0, addsub8_1_out1, addsub8_1_out2, addsub8_1_out3, addsub8_1_out4,
       addsub8_1_out5, addsub8_1_out6, addsub8_1_out7, addsub8_1_overflow, ander8_1_out0, ander8_1_out1,
       ander8_1_out2, ander8_1_out3, ander8_1_out4, ander8_1_out5, ander8_1_out6, ander8_1_out7,
       leftshifter8_1_cout, leftshifter8_1_out0, leftshifter8_1_out1, leftshifter8_1_out2,
       leftshifter8_1_out3, leftshifter8_1_out4, leftshifter8_1_out6, leftshifter8_1_out6_2,
       leftshifter8_1_out7, nor_2_out, or_1_out, orer8_1_out0, orer8_1_out1, orer8_1_out2, orer8_1_out3,
       orer8_1_out4, orer8_1_out5, orer8_1_out6, orer8_1_out7, rightshifter8_1_cout, rightshifter8_1_out0,
       rightshifter8_1_out1, rightshifter8_1_out2, rightshifter8_1_out3, rightshifter8_1_out4,
       rightshifter8_1_out6, rightshifter8_1_out6_2, rightshifter8_1_out7, xorer8_1_out0, xorer8_1_out1,
       xorer8_1_out2, xorer8_1_out3, xorer8_1_out4, xorer8_1_out5, xorer8_1_out6, xorer8_1_out7;
  wire [7:0] decoder_1_out0;

  Ander8 ander8_1 (
    .a0(a0), .b0(b0), .a1(a1), .b1(b1), .a2(a2), .b2(b2), .a3(a3), .b3(b3), .a4(a4), .b4(b4), .a5(a5),
    .b5(b5), .a6(a6), .b6(b6), .a7(a7), .b7(b7), .out0(ander8_1_out0), .out1(ander8_1_out1),
    .out2(ander8_1_out2), .out3(ander8_1_out3), .out4(ander8_1_out4), .out5(ander8_1_out5),
    .out6(ander8_1_out6), .out7(ander8_1_out7));
  Orer8 orer8_1 (
    .a0(a0), .b0(b0), .a1(a1), .b1(b1), .a2(a2), .b2(b2), .a3(a3), .b3(b3), .a4(a4), .b4(b4), .a5(a5),
    .b5(b5), .a6(a6), .b6(b6), .a7(a7), .b7(b7), .out0(orer8_1_out0), .out1(orer8_1_out1),
    .out2(orer8_1_out2), .out3(orer8_1_out3), .out4(orer8_1_out4), .out5(orer8_1_out5), .out6(orer8_1_out6),
    .out7(orer8_1_out7));
  Xorer8 xorer8_1 (
    .a0(a0), .b0(b0), .a1(a1), .b1(b1), .a2(a2), .b2(b2), .a3(a3), .b3(b3), .a4(a4), .b4(b4), .a5(a5),
    .b5(b5), .a6(a6), .b6(b6), .a7(a7), .b7(b7), .out0(xorer8_1_out0), .out1(xorer8_1_out1),
    .out2(xorer8_1_out2), .out3(xorer8_1_out3), .out4(xorer8_1_out4), .out5(xorer8_1_out5),
    .out6(xorer8_1_out6), .out7(xorer8_1_out7));
  AddSub8 addsub8_1 (
    .cin(cin), .a0(a0), .b0(b0), .a1(a1), .b1(b1), .a2(a2), .b2(b2), .a3(a3), .b3(b3), .a4(a4), .b4(b4),
    .a5(a5), .b5(b5), .a6(a6), .b6(b6), .a7(a7), .b7(b7), .out0(addsub8_1_out0), .out1(addsub8_1_out1),
    .out2(addsub8_1_out2), .out3(addsub8_1_out3), .out4(addsub8_1_out4), .out5(addsub8_1_out5),
    .out6(addsub8_1_out6), .out7(addsub8_1_out7), .carry(addsub8_1_carry), .sub(decoder_1_out0[5]),
    .overflow(addsub8_1_overflow));
  LeftShifter8 leftshifter8_1 (
    .cin(cin), .in0(a0), .in1(a1), .in2(a2), .in3(a3), .in4(a4), .in5(a5), .in6(a6), .in7(a7),
    .out0(leftshifter8_1_out0), .out1(leftshifter8_1_out1), .out2(leftshifter8_1_out2),
    .out3(leftshifter8_1_out3), .out4(leftshifter8_1_out4), .out6(leftshifter8_1_out6),
    .out6_2(leftshifter8_1_out6_2), .out7(leftshifter8_1_out7), .cout(leftshifter8_1_cout));
  RightShifter8 rightshifter8_1 (
    .in0(a0), .in1(a1), .in2(a2), .in3(a3), .in4(a4), .in5(a5), .in6(a6), .in7(a7), .cin(cin),
    .cout(rightshifter8_1_cout), .out0(rightshifter8_1_out0), .out1(rightshifter8_1_out1),
    .out2(rightshifter8_1_out2), .out3(rightshifter8_1_out3), .out4(rightshifter8_1_out4),
    .out6(rightshifter8_1_out6), .out6_2(rightshifter8_1_out6_2), .out7(rightshifter8_1_out7));
  Decoder #(.select(3), .enable("false")) decoder_1 (
    .out0(decoder_1_out0[0]), .out1(decoder_1_out0[1]), .out2(decoder_1_out0[2]), .out3(decoder_1_out0[3]),
    .out4(decoder_1_out0[4]), .out5(decoder_1_out0[5]), .out6(decoder_1_out0[6]), .out7(decoder_1_out0[7]),
    .sel({op2, op1, op0}));
  Enabler8 enabler8_1 (
    .in0(a0), .in1(a1), .in2(a2), .in3(a3), .in4(a4), .in5(a5), .in6(a6), .in7(a7),
    .enable(decoder_1_out0[0]), .out0(out0), .out1(out1), .out2(out2), .out3(out3), .out4(out4), .out6(out5),
    .out6_2(out6), .out7(out7));
  Enabler8 enabler8_2 (
    .in0(ander8_1_out0), .in1(ander8_1_out1), .in2(ander8_1_out2), .in3(ander8_1_out3), .in4(ander8_1_out4),
    .in5(ander8_1_out5), .in6(ander8_1_out6), .in7(ander8_1_out7), .enable(decoder_1_out0[1]), .out0(out0),
    .out1(out1), .out2(out2), .out3(out3), .out4(out4), .out6(out5), .out6_2(out6), .out7(out7));
  Enabler8 enabler8_3 (
    .in0(orer8_1_out0), .in1(orer8_1_out1), .in2(orer8_1_out2), .in3(orer8_1_out3), .in4(orer8_1_out4),
    .in5(orer8_1_out5), .in6(orer8_1_out6), .in7(orer8_1_out7), .enable(decoder_1_out0[2]), .out0(out0),
    .out1(out1), .out2(out2), .out3(out3), .out4(out4), .out6(out5), .out6_2(out6), .out7(out7));
  Enabler8 enabler8_4 (
    .in0(xorer8_1_out0), .in1(xorer8_1_out1), .in2(xorer8_1_out2), .in3(xorer8_1_out3), .in4(xorer8_1_out4),
    .in5(xorer8_1_out5), .in6(xorer8_1_out6), .in7(xorer8_1_out7), .enable(decoder_1_out0[3]), .out0(out0),
    .out1(out1), .out2(out2), .out3(out3), .out4(out4), .out6(out5), .out6_2(out6), .out7(out7));
  or or_1 (or_1_out, decoder_1_out0[4], decoder_1_out0[5]);
  Enabler8 enabler8_5 (
    .in0(addsub8_1_out0), .in1(addsub8_1_out1), .in2(addsub8_1_out2), .in3(addsub8_1_out3),
    .in4(addsub8_1_out4), .in5(addsub8_1_out5), .in6(addsub8_1_out6), .in7(addsub8_1_out7),
    .enable(or_1_out), .out0(out0), .out1(out1), .out2(out2), .out3(out3), .out4(out4), .out6(out5),
    .out6_2(out6), .out7(out7));
  Enabler8 enabler8_6 (
    .in0(leftshifter8_1_out0), .in1(leftshifter8_1_out1), .in2(leftshifter8_1_out2),
    .in3(leftshifter8_1_out3), .in4(leftshifter8_1_out4), .in5(leftshifter8_1_out6),
    .in6(leftshifter8_1_out6_2), .in7(leftshifter8_1_out7), .enable(decoder_1_out0[6]), .out0(out0),
    .out1(out1), .out2(out2), .out3(out3), .out4(out4), .out6(out5), .out6_2(out6), .out7(out7));
  Enabler8 enabler8_7 (
    .in0(rightshifter8_1_out0), .in1(rightshifter8_1_out1), .in2(rightshifter8_1_out2),
    .in3(rightshifter8_1_out3), .in4(rightshifter8_1_out4), .in5(rightshifter8_1_out6),
    .in6(rightshifter8_1_out6_2), .in7(rightshifter8_1_out7), .enable(decoder_1_out0[7]), .out0(out0),
    .out1(out1), .out2(out2), .out3(out3), .out4(out4), .out6(out5), .out6_2(out6), .out7(out7));
  nor nor_1 (zero, out7, out6, out5, out4, out3, out2, out1, out0);
  Multiplexer #(.enable("false")) multiplexer_1 (.in0(1'b0), .in1(addsub8_1_overflow), .out(overflow), .sel(or_1_out));
  nor nor_2 (nor_2_out, or_1_out, decoder_1_out0[6], decoder_1_out0[7]);
  assign carry = nor_2_out ? 1'b0 : 1'bz;  // Controlled_Buffer controlled_buffer_1
  assign carry = or_1_out ? addsub8_1_carry : 1'bz;  // Controlled_Buffer controlled_buffer_2
  assign carry = decoder_1_out0[6] ? leftshifter8_1_cout : 1'bz;  // Controlled_Buffer controlled_buffer_3
  assign carry = decoder_1_out0[7] ? rightshifter8_1_cout : 1'bz;  // Controlled_Buffer controlled_buffer_4

  assign sign = out7;
endmodule

module ControlUnit (
  input  rst,
  input  zero,
  input  sign,
  input  carry,
  input  overflow,
  input  clk,
  input  ir7,
  input  ir6,
  input  ir5,
  input  ir4,
  input  ir3,
  input  ir2,
  input  ir1,
  input  ir0,
  output rd_r,
  output ra_w,
  output rb_w,
  output bus_0,
  output io,
  output io_in_out,
  output io_data_addr,
  output rx_r,
  output rx_w,
  output fr_w,
  output rx1,
  output pc_w,
  output rx0,
  output pc_r,
  output ir_w,
  output cin,
  output mar_w,
  output op2,
  output ram_w,
  output op1,
  output op0,
  output ram_r,
  output halt,
  output new_cycle,
  output new_instr
);

  wire and_10_out, and_13_out, and_14_out, and_15_out, and_16_out, and_17_out, and_18_out, and_19_out,
       clock_1_clk_r, clock_1_clk_w, delayer_1_out, instr_state_qn, nor_2_out, or_1_out, or_2_out, or_3_out,
       or_4_out;
  wire [1:0] multiplexer_2_out, multiplexer_3_out;
  wire [6:0] adder_1_out, mPC_q, multiplexer_1_out, rom_1_data;
  wire [6:6] instr_state_q;
  wire [31:4] rom_1_data_2;

  and and_1 (fr_w, rom_1_data_2[12], clock_1_clk_w);
  and and_2 (pc_w, rom_1_data_2[13], clock_1_clk_w);
  and and_3 (pc_r, rom_1_data_2[14], clock_1_clk_r);
  and and_4 (ir_w, rom_1_data_2[15], clock_1_clk_w);
  and and_5 (mar_w, rom_1_data_2[16], clock_1_clk_w);
  and and_6 (ram_w, rom_1_data_2[17], clock_1_clk_w);
  and and_7 (ram_r, rom_1_data_2[18], clock_1_clk_r);
  Clock clock_1 (.clk_r(clock_1_clk_r), .clk(clk), .clk_w(clock_1_clk_w), .rst(or_1_out));
  nor nor_1 (new_cycle, clock_1_clk_r, clock_1_clk_w);
  or or_1 (or_1_out, rst, halt);
  and and_8 (rd_r, clock_1_clk_r, rom_1_data_2[11]);
  and and_9 (ra_w, clock_1_clk_w, rom_1_data_2[10]);
  Register #(.width(7)) mPC (.D(multiplexer_1_out), .en(1'b1), .Q(mPC_q), .clk(new_cycle), .clr(or_1_out));
  Multiplexer #(.select(2), .width(7), .enable("false")) multiplexer_1 (
    .in0(adder_1_out), .in1(adder_1_out), .in2(rom_1_data),
    .in3({instr_state_q[6], ir7, ir6, ir5, ir4, 2'b00}), .out(multiplexer_1_out), .sel(multiplexer_2_out));
  and and_10 (and_10_out, clock_1_clk_w, rom_1_data_2[31]);
  and and_11 (rb_w, clock_1_clk_w, rom_1_data_2[9]);
  Delayer delayer_1 (.in(new_cycle), .out(delayer_1_out));
  and and_12 (new_instr, delayer_1_out, and_13_out);
  and and_13 (and_13_out, ~mPC_q[6], ~mPC_q[5], ~mPC_q[4], ~mPC_q[3], ~mPC_q[2], ~mPC_q[1], mPC_q[0]);  // AND_Gate
  Adder #(.width(7)) adder_1 (.a(mPC_q), .b({7{1'b0}}), .out(adder_1_out), .cin(1'b1));  // open: cout
  D_Flip_Flop instr_state (
    .clk(and_10_out), .D(instr_state_qn), .Q(instr_state_q[6]), .Qn(instr_state_qn), .en(1'b1),
    .reset(or_1_out));  // open: preset
  ROM #(.addrWidth(7), .dataWidth(32)) rom_1 (
    .addr(mPC_q),
    .data({rom_1_data_2[31:27], rom_1_data, halt, rom_1_data_2[18:9], bus_0, io, rom_1_data_2[6:4], cin, op2, op1, op0}),
    .sel(1'b1));
  Multiplexer #(.select(2), .width(2), .enable("false")) multiplexer_2 (
    .in0(2'b00), .in1(multiplexer_3_out), .in2(2'b10), .in3(2'b11), .out(multiplexer_2_out),
    .sel(rom_1_data_2[29:28]));
  or or_2 (or_2_out, nor_2_out, and_16_out, and_17_out, and_18_out, and_19_out);
  Multiplexer #(.width(2), .enable("false")) multiplexer_3 (
    .in0(2'b00), .in1(2'b10), .out(multiplexer_3_out), .sel(or_2_out));
  and and_14 (and_14_out, ir3, io);
  and and_15 (and_15_out, io, ~ir3);  // AND_Gate
  nor nor_2 (nor_2_out, ir0, ir1, ir2, ir3);
  and and_16 (and_16_out, zero, ir0);
  and and_17 (and_17_out, sign, ir1);
  and and_18 (and_18_out, carry, ir2);
  and and_19 (and_19_out, overflow, ir3);
  and and_20 (rx_r, clock_1_clk_r, or_3_out);
  or or_3 (or_3_out, rom_1_data_2[6], and_15_out);
  and and_21 (rx_w, clock_1_clk_w, or_4_out);
  or or_4 (or_4_out, rom_1_data_2[5], and_14_out);
  Multiplexer #(.width(2), .enable("false")) multiplexer_4 (
    .in0({ir3, ir2}), .in1({ir1, ir0}), .out({rx1, rx0}), .sel(rom_1_data_2[4]));

  assign io_data_addr = ir2;
  assign io_in_out = ir3;

  // Notes on the sheet:
  //   Map instructions to 1xxxx00 with xxxx=OPCODE
  //   to avoid collision with IFETCH.
  //   Instructions must complete in 4 steps.
  //   0x00 has no instruction since after reset it won't be executed.
  //   00xy -> jump to addr mPC+1
  //   01xy -> branch to either addr mPC+1 or ROM[mPC]
  //   10xy -> jump to addr ROM[mPC]
  //   11xy -> jump to instr in IR
  //   contents of rom_1 (hex, n*v repeats v):
  //   0 14700 280c b0048000
endmodule

module Clock (
  input  clk,
  input  rst,
  output clk_r,
  output clk_w
);

  wire j_k_ff_1_q, j_k_ff_1_qn, nand_1_out, nand_2_out, not_1_out;

  not not_1 (not_1_out, clk);
  nand nand_1 (nand_1_out, clk, j_k_ff_1_q);
  J_K_Flip_Flop j_k_ff_1 (
    .J(1'b1), .clk(not_1_out), .K(1'b1), .Q(j_k_ff_1_q), .Qn(j_k_ff_1_qn), .preset(rst), .en(1'b1),
    .reset(1'b0));
  nand nand_2 (nand_2_out, j_k_ff_1_qn, clk);
  buf buffer_1 (clk_r, nand_1_out);
  not not_2 (clk_w, nand_2_out);
endmodule

module Delayer (
  input  in,
  output out
);

  wire not_1_out, not_2_out, not_3_out, not_4_out, not_5_out, not_6_out, not_7_out;

  not not_1 (not_1_out, in);
  not not_2 (not_2_out, not_1_out);
  not not_3 (not_3_out, not_4_out);
  not not_4 (not_4_out, not_2_out);
  not not_5 (not_5_out, not_3_out);
  not not_6 (not_6_out, not_7_out);
  not not_7 (not_7_out, not_5_out);
  not not_8 (out, not_6_out);
endmodule

module CPU (
  input  in_1,
  input  in_2,
  input  in_3,
  input  in_4,
  input  in_5,
  input  in_6,
  input  in_7,
  input  in_8,
  input  MANUAL,
  input  in_10,
  input  in_11,
  input  in_12,
  input  in_13,
  input  in_14,
  input  in_15,
  input  in_16,
  input  in_17,
  output out_18,
  output out_19,
  output out_20,
  output out_21,
  output out_22,
  output out_23,
  output out_24,
  output out_25
);

  wire ADDR_out, alu_1_carry, alu_1_out0, alu_1_out1, alu_1_out2, alu_1_out3, alu_1_out4, alu_1_out5,
       alu_1_out6, alu_1_out7, alu_1_overflow, alu_1_sign, alu_1_zero, and_1_out, and_2_out, and_3_out,
       and_4_out, and_5_out, and_6_out, and_7_out, and_8_out, and_9_out, and_10_out, and_11_out, and_12_out,
       bus0gate_1_out0, bus0gate_1_out1, bus0gate_1_out2, bus0gate_1_out3, bus0gate_1_out4, bus0gate_1_out5,
       bus0gate_1_out6, bus0gate_1_out7, CLOCK_out, controlled_buffer_1_out, controlled_buffer_2_out,
       controlunit_1_bus_0, controlunit_1_cin, controlunit_1_fr_w, controlunit_1_halt, controlunit_1_ir_w,
       controlunit_1_mar_w, controlunit_1_new_cycle, controlunit_1_new_instr, controlunit_1_op0,
       controlunit_1_op1, controlunit_1_op2, controlunit_1_pc_r, controlunit_1_pc_w, controlunit_1_ra_w,
       controlunit_1_ram_r, controlunit_1_ram_w, controlunit_1_rb_w, controlunit_1_rd_r, controlunit_1_rx_r,
       controlunit_1_rx_w, decoder_1_out0, decoder_1_out1, decoder_1_out2, decoder_1_out3, FR_out0, FR_out1,
       FR_out2, FR_out3, HALT_2_q, HALT_2_qn, LDR_out, not_1_out, not_2_out, not_3_out, or_1_out, or_2_out,
       or_3_out, or_4_out, or_5_out, or_6_out, or_7_out, RA_out0, RA_out1, RA_out2, RA_out3, RA_out4,
       RA_out5, RA_out6, RA_out7, RB_out0, RB_out1, RB_out2, RB_out3, RB_out4, RB_out5, RB_out6, RB_out7,
       RESET_3_out, RESET_out, RESUME_out, STEP_out, STR_out;
  wire [1:0] controlunit_1_rx0;
  wire [3:0] CYCLES_q, CYCLES_q_2;
  wire [7:0] INSTR_q, IR_out0;

  ALU alu_1 (
    .a7(RA_out7), .a6(RA_out6), .a5(RA_out5), .a4(RA_out4), .a3(RA_out3), .a2(RA_out2), .a1(RA_out1),
    .a0(RA_out0), .b7(RB_out7), .b6(RB_out6), .b5(RB_out5), .b4(RB_out4), .b3(RB_out3), .b2(RB_out2),
    .b1(RB_out1), .b0(RB_out0), .cin(controlunit_1_cin), .op2(controlunit_1_op2), .op1(controlunit_1_op1),
    .op0(controlunit_1_op0), .out0(alu_1_out0), .out1(alu_1_out1), .out2(alu_1_out2), .out3(alu_1_out3),
    .out4(alu_1_out4), .out5(alu_1_out5), .out6(alu_1_out6), .out7(alu_1_out7), .overflow(alu_1_overflow),
    .sign(alu_1_sign), .zero(alu_1_zero), .carry(alu_1_carry));
  Button RESET (.out(RESET_out));
  LED Reset_2 (.in(RESET_out));
  Button RESUME (.out(RESUME_out));
  not not_1 (not_1_out, MANUAL);
  assign controlled_buffer_1_out = MANUAL ? STEP_out : 1'bz;  // Controlled_Buffer controlled_buffer_1
  Button STEP (.out(STEP_out));
  Clock_part CLOCK (.out(CLOCK_out));
  Pull_Resistor pull_resistor_1 (.node(controlled_buffer_1_out));
  Reg8 RA (
    .in0(out_25), .in1(out_24), .in2(out_23), .in3(out_22), .in4(out_21), .in5(out_20), .in6(out_19),
    .in7(out_18), .read(1'b1), .write(controlunit_1_ra_w), .reset(RESET_out), .out0(RA_out0), .out1(RA_out1),
    .out2(RA_out2), .out3(RA_out3), .out4(RA_out4), .out5(RA_out5), .out6(RA_out6), .out7(RA_out7));
  LED Auto (.in(not_2_out));
  LED u_Manual (.in(MANUAL));
  not not_2 (not_2_out, MANUAL);
  or or_1 (or_1_out, controlled_buffer_1_out, controlled_buffer_2_out);
  assign controlled_buffer_2_out = not_1_out ? CLOCK_out : 1'bz;  // Controlled_Buffer controlled_buffer_2
  Pull_Resistor pull_resistor_2 (.node(controlled_buffer_2_out));
  Reg8 RB (
    .in0(bus0gate_1_out0), .in1(bus0gate_1_out1), .in2(bus0gate_1_out2), .in3(bus0gate_1_out3),
    .in4(bus0gate_1_out4), .in5(bus0gate_1_out5), .in6(bus0gate_1_out6), .in7(bus0gate_1_out7), .read(1'b1),
    .write(controlunit_1_rb_w), .reset(RESET_out), .out0(RB_out0), .out1(RB_out1), .out2(RB_out2),
    .out3(RB_out3), .out4(RB_out4), .out5(RB_out5), .out6(RB_out6), .out7(RB_out7));
  Reg8 RD (
    .in0(alu_1_out0), .in1(alu_1_out1), .in2(alu_1_out2), .in3(alu_1_out3), .in4(alu_1_out4),
    .in5(alu_1_out5), .in6(alu_1_out6), .in7(alu_1_out7), .read(controlunit_1_rd_r), .write(1'b1),
    .reset(RESET_out), .out0(out_25), .out1(out_24), .out2(out_23), .out3(out_22), .out4(out_21),
    .out5(out_20), .out6(out_19), .out7(out_18));
  LED Clock_2 (.in(or_1_out));
  LED Halt (.in(HALT_2_q));
  not not_3 (not_3_out, not_2_out);
  Bus0Gate bus0gate_1 (
    .bus_0(controlunit_1_bus_0), .in7(out_18), .in6(out_19), .in5(out_20), .in4(out_21), .in3(out_22),
    .in2(out_23), .in1(out_24), .in0(out_25), .out7(bus0gate_1_out7), .out6(bus0gate_1_out6),
    .out5(bus0gate_1_out5), .out4(bus0gate_1_out4), .out3(bus0gate_1_out3), .out2(bus0gate_1_out2),
    .out1(bus0gate_1_out1), .out0(bus0gate_1_out0));
  and and_1 (and_1_out, ~HALT_2_q, or_1_out);  // AND_Gate
  Reg4 FR (
    .in0(alu_1_zero), .in1(alu_1_sign), .in2(alu_1_carry), .in3(alu_1_overflow), .read(1'b1),
    .write(controlunit_1_fr_w), .out0(FR_out0), .out1(FR_out1), .out2(FR_out2), .out3(FR_out3),
    .reset(RESET_out));
  ControlUnit controlunit_1 (
    .op0(controlunit_1_op0), .op1(controlunit_1_op1), .op2(controlunit_1_op2), .fr_w(controlunit_1_fr_w),
    .mar_w(controlunit_1_mar_w), .ram_r(controlunit_1_ram_r), .ram_w(controlunit_1_ram_w), .carry(FR_out2),
    .sign(FR_out1), .zero(FR_out0), .ra_w(controlunit_1_ra_w), .rb_w(controlunit_1_rb_w),
    .bus_0(controlunit_1_bus_0), .rx_r(controlunit_1_rx_r), .rx_w(controlunit_1_rx_w), .clk(and_1_out),
    .rst(RESET_out), .rd_r(controlunit_1_rd_r), .ir0(IR_out0[0]), .ir1(IR_out0[1]), .ir2(IR_out0[2]),
    .ir3(IR_out0[3]), .ir4(IR_out0[4]), .ir5(IR_out0[5]), .ir6(IR_out0[6]), .ir7(IR_out0[7]),
    .ir_w(controlunit_1_ir_w), .pc_w(controlunit_1_pc_w), .pc_r(controlunit_1_pc_r), .overflow(FR_out3),
    .halt(controlunit_1_halt), .cin(controlunit_1_cin), .new_instr(controlunit_1_new_instr),
    .new_cycle(controlunit_1_new_cycle), .rx0(controlunit_1_rx0[0]), .rx1(controlunit_1_rx0[1]));  // open: io_in_out, io_data_addr, io
  D_Flip_Flop HALT_2 (
    .clk(controlunit_1_halt), .D(HALT_2_qn), .Q(HALT_2_q), .Qn(HALT_2_qn), .en(1'b1), .reset(or_2_out));  // open: preset
  or or_2 (or_2_out, RESUME_out, RESET_out);
  Reg8 R0 (
    .in0(out_25), .in1(out_24), .in2(out_23), .in3(out_22), .in4(out_21), .in5(out_20), .in6(out_19),
    .in7(out_18), .read(and_2_out), .write(and_3_out), .reset(RESET_out), .out0(out_25), .out1(out_24),
    .out2(out_23), .out3(out_22), .out4(out_21), .out5(out_20), .out6(out_19), .out7(out_18));
  and and_2 (and_2_out, controlunit_1_rx_r, decoder_1_out0);
  Decoder #(.select(2), .enable("false")) decoder_1 (
    .out0(decoder_1_out0), .out1(decoder_1_out1), .out2(decoder_1_out2), .out3(decoder_1_out3),
    .sel(controlunit_1_rx0));
  Counter #(.trigger("falling")) INSTR (
    .load(1'b0), .count(1'b1), .Q(INSTR_q), .clk(controlunit_1_new_instr), .clr(RESET_out));  // open: D, carry
  Hex_Digit_Display hex_digit_display_1 (.value(INSTR_q[3:0]));  // open: dp
  Hex_Digit_Display hex_digit_display_2 (.value(INSTR_q[7:4]));  // open: dp
  and and_3 (and_3_out, decoder_1_out0, controlunit_1_rx_w);
  Counter CYCLES (
    .load(1'b0), .count(1'b1), .Q({CYCLES_q_2, CYCLES_q}), .clk(controlunit_1_new_cycle), .clr(or_3_out));  // open: D, carry
  or or_3 (or_3_out, controlunit_1_new_instr, RESET_out);
  Hex_Digit_Display hex_digit_display_3 (.value(CYCLES_q_2));  // open: dp
  Reg8 IR (
    .in0(out_25), .in1(out_24), .in2(out_23), .in3(out_22), .in4(out_21), .in5(out_20), .in6(out_19),
    .in7(out_18), .read(1'b1), .write(controlunit_1_ir_w), .reset(RESET_out), .out0(IR_out0[0]),
    .out1(IR_out0[1]), .out2(IR_out0[2]), .out3(IR_out0[3]), .out4(IR_out0[4]), .out5(IR_out0[5]),
    .out6(IR_out0[6]), .out7(IR_out0[7]));
  Hex_Digit_Display hex_digit_display_4 (.value(CYCLES_q));  // open: dp
  Reg8 R1 (
    .in0(out_25), .in1(out_24), .in2(out_23), .in3(out_22), .in4(out_21), .in5(out_20), .in6(out_19),
    .in7(out_18), .read(and_4_out), .write(and_5_out), .reset(RESET_out), .out0(out_25), .out1(out_24),
    .out2(out_23), .out3(out_22), .out4(out_21), .out5(out_20), .out6(out_19), .out7(out_18));
  and and_4 (and_4_out, controlunit_1_rx_r, decoder_1_out1);
  and and_5 (and_5_out, decoder_1_out1, controlunit_1_rx_w);
  and and_6 (and_6_out, not_3_out, LDR_out);
  and and_7 (and_7_out, ADDR_out, not_3_out);
  Button LDR (.out(LDR_out));
  Button ADDR (.out(ADDR_out));
  Reg8 R2 (
    .in0(out_25), .in1(out_24), .in2(out_23), .in3(out_22), .in4(out_21), .in5(out_20), .in6(out_19),
    .in7(out_18), .read(and_8_out), .write(and_10_out), .reset(RESET_out), .out0(out_25), .out1(out_24),
    .out2(out_23), .out3(out_22), .out4(out_21), .out5(out_20), .out6(out_19), .out7(out_18));
  and and_8 (and_8_out, controlunit_1_rx_r, decoder_1_out2);
  Reg8 PC (
    .in0(out_25), .in1(out_24), .in2(out_23), .in3(out_22), .in4(out_21), .in5(out_20), .in6(out_19),
    .in7(out_18), .read(controlunit_1_pc_r), .write(controlunit_1_pc_w), .reset(RESET_out), .out0(out_25),
    .out1(out_24), .out2(out_23), .out3(out_22), .out4(out_21), .out5(out_20), .out6(out_19), .out7(out_18));
  and and_9 (and_9_out, not_3_out, STR_out);
  Button STR (.out(STR_out));
  and and_10 (and_10_out, decoder_1_out2, controlunit_1_rx_w);
  assign out_20 = and_7_out ? in_3 : 1'bz;  // Controlled_Buffer controlled_buffer_3
  assign out_19 = and_7_out ? in_2 : 1'bz;  // Controlled_Buffer controlled_buffer_4
  assign out_18 = and_7_out ? in_1 : 1'bz;  // Controlled_Buffer controlled_buffer_5
  assign out_21 = and_7_out ? in_4 : 1'bz;  // Controlled_Buffer controlled_buffer_6
  assign out_20 = and_9_out ? in_12 : 1'bz;  // Controlled_Buffer controlled_buffer_7
  assign out_21 = and_9_out ? in_13 : 1'bz;  // Controlled_Buffer controlled_buffer_8
  assign out_19 = and_9_out ? in_11 : 1'bz;  // Controlled_Buffer controlled_buffer_9
  assign out_18 = and_9_out ? in_10 : 1'bz;  // Controlled_Buffer controlled_buffer_10
  assign out_23 = and_7_out ? in_6 : 1'bz;  // Controlled_Buffer controlled_buffer_11
  assign out_25 = and_7_out ? in_8 : 1'bz;  // Controlled_Buffer controlled_buffer_12
  assign out_22 = and_7_out ? in_5 : 1'bz;  // Controlled_Buffer controlled_buffer_13
  assign out_24 = and_7_out ? in_7 : 1'bz;  // Controlled_Buffer controlled_buffer_14
  assign out_25 = and_9_out ? in_17 : 1'bz;  // Controlled_Buffer controlled_buffer_15
  assign out_23 = and_9_out ? in_15 : 1'bz;  // Controlled_Buffer controlled_buffer_16
  assign out_24 = and_9_out ? in_16 : 1'bz;  // Controlled_Buffer controlled_buffer_17
  assign out_22 = and_9_out ? in_14 : 1'bz;  // Controlled_Buffer controlled_buffer_18
  Reg8 R3 (
    .in0(out_25), .in1(out_24), .in2(out_23), .in3(out_22), .in4(out_21), .in5(out_20), .in6(out_19),
    .in7(out_18), .read(and_11_out), .write(and_12_out), .reset(RESET_out), .out0(out_25), .out1(out_24),
    .out2(out_23), .out3(out_22), .out4(out_21), .out5(out_20), .out6(out_19), .out7(out_18));
  and and_11 (and_11_out, controlunit_1_rx_r, decoder_1_out3);
  and and_12 (and_12_out, decoder_1_out3, controlunit_1_rx_w);
  or or_4 (or_4_out, controlunit_1_mar_w, and_7_out);
  or or_5 (or_5_out, controlunit_1_ram_r, and_6_out);
  or or_6 (or_6_out, controlunit_1_ram_w, and_9_out);
  or or_7 (or_7_out, and_1_out, and_7_out, and_6_out, and_9_out);
  Button RESET_3 (.out(RESET_3_out));
  Ram256 ram256_1 (
    .addr0(out_25), .addr1(out_24), .addr2(out_23), .addr3(out_22), .addr4(out_21), .addr5(out_20),
    .addr6(out_19), .addr7(out_18), .marw(or_4_out), .read(or_5_out), .write(or_6_out), .reset(RESET_3_out),
    .in0(out_25), .in1(out_24), .in2(out_23), .in3(out_22), .in4(out_21), .in5(out_20), .in6(out_19),
    .in7(out_18), .out0(out_25), .out1(out_24), .out2(out_23), .out3(out_22), .out4(out_21), .out5(out_20),
    .out6(out_19), .out7(out_18), .clk(or_7_out));

  // Notes on the sheet:
  //   0000 00 00  ->  nop            ->  do nothing
  //   0001 00 rb  ->  data rb, imm8  ->  rb = ram[pc++]
  //   0010 ra rb  ->  ldr  ra, [rb]  ->  ra = ram[rb]
  //   0011 ra rb  ->  str  ra, [rb]  ->  ram[rb] = ra
  //   0100 00 00  ->  jalr rb        ->  pc <-> rb
  //   0101 vc sz  ->  b<cond> imm8   ->  pc = cond ? ram[pc] : pc+1
  //   0110 00 00  ->  halt           ->  stop computer
  //   0111 00 rb  ->  in   data, rb  ->  rb = io[active].data
  //   0111 10 rb  ->  out  data, rb  ->  io[active].data = rb
  //   0111 01 rb  ->  in   addr, rb  ->  rb = io[active].addr
  //   0111 11 rb  ->  out  addr, rb  ->  io[rb].active = true
  //   1000 ra rb  ->  add ra, rb  ->  ra = ra + rb       [vcsz]
  //   1001 ra rb  ->  sub ra, rb  ->  ra = ra - rb       [vcsz]
  //   1010 ra rb  ->  shl ra, rb  ->  ra = [rb << 1, 0]  [0csz]
  //   1011 ra rb  ->  shr ra, rb  ->  ra = [0, rb >> 1]  [0csz]
  //   1100 ra rb  ->  and ra, rb  ->  ra = ra & rb       [00sz]
  //   1101 ra rb  ->  orr ra, rb  ->  ra = ra | rb       [00sz]
  //   1110 ra rb  ->  xor ra, rb  ->  ra = ra ^ rb       [00sz]
  //   1111 ra rb  ->  cmp ra, rb  ->  fr = ra >= rb ?    [vcsz]
endmodule
