// Logisim project scottV3.circ as structural Verilog: 17 circuits, main circuit CPU
module Ram256 (
  input  addr0,
  input  addr1,
  input  addr2,
  input  addr3,
  input  addr4,
  input  addr5,
  input  addr6,
  input  addr7,
  input  read,
  input  write,
  input  clk,
  input  reset,
  input  in0,
  input  in1,
  input  in2,
  input  in3,
  input  in4,
  input  in5,
  input  in6,
  input  in7,
  output out0,
  output out1,
  output out2,
  output out3,
  output out4,
  output out5,
  output out6,
  output out7
);

  wire or_1_out;

  or or_1 (or_1_out, read, write);
  RAM #(.bus("separate")) ram_1 (
    .addr({addr7, addr6, addr5, addr4, addr3, addr2, addr1, addr0}),
    .din({in7, in6, in5, in4, in3, in2, in1, in0}), .data({out7, out6, out5, out4, out3, out2, out1, out0}),
    .str(write), .sel(or_1_out), .clk(clk), .ld(read), .clr(reset));
endmodule

module Enabler8 (
  input  enable,
  input  in0,
  input  in1,
  input  in2,
  input  in3,
  input  in4,
  input  in5,
  input  in6,
  input  in7,
  output out0,
  output out1,
  output out2,
  output out3,
  output out4,
  output out6,
  output out6_2,
  output out7
);

  assign out0 = enable ? in0 : 1'bz;  // Controlled_Buffer controlled_buffer_1
  assign out1 = enable ? in1 : 1'bz;  // Controlled_Buffer controlled_buffer_2
  assign out2 = enable ? in2 : 1'bz;  // Controlled_Buffer controlled_buffer_3
  assign out3 = enable ? in3 : 1'bz;  // Controlled_Buffer controlled_buffer_4
  assign out4 = enable ? in4 : 1'bz;  // Controlled_Buffer controlled_buffer_5
  assign out6 = enable ? in5 : 1'bz;  // Controlled_Buffer controlled_buffer_6
  assign out6_2 = enable ? in6 : 1'bz;  // Controlled_Buffer controlled_buffer_7
  assign out7 = enable ? in7 : 1'bz;  // Controlled_Buffer controlled_buffer_8
endmodule

module LeftShifter8 (
  input  cin,
  input  in0,
  input  in1,
  input  in2,
  input  in3,
  input  in4,
  input  in5,
  input  in6,
  input  in7,
  output out0,
  output out1,
  output out2,
  output out3,
  output out4,
  output out6,
  output out6_2,
  output out7,
  output cout
);


  assign cout = in7;
  assign out0 = cin;
  assign out1 = in0;
  assign out2 = in1;
  assign out3 = in2;
  assign out4 = in3;
  assign out6 = in4;
  assign out6_2 = in5;
  assign out7 = in6;
endmodule

module RightShifter8 (
  input  in0,
  input  in1,
  input  in2,
  input  in3,
  input  in4,
  input  in5,
  input  in6,
  input  in7,
  input  cin,
  output cout,
  output out0,
  output out1,
  output out2,
  output out3,
  output out4,
  output out6,
  output out6_2,
  output out7
);


  assign cout = in0;
  assign out0 = in1;
  assign out1 = in2;
  assign out2 = in3;
  assign out3 = in4;
  assign out4 = in5;
  assign out6 = in6;
  assign out6_2 = in7;
  assign out7 = cin;
endmodule

module Notter8 (
  input  in0,
  input  in1,
  input  in2,
  input  in3,
  input  in4,
  input  in5,
  input  in6,
  input  in7,
  output out0,
  output out1,
  output out2,
  output out3,
  output out4,
  output out6,
  output out6_2,
  output out7
);

  not not_1 (out0, in0);
  not not_2 (out1, in1);
  not not_3 (out2, in2);
  not not_4 (out3, in3);
  not not_5 (out4, in4);
  not not_6 (out6, in5);
  not not_7 (out6_2, in6);
  not not_8 (out7, in7);
endmodule

module Ander8 (
  input  a0,
  input  b0,
  input  a1,
  input  b1,
  input  a2,
  input  b2,
  input  a3,
  input  b3,
  input  a4,
  input  b4,
  input  a5,
  input  b5,
  input  a6,
  input  b6,
  input  a7,
  input  b7,
  output out0,
  output out1,
  output out2,
  output out3,
  output out4,
  output out5,
  output out6,
  output out7
);

  and and_1 (out0, a0, b0);
  and and_2 (out1, a1, b1);
  and and_3 (out2, a2, b2);
  and and_4 (out3, a3, b3);
  and and_5 (out4, a4, b4);
  and and_6 (out5, a5, b5);
  and and_7 (out6, a6, b6);
  and and_8 (out7, a7, b7);
endmodule

module Orer8 (
  input  a0,
  input  b0,
  input  a1,
  input  b1,
  input  a2,
  input  b2,
  input  a3,
  input  b3,
  input  a4,
  input  b4,
  input  a5,
  input  b5,
  input  a6,
  input  b6,
  input  a7,
  input  b7,
  output out0,
  output out1,
  output out2,
  output out3,
  output out4,
  output out5,
  output out6,
  output out7
);

  or or_1 (out0, a0, b0);
  or or_2 (out1, a1, b1);
  or or_3 (out2, a2, b2);
  or or_4 (out3, a3, b3);
  or or_5 (out4, a4, b4);
  or or_6 (out5, a5, b5);
  or or_7 (out6, a6, b6);
  or or_8 (out7, a7, b7);
endmodule

module Xorer8 (
  input  a0,
  input  b0,
  input  a1,
  input  b1,
  input  a2,
  input  b2,
  input  a3,
  input  b3,
  input  a4,
  input  b4,
  input  a5,
  input  b5,
  input  a6,
  input  b6,
  input  a7,
  input  b7,
  output out0,
  output out1,
  output out2,
  output out3,
  output out4,
  output out5,
  output out6,
  output out7
);

  xor xor_1 (out0, a0, b0);
  xor xor_2 (out1, a1, b1);
  xor xor_3 (out2, a2, b2);
  xor xor_4 (out3, a3, b3);
  xor xor_5 (out4, a4, b4);
  xor xor_6 (out5, a5, b5);
  xor xor_7 (out6, a6, b6);
  xor xor_8 (out7, a7, b7);
endmodule

module FullAdder (
  input  a,
  input  b,
  input  cin,
  output sum,
  output cout
);

  wire and_1_out, and_2_out, xor_1_out;

  xor xor_1 (xor_1_out, a, b);
  xor xor_2 (sum, xor_1_out, cin);
  and and_1 (and_1_out, xor_1_out, cin);
  and and_2 (and_2_out, a, b);
  or or_1 (cout, and_1_out, and_2_out);
endmodule

module Adder8 (
  input  cin,
  input  a0,
  input  b0,
  input  a1,
  input  b1,
  input  a2,
  input  b2,
  input  a3,
  input  b3,
  input  a4,
  input  b4,
  input  a5,
  input  b5,
  input  a6,
  input  b6,
  input  a7,
  input  b7,
  output out0,
  output out1,
  output out2,
  output out3,
  output out4,
  output out5,
  output out6,
  output out7,
  output ovcarry,
  output cout
);

  wire fulladder_1_cout, fulladder_2_cout, fulladder_3_cout, fulladder_4_cout, fulladder_5_cout,
       fulladder_6_cout;

  FullAdder fulladder_1 (.a(a0), .b(b0), .cin(cin), .sum(out0), .cout(fulladder_1_cout));
  FullAdder fulladder_2 (.a(a1), .b(b1), .cin(fulladder_1_cout), .sum(out1), .cout(fulladder_2_cout));
  FullAdder fulladder_3 (.a(a2), .b(b2), .cin(fulladder_2_cout), .sum(out2), .cout(fulladder_3_cout));
  FullAdder fulladder_4 (.a(a3), .b(b3), .cin(fulladder_3_cout), .sum(out3), .cout(fulladder_4_cout));
  FullAdder fulladder_5 (.a(a4), .b(b4), .cin(fulladder_4_cout), .sum(out4), .cout(fulladder_5_cout));
  FullAdder fulladder_6 (.a(a5), .b(b5), .cin(fulladder_5_cout), .sum(out5), .cout(fulladder_6_cout));
  FullAdder fulladder_7 (.a(a6), .b(b6), .cin(fulladder_6_cout), .sum(out6), .cout(ovcarry));
  FullAdder fulladder_8 (.a(a7), .b(b7), .cin(ovcarry), .sum(out7), .cout(cout));
endmodule

module AddSub8 (
  input  sub,
  input  a0,
  input  b0,
  input  a1,
  input  b1,
  input  a2,
  input  b2,
  input  a3,
  input  b3,
  input  a4,
  input  b4,
  input  a5,
  input  b5,
  input  a6,
  input  b6,
  input  a7,
  input  b7,
  input  cin,
  output carry,
  output overflow,
  output out7,
  output out6,
  output out5,
  output out4,
  output out3,
  output out2,
  output out1,
  output out0
);

  wire adder8_1_cout, adder8_1_ovcarry, xor_3_out, xor_4_out, xor_5_out, xor_6_out, xor_7_out, xor_8_out,
       xor_9_out, xor_10_out, xor_11_out;

  xor xor_1 (carry, sub, adder8_1_cout);
  xor xor_2 (overflow, adder8_1_ovcarry, adder8_1_cout);
  xor xor_3 (xor_3_out, sub, b0);
  xor xor_4 (xor_4_out, sub, b1);
  xor xor_5 (xor_5_out, sub, b2);
  xor xor_6 (xor_6_out, sub, b3);
  xor xor_7 (xor_7_out, sub, b4);
  xor xor_8 (xor_8_out, sub, b5);
  xor xor_9 (xor_9_out, sub, b6);
  xor xor_10 (xor_10_out, sub, b7);
  Adder8 adder8_1 (
    .cin(xor_11_out), .a0(a0), .b0(xor_3_out), .a1(a1), .b1(xor_4_out), .a2(a2), .b2(xor_5_out), .a3(a3),
    .b3(xor_6_out), .a4(a4), .b4(xor_7_out), .a5(a5), .b5(xor_8_out), .a6(a6), .b6(xor_9_out), .a7(a7),
    .b7(xor_10_out), .out0(out0), .out1(out1), .out2(out2), .out3(out3), .out4(out4), .out5(out5),
    .out6(out6), .out7(out7), .ovcarry(adder8_1_ovcarry), .cout(adder8_1_cout));
  xor xor_11 (xor_11_out, sub, cin);
endmodule

module Bus0Gate (
  input  in7,
  input  in6,
  input  in5,
  input  in4,
  input  in3,
  input  in2,
  input  in1,
  input  in0,
  input  bus_0,
  output out7,
  output out6,
  output out5,
  output out4,
  output out3,
  output out2,
  output out1,
  output out0
);

  wire not_1_out;

  and and_1 (out6, in6, not_1_out);
  and and_2 (out7, in7, not_1_out);
  and and_3 (out5, in5, not_1_out);
  and and_4 (out4, in4, not_1_out);
  and and_5 (out2, in2, not_1_out);
  and and_6 (out1, in1, not_1_out);
  and and_7 (out3, in3, not_1_out);
  not not_1 (not_1_out, bus_0);
  and and_8 (out0, in0, not_1_out);
endmodule

module ALU (
  input  a7,
  input  a6,
  input  a5,
  input  a4,
  input  a3,
  input  a2,
  input  a1,
  input  a0,
  input  b7,
  input  b6,
  input  b5,
  input  b4,
  input  b3,
  input  b2,
  input  b1,
  input  b0,
  input  op2,
  input  op1,
  input  op0,
  input  cin,
  output out0,
  output out1,
  output out2,
  output out3,
  output out4,
  output out5,
  output out6,
  output out7,
  output overflow,
  output carry,
  output sign,
  output zero
);

  wire addsub8_1_carry, addsub8_1_out0, addsub8_1_out1, addsub8_1_out2, addsub8_1_out3, addsub8_1_out4,
       addsub8_1_out5, addsub8_1_out6, addsub8_1_out7, addsub8_1_overflow, ander8_1_out0, ander8_1_out1,
       ander8_1_out2, ander8_1_out3, ander8_1_out4, ander8_1_out5, ander8_1_out6, ander8_1_out7,
       leftshifter8_1_cout, leftshifter8_1_out0, leftshifter8_1_out1, leftshifter8_1_out2,
       leftshifter8_1_out3, leftshifter8_1_out4, leftshifter8_1_out6, leftshifter8_1_out6_2,
       leftshifter8_1_out7, nor_2_out, or_1_out, orer8_1_out0, orer8_1_out1, orer8_1_out2, orer8_1_out3,
       orer8_1_out4, orer8_1_out5, orer8_1_out6, orer8_1_out7, rightshifter8_1_cout, rightshifter8_1_out0,
       rightshifter8_1_out1, rightshifter8_1_out2, rightshifter8_1_out3, rightshifter8_1_out4,
       rightshifter8_1_out6, rightshifter8_1_out6_2, rightshifter8_1_out7, xorer8_1_out0, xorer8_1_out1,
       xorer8_1_out2, xorer8_1_out3, xorer8_1_out4, xorer8_1_out5, xorer8_1_out6, xorer8_1_out7;
  wire [7:0] decoder_1_out0;

  Ander8 ander8_1 (
    .a0(a0), .b0(b0), .a1(a1), .b1(b1), .a2(a2), .b2(b2), .a3(a3), .b3(b3), .a4(a4), .b4(b4), .a5(a5),
    .b5(b5), .a6(a6), .b6(b6), .a7(a7), .b7(b7), .out0(ander8_1_out0), .out1(ander8_1_out1),
    .out2(ander8_1_out2), .out3(ander8_1_out3), .out4(ander8_1_out4), .out5(ander8_1_out5),
    .out6(ander8_1_out6), .out7(ander8_1_out7));
  Orer8 orer8_1 (
    .a0(a0), .b0(b0), .a1(a1), .b1(b1), .a2(a2), .b2(b2), .a3(a3), .b3(b3), .a4(a4), .b4(b4), .a5(a5),
    .b5(b5), .a6(a6), .b6(b6), .a7(a7), .b7(b7), .out0(orer8_1_out0), .out1(orer8_1_out1),
    .out2(orer8_1_out2), .out3(orer8_1_out3), .out4(orer8_1_out4), .out5(orer8_1_out5), .out6(orer8_1_out6),
    .out7(orer8_1_out7));
  Xorer8 xorer8_1 (
    .a0(a0), .b0(b0), .a1(a1), .b1(b1), .a2(a2), .b2(b2), .a3(a3), .b3(b3), .a4(a4), .b4(b4), .a5(a5),
    .b5(b5), .a6(a6), .b6(b6), .a7(a7), .b7(b7), .out0(xorer8_1_out0), .out1(xorer8_1_out1),
    .out2(xorer8_1_out2), .out3(xorer8_1_out3), .out4(xorer8_1_out4), .out5(xorer8_1_out5),
    .out6(xorer8_1_out6), .out7(xorer8_1_out7));
  AddSub8 addsub8_1 (
    .cin(cin), .a0(a0), .b0(b0), .a1(a1), .b1(b1), .a2(a2), .b2(b2), .a3(a3), .b3(b3), .a4(a4), .b4(b4),
    .a5(a5), .b5(b5), .a6(a6), .b6(b6), .a7(a7), .b7(b7), .out0(addsub8_1_out0), .out1(addsub8_1_out1),
    .out2(addsub8_1_out2), .out3(addsub8_1_out3), .out4(addsub8_1_out4), .out5(addsub8_1_out5),
    .out6(addsub8_1_out6), .out7(addsub8_1_out7), .carry(addsub8_1_carry), .sub(decoder_1_out0[5]),
    .overflow(addsub8_1_overflow));
  LeftShifter8 leftshifter8_1 (
    .cin(cin), .in0(b0), .in1(b1), .in2(b2), .in3(b3), .in4(b4), .in5(b5), .in6(b6), .in7(b7),
    .out0(leftshifter8_1_out0), .out1(leftshifter8_1_out1), .out2(leftshifter8_1_out2),
    .out3(leftshifter8_1_out3), .out4(leftshifter8_1_out4), .out6(leftshifter8_1_out6),
    .out6_2(leftshifter8_1_out6_2), .out7(leftshifter8_1_out7), .cout(leftshifter8_1_cout));
  RightShifter8 rightshifter8_1 (
    .in0(b0), .in1(b1), .in2(b2), .in3(b3), .in4(b4), .in5(b5), .in6(b6), .in7(b7), .cin(cin),
    .cout(rightshifter8_1_cout), .out0(rightshifter8_1_out0), .out1(rightshifter8_1_out1),
    .out2(rightshifter8_1_out2), .out3(rightshifter8_1_out3), .out4(rightshifter8_1_out4),
    .out6(rightshifter8_1_out6), .out6_2(rightshifter8_1_out6_2), .out7(rightshifter8_1_out7));
  Decoder #(.select(3), .enable("false")) decoder_1 (
    .out0(decoder_1_out0[0]), .out1(decoder_1_out0[1]), .out2(decoder_1_out0[2]), .out3(decoder_1_out0[3]),
    .out4(decoder_1_out0[4]), .out5(decoder_1_out0[5]), .out6(decoder_1_out0[6]), .out7(decoder_1_out0[7]),
    .sel({op2, op1, op0}));
  Enabler8 enabler8_1 (
    .in0(b0), .in1(b1), .in2(b2), .in3(b3), .in4(b4), .in5(b5), .in6(b6), .in7(b7),
    .enable(decoder_1_out0[0]), .out0(out0), .out1(out1), .out2(out2), .out3(out3), .out4(out4), .out6(out5),
    .out6_2(out6), .out7(out7));
  Enabler8 enabler8_2 (
    .in0(ander8_1_out0), .in1(ander8_1_out1), .in2(ander8_1_out2), .in3(ander8_1_out3), .in4(ander8_1_out4),
    .in5(ander8_1_out5), .in6(ander8_1_out6), .in7(ander8_1_out7), .enable(decoder_1_out0[1]), .out0(out0),
    .out1(out1), .out2(out2), .out3(out3), .out4(out4), .out6(out5), .out6_2(out6), .out7(out7));
  Enabler8 enabler8_3 (
    .in0(orer8_1_out0), .in1(orer8_1_out1), .in2(orer8_1_out2), .in3(orer8_1_out3), .in4(orer8_1_out4),
    .in5(orer8_1_out5), .in6(orer8_1_out6), .in7(orer8_1_out7), .enable(decoder_1_out0[2]), .out0(out0),
    .out1(out1), .out2(out2), .out3(out3), .out4(out4), .out6(out5), .out6_2(out6), .out7(out7));
  Enabler8 enabler8_4 (
    .in0(xorer8_1_out0), .in1(xorer8_1_out1), .in2(xorer8_1_out2), .in3(xorer8_1_out3), .in4(xorer8_1_out4),
    .in5(xorer8_1_out5), .in6(xorer8_1_out6), .in7(xorer8_1_out7), .enable(decoder_1_out0[3]), .out0(out0),
    .out1(out1), .out2(out2), .out3(out3), .out4(out4), .out6(out5), .out6_2(out6), .out7(out7));
  or or_1 (or_1_out, decoder_1_out0[4], decoder_1_out0[5]);
  Enabler8 enabler8_5 (
    .in0(addsub8_1_out0), .in1(addsub8_1_out1), .in2(addsub8_1_out2), .in3(addsub8_1_out3),
    .in4(addsub8_1_out4), .in5(addsub8_1_out5), .in6(addsub8_1_out6), .in7(addsub8_1_out7),
    .enable(or_1_out), .out0(out0), .out1(out1), .out2(out2), .out3(out3), .out4(out4), .out6(out5),
    .out6_2(out6), .out7(out7));
  Enabler8 enabler8_6 (
    .in0(leftshifter8_1_out0), .in1(leftshifter8_1_out1), .in2(leftshifter8_1_out2),
    .in3(leftshifter8_1_out3), .in4(leftshifter8_1_out4), .in5(leftshifter8_1_out6),
    .in6(leftshifter8_1_out6_2), .in7(leftshifter8_1_out7), .enable(decoder_1_out0[6]), .out0(out0),
    .out1(out1), .out2(out2), .out3(out3), .out4(out4), .out6(out5), .out6_2(out6), .out7(out7));
  Enabler8 enabler8_7 (
    .in0(rightshifter8_1_out0), .in1(rightshifter8_1_out1), .in2(rightshifter8_1_out2),
    .in3(rightshifter8_1_out3), .in4(rightshifter8_1_out4), .in5(rightshifter8_1_out6),
    .in6(rightshifter8_1_out6_2), .in7(rightshifter8_1_out7), .enable(decoder_1_out0[7]), .out0(out0),
    .out1(out1), .out2(out2), .out3(out3), .out4(out4), .out6(out5), .out6_2(out6), .out7(out7));
  nor nor_1 (zero, out7, out6, out5, out4, out3, out2, out1, out0);
  Multiplexer #(.enable("false")) multiplexer_1 (.in0(1'b0), .in1(addsub8_1_overflow), .out(overflow), .sel(or_1_out));
  nor nor_2 (nor_2_out, or_1_out, decoder_1_out0[6], decoder_1_out0[7]);
  assign carry = nor_2_out ? 1'b0 : 1'bz;  // Controlled_Buffer controlled_buffer_1
  assign carry = or_1_out ? addsub8_1_carry : 1'bz;  // Controlled_Buffer controlled_buffer_2
  assign carry = decoder_1_out0[6] ? leftshifter8_1_cout : 1'bz;  // Controlled_Buffer controlled_buffer_3
  assign carry = decoder_1_out0[7] ? rightshifter8_1_cout : 1'bz;  // Controlled_Buffer controlled_buffer_4

  assign sign = out7;
endmodule

module Delayer (
  input  in,
  output out
);

  wire not_1_out, not_2_out, not_3_out, not_4_out, not_5_out, not_6_out, not_7_out;

  not not_1 (not_1_out, not_2_out);
  not not_2 (not_2_out, in);
  not not_3 (not_3_out, not_5_out);
  not not_4 (not_4_out, not_3_out);
  not not_5 (not_5_out, not_1_out);
  not not_6 (not_6_out, not_4_out);
  not not_7 (not_7_out, not_6_out);
  not not_8 (out, not_7_out);
endmodule

module BranchChecker (
  input  zero,
  input  sign,
  input  carry,
  input  overflow,
  input  op2,
  input  op1,
  input  op0,
  output result
);

  wire and_1_out, and_2_out, and_3_out, and_4_out, and_5_out, and_6_out, and_7_out, decoder_1_out0,
       decoder_1_out1, decoder_1_out2, decoder_1_out3, decoder_1_out4, decoder_1_out5, decoder_1_out6,
       decoder_1_out7, or_1_out, or_2_out, xor_1_out;

  Decoder #(.select(3), .enable("false")) decoder_1 (
    .out0(decoder_1_out0), .out1(decoder_1_out1), .out2(decoder_1_out2), .out3(decoder_1_out3),
    .out4(decoder_1_out4), .out5(decoder_1_out5), .out6(decoder_1_out6), .out7(decoder_1_out7),
    .sel({op2, op1, op0}));
  or or_1 (or_1_out, zero, xor_1_out);
  xor xor_1 (xor_1_out, overflow, sign);
  or or_2 (or_2_out, carry, zero);
  and and_1 (and_1_out, decoder_1_out1, zero);
  and and_2 (and_2_out, decoder_1_out2, sign);
  and and_3 (and_3_out, decoder_1_out3, overflow);
  and and_4 (and_4_out, decoder_1_out4, carry);
  and and_5 (and_5_out, decoder_1_out5, or_2_out);
  and and_6 (and_6_out, decoder_1_out6, xor_1_out);
  and and_7 (and_7_out, decoder_1_out7, or_1_out);
  or or_3 (result, and_7_out, and_6_out, and_5_out, and_4_out, and_3_out, and_2_out, and_1_out, decoder_1_out0);
endmodule

module CPU (
  input  in_1,
  input  in_2,
  input  in_3,
  input  in_4,
  input  in_5,
  input  in_6,
  input  in_7,
  input  in_8,
  input  MANUAL,
  input  in_10,
  input  in_11,
  input  in_12,
  input  in_13,
  input  in_14,
  input  in_15,
  input  in_16,
  input  in_17,
  output out_18,
  output out_19,
  output out_20,
  output out_21,
  output out_22,
  output out_23,
  output out_24,
  output out_25
);

  wire ADDR_out, and_1_out, and_2_out, and_3_out, and_4_out, CLOCK_out, controlled_buffer_1_out,
       controlled_buffer_2_out, delayer_1_out, HALT_2_q, HALT_2_qn, LDR_out, not_1_out, not_2_out, not_3_out,
       or_1_out, or_2_out, or_3_out, or_4_out, or_5_out, or_6_out, or_7_out, RESET_2_out, RESET_3_out,
       RESUME_out, STEP_out, STR_out, undriven, undriven_2, undriven_3, undriven_4, undriven_5, undriven_6,
       undriven_7, undriven_8;
  wire [3:0] CYCLES_q, CYCLES_q_2;
  wire [7:0] INSTR_q;

  LED Reset (.in(RESET_2_out));
  Button RESET_2 (.out(RESET_2_out));
  Button RESUME (.out(RESUME_out));
  not not_1 (not_1_out, MANUAL);
  Button STEP (.out(STEP_out));
  assign controlled_buffer_1_out = MANUAL ? STEP_out : 1'bz;  // Controlled_Buffer controlled_buffer_1
  Clock CLOCK (.out(CLOCK_out));
  Pull_Resistor pull_resistor_1 (.node(controlled_buffer_1_out));
  LED Auto (.in(not_2_out));
  LED u_Manual (.in(MANUAL));
  not not_2 (not_2_out, MANUAL);
  or or_1 (or_1_out, controlled_buffer_1_out, controlled_buffer_2_out);
  assign controlled_buffer_2_out = not_1_out ? CLOCK_out : 1'bz;  // Controlled_Buffer controlled_buffer_2
  Pull_Resistor pull_resistor_2 (.node(controlled_buffer_2_out));
  LED Halt (.in(HALT_2_q));
  LED Clock_2 (.in(or_1_out));
  not not_3 (not_3_out, not_2_out);
  and and_1 (and_1_out, ~HALT_2_q, or_1_out);  // AND_Gate
  D_Flip_Flop HALT_2 (
    .clk(undriven_2), .D(HALT_2_qn), .Q(HALT_2_q), .Qn(HALT_2_qn), .en(1'b1), .reset(or_2_out));  // open: preset
  or or_2 (or_2_out, RESUME_out, undriven);
  ALU alu_1 ();  // open: a7, a6, a5, a4, a3, a2, a1, a0, b7, b6, b5, b4, b3, b2, b1, b0, cin, op2, op1, op0, out0, out1, out2, out3, out4, out5, out6, out7, overflow, sign, zero, carry
  Counter #(.trigger("falling")) INSTR (
    .load(1'b0), .count(1'b1), .Q(INSTR_q), .clk(undriven_3), .clr(undriven));  // open: D, carry
  Hex_Digit_Display hex_digit_display_1 (.value(INSTR_q[3:0]));  // open: dp
  Hex_Digit_Display hex_digit_display_2 (.value(INSTR_q[7:4]));  // open: dp
  Counter CYCLES (
    .load(1'b0), .count(1'b1), .Q({CYCLES_q_2, CYCLES_q}), .clk(undriven_4), .clr(or_3_out));  // open: D, carry
  or or_3 (or_3_out, undriven_3, undriven);
  Hex_Digit_Display hex_digit_display_3 (.value(CYCLES_q_2));  // open: dp
  Hex_Digit_Display hex_digit_display_4 (.value(CYCLES_q));  // open: dp
  and and_2 (and_2_out, ADDR_out, not_3_out);
  and and_3 (and_3_out, not_3_out, LDR_out);
  Button LDR (.out(LDR_out));
  Button ADDR (.out(ADDR_out));
  and and_4 (and_4_out, not_3_out, STR_out);
  Button STR (.out(STR_out));
  assign out_20 = and_2_out ? in_3 : 1'bz;  // Controlled_Buffer controlled_buffer_3
  assign out_19 = and_2_out ? in_2 : 1'bz;  // Controlled_Buffer controlled_buffer_4
  assign out_18 = and_2_out ? in_1 : 1'bz;  // Controlled_Buffer controlled_buffer_5
  assign out_21 = and_2_out ? in_4 : 1'bz;  // Controlled_Buffer controlled_buffer_6
  assign out_19 = and_4_out ? in_11 : 1'bz;  // Controlled_Buffer controlled_buffer_7
  assign out_18 = and_4_out ? in_10 : 1'bz;  // Controlled_Buffer controlled_buffer_8
  assign out_21 = and_4_out ? in_13 : 1'bz;  // Controlled_Buffer controlled_buffer_9
  assign out_20 = and_4_out ? in_12 : 1'bz;  // Controlled_Buffer controlled_buffer_10
  assign out_25 = and_2_out ? in_8 : 1'bz;  // Controlled_Buffer controlled_buffer_11
  assign out_23 = and_2_out ? in_6 : 1'bz;  // Controlled_Buffer controlled_buffer_12
  assign out_24 = and_2_out ? in_7 : 1'bz;  // Controlled_Buffer controlled_buffer_13
  assign out_22 = and_2_out ? in_5 : 1'bz;  // Controlled_Buffer controlled_buffer_14
  assign out_25 = and_4_out ? in_17 : 1'bz;  // Controlled_Buffer controlled_buffer_15
  assign out_22 = and_4_out ? in_14 : 1'bz;  // Controlled_Buffer controlled_buffer_16
  assign out_24 = and_4_out ? in_16 : 1'bz;  // Controlled_Buffer controlled_buffer_17
  assign out_23 = and_4_out ? in_15 : 1'bz;  // Controlled_Buffer controlled_buffer_18
  or or_4 (or_4_out, undriven_7, and_2_out);
  or or_5 (or_5_out, undriven_5, and_3_out);
  or or_6 (or_6_out, undriven_8, and_4_out);
  Delayer delayer_1 (.in(or_7_out), .out(delayer_1_out));
  or or_7 (or_7_out, undriven_6, and_2_out, and_3_out, and_4_out);
  Button RESET_3 (.out(RESET_3_out));
  // Ram256 ram256_1: pin names not known; wires that end beside it: or_4_out, or_5_out, or_6_out, delayer_1_out, RESET_3_out, out_25, out_24, out_23, out_22, out_21, out_20, out_19, out_18, out_25, out_24, out_23, out_22, out_21, out_20, out_19, out_18

  // Notes on the sheet:
  //   bits | cond   | flag test  | description
  //   0000 | r      | -----      | branch always
  //   0001 | zs/eq  | z=1        | branch if equal
  //   0010 | ss/neg | s=1        | branch if negative
  //   0011 | ov     | v=1        | branch if overflow
  //   0100 | cs/ltu | c=1        | branch if uint <
  //   0101 | leu    | c=1 or z=1 | branch if uint <=
  //   0110 | lt     | v+s        | branch if int <
  //   0111 | le     | v+s or z=1 | branch if int <=
  //   0000 00 00  ->  mov  ra, rb    ->  ra = rb
  //   0001 00 rb  ->  data rb, imm8  ->  rb = ram[pc++]
  //   0010 ra rb  ->  ldr  ra, [rb]  ->  ra = ram[rb]
  //   0011 ra rb  ->  str  ra, [rb]  ->  ram[rb] = ra
  //   0100 00 rb  ->  jalr rb        ->  pc <-> rb
  //   0101  cond  ->  b<cond> imm8   ->  pc += cond ? ram[pc] : 1
  //   0110 00 00  ->  halt           ->  stop computer
  //   0111 00 rb  ->  in   data, rb  ->  rb = io[active].data
  //   0111 10 rb  ->  out  data, rb  ->  io[active].data = rb
  //   0111 01 rb  ->  in   addr, rb  ->  rb = io[active].addr
  //   0111 11 rb  ->  out  addr, rb  ->  io[rb].active = true
  //   1000 ra rb  ->  add ra, rb  ->  ra = ra + rb       [vcsz]
  //   1001 ra rb  ->  sub ra, rb  ->  ra = ra - rb       [vcsz]
  //   1010 ra rb  ->  shl ra, rb  ->  ra = [rb << 1, 0]  [0csz]
  //   1011 ra rb  ->  shr ra, rb  ->  ra = [0, rb >> 1]  [0csz]
  //   1100 ra rb  ->  and ra, rb  ->  ra = ra & rb       [00sz]
  //   1101 ra rb  ->  orr ra, rb  ->  ra = ra | rb       [00sz]
  //   1110 ra rb  ->  xor ra, rb  ->  ra = ra ^ rb       [00sz]
  //   1111 ra rb  ->  cmp ra, rb  ->  fr = ra - rb       [vcsz]
endmodule

module TEST (
  input  in_1,
  input  rst,
  output [7:0] instr
);

  wire and_1_out, d_ff_1_q, d_ff_1_qn, not_1_out, not_2_out;
  wire [7:0] adder_1_out, NPC_q, PC_q, rom_1_data;
  wire [15:0] rom_2_data;

  Clock clock_1 ();  // open: out
  Register NPC (.D(adder_1_out), .en(1'b1), .Q(NPC_q), .clk(not_1_out), .clr(rst));
  not not_1 (not_1_out, in_1);
  Register PC (.D(NPC_q), .en(1'b1), .Q(PC_q), .clk(in_1), .clr(rst));
  Adder adder_1 (.a(PC_q), .b({8{1'b0}}), .out(adder_1_out), .cin(1'b1));  // open: cout
  ROM rom_1 (.addr(PC_q), .data(rom_1_data), .sel(1'b1));
  Multiplexer #(.width(8), .enable("false")) multiplexer_1 (.in0(rom_1_data), .in1(instr), .out(instr), .sel(d_ff_1_q));
  not not_2 (not_2_out, in_1);
  ROM #(.addrWidth(4), .dataWidth(16)) rom_2 (.addr(instr[3:0]), .data(rom_2_data), .sel(1'b1));
  and and_1 (and_1_out, rom_2_data[15], not_2_out);
  D_Flip_Flop d_ff_1 (
    .clk(and_1_out), .D(d_ff_1_qn), .Q(d_ff_1_q), .Qn(d_ff_1_qn), .en(1'b1), .reset(rst));  // open: preset

  // Notes on the sheet:
  //   contents of rom_1 (hex, n*v repeats v):
  //   0 ff 2 3 11*0 ff
  //   contents of rom_2 (hex, n*v repeats v):
  //   15*0 8000
endmodule
