// Logisim project transistor.circ as structural Verilog
module DATAPATH (
  input  cin,
  input  op2,
  input  op1,
  input  op0,
  input  fr_w,
  input  rd_r,
  input  mar,
  input  r,
  input  w,
  input  rst,
  input  r0_w,
  input  r0_r,
  input  r1_w,
  input  r1_r,
  input  r2_w,
  input  r2_r,
  input  r3_w,
  input  r3_r,
  input  pc_w,
  input  pc_r,
  input  bus0,
  input  ra_w,
  input  rb_w,
  output v,
  output c,
  output s,
  output z
);

  wire transistor_1_out, transistor_3_out, transistor_5_out, transistor_7_out, transistor_9_out,
       transistor_11_out, transistor_13_out, transistor_15_out, transistor_17_out, transistor_19_out,
       transistor_23_out, transistor_27_out, transistor_31_out, transistor_35_out, transistor_39_out,
       transistor_43_out, transistor_47_out, transistor_51_out, transistor_55_out, transistor_57_out,
       transistor_59_out, transistor_61_out, transistor_63_out, transistor_65_out, transistor_67_out,
       transistor_69_out, transistor_71_out, transistor_73_out, transistor_77_out, transistor_81_out,
       transistor_85_out, transistor_89_out, transistor_93_out, transistor_97_out, transistor_101_out,
       transistor_105_out, transistor_109_out, transistor_111_out, transistor_113_out, transistor_115_out,
       transistor_117_out, transistor_119_out, transistor_121_out, transistor_123_out, transistor_125_out,
       transistor_127_out, transistor_129_out, transistor_131_out, transistor_133_out, transistor_135_out,
       transistor_137_out, transistor_139_out, transistor_141_out, transistor_143_out, transistor_145_out,
       transistor_147_out, transistor_149_out, transistor_151_out, transistor_153_out, transistor_155_out,
       transistor_157_out, transistor_159_out, transistor_161_out, transistor_165_out, transistor_169_out,
       transistor_173_out, transistor_177_out, transistor_181_out, transistor_185_out, transistor_189_out,
       transistor_193_out, transistor_197_out, transistor_201_out, transistor_203_out, transistor_205_out,
       transistor_207_out, transistor_209_out, transistor_211_out, transistor_213_out, transistor_215_out,
       transistor_217_out, transistor_219_out, transistor_224_out, transistor_229_out, transistor_234_out,
       transistor_239_out, transistor_244_out, transistor_249_out, transistor_254_out, transistor_259_out,
       transistor_263_out, transistor_266_out, transistor_269_out, transistor_272_out, transistor_275_out,
       transistor_278_out, transistor_281_out, transistor_284_out, transistor_287_out, transistor_289_out,
       transistor_291_out, transistor_293_out, transistor_295_out, transistor_297_out, transistor_299_out,
       transistor_301_out, transistor_303_out, transistor_305_out, transistor_309_out, transistor_313_out,
       transistor_317_out, transistor_321_out, transistor_325_out, transistor_329_out, transistor_333_out,
       transistor_337_out, transistor_341_out, transistor_343_out, transistor_347_out, transistor_349_out,
       transistor_353_out, transistor_355_out, transistor_359_out, transistor_361_out, transistor_365_out,
       transistor_367_out, transistor_371_out, transistor_373_out, transistor_377_out, transistor_379_out,
       transistor_383_out, transistor_385_out, transistor_389_out, transistor_391_out, transistor_395_out,
       transistor_397_out, transistor_401_out, transistor_405_out, transistor_409_out, transistor_413_out,
       transistor_417_out, transistor_421_out, transistor_425_out, transistor_429_out, transistor_433_out,
       transistor_435_out, transistor_437_out, transistor_441_out, transistor_443_out, transistor_447_out,
       transistor_449_out, transistor_453_out, transistor_455_out, transistor_459_out, transistor_461_out,
       transistor_465_out, transistor_467_out, transistor_471_out, transistor_473_out, transistor_477_out,
       transistor_479_out, transistor_483_out, transistor_487_out, transistor_489_out, transistor_491_out,
       transistor_493_out, transistor_495_out, transistor_497_out, transistor_499_out, transistor_501_out,
       transistor_503_out, transistor_505_out, transistor_509_out, transistor_513_out, transistor_517_out,
       transistor_521_out, transistor_525_out, transistor_529_out, transistor_533_out, transistor_537_out,
       transistor_541_out, transistor_543_out, transistor_547_out, transistor_551_out, transistor_555_out,
       transistor_559_out, transistor_563_out, transistor_567_out, transistor_571_out, transistor_575_out,
       transistor_579_out, transistor_581_out, transistor_583_out, transistor_585_out, transistor_587_out,
       transistor_589_out, transistor_591_out, transistor_593_out, transistor_595_out, transistor_597_out,
       transistor_601_out, transistor_605_out, transistor_609_out, transistor_613_out, transistor_617_out,
       transistor_621_out, transistor_625_out, transistor_629_out, transistor_633_out, transistor_635_out,
       transistor_637_out, transistor_639_out, transistor_641_out, transistor_643_out, transistor_645_out,
       transistor_647_out, transistor_649_out, transistor_651_out, transistor_655_out, transistor_659_out,
       transistor_663_out, transistor_667_out, transistor_671_out, transistor_675_out, transistor_679_out,
       transistor_683_out, transistor_687_out, transistor_689_out, transistor_693_out, transistor_697_out,
       transistor_701_out, transistor_705_out, transistor_709_out, transistor_713_out, transistor_717_out,
       transistor_721_out, transistor_725_out, transistor_727_out, transistor_729_out, transistor_731_out,
       transistor_733_out, transistor_735_out, transistor_737_out, transistor_739_out, transistor_741_out,
       transistor_743_out, transistor_747_out, transistor_751_out, transistor_755_out, transistor_759_out,
       transistor_763_out, transistor_767_out, transistor_771_out, transistor_775_out, transistor_779_out,
       transistor_781_out, transistor_783_out, transistor_785_out, transistor_787_out, transistor_789_out,
       transistor_791_out, transistor_793_out, transistor_795_out, transistor_797_out, transistor_801_out,
       transistor_805_out, transistor_809_out, transistor_813_out, transistor_817_out, transistor_821_out,
       transistor_825_out, transistor_829_out, transistor_833_out, transistor_835_out, transistor_839_out,
       transistor_841_out, transistor_845_out, transistor_847_out, transistor_851_out, transistor_853_out,
       transistor_857_out, transistor_859_out, transistor_863_out, transistor_865_out, transistor_869_out,
       transistor_871_out, transistor_875_out, transistor_877_out, transistor_881_out, transistor_883_out,
       transistor_887_out, transistor_889_out, transistor_893_out, transistor_895_out, transistor_899_out,
       transistor_901_out, transistor_905_out, transistor_907_out, transistor_911_out, transistor_913_out,
       transistor_917_out, transistor_919_out, transistor_923_out, transistor_925_out, transistor_929_out,
       transistor_931_out, transistor_933_out, transistor_935_out, transistor_937_out, transistor_939_out,
       transistor_941_out, transistor_943_out, transistor_945_out, transistor_949_out, transistor_953_out,
       transistor_957_out, transistor_961_out, transistor_965_out, transistor_969_out, transistor_973_out,
       transistor_977_out, transistor_978_out, transistor_979_out, transistor_980_out, transistor_981_out,
       transistor_982_out, transistor_983_out, transistor_984_out, transistor_987_out, transistor_990_out,
       transistor_993_out, transistor_996_out, transistor_999_out, transistor_1002_out, transistor_1005_out,
       transistor_1008_out, transistor_1009_out, transistor_1011_out, transistor_1013_out,
       transistor_1015_out, transistor_1017_out, transistor_1019_out, transistor_1021_out,
       transistor_1023_out, transistor_1025_out, transistor_1026_out, transistor_1029_out,
       transistor_1030_out, transistor_1033_out, transistor_1034_out, transistor_1037_out,
       transistor_1038_out, transistor_1041_out, transistor_1042_out, transistor_1045_out,
       transistor_1046_out, transistor_1049_out, transistor_1050_out, transistor_1053_out,
       transistor_1054_out, transistor_1057_out, transistor_1059_out, transistor_1061_out,
       transistor_1063_out, transistor_1065_out, transistor_1067_out, transistor_1069_out,
       transistor_1071_out, transistor_1073_out, transistor_1074_out, transistor_1075_out,
       transistor_1076_out, transistor_1077_out, transistor_1078_out, transistor_1079_out,
       transistor_1080_out, transistor_1081_out, transistor_1083_out, transistor_1086_out,
       transistor_1088_out, transistor_1090_out, transistor_1092_out, transistor_1094_out,
       transistor_1096_out, transistor_1097_out, transistor_1100_out, transistor_1102_out,
       transistor_1104_out, transistor_1106_out, transistor_1108_out, transistor_1109_out,
       transistor_1112_out, transistor_1114_out, transistor_1116_out, transistor_1117_out,
       transistor_1121_out, transistor_1124_out, transistor_1127_out, transistor_1130_out,
       transistor_1133_out, transistor_1136_out, transistor_1139_out, transistor_1142_out,
       transistor_1143_out, transistor_1145_out, transistor_1148_out, transistor_1149_out,
       transistor_1152_out, transistor_1153_out, transistor_1156_out, transistor_1157_out,
       transistor_1160_out, transistor_1161_out, transistor_1164_out, transistor_1165_out,
       transistor_1168_out, transistor_1169_out, transistor_1172_out, transistor_1173_out,
       transistor_1176_out, transistor_1177_out, transistor_1179_out, transistor_1181_out,
       transistor_1182_out, transistor_1183_out, transistor_1184_out, transistor_1185_out,
       transistor_1186_out, transistor_1187_out, transistor_1188_out, transistor_1191_out,
       transistor_1194_out, transistor_1197_out, transistor_1200_out, transistor_1203_out,
       transistor_1206_out, transistor_1209_out, transistor_1212_out, transistor_1213_out,
       transistor_1215_out, transistor_1217_out, transistor_1220_out, transistor_1221_out,
       transistor_1224_out, transistor_1225_out, transistor_1228_out, transistor_1229_out,
       transistor_1232_out, transistor_1233_out, transistor_1236_out, transistor_1237_out,
       transistor_1240_out, transistor_1241_out, transistor_1244_out, transistor_1245_out,
       transistor_1248_out, transistor_1249_out, transistor_1251_out, transistor_1252_out,
       transistor_1253_out, transistor_1254_out, transistor_1255_out, transistor_1256_out,
       transistor_1257_out, transistor_1258_out, transistor_1259_out, transistor_1263_out,
       transistor_1266_out, transistor_1269_out, transistor_1272_out, transistor_1275_out,
       transistor_1278_out, transistor_1281_out, transistor_1284_out, transistor_1285_out,
       transistor_1287_out, transistor_1289_out, transistor_1292_out, transistor_1293_out,
       transistor_1296_out, transistor_1297_out, transistor_1300_out, transistor_1301_out,
       transistor_1304_out, transistor_1305_out, transistor_1308_out, transistor_1309_out,
       transistor_1312_out, transistor_1313_out, transistor_1316_out, transistor_1317_out,
       transistor_1320_out, transistor_1321_out, transistor_1324_out, transistor_1325_out,
       transistor_1328_out, transistor_1329_out, transistor_1332_out, transistor_1333_out,
       transistor_1336_out, transistor_1337_out, transistor_1340_out, transistor_1341_out,
       transistor_1344_out, transistor_1345_out, transistor_1348_out, transistor_1349_out,
       transistor_1352_out, transistor_1353_out, transistor_1355_out, transistor_1357_out,
       transistor_1358_out, transistor_1359_out, transistor_1360_out, transistor_1361_out,
       transistor_1362_out, transistor_1363_out, transistor_1364_out, transistor_1365_out,
       transistor_1367_out, transistor_1370_out, transistor_1373_out, transistor_1376_out,
       transistor_1379_out, transistor_1382_out, transistor_1385_out, transistor_1388_out,
       transistor_1391_out, transistor_1393_out, transistor_1395_out, transistor_1397_out,
       transistor_1399_out, transistor_1401_out, transistor_1403_out, transistor_1405_out,
       transistor_1407_out, transistor_1409_out, transistor_1410_out, transistor_1413_out,
       transistor_1414_out, transistor_1417_out, transistor_1418_out, transistor_1421_out,
       transistor_1422_out, transistor_1425_out, transistor_1426_out, transistor_1429_out,
       transistor_1430_out, transistor_1433_out, transistor_1434_out, transistor_1437_out,
       transistor_1438_out, transistor_1441_out, transistor_1442_out, transistor_1445_out,
       transistor_1446_out, transistor_1447_out, transistor_1448_out, transistor_1449_out,
       transistor_1450_out, transistor_1451_out, transistor_1452_out, transistor_1453_out,
       transistor_1456_out, transistor_1458_out, transistor_1460_out, transistor_1462_out,
       transistor_1464_out, transistor_1466_out, transistor_1468_out, transistor_1470_out,
       transistor_1472_out, transistor_1474_out, transistor_1476_out, transistor_1478_out,
       transistor_1480_out, transistor_1481_out, transistor_1484_out, transistor_1486_out,
       transistor_1488_out, transistor_1489_out, transistor_1490_out, transistor_1494_out,
       transistor_1497_out, transistor_1500_out, transistor_1503_out, transistor_1506_out,
       transistor_1509_out, transistor_1512_out, transistor_1515_out, transistor_1516_out,
       transistor_1519_out, transistor_1520_out, transistor_1524_out, transistor_1527_out,
       transistor_1528_out, transistor_1531_out, transistor_1532_out, transistor_1535_out,
       transistor_1536_out, transistor_1539_out, transistor_1540_out, transistor_1543_out,
       transistor_1544_out, transistor_1547_out, transistor_1548_out, transistor_1551_out,
       transistor_1552_out, transistor_1555_out, transistor_1558_out, transistor_1559_out,
       transistor_1561_out, transistor_1565_out, transistor_1566_out, transistor_1567_out,
       transistor_1568_out, transistor_1569_out, transistor_1570_out, transistor_1571_out,
       transistor_1572_out, transistor_1573_out, transistor_1575_out, transistor_1577_out,
       transistor_1580_out, transistor_1583_out, transistor_1586_out, transistor_1589_out,
       transistor_1592_out, transistor_1595_out, transistor_1598_out, transistor_1601_out,
       transistor_1604_out, transistor_1605_out, transistor_1609_out, transistor_1610_out,
       transistor_1612_out, transistor_1613_out, transistor_1615_out, transistor_1616_out,
       transistor_1618_out, transistor_1619_out, transistor_1621_out, transistor_1622_out,
       transistor_1624_out, transistor_1625_out, transistor_1627_out, transistor_1628_out,
       transistor_1630_out, transistor_1631_out, transistor_1633_out, transistor_1635_out,
       transistor_1638_out, transistor_1641_out, transistor_1643_out, transistor_1646_out,
       transistor_1648_out, transistor_1651_out, transistor_1653_out, transistor_1656_out,
       transistor_1658_out, transistor_1661_out, transistor_1662_out, transistor_1666_out,
       transistor_1667_out, transistor_1671_out, transistor_1673_out, transistor_1676_out,
       transistor_1677_out, transistor_1680_out, transistor_1681_out, transistor_1685_out,
       transistor_1686_out, transistor_1687_out, transistor_1688_out, transistor_1689_out,
       transistor_1690_out, transistor_1691_out, transistor_1692_out, transistor_1693_out,
       transistor_1694_out, transistor_1696_out, transistor_1700_out, transistor_1703_out,
       transistor_1706_out, transistor_1709_out, transistor_1712_out, transistor_1715_out,
       transistor_1718_out, transistor_1721_out, transistor_1724_out, transistor_1725_out,
       transistor_1726_out, transistor_1728_out, transistor_1732_out, transistor_1735_out,
       transistor_1736_out, transistor_1739_out, transistor_1740_out, transistor_1743_out,
       transistor_1744_out, transistor_1747_out, transistor_1748_out, transistor_1751_out,
       transistor_1752_out, transistor_1755_out, transistor_1756_out, transistor_1759_out,
       transistor_1760_out, transistor_1763_out, transistor_1764_out, transistor_1767_out,
       transistor_1769_out, transistor_1771_out, transistor_1772_out, transistor_1776_out,
       transistor_1777_out, transistor_1778_out, transistor_1779_out, transistor_1780_out,
       transistor_1781_out, transistor_1782_out, transistor_1783_out, transistor_1784_out,
       transistor_1787_out, transistor_1788_out, transistor_1790_out, transistor_1793_out,
       transistor_1794_out, transistor_1797_out, transistor_1799_out, transistor_1801_out,
       transistor_1802_out, transistor_1805_out, transistor_1807_out, transistor_1809_out,
       transistor_1811_out, transistor_1813_out, transistor_1815_out, transistor_1817_out,
       transistor_1819_out, transistor_1821_out, transistor_1823_out, transistor_1825_out,
       transistor_1826_out, transistor_1829_out, transistor_1830_out, transistor_1836_out,
       transistor_1839_out, transistor_1842_out, transistor_1845_out, transistor_1848_out,
       transistor_1851_out, transistor_1854_out, transistor_1857_out, transistor_1860_out,
       transistor_1861_out, transistor_1862_out, transistor_1866_out, transistor_1867_out,
       transistor_1871_out, transistor_1873_out, transistor_1875_out, transistor_1879_out,
       transistor_1883_out, transistor_1885_out, transistor_1887_out, transistor_1889_out,
       transistor_1891_out, transistor_1893_out, transistor_1895_out, transistor_1897_out,
       transistor_1899_out, transistor_1901_out, transistor_1903_out, transistor_1905_out,
       transistor_1907_out, transistor_1909_out, transistor_1911_out, transistor_1913_out,
       transistor_1915_out, transistor_1917_out, transistor_1937_out, transistor_1938_out,
       transistor_1940_out, transistor_1942_out, transistor_1944_out, transistor_1946_out,
       transistor_1948_out, transistor_1950_out, transistor_1952_out, transistor_1954_out,
       transistor_1956_out, transistor_1961_out, transistor_1965_out, transistor_1969_out,
       transistor_1973_out, transistor_1977_out, transistor_1981_out, transistor_1985_out,
       transistor_1989_out, transistor_1993_out, transistor_1997_out, transistor_1998_out,
       transistor_2000_out, transistor_2004_out, transistor_2008_out, transistor_2010_out,
       transistor_2012_out, transistor_2014_out, transistor_2016_out, transistor_2018_out,
       transistor_2020_out, transistor_2022_out, transistor_2024_out, transistor_2026_out,
       transistor_2028_out, transistor_2030_out, transistor_2032_out, transistor_2034_out,
       transistor_2036_out, transistor_2038_out, transistor_2040_out, transistor_2043_out,
       transistor_2063_out, transistor_2065_out, transistor_2067_out, transistor_2069_out,
       transistor_2071_out, transistor_2073_out, transistor_2075_out, transistor_2077_out,
       transistor_2079_out, transistor_2081_out, transistor_2083_out, transistor_2087_out,
       transistor_2091_out, transistor_2095_out, transistor_2099_out, transistor_2103_out,
       transistor_2107_out, transistor_2111_out, transistor_2115_out, transistor_2119_out,
       transistor_2123_out, transistor_2125_out, transistor_2127_out, transistor_2135_out,
       transistor_2137_out, transistor_2139_out, transistor_2141_out, transistor_2143_out,
       transistor_2145_out, transistor_2147_out, transistor_2149_out, transistor_2151_out,
       transistor_2153_out, transistor_2155_out, transistor_2157_out, transistor_2159_out,
       transistor_2161_out, transistor_2163_out, transistor_2165_out, transistor_2167_out,
       transistor_2169_out, transistor_2171_out, transistor_2191_out, transistor_2195_out,
       transistor_2197_out, transistor_2199_out, transistor_2201_out, transistor_2203_out,
       transistor_2205_out, transistor_2207_out, transistor_2209_out, transistor_2211_out,
       transistor_2213_out, transistor_2217_out, transistor_2221_out, transistor_2225_out,
       transistor_2229_out, transistor_2233_out, transistor_2237_out, transistor_2241_out,
       transistor_2249_out, transistor_2251_out, transistor_2253_out, transistor_2255_out,
       transistor_2257_out, transistor_2259_out, transistor_2261_out, transistor_2263_out,
       transistor_2265_out, transistor_2267_out, transistor_2271_out, transistor_2275_out,
       transistor_2279_out, transistor_2283_out, transistor_2287_out, transistor_2291_out,
       transistor_2295_out, transistor_2299_out, transistor_2305_out, transistor_2309_out,
       transistor_2311_out, transistor_2315_out, transistor_2317_out, transistor_2321_out,
       transistor_2323_out, transistor_2327_out, transistor_2329_out, transistor_2333_out,
       transistor_2335_out, transistor_2339_out, transistor_2341_out, transistor_2345_out,
       transistor_2347_out, transistor_2351_out, transistor_2353_out, transistor_2357_out,
       transistor_2358_out, transistor_2359_out, transistor_2360_out, transistor_2361_out,
       transistor_2362_out, transistor_2363_out, transistor_2364_out, transistor_2366_out,
       transistor_2370_out, transistor_2373_out, transistor_2376_out, transistor_2379_out,
       transistor_2382_out, transistor_2385_out, transistor_2388_out, transistor_2391_out,
       transistor_2393_out, transistor_2395_out, transistor_2397_out, transistor_2399_out,
       transistor_2401_out, transistor_2403_out, transistor_2409_out, transistor_2412_out,
       transistor_2415_out, transistor_2418_out, transistor_2421_out, transistor_2424_out,
       transistor_2427_out, transistor_2430_out, undriven, undriven_2, undriven_3, undriven_4, undriven_5,
       undriven_6, undriven_7, undriven_8;

  Transistor transistor_1 (.in(1'b1), .out(transistor_1_out), .gate(r0_w));
  Transistor #(.\type ("n")) transistor_2 (.in(1'b0), .out(transistor_1_out), .gate(r0_w));
  Transistor transistor_3 (.in(1'b1), .out(transistor_3_out), .gate(r0_w));
  Transistor #(.\type ("n")) transistor_4 (.in(1'b0), .out(transistor_3_out), .gate(r0_w));
  Transistor transistor_5 (.in(1'b1), .out(transistor_5_out), .gate(r0_w));
  Transistor #(.\type ("n")) transistor_6 (.in(1'b0), .out(transistor_5_out), .gate(r0_w));
  Transistor transistor_7 (.in(1'b1), .out(transistor_7_out), .gate(r0_w));
  Transistor #(.\type ("n")) transistor_8 (.in(1'b0), .out(transistor_7_out), .gate(r0_w));
  Transistor transistor_9 (.in(1'b1), .out(transistor_9_out), .gate(r0_w));
  Transistor #(.\type ("n")) transistor_10 (.in(1'b0), .out(transistor_9_out), .gate(r0_w));
  Transistor transistor_11 (.in(1'b1), .out(transistor_11_out), .gate(r0_w));
  Transistor #(.\type ("n")) transistor_12 (.in(1'b0), .out(transistor_11_out), .gate(r0_w));
  Transistor transistor_13 (.in(1'b1), .out(transistor_13_out), .gate(r0_w));
  Transistor #(.\type ("n")) transistor_14 (.in(1'b0), .out(transistor_13_out), .gate(r0_w));
  Transistor transistor_15 (.in(1'b1), .out(transistor_15_out), .gate(r0_w));
  Transistor #(.\type ("n")) transistor_16 (.in(1'b0), .out(transistor_15_out), .gate(r0_w));
  Transistor transistor_17 (.in(1'b1), .out(transistor_17_out), .gate(mar));
  Transistor #(.\type ("n")) transistor_18 (.in(1'b0), .out(transistor_17_out), .gate(mar));
  Transistor #(.\type ("n")) transistor_19 (.in(transistor_1367_out), .out(transistor_19_out), .gate(r0_w));
  Transistor #(.gate("br")) transistor_20 (.in(transistor_1367_out), .out(transistor_19_out), .gate(transistor_1_out));
  Transistor #(.\type ("n")) transistor_21 (.in(transistor_73_out), .out(transistor_19_out), .gate(transistor_1_out));
  Transistor #(.gate("br")) transistor_22 (.in(transistor_73_out), .out(transistor_19_out), .gate(r0_w));
  Transistor #(.\type ("n")) transistor_23 (.in(transistor_1355_out), .out(transistor_23_out), .gate(r0_w));
  Transistor #(.gate("br")) transistor_24 (.in(transistor_1355_out), .out(transistor_23_out), .gate(transistor_3_out));
  Transistor #(.\type ("n")) transistor_25 (.in(transistor_77_out), .out(transistor_23_out), .gate(transistor_3_out));
  Transistor #(.gate("br")) transistor_26 (.in(transistor_77_out), .out(transistor_23_out), .gate(r0_w));
  Transistor #(.\type ("n")) transistor_27 (.in(transistor_1287_out), .out(transistor_27_out), .gate(r0_w));
  Transistor #(.gate("br")) transistor_28 (.in(transistor_1287_out), .out(transistor_27_out), .gate(transistor_5_out));
  Transistor #(.\type ("n")) transistor_29 (.in(transistor_81_out), .out(transistor_27_out), .gate(transistor_5_out));
  Transistor #(.gate("br")) transistor_30 (.in(transistor_81_out), .out(transistor_27_out), .gate(r0_w));
  Transistor #(.\type ("n")) transistor_31 (.in(transistor_1251_out), .out(transistor_31_out), .gate(r0_w));
  Transistor #(.gate("br")) transistor_32 (.in(transistor_1251_out), .out(transistor_31_out), .gate(transistor_7_out));
  Transistor #(.\type ("n")) transistor_33 (.in(transistor_85_out), .out(transistor_31_out), .gate(transistor_7_out));
  Transistor #(.gate("br")) transistor_34 (.in(transistor_85_out), .out(transistor_31_out), .gate(r0_w));
  Transistor #(.\type ("n")) transistor_35 (.in(transistor_1215_out), .out(transistor_35_out), .gate(r0_w));
  Transistor #(.gate("br")) transistor_36 (.in(transistor_1215_out), .out(transistor_35_out), .gate(transistor_9_out));
  Transistor #(.\type ("n")) transistor_37 (.in(transistor_89_out), .out(transistor_35_out), .gate(transistor_9_out));
  Transistor #(.gate("br")) transistor_38 (.in(transistor_89_out), .out(transistor_35_out), .gate(r0_w));
  Transistor #(.\type ("n")) transistor_39 (.in(transistor_1179_out), .out(transistor_39_out), .gate(r0_w));
  Transistor #(.gate("br")) transistor_40 (.in(transistor_1179_out), .out(transistor_39_out), .gate(transistor_11_out));
  Transistor #(.\type ("n")) transistor_41 (.in(transistor_93_out), .out(transistor_39_out), .gate(transistor_11_out));
  Transistor #(.gate("br")) transistor_42 (.in(transistor_93_out), .out(transistor_39_out), .gate(r0_w));
  Transistor #(.\type ("n")) transistor_43 (.in(transistor_1143_out), .out(transistor_43_out), .gate(r0_w));
  Transistor #(.gate("br")) transistor_44 (.in(transistor_1143_out), .out(transistor_43_out), .gate(transistor_13_out));
  Transistor #(.\type ("n")) transistor_45 (.in(transistor_97_out), .out(transistor_43_out), .gate(transistor_13_out));
  Transistor #(.gate("br")) transistor_46 (.in(transistor_97_out), .out(transistor_43_out), .gate(r0_w));
  Transistor #(.\type ("n")) transistor_47 (.in(transistor_1083_out), .out(transistor_47_out), .gate(r0_w));
  Transistor #(.gate("br")) transistor_48 (.in(transistor_1083_out), .out(transistor_47_out), .gate(transistor_15_out));
  Transistor #(.\type ("n")) transistor_49 (.in(transistor_101_out), .out(transistor_47_out), .gate(transistor_15_out));
  Transistor #(.gate("br")) transistor_50 (.in(transistor_101_out), .out(transistor_47_out), .gate(r0_w));
  Transistor #(.\type ("n")) transistor_51 (.in(transistor_1083_out), .out(transistor_51_out), .gate(mar));
  Transistor #(.gate("br")) transistor_52 (.in(transistor_1083_out), .out(transistor_51_out), .gate(transistor_17_out));
  Transistor #(.\type ("n")) transistor_53 (.in(transistor_105_out), .out(transistor_51_out), .gate(transistor_17_out));
  Transistor #(.gate("br")) transistor_54 (.in(transistor_105_out), .out(transistor_51_out), .gate(mar));
  Transistor transistor_55 (.in(1'b1), .out(transistor_55_out), .gate(rst));
  Transistor #(.\type ("n")) transistor_56 (.in(1'b0), .out(transistor_55_out), .gate(rst));
  Transistor transistor_57 (.in(1'b1), .out(transistor_57_out), .gate(rst));
  Transistor #(.\type ("n")) transistor_58 (.in(1'b0), .out(transistor_57_out), .gate(rst));
  Transistor transistor_59 (.in(1'b1), .out(transistor_59_out), .gate(rst));
  Transistor #(.\type ("n")) transistor_60 (.in(1'b0), .out(transistor_59_out), .gate(rst));
  Transistor transistor_61 (.in(1'b1), .out(transistor_61_out), .gate(rst));
  Transistor #(.\type ("n")) transistor_62 (.in(1'b0), .out(transistor_61_out), .gate(rst));
  Transistor transistor_63 (.in(1'b1), .out(transistor_63_out), .gate(rst));
  Transistor #(.\type ("n")) transistor_64 (.in(1'b0), .out(transistor_63_out), .gate(rst));
  Transistor transistor_65 (.in(1'b1), .out(transistor_65_out), .gate(rst));
  Transistor #(.\type ("n")) transistor_66 (.in(1'b0), .out(transistor_65_out), .gate(rst));
  Transistor transistor_67 (.in(1'b1), .out(transistor_67_out), .gate(rst));
  Transistor #(.\type ("n")) transistor_68 (.in(1'b0), .out(transistor_67_out), .gate(rst));
  Transistor transistor_69 (.in(1'b1), .out(transistor_69_out), .gate(rst));
  Transistor #(.\type ("n")) transistor_70 (.in(1'b0), .out(transistor_69_out), .gate(rst));
  Transistor transistor_71 (.in(1'b1), .out(transistor_71_out), .gate(rst));
  Transistor #(.\type ("n")) transistor_72 (.in(1'b0), .out(transistor_71_out), .gate(rst));
  LED led_1 (.in(transistor_105_out));
  Transistor #(.\type ("n")) transistor_73 (.in(1'b0), .out(transistor_73_out), .gate(rst));
  Transistor #(.gate("br")) transistor_74 (.in(1'b0), .out(transistor_73_out), .gate(transistor_55_out));
  Transistor #(.\type ("n")) transistor_75 (.in(transistor_19_out), .out(transistor_73_out), .gate(transistor_55_out));
  Transistor #(.gate("br")) transistor_76 (.in(transistor_19_out), .out(transistor_73_out), .gate(rst));
  Transistor #(.\type ("n")) transistor_77 (.in(1'b0), .out(transistor_77_out), .gate(rst));
  Transistor #(.gate("br")) transistor_78 (.in(1'b0), .out(transistor_77_out), .gate(transistor_57_out));
  Transistor #(.\type ("n")) transistor_79 (.in(transistor_23_out), .out(transistor_77_out), .gate(transistor_57_out));
  Transistor #(.gate("br")) transistor_80 (.in(transistor_23_out), .out(transistor_77_out), .gate(rst));
  Transistor #(.\type ("n")) transistor_81 (.in(1'b0), .out(transistor_81_out), .gate(rst));
  Transistor #(.gate("br")) transistor_82 (.in(1'b0), .out(transistor_81_out), .gate(transistor_59_out));
  Transistor #(.\type ("n")) transistor_83 (.in(transistor_27_out), .out(transistor_81_out), .gate(transistor_59_out));
  Transistor #(.gate("br")) transistor_84 (.in(transistor_27_out), .out(transistor_81_out), .gate(rst));
  Transistor #(.\type ("n")) transistor_85 (.in(1'b0), .out(transistor_85_out), .gate(rst));
  Transistor #(.gate("br")) transistor_86 (.in(1'b0), .out(transistor_85_out), .gate(transistor_61_out));
  Transistor #(.\type ("n")) transistor_87 (.in(transistor_31_out), .out(transistor_85_out), .gate(transistor_61_out));
  Transistor #(.gate("br")) transistor_88 (.in(transistor_31_out), .out(transistor_85_out), .gate(rst));
  Transistor #(.\type ("n")) transistor_89 (.in(1'b0), .out(transistor_89_out), .gate(rst));
  Transistor #(.gate("br")) transistor_90 (.in(1'b0), .out(transistor_89_out), .gate(transistor_63_out));
  Transistor #(.\type ("n")) transistor_91 (.in(transistor_35_out), .out(transistor_89_out), .gate(transistor_63_out));
  Transistor #(.gate("br")) transistor_92 (.in(transistor_35_out), .out(transistor_89_out), .gate(rst));
  Transistor #(.\type ("n")) transistor_93 (.in(1'b0), .out(transistor_93_out), .gate(rst));
  Transistor #(.gate("br")) transistor_94 (.in(1'b0), .out(transistor_93_out), .gate(transistor_65_out));
  Transistor #(.\type ("n")) transistor_95 (.in(transistor_39_out), .out(transistor_93_out), .gate(transistor_65_out));
  Transistor #(.gate("br")) transistor_96 (.in(transistor_39_out), .out(transistor_93_out), .gate(rst));
  Transistor #(.\type ("n")) transistor_97 (.in(1'b0), .out(transistor_97_out), .gate(rst));
  Transistor #(.gate("br")) transistor_98 (.in(1'b0), .out(transistor_97_out), .gate(transistor_67_out));
  Transistor #(.\type ("n")) transistor_99 (.in(transistor_43_out), .out(transistor_97_out), .gate(transistor_67_out));
  Transistor #(.gate("br")) transistor_100 (.in(transistor_43_out), .out(transistor_97_out), .gate(rst));
  Transistor #(.\type ("n")) transistor_101 (.in(1'b0), .out(transistor_101_out), .gate(rst));
  Transistor #(.gate("br")) transistor_102 (.in(1'b0), .out(transistor_101_out), .gate(transistor_69_out));
  Transistor #(.\type ("n")) transistor_103 (
    .in(transistor_47_out), .out(transistor_101_out), .gate(transistor_69_out));
  Transistor #(.gate("br")) transistor_104 (.in(transistor_47_out), .out(transistor_101_out), .gate(rst));
  Transistor #(.\type ("n")) transistor_105 (.in(1'b0), .out(transistor_105_out), .gate(rst));
  Transistor #(.gate("br")) transistor_106 (.in(1'b0), .out(transistor_105_out), .gate(transistor_71_out));
  Transistor #(.\type ("n")) transistor_107 (
    .in(transistor_51_out), .out(transistor_105_out), .gate(transistor_71_out));
  Transistor #(.gate("br")) transistor_108 (.in(transistor_51_out), .out(transistor_105_out), .gate(rst));
  Transistor transistor_109 (.in(1'b1), .out(transistor_109_out), .gate(r0_r));
  Transistor #(.\type ("n")) transistor_110 (.in(1'b0), .out(transistor_109_out), .gate(r0_r));
  Transistor #(.\type ("n")) transistor_111 (.in(transistor_73_out), .out(transistor_111_out), .gate(r0_r));
  Transistor #(.gate("br")) transistor_112 (
    .in(transistor_73_out), .out(transistor_111_out), .gate(transistor_109_out));
  Transistor transistor_113 (.in(1'b1), .out(transistor_113_out), .gate(r0_r));
  Transistor #(.\type ("n")) transistor_114 (.in(1'b0), .out(transistor_113_out), .gate(r0_r));
  Transistor #(.\type ("n")) transistor_115 (.in(transistor_77_out), .out(transistor_115_out), .gate(r0_r));
  Transistor #(.gate("br")) transistor_116 (
    .in(transistor_77_out), .out(transistor_115_out), .gate(transistor_113_out));
  Transistor transistor_117 (.in(1'b1), .out(transistor_117_out), .gate(r0_r));
  Transistor #(.\type ("n")) transistor_118 (.in(1'b0), .out(transistor_117_out), .gate(r0_r));
  Transistor #(.gate("br")) transistor_119 (
    .in(transistor_81_out), .out(transistor_119_out), .gate(transistor_117_out));
  Transistor #(.\type ("n")) transistor_120 (.in(transistor_81_out), .out(transistor_119_out), .gate(r0_r));
  Transistor transistor_121 (.in(1'b1), .out(transistor_121_out), .gate(r0_r));
  Transistor #(.\type ("n")) transistor_122 (.in(1'b0), .out(transistor_121_out), .gate(r0_r));
  Transistor #(.\type ("n")) transistor_123 (.in(transistor_85_out), .out(transistor_123_out), .gate(r0_r));
  Transistor #(.gate("br")) transistor_124 (
    .in(transistor_85_out), .out(transistor_123_out), .gate(transistor_121_out));
  Transistor transistor_125 (.in(1'b1), .out(transistor_125_out), .gate(r0_r));
  Transistor #(.\type ("n")) transistor_126 (.in(1'b0), .out(transistor_125_out), .gate(r0_r));
  Transistor #(.\type ("n")) transistor_127 (.in(transistor_89_out), .out(transistor_127_out), .gate(r0_r));
  Transistor #(.gate("br")) transistor_128 (
    .in(transistor_89_out), .out(transistor_127_out), .gate(transistor_125_out));
  Transistor transistor_129 (.in(1'b1), .out(transistor_129_out), .gate(r0_r));
  Transistor #(.\type ("n")) transistor_130 (.in(1'b0), .out(transistor_129_out), .gate(r0_r));
  Transistor #(.\type ("n")) transistor_131 (.in(transistor_93_out), .out(transistor_131_out), .gate(r0_r));
  Transistor #(.gate("br")) transistor_132 (
    .in(transistor_93_out), .out(transistor_131_out), .gate(transistor_129_out));
  Transistor transistor_133 (.in(1'b1), .out(transistor_133_out), .gate(r0_r));
  Transistor #(.\type ("n")) transistor_134 (.in(1'b0), .out(transistor_133_out), .gate(r0_r));
  Transistor #(.gate("br")) transistor_135 (
    .in(transistor_97_out), .out(transistor_135_out), .gate(transistor_133_out));
  Transistor #(.\type ("n")) transistor_136 (.in(transistor_97_out), .out(transistor_135_out), .gate(r0_r));
  Transistor transistor_137 (.in(1'b1), .out(transistor_137_out), .gate(r0_r));
  Transistor #(.\type ("n")) transistor_138 (.in(1'b0), .out(transistor_137_out), .gate(r0_r));
  Transistor #(.\type ("n")) transistor_139 (.in(transistor_101_out), .out(transistor_139_out), .gate(r0_r));
  Transistor #(.gate("br")) transistor_140 (
    .in(transistor_101_out), .out(transistor_139_out), .gate(transistor_137_out));
  Transistor transistor_141 (.in(1'b1), .out(transistor_141_out), .gate(mar));
  Transistor #(.\type ("n")) transistor_142 (.in(1'b0), .out(transistor_141_out), .gate(mar));
  Transistor transistor_143 (.in(1'b1), .out(transistor_143_out), .gate(r1_w));
  Transistor #(.\type ("n")) transistor_144 (.in(1'b0), .out(transistor_143_out), .gate(r1_w));
  Transistor transistor_145 (.in(1'b1), .out(transistor_145_out), .gate(r1_w));
  Transistor #(.\type ("n")) transistor_146 (.in(1'b0), .out(transistor_145_out), .gate(r1_w));
  Transistor transistor_147 (.in(1'b1), .out(transistor_147_out), .gate(r1_w));
  Transistor #(.\type ("n")) transistor_148 (.in(1'b0), .out(transistor_147_out), .gate(r1_w));
  Transistor transistor_149 (.in(1'b1), .out(transistor_149_out), .gate(r1_w));
  Transistor #(.\type ("n")) transistor_150 (.in(1'b0), .out(transistor_149_out), .gate(r1_w));
  Transistor transistor_151 (.in(1'b1), .out(transistor_151_out), .gate(r1_w));
  Transistor #(.\type ("n")) transistor_152 (.in(1'b0), .out(transistor_151_out), .gate(r1_w));
  Transistor transistor_153 (.in(1'b1), .out(transistor_153_out), .gate(r1_w));
  Transistor #(.\type ("n")) transistor_154 (.in(1'b0), .out(transistor_153_out), .gate(r1_w));
  Transistor transistor_155 (.in(1'b1), .out(transistor_155_out), .gate(r1_w));
  Transistor #(.\type ("n")) transistor_156 (.in(1'b0), .out(transistor_155_out), .gate(r1_w));
  Transistor transistor_157 (.in(1'b1), .out(transistor_157_out), .gate(r1_w));
  Transistor #(.\type ("n")) transistor_158 (.in(1'b0), .out(transistor_157_out), .gate(r1_w));
  Transistor #(.\type ("n")) transistor_159 (.in(transistor_1143_out), .out(transistor_159_out), .gate(mar));
  Transistor #(.gate("br")) transistor_160 (
    .in(transistor_1143_out), .out(transistor_159_out), .gate(transistor_141_out));
  Transistor transistor_161 (.in(1'b1), .out(transistor_161_out), .gate(rst));
  Transistor #(.\type ("n")) transistor_162 (.in(1'b0), .out(transistor_161_out), .gate(rst));
  Transistor #(.\type ("n")) transistor_163 (
    .in(transistor_197_out), .out(transistor_159_out), .gate(transistor_141_out));
  Transistor #(.gate("br")) transistor_164 (.in(transistor_197_out), .out(transistor_159_out), .gate(mar));
  LED led_2 (.in(transistor_197_out));
  Transistor #(.\type ("n")) transistor_165 (.in(transistor_1367_out), .out(transistor_165_out), .gate(r1_w));
  Transistor #(.gate("br")) transistor_166 (
    .in(transistor_1367_out), .out(transistor_165_out), .gate(transistor_143_out));
  Transistor #(.\type ("n")) transistor_167 (
    .in(transistor_219_out), .out(transistor_165_out), .gate(transistor_143_out));
  Transistor #(.gate("br")) transistor_168 (.in(transistor_219_out), .out(transistor_165_out), .gate(r1_w));
  Transistor #(.\type ("n")) transistor_169 (.in(transistor_1355_out), .out(transistor_169_out), .gate(r1_w));
  Transistor #(.gate("br")) transistor_170 (
    .in(transistor_1355_out), .out(transistor_169_out), .gate(transistor_145_out));
  Transistor #(.\type ("n")) transistor_171 (
    .in(transistor_224_out), .out(transistor_169_out), .gate(transistor_145_out));
  Transistor #(.gate("br")) transistor_172 (.in(transistor_224_out), .out(transistor_169_out), .gate(r1_w));
  Transistor #(.\type ("n")) transistor_173 (.in(transistor_1287_out), .out(transistor_173_out), .gate(r1_w));
  Transistor #(.gate("br")) transistor_174 (
    .in(transistor_1287_out), .out(transistor_173_out), .gate(transistor_147_out));
  Transistor #(.\type ("n")) transistor_175 (
    .in(transistor_229_out), .out(transistor_173_out), .gate(transistor_147_out));
  Transistor #(.gate("br")) transistor_176 (.in(transistor_229_out), .out(transistor_173_out), .gate(r1_w));
  Transistor #(.\type ("n")) transistor_177 (.in(transistor_1251_out), .out(transistor_177_out), .gate(r1_w));
  Transistor #(.gate("br")) transistor_178 (
    .in(transistor_1251_out), .out(transistor_177_out), .gate(transistor_149_out));
  Transistor #(.\type ("n")) transistor_179 (
    .in(transistor_234_out), .out(transistor_177_out), .gate(transistor_149_out));
  Transistor #(.gate("br")) transistor_180 (.in(transistor_234_out), .out(transistor_177_out), .gate(r1_w));
  Transistor #(.\type ("n")) transistor_181 (.in(transistor_1215_out), .out(transistor_181_out), .gate(r1_w));
  Transistor #(.gate("br")) transistor_182 (
    .in(transistor_1215_out), .out(transistor_181_out), .gate(transistor_151_out));
  Transistor #(.\type ("n")) transistor_183 (
    .in(transistor_239_out), .out(transistor_181_out), .gate(transistor_151_out));
  Transistor #(.gate("br")) transistor_184 (.in(transistor_239_out), .out(transistor_181_out), .gate(r1_w));
  Transistor #(.\type ("n")) transistor_185 (.in(transistor_1179_out), .out(transistor_185_out), .gate(r1_w));
  Transistor #(.gate("br")) transistor_186 (
    .in(transistor_1179_out), .out(transistor_185_out), .gate(transistor_153_out));
  Transistor #(.\type ("n")) transistor_187 (
    .in(transistor_244_out), .out(transistor_185_out), .gate(transistor_153_out));
  Transistor #(.gate("br")) transistor_188 (.in(transistor_244_out), .out(transistor_185_out), .gate(r1_w));
  Transistor #(.\type ("n")) transistor_189 (.in(transistor_1143_out), .out(transistor_189_out), .gate(r1_w));
  Transistor #(.gate("br")) transistor_190 (
    .in(transistor_1143_out), .out(transistor_189_out), .gate(transistor_155_out));
  Transistor #(.\type ("n")) transistor_191 (
    .in(transistor_249_out), .out(transistor_189_out), .gate(transistor_155_out));
  Transistor #(.gate("br")) transistor_192 (.in(transistor_249_out), .out(transistor_189_out), .gate(r1_w));
  Transistor #(.\type ("n")) transistor_193 (.in(transistor_1083_out), .out(transistor_193_out), .gate(r1_w));
  Transistor #(.gate("br")) transistor_194 (
    .in(transistor_1083_out), .out(transistor_193_out), .gate(transistor_157_out));
  Transistor #(.\type ("n")) transistor_195 (
    .in(transistor_254_out), .out(transistor_193_out), .gate(transistor_157_out));
  Transistor #(.gate("br")) transistor_196 (.in(transistor_254_out), .out(transistor_193_out), .gate(r1_w));
  Transistor #(.\type ("n")) transistor_197 (.in(1'b0), .out(transistor_197_out), .gate(rst));
  Transistor #(.gate("br")) transistor_198 (.in(1'b0), .out(transistor_197_out), .gate(transistor_161_out));
  Transistor #(.\type ("n")) transistor_199 (
    .in(transistor_159_out), .out(transistor_197_out), .gate(transistor_161_out));
  Transistor #(.gate("br")) transistor_200 (.in(transistor_159_out), .out(transistor_197_out), .gate(rst));
  Transistor transistor_201 (.in(1'b1), .out(transistor_201_out), .gate(rst));
  Transistor #(.\type ("n")) transistor_202 (.in(1'b0), .out(transistor_201_out), .gate(rst));
  Transistor transistor_203 (.in(1'b1), .out(transistor_203_out), .gate(rst));
  Transistor #(.\type ("n")) transistor_204 (.in(1'b0), .out(transistor_203_out), .gate(rst));
  Transistor transistor_205 (.in(1'b1), .out(transistor_205_out), .gate(rst));
  Transistor #(.\type ("n")) transistor_206 (.in(1'b0), .out(transistor_205_out), .gate(rst));
  Transistor transistor_207 (.in(1'b1), .out(transistor_207_out), .gate(rst));
  Transistor #(.\type ("n")) transistor_208 (.in(1'b0), .out(transistor_207_out), .gate(rst));
  Transistor transistor_209 (.in(1'b1), .out(transistor_209_out), .gate(rst));
  Transistor #(.\type ("n")) transistor_210 (.in(1'b0), .out(transistor_209_out), .gate(rst));
  Transistor transistor_211 (.in(1'b1), .out(transistor_211_out), .gate(rst));
  Transistor #(.\type ("n")) transistor_212 (.in(1'b0), .out(transistor_211_out), .gate(rst));
  Transistor transistor_213 (.in(1'b1), .out(transistor_213_out), .gate(rst));
  Transistor #(.\type ("n")) transistor_214 (.in(1'b0), .out(transistor_213_out), .gate(rst));
  Transistor transistor_215 (.in(1'b1), .out(transistor_215_out), .gate(rst));
  Transistor #(.\type ("n")) transistor_216 (.in(1'b0), .out(transistor_215_out), .gate(rst));
  Transistor transistor_217 (.in(1'b1), .out(transistor_217_out), .gate(mar));
  Transistor #(.\type ("n")) transistor_218 (.in(1'b0), .out(transistor_217_out), .gate(mar));
  Transistor #(.\type ("n")) transistor_219 (.in(1'b0), .out(transistor_219_out), .gate(rst));
  Transistor #(.gate("br")) transistor_220 (.in(1'b0), .out(transistor_219_out), .gate(transistor_201_out));
  Transistor #(.\type ("n")) transistor_221 (
    .in(transistor_165_out), .out(transistor_219_out), .gate(transistor_201_out));
  Transistor #(.gate("br")) transistor_222 (.in(transistor_165_out), .out(transistor_219_out), .gate(rst));
  Transistor #(.\type ("n")) transistor_223 (.in(transistor_219_out), .out(transistor_111_out), .gate(r1_r));
  Transistor #(.\type ("n")) transistor_224 (.in(1'b0), .out(transistor_224_out), .gate(rst));
  Transistor #(.gate("br")) transistor_225 (.in(1'b0), .out(transistor_224_out), .gate(transistor_203_out));
  Transistor #(.\type ("n")) transistor_226 (
    .in(transistor_169_out), .out(transistor_224_out), .gate(transistor_203_out));
  Transistor #(.gate("br")) transistor_227 (.in(transistor_169_out), .out(transistor_224_out), .gate(rst));
  Transistor #(.\type ("n")) transistor_228 (.in(transistor_224_out), .out(transistor_115_out), .gate(r1_r));
  Transistor #(.\type ("n")) transistor_229 (.in(1'b0), .out(transistor_229_out), .gate(rst));
  Transistor #(.gate("br")) transistor_230 (.in(1'b0), .out(transistor_229_out), .gate(transistor_205_out));
  Transistor #(.\type ("n")) transistor_231 (
    .in(transistor_173_out), .out(transistor_229_out), .gate(transistor_205_out));
  Transistor #(.gate("br")) transistor_232 (.in(transistor_173_out), .out(transistor_229_out), .gate(rst));
  Transistor #(.\type ("n")) transistor_233 (.in(transistor_229_out), .out(transistor_119_out), .gate(r1_r));
  Transistor #(.\type ("n")) transistor_234 (.in(1'b0), .out(transistor_234_out), .gate(rst));
  Transistor #(.gate("br")) transistor_235 (.in(1'b0), .out(transistor_234_out), .gate(transistor_207_out));
  Transistor #(.\type ("n")) transistor_236 (
    .in(transistor_177_out), .out(transistor_234_out), .gate(transistor_207_out));
  Transistor #(.gate("br")) transistor_237 (.in(transistor_177_out), .out(transistor_234_out), .gate(rst));
  Transistor #(.\type ("n")) transistor_238 (.in(transistor_234_out), .out(transistor_123_out), .gate(r1_r));
  Transistor #(.\type ("n")) transistor_239 (.in(1'b0), .out(transistor_239_out), .gate(rst));
  Transistor #(.gate("br")) transistor_240 (.in(1'b0), .out(transistor_239_out), .gate(transistor_209_out));
  Transistor #(.\type ("n")) transistor_241 (
    .in(transistor_181_out), .out(transistor_239_out), .gate(transistor_209_out));
  Transistor #(.gate("br")) transistor_242 (.in(transistor_181_out), .out(transistor_239_out), .gate(rst));
  Transistor #(.\type ("n")) transistor_243 (.in(transistor_239_out), .out(transistor_127_out), .gate(r1_r));
  Transistor #(.\type ("n")) transistor_244 (.in(1'b0), .out(transistor_244_out), .gate(rst));
  Transistor #(.gate("br")) transistor_245 (.in(1'b0), .out(transistor_244_out), .gate(transistor_211_out));
  Transistor #(.\type ("n")) transistor_246 (
    .in(transistor_185_out), .out(transistor_244_out), .gate(transistor_211_out));
  Transistor #(.gate("br")) transistor_247 (.in(transistor_185_out), .out(transistor_244_out), .gate(rst));
  Transistor #(.\type ("n")) transistor_248 (.in(transistor_244_out), .out(transistor_131_out), .gate(r1_r));
  Transistor #(.\type ("n")) transistor_249 (.in(1'b0), .out(transistor_249_out), .gate(rst));
  Transistor #(.gate("br")) transistor_250 (.in(1'b0), .out(transistor_249_out), .gate(transistor_213_out));
  Transistor #(.\type ("n")) transistor_251 (
    .in(transistor_189_out), .out(transistor_249_out), .gate(transistor_213_out));
  Transistor #(.gate("br")) transistor_252 (.in(transistor_189_out), .out(transistor_249_out), .gate(rst));
  Transistor #(.\type ("n")) transistor_253 (.in(transistor_249_out), .out(transistor_135_out), .gate(r1_r));
  Transistor #(.\type ("n")) transistor_254 (.in(1'b0), .out(transistor_254_out), .gate(rst));
  Transistor #(.gate("br")) transistor_255 (.in(1'b0), .out(transistor_254_out), .gate(transistor_215_out));
  Transistor #(.\type ("n")) transistor_256 (
    .in(transistor_193_out), .out(transistor_254_out), .gate(transistor_215_out));
  Transistor #(.gate("br")) transistor_257 (.in(transistor_193_out), .out(transistor_254_out), .gate(rst));
  Transistor #(.\type ("n")) transistor_258 (.in(transistor_254_out), .out(transistor_139_out), .gate(r1_r));
  Transistor #(.\type ("n")) transistor_259 (.in(transistor_1179_out), .out(transistor_259_out), .gate(mar));
  Transistor #(.gate("br")) transistor_260 (
    .in(transistor_1179_out), .out(transistor_259_out), .gate(transistor_217_out));
  Transistor #(.\type ("n")) transistor_261 (
    .in(transistor_305_out), .out(transistor_259_out), .gate(transistor_217_out));
  Transistor #(.gate("br")) transistor_262 (.in(transistor_305_out), .out(transistor_259_out), .gate(mar));
  LED led_3 (.in(transistor_305_out));
  Transistor transistor_263 (.in(1'b1), .out(transistor_263_out), .gate(r1_r));
  Transistor #(.\type ("n")) transistor_264 (.in(1'b0), .out(transistor_263_out), .gate(r1_r));
  Transistor #(.gate("br")) transistor_265 (
    .in(transistor_219_out), .out(transistor_111_out), .gate(transistor_263_out));
  Transistor transistor_266 (.in(1'b1), .out(transistor_266_out), .gate(r1_r));
  Transistor #(.\type ("n")) transistor_267 (.in(1'b0), .out(transistor_266_out), .gate(r1_r));
  Transistor #(.gate("br")) transistor_268 (
    .in(transistor_224_out), .out(transistor_115_out), .gate(transistor_266_out));
  Transistor transistor_269 (.in(1'b1), .out(transistor_269_out), .gate(r1_r));
  Transistor #(.\type ("n")) transistor_270 (.in(1'b0), .out(transistor_269_out), .gate(r1_r));
  Transistor #(.gate("br")) transistor_271 (
    .in(transistor_229_out), .out(transistor_119_out), .gate(transistor_269_out));
  Transistor transistor_272 (.in(1'b1), .out(transistor_272_out), .gate(r1_r));
  Transistor #(.\type ("n")) transistor_273 (.in(1'b0), .out(transistor_272_out), .gate(r1_r));
  Transistor #(.gate("br")) transistor_274 (
    .in(transistor_234_out), .out(transistor_123_out), .gate(transistor_272_out));
  Transistor transistor_275 (.in(1'b1), .out(transistor_275_out), .gate(r1_r));
  Transistor #(.\type ("n")) transistor_276 (.in(1'b0), .out(transistor_275_out), .gate(r1_r));
  Transistor #(.gate("br")) transistor_277 (
    .in(transistor_239_out), .out(transistor_127_out), .gate(transistor_275_out));
  Transistor transistor_278 (.in(1'b1), .out(transistor_278_out), .gate(r1_r));
  Transistor #(.\type ("n")) transistor_279 (.in(1'b0), .out(transistor_278_out), .gate(r1_r));
  Transistor #(.gate("br")) transistor_280 (
    .in(transistor_244_out), .out(transistor_131_out), .gate(transistor_278_out));
  Transistor transistor_281 (.in(1'b1), .out(transistor_281_out), .gate(r1_r));
  Transistor #(.\type ("n")) transistor_282 (.in(1'b0), .out(transistor_281_out), .gate(r1_r));
  Transistor #(.gate("br")) transistor_283 (
    .in(transistor_249_out), .out(transistor_135_out), .gate(transistor_281_out));
  Transistor transistor_284 (.in(1'b1), .out(transistor_284_out), .gate(r1_r));
  Transistor #(.\type ("n")) transistor_285 (.in(1'b0), .out(transistor_284_out), .gate(r1_r));
  Transistor #(.gate("br")) transistor_286 (
    .in(transistor_254_out), .out(transistor_139_out), .gate(transistor_284_out));
  Transistor transistor_287 (.in(1'b1), .out(transistor_287_out), .gate(rst));
  Transistor #(.\type ("n")) transistor_288 (.in(1'b0), .out(transistor_287_out), .gate(rst));
  Transistor transistor_289 (.in(1'b1), .out(transistor_289_out), .gate(r2_w));
  Transistor #(.\type ("n")) transistor_290 (.in(1'b0), .out(transistor_289_out), .gate(r2_w));
  Transistor transistor_291 (.in(1'b1), .out(transistor_291_out), .gate(r2_w));
  Transistor #(.\type ("n")) transistor_292 (.in(1'b0), .out(transistor_291_out), .gate(r2_w));
  Transistor transistor_293 (.in(1'b1), .out(transistor_293_out), .gate(r2_w));
  Transistor #(.\type ("n")) transistor_294 (.in(1'b0), .out(transistor_293_out), .gate(r2_w));
  Transistor transistor_295 (.in(1'b1), .out(transistor_295_out), .gate(r2_w));
  Transistor #(.\type ("n")) transistor_296 (.in(1'b0), .out(transistor_295_out), .gate(r2_w));
  Transistor transistor_297 (.in(1'b1), .out(transistor_297_out), .gate(r2_w));
  Transistor #(.\type ("n")) transistor_298 (.in(1'b0), .out(transistor_297_out), .gate(r2_w));
  Transistor transistor_299 (.in(1'b1), .out(transistor_299_out), .gate(r2_w));
  Transistor #(.\type ("n")) transistor_300 (.in(1'b0), .out(transistor_299_out), .gate(r2_w));
  Transistor transistor_301 (.in(1'b1), .out(transistor_301_out), .gate(r2_w));
  Transistor #(.\type ("n")) transistor_302 (.in(1'b0), .out(transistor_301_out), .gate(r2_w));
  Transistor transistor_303 (.in(1'b1), .out(transistor_303_out), .gate(r2_w));
  Transistor #(.\type ("n")) transistor_304 (.in(1'b0), .out(transistor_303_out), .gate(r2_w));
  Transistor #(.\type ("n")) transistor_305 (.in(1'b0), .out(transistor_305_out), .gate(rst));
  Transistor #(.gate("br")) transistor_306 (.in(1'b0), .out(transistor_305_out), .gate(transistor_287_out));
  Transistor #(.\type ("n")) transistor_307 (
    .in(transistor_259_out), .out(transistor_305_out), .gate(transistor_287_out));
  Transistor #(.gate("br")) transistor_308 (.in(transistor_259_out), .out(transistor_305_out), .gate(rst));
  Transistor #(.\type ("n")) transistor_309 (.in(transistor_1367_out), .out(transistor_309_out), .gate(r2_w));
  Transistor #(.gate("br")) transistor_310 (
    .in(transistor_1367_out), .out(transistor_309_out), .gate(transistor_289_out));
  Transistor #(.\type ("n")) transistor_311 (
    .in(transistor_347_out), .out(transistor_309_out), .gate(transistor_289_out));
  Transistor #(.gate("br")) transistor_312 (.in(transistor_347_out), .out(transistor_309_out), .gate(r2_w));
  Transistor #(.\type ("n")) transistor_313 (.in(transistor_1355_out), .out(transistor_313_out), .gate(r2_w));
  Transistor #(.gate("br")) transistor_314 (
    .in(transistor_1355_out), .out(transistor_313_out), .gate(transistor_291_out));
  Transistor #(.\type ("n")) transistor_315 (
    .in(transistor_353_out), .out(transistor_313_out), .gate(transistor_291_out));
  Transistor #(.gate("br")) transistor_316 (.in(transistor_353_out), .out(transistor_313_out), .gate(r2_w));
  Transistor #(.\type ("n")) transistor_317 (.in(transistor_1287_out), .out(transistor_317_out), .gate(r2_w));
  Transistor #(.gate("br")) transistor_318 (
    .in(transistor_1287_out), .out(transistor_317_out), .gate(transistor_293_out));
  Transistor #(.\type ("n")) transistor_319 (
    .in(transistor_359_out), .out(transistor_317_out), .gate(transistor_293_out));
  Transistor #(.gate("br")) transistor_320 (.in(transistor_359_out), .out(transistor_317_out), .gate(r2_w));
  Transistor #(.\type ("n")) transistor_321 (.in(transistor_1251_out), .out(transistor_321_out), .gate(r2_w));
  Transistor #(.gate("br")) transistor_322 (
    .in(transistor_1251_out), .out(transistor_321_out), .gate(transistor_295_out));
  Transistor #(.\type ("n")) transistor_323 (
    .in(transistor_365_out), .out(transistor_321_out), .gate(transistor_295_out));
  Transistor #(.gate("br")) transistor_324 (.in(transistor_365_out), .out(transistor_321_out), .gate(r2_w));
  Transistor #(.\type ("n")) transistor_325 (.in(transistor_1215_out), .out(transistor_325_out), .gate(r2_w));
  Transistor #(.gate("br")) transistor_326 (
    .in(transistor_1215_out), .out(transistor_325_out), .gate(transistor_297_out));
  Transistor #(.\type ("n")) transistor_327 (
    .in(transistor_371_out), .out(transistor_325_out), .gate(transistor_297_out));
  Transistor #(.gate("br")) transistor_328 (.in(transistor_371_out), .out(transistor_325_out), .gate(r2_w));
  Transistor #(.\type ("n")) transistor_329 (.in(transistor_1179_out), .out(transistor_329_out), .gate(r2_w));
  Transistor #(.gate("br")) transistor_330 (
    .in(transistor_1179_out), .out(transistor_329_out), .gate(transistor_299_out));
  Transistor #(.\type ("n")) transistor_331 (
    .in(transistor_377_out), .out(transistor_329_out), .gate(transistor_299_out));
  Transistor #(.gate("br")) transistor_332 (.in(transistor_377_out), .out(transistor_329_out), .gate(r2_w));
  Transistor #(.\type ("n")) transistor_333 (.in(transistor_1143_out), .out(transistor_333_out), .gate(r2_w));
  Transistor #(.gate("br")) transistor_334 (
    .in(transistor_1143_out), .out(transistor_333_out), .gate(transistor_301_out));
  Transistor #(.\type ("n")) transistor_335 (
    .in(transistor_383_out), .out(transistor_333_out), .gate(transistor_301_out));
  Transistor #(.gate("br")) transistor_336 (.in(transistor_383_out), .out(transistor_333_out), .gate(r2_w));
  Transistor #(.\type ("n")) transistor_337 (.in(transistor_1083_out), .out(transistor_337_out), .gate(r2_w));
  Transistor #(.gate("br")) transistor_338 (
    .in(transistor_1083_out), .out(transistor_337_out), .gate(transistor_303_out));
  Transistor #(.\type ("n")) transistor_339 (
    .in(transistor_389_out), .out(transistor_337_out), .gate(transistor_303_out));
  Transistor #(.gate("br")) transistor_340 (.in(transistor_389_out), .out(transistor_337_out), .gate(r2_w));
  Transistor #(.\type ("n")) transistor_341 (.in(transistor_1215_out), .out(transistor_341_out), .gate(mar));
  Transistor #(.gate("br")) transistor_342 (
    .in(transistor_1215_out), .out(transistor_341_out), .gate(transistor_343_out));
  Transistor transistor_343 (.in(1'b1), .out(transistor_343_out), .gate(mar));
  Transistor #(.\type ("n")) transistor_344 (.in(1'b0), .out(transistor_343_out), .gate(mar));
  Transistor #(.\type ("n")) transistor_345 (
    .in(transistor_429_out), .out(transistor_341_out), .gate(transistor_343_out));
  Transistor #(.gate("br")) transistor_346 (.in(transistor_429_out), .out(transistor_341_out), .gate(mar));
  Transistor #(.\type ("n")) transistor_347 (.in(1'b0), .out(transistor_347_out), .gate(rst));
  Transistor #(.gate("br")) transistor_348 (.in(1'b0), .out(transistor_347_out), .gate(transistor_349_out));
  Transistor transistor_349 (.in(1'b1), .out(transistor_349_out), .gate(rst));
  Transistor #(.\type ("n")) transistor_350 (.in(1'b0), .out(transistor_349_out), .gate(rst));
  Transistor #(.\type ("n")) transistor_351 (
    .in(transistor_309_out), .out(transistor_347_out), .gate(transistor_349_out));
  Transistor #(.gate("br")) transistor_352 (.in(transistor_309_out), .out(transistor_347_out), .gate(rst));
  Transistor #(.\type ("n")) transistor_353 (.in(1'b0), .out(transistor_353_out), .gate(rst));
  Transistor #(.gate("br")) transistor_354 (.in(1'b0), .out(transistor_353_out), .gate(transistor_355_out));
  Transistor transistor_355 (.in(1'b1), .out(transistor_355_out), .gate(rst));
  Transistor #(.\type ("n")) transistor_356 (.in(1'b0), .out(transistor_355_out), .gate(rst));
  Transistor #(.\type ("n")) transistor_357 (
    .in(transistor_313_out), .out(transistor_353_out), .gate(transistor_355_out));
  Transistor #(.gate("br")) transistor_358 (.in(transistor_313_out), .out(transistor_353_out), .gate(rst));
  Transistor #(.\type ("n")) transistor_359 (.in(1'b0), .out(transistor_359_out), .gate(rst));
  Transistor #(.gate("br")) transistor_360 (.in(1'b0), .out(transistor_359_out), .gate(transistor_361_out));
  Transistor transistor_361 (.in(1'b1), .out(transistor_361_out), .gate(rst));
  Transistor #(.\type ("n")) transistor_362 (.in(1'b0), .out(transistor_361_out), .gate(rst));
  Transistor #(.\type ("n")) transistor_363 (
    .in(transistor_317_out), .out(transistor_359_out), .gate(transistor_361_out));
  Transistor #(.gate("br")) transistor_364 (.in(transistor_317_out), .out(transistor_359_out), .gate(rst));
  Transistor #(.\type ("n")) transistor_365 (.in(1'b0), .out(transistor_365_out), .gate(rst));
  Transistor #(.gate("br")) transistor_366 (.in(1'b0), .out(transistor_365_out), .gate(transistor_367_out));
  Transistor transistor_367 (.in(1'b1), .out(transistor_367_out), .gate(rst));
  Transistor #(.\type ("n")) transistor_368 (.in(1'b0), .out(transistor_367_out), .gate(rst));
  Transistor #(.\type ("n")) transistor_369 (
    .in(transistor_321_out), .out(transistor_365_out), .gate(transistor_367_out));
  Transistor #(.gate("br")) transistor_370 (.in(transistor_321_out), .out(transistor_365_out), .gate(rst));
  Transistor #(.\type ("n")) transistor_371 (.in(1'b0), .out(transistor_371_out), .gate(rst));
  Transistor #(.gate("br")) transistor_372 (.in(1'b0), .out(transistor_371_out), .gate(transistor_373_out));
  Transistor transistor_373 (.in(1'b1), .out(transistor_373_out), .gate(rst));
  Transistor #(.\type ("n")) transistor_374 (.in(1'b0), .out(transistor_373_out), .gate(rst));
  Transistor #(.\type ("n")) transistor_375 (
    .in(transistor_325_out), .out(transistor_371_out), .gate(transistor_373_out));
  Transistor #(.gate("br")) transistor_376 (.in(transistor_325_out), .out(transistor_371_out), .gate(rst));
  Transistor #(.\type ("n")) transistor_377 (.in(1'b0), .out(transistor_377_out), .gate(rst));
  Transistor #(.gate("br")) transistor_378 (.in(1'b0), .out(transistor_377_out), .gate(transistor_379_out));
  Transistor transistor_379 (.in(1'b1), .out(transistor_379_out), .gate(rst));
  Transistor #(.\type ("n")) transistor_380 (.in(1'b0), .out(transistor_379_out), .gate(rst));
  Transistor #(.\type ("n")) transistor_381 (
    .in(transistor_329_out), .out(transistor_377_out), .gate(transistor_379_out));
  Transistor #(.gate("br")) transistor_382 (.in(transistor_329_out), .out(transistor_377_out), .gate(rst));
  Transistor #(.\type ("n")) transistor_383 (.in(1'b0), .out(transistor_383_out), .gate(rst));
  Transistor #(.gate("br")) transistor_384 (.in(1'b0), .out(transistor_383_out), .gate(transistor_385_out));
  Transistor transistor_385 (.in(1'b1), .out(transistor_385_out), .gate(rst));
  Transistor #(.\type ("n")) transistor_386 (.in(1'b0), .out(transistor_385_out), .gate(rst));
  Transistor #(.\type ("n")) transistor_387 (
    .in(transistor_333_out), .out(transistor_383_out), .gate(transistor_385_out));
  Transistor #(.gate("br")) transistor_388 (.in(transistor_333_out), .out(transistor_383_out), .gate(rst));
  Transistor #(.\type ("n")) transistor_389 (.in(1'b0), .out(transistor_389_out), .gate(rst));
  Transistor #(.gate("br")) transistor_390 (.in(1'b0), .out(transistor_389_out), .gate(transistor_391_out));
  Transistor transistor_391 (.in(1'b1), .out(transistor_391_out), .gate(rst));
  Transistor #(.\type ("n")) transistor_392 (.in(1'b0), .out(transistor_391_out), .gate(rst));
  Transistor #(.\type ("n")) transistor_393 (
    .in(transistor_337_out), .out(transistor_389_out), .gate(transistor_391_out));
  Transistor #(.gate("br")) transistor_394 (.in(transistor_337_out), .out(transistor_389_out), .gate(rst));
  Transistor transistor_395 (.in(1'b1), .out(transistor_395_out), .gate(rst));
  Transistor #(.\type ("n")) transistor_396 (.in(1'b0), .out(transistor_395_out), .gate(rst));
  LED led_4 (.in(transistor_429_out));
  Transistor transistor_397 (.in(1'b1), .out(transistor_397_out), .gate(r2_r));
  Transistor #(.\type ("n")) transistor_398 (.in(1'b0), .out(transistor_397_out), .gate(r2_r));
  Transistor #(.\type ("n")) transistor_399 (.in(transistor_347_out), .out(transistor_111_out), .gate(r2_r));
  Transistor #(.gate("br")) transistor_400 (
    .in(transistor_347_out), .out(transistor_111_out), .gate(transistor_397_out));
  Transistor transistor_401 (.in(1'b1), .out(transistor_401_out), .gate(r2_r));
  Transistor #(.\type ("n")) transistor_402 (.in(1'b0), .out(transistor_401_out), .gate(r2_r));
  Transistor #(.\type ("n")) transistor_403 (.in(transistor_353_out), .out(transistor_115_out), .gate(r2_r));
  Transistor #(.gate("br")) transistor_404 (
    .in(transistor_353_out), .out(transistor_115_out), .gate(transistor_401_out));
  Transistor transistor_405 (.in(1'b1), .out(transistor_405_out), .gate(r2_r));
  Transistor #(.\type ("n")) transistor_406 (.in(1'b0), .out(transistor_405_out), .gate(r2_r));
  Transistor #(.gate("br")) transistor_407 (
    .in(transistor_359_out), .out(transistor_119_out), .gate(transistor_405_out));
  Transistor #(.\type ("n")) transistor_408 (.in(transistor_359_out), .out(transistor_119_out), .gate(r2_r));
  Transistor transistor_409 (.in(1'b1), .out(transistor_409_out), .gate(r2_r));
  Transistor #(.\type ("n")) transistor_410 (.in(1'b0), .out(transistor_409_out), .gate(r2_r));
  Transistor #(.\type ("n")) transistor_411 (.in(transistor_365_out), .out(transistor_123_out), .gate(r2_r));
  Transistor #(.gate("br")) transistor_412 (
    .in(transistor_365_out), .out(transistor_123_out), .gate(transistor_409_out));
  Transistor transistor_413 (.in(1'b1), .out(transistor_413_out), .gate(r2_r));
  Transistor #(.\type ("n")) transistor_414 (.in(1'b0), .out(transistor_413_out), .gate(r2_r));
  Transistor #(.\type ("n")) transistor_415 (.in(transistor_371_out), .out(transistor_127_out), .gate(r2_r));
  Transistor #(.gate("br")) transistor_416 (
    .in(transistor_371_out), .out(transistor_127_out), .gate(transistor_413_out));
  Transistor transistor_417 (.in(1'b1), .out(transistor_417_out), .gate(r2_r));
  Transistor #(.\type ("n")) transistor_418 (.in(1'b0), .out(transistor_417_out), .gate(r2_r));
  Transistor #(.gate("br")) transistor_419 (
    .in(transistor_377_out), .out(transistor_131_out), .gate(transistor_417_out));
  Transistor #(.\type ("n")) transistor_420 (.in(transistor_377_out), .out(transistor_131_out), .gate(r2_r));
  Transistor transistor_421 (.in(1'b1), .out(transistor_421_out), .gate(r2_r));
  Transistor #(.\type ("n")) transistor_422 (.in(1'b0), .out(transistor_421_out), .gate(r2_r));
  Transistor #(.\type ("n")) transistor_423 (.in(transistor_383_out), .out(transistor_135_out), .gate(r2_r));
  Transistor #(.gate("br")) transistor_424 (
    .in(transistor_383_out), .out(transistor_135_out), .gate(transistor_421_out));
  Transistor transistor_425 (.in(1'b1), .out(transistor_425_out), .gate(r2_r));
  Transistor #(.\type ("n")) transistor_426 (.in(1'b0), .out(transistor_425_out), .gate(r2_r));
  Transistor #(.gate("br")) transistor_427 (
    .in(transistor_389_out), .out(transistor_139_out), .gate(transistor_425_out));
  Transistor #(.\type ("n")) transistor_428 (.in(transistor_389_out), .out(transistor_139_out), .gate(r2_r));
  Transistor #(.\type ("n")) transistor_429 (.in(1'b0), .out(transistor_429_out), .gate(rst));
  Transistor #(.gate("br")) transistor_430 (.in(1'b0), .out(transistor_429_out), .gate(transistor_395_out));
  Transistor #(.\type ("n")) transistor_431 (
    .in(transistor_341_out), .out(transistor_429_out), .gate(transistor_395_out));
  Transistor #(.gate("br")) transistor_432 (.in(transistor_341_out), .out(transistor_429_out), .gate(rst));
  Transistor transistor_433 (.in(1'b1), .out(transistor_433_out), .gate(mar));
  Transistor #(.\type ("n")) transistor_434 (.in(1'b0), .out(transistor_433_out), .gate(mar));
  Transistor #(.\type ("n")) transistor_435 (.in(transistor_1367_out), .out(transistor_435_out), .gate(r3_w));
  Transistor #(.gate("br")) transistor_436 (
    .in(transistor_1367_out), .out(transistor_435_out), .gate(transistor_437_out));
  Transistor transistor_437 (.in(1'b1), .out(transistor_437_out), .gate(r3_w));
  Transistor #(.\type ("n")) transistor_438 (.in(1'b0), .out(transistor_437_out), .gate(r3_w));
  Transistor #(.\type ("n")) transistor_439 (
    .in(transistor_509_out), .out(transistor_435_out), .gate(transistor_437_out));
  Transistor #(.gate("br")) transistor_440 (.in(transistor_509_out), .out(transistor_435_out), .gate(r3_w));
  Transistor #(.\type ("n")) transistor_441 (.in(transistor_1355_out), .out(transistor_441_out), .gate(r3_w));
  Transistor #(.gate("br")) transistor_442 (
    .in(transistor_1355_out), .out(transistor_441_out), .gate(transistor_443_out));
  Transistor transistor_443 (.in(1'b1), .out(transistor_443_out), .gate(r3_w));
  Transistor #(.\type ("n")) transistor_444 (.in(1'b0), .out(transistor_443_out), .gate(r3_w));
  Transistor #(.\type ("n")) transistor_445 (
    .in(transistor_513_out), .out(transistor_441_out), .gate(transistor_443_out));
  Transistor #(.gate("br")) transistor_446 (.in(transistor_513_out), .out(transistor_441_out), .gate(r3_w));
  Transistor #(.\type ("n")) transistor_447 (.in(transistor_1287_out), .out(transistor_447_out), .gate(r3_w));
  Transistor #(.gate("br")) transistor_448 (
    .in(transistor_1287_out), .out(transistor_447_out), .gate(transistor_449_out));
  Transistor transistor_449 (.in(1'b1), .out(transistor_449_out), .gate(r3_w));
  Transistor #(.\type ("n")) transistor_450 (.in(1'b0), .out(transistor_449_out), .gate(r3_w));
  Transistor #(.\type ("n")) transistor_451 (
    .in(transistor_517_out), .out(transistor_447_out), .gate(transistor_449_out));
  Transistor #(.gate("br")) transistor_452 (.in(transistor_517_out), .out(transistor_447_out), .gate(r3_w));
  Transistor #(.\type ("n")) transistor_453 (.in(transistor_1251_out), .out(transistor_453_out), .gate(r3_w));
  Transistor #(.gate("br")) transistor_454 (
    .in(transistor_1251_out), .out(transistor_453_out), .gate(transistor_455_out));
  Transistor transistor_455 (.in(1'b1), .out(transistor_455_out), .gate(r3_w));
  Transistor #(.\type ("n")) transistor_456 (.in(1'b0), .out(transistor_455_out), .gate(r3_w));
  Transistor #(.\type ("n")) transistor_457 (
    .in(transistor_521_out), .out(transistor_453_out), .gate(transistor_455_out));
  Transistor #(.gate("br")) transistor_458 (.in(transistor_521_out), .out(transistor_453_out), .gate(r3_w));
  Transistor #(.\type ("n")) transistor_459 (.in(transistor_1215_out), .out(transistor_459_out), .gate(r3_w));
  Transistor #(.gate("br")) transistor_460 (
    .in(transistor_1215_out), .out(transistor_459_out), .gate(transistor_461_out));
  Transistor transistor_461 (.in(1'b1), .out(transistor_461_out), .gate(r3_w));
  Transistor #(.\type ("n")) transistor_462 (.in(1'b0), .out(transistor_461_out), .gate(r3_w));
  Transistor #(.\type ("n")) transistor_463 (
    .in(transistor_525_out), .out(transistor_459_out), .gate(transistor_461_out));
  Transistor #(.gate("br")) transistor_464 (.in(transistor_525_out), .out(transistor_459_out), .gate(r3_w));
  Transistor #(.\type ("n")) transistor_465 (.in(transistor_1179_out), .out(transistor_465_out), .gate(r3_w));
  Transistor #(.gate("br")) transistor_466 (
    .in(transistor_1179_out), .out(transistor_465_out), .gate(transistor_467_out));
  Transistor transistor_467 (.in(1'b1), .out(transistor_467_out), .gate(r3_w));
  Transistor #(.\type ("n")) transistor_468 (.in(1'b0), .out(transistor_467_out), .gate(r3_w));
  Transistor #(.\type ("n")) transistor_469 (
    .in(transistor_529_out), .out(transistor_465_out), .gate(transistor_467_out));
  Transistor #(.gate("br")) transistor_470 (.in(transistor_529_out), .out(transistor_465_out), .gate(r3_w));
  Transistor #(.\type ("n")) transistor_471 (.in(transistor_1143_out), .out(transistor_471_out), .gate(r3_w));
  Transistor #(.gate("br")) transistor_472 (
    .in(transistor_1143_out), .out(transistor_471_out), .gate(transistor_473_out));
  Transistor transistor_473 (.in(1'b1), .out(transistor_473_out), .gate(r3_w));
  Transistor #(.\type ("n")) transistor_474 (.in(1'b0), .out(transistor_473_out), .gate(r3_w));
  Transistor #(.\type ("n")) transistor_475 (
    .in(transistor_533_out), .out(transistor_471_out), .gate(transistor_473_out));
  Transistor #(.gate("br")) transistor_476 (.in(transistor_533_out), .out(transistor_471_out), .gate(r3_w));
  Transistor #(.\type ("n")) transistor_477 (.in(transistor_1083_out), .out(transistor_477_out), .gate(r3_w));
  Transistor #(.gate("br")) transistor_478 (
    .in(transistor_1083_out), .out(transistor_477_out), .gate(transistor_479_out));
  Transistor transistor_479 (.in(1'b1), .out(transistor_479_out), .gate(r3_w));
  Transistor #(.\type ("n")) transistor_480 (.in(1'b0), .out(transistor_479_out), .gate(r3_w));
  Transistor #(.\type ("n")) transistor_481 (
    .in(transistor_537_out), .out(transistor_477_out), .gate(transistor_479_out));
  Transistor #(.gate("br")) transistor_482 (.in(transistor_537_out), .out(transistor_477_out), .gate(r3_w));
  Transistor #(.\type ("n")) transistor_483 (.in(transistor_1251_out), .out(transistor_483_out), .gate(mar));
  Transistor #(.gate("br")) transistor_484 (
    .in(transistor_1251_out), .out(transistor_483_out), .gate(transistor_433_out));
  Transistor #(.\type ("n")) transistor_485 (
    .in(transistor_503_out), .out(transistor_483_out), .gate(transistor_433_out));
  Transistor #(.gate("br")) transistor_486 (.in(transistor_503_out), .out(transistor_483_out), .gate(mar));
  LED led_5 (.in(transistor_503_out));
  Transistor transistor_487 (.in(1'b1), .out(transistor_487_out), .gate(rst));
  Transistor #(.\type ("n")) transistor_488 (.in(1'b0), .out(transistor_487_out), .gate(rst));
  Transistor transistor_489 (.in(1'b1), .out(transistor_489_out), .gate(rst));
  Transistor #(.\type ("n")) transistor_490 (.in(1'b0), .out(transistor_489_out), .gate(rst));
  Transistor transistor_491 (.in(1'b1), .out(transistor_491_out), .gate(rst));
  Transistor #(.\type ("n")) transistor_492 (.in(1'b0), .out(transistor_491_out), .gate(rst));
  Transistor transistor_493 (.in(1'b1), .out(transistor_493_out), .gate(rst));
  Transistor #(.\type ("n")) transistor_494 (.in(1'b0), .out(transistor_493_out), .gate(rst));
  Transistor transistor_495 (.in(1'b1), .out(transistor_495_out), .gate(rst));
  Transistor #(.\type ("n")) transistor_496 (.in(1'b0), .out(transistor_495_out), .gate(rst));
  Transistor transistor_497 (.in(1'b1), .out(transistor_497_out), .gate(rst));
  Transistor #(.\type ("n")) transistor_498 (.in(1'b0), .out(transistor_497_out), .gate(rst));
  Transistor transistor_499 (.in(1'b1), .out(transistor_499_out), .gate(rst));
  Transistor #(.\type ("n")) transistor_500 (.in(1'b0), .out(transistor_499_out), .gate(rst));
  Transistor transistor_501 (.in(1'b1), .out(transistor_501_out), .gate(rst));
  Transistor #(.\type ("n")) transistor_502 (.in(1'b0), .out(transistor_501_out), .gate(rst));
  Transistor #(.\type ("n")) transistor_503 (.in(1'b0), .out(transistor_503_out), .gate(rst));
  Transistor #(.gate("br")) transistor_504 (.in(1'b0), .out(transistor_503_out), .gate(transistor_505_out));
  Transistor transistor_505 (.in(1'b1), .out(transistor_505_out), .gate(rst));
  Transistor #(.\type ("n")) transistor_506 (.in(1'b0), .out(transistor_505_out), .gate(rst));
  Transistor #(.\type ("n")) transistor_507 (
    .in(transistor_483_out), .out(transistor_503_out), .gate(transistor_505_out));
  Transistor #(.gate("br")) transistor_508 (.in(transistor_483_out), .out(transistor_503_out), .gate(rst));
  Transistor #(.\type ("n")) transistor_509 (.in(1'b0), .out(transistor_509_out), .gate(rst));
  Transistor #(.gate("br")) transistor_510 (.in(1'b0), .out(transistor_509_out), .gate(transistor_487_out));
  Transistor #(.\type ("n")) transistor_511 (
    .in(transistor_435_out), .out(transistor_509_out), .gate(transistor_487_out));
  Transistor #(.gate("br")) transistor_512 (.in(transistor_435_out), .out(transistor_509_out), .gate(rst));
  Transistor #(.\type ("n")) transistor_513 (.in(1'b0), .out(transistor_513_out), .gate(rst));
  Transistor #(.gate("br")) transistor_514 (.in(1'b0), .out(transistor_513_out), .gate(transistor_489_out));
  Transistor #(.\type ("n")) transistor_515 (
    .in(transistor_441_out), .out(transistor_513_out), .gate(transistor_489_out));
  Transistor #(.gate("br")) transistor_516 (.in(transistor_441_out), .out(transistor_513_out), .gate(rst));
  Transistor #(.\type ("n")) transistor_517 (.in(1'b0), .out(transistor_517_out), .gate(rst));
  Transistor #(.gate("br")) transistor_518 (.in(1'b0), .out(transistor_517_out), .gate(transistor_491_out));
  Transistor #(.\type ("n")) transistor_519 (
    .in(transistor_447_out), .out(transistor_517_out), .gate(transistor_491_out));
  Transistor #(.gate("br")) transistor_520 (.in(transistor_447_out), .out(transistor_517_out), .gate(rst));
  Transistor #(.\type ("n")) transistor_521 (.in(1'b0), .out(transistor_521_out), .gate(rst));
  Transistor #(.gate("br")) transistor_522 (.in(1'b0), .out(transistor_521_out), .gate(transistor_493_out));
  Transistor #(.\type ("n")) transistor_523 (
    .in(transistor_453_out), .out(transistor_521_out), .gate(transistor_493_out));
  Transistor #(.gate("br")) transistor_524 (.in(transistor_453_out), .out(transistor_521_out), .gate(rst));
  Transistor #(.\type ("n")) transistor_525 (.in(1'b0), .out(transistor_525_out), .gate(rst));
  Transistor #(.gate("br")) transistor_526 (.in(1'b0), .out(transistor_525_out), .gate(transistor_495_out));
  Transistor #(.\type ("n")) transistor_527 (
    .in(transistor_459_out), .out(transistor_525_out), .gate(transistor_495_out));
  Transistor #(.gate("br")) transistor_528 (.in(transistor_459_out), .out(transistor_525_out), .gate(rst));
  Transistor #(.\type ("n")) transistor_529 (.in(1'b0), .out(transistor_529_out), .gate(rst));
  Transistor #(.gate("br")) transistor_530 (.in(1'b0), .out(transistor_529_out), .gate(transistor_497_out));
  Transistor #(.\type ("n")) transistor_531 (
    .in(transistor_465_out), .out(transistor_529_out), .gate(transistor_497_out));
  Transistor #(.gate("br")) transistor_532 (.in(transistor_465_out), .out(transistor_529_out), .gate(rst));
  Transistor #(.\type ("n")) transistor_533 (.in(1'b0), .out(transistor_533_out), .gate(rst));
  Transistor #(.gate("br")) transistor_534 (.in(1'b0), .out(transistor_533_out), .gate(transistor_499_out));
  Transistor #(.\type ("n")) transistor_535 (
    .in(transistor_471_out), .out(transistor_533_out), .gate(transistor_499_out));
  Transistor #(.gate("br")) transistor_536 (.in(transistor_471_out), .out(transistor_533_out), .gate(rst));
  Transistor #(.\type ("n")) transistor_537 (.in(1'b0), .out(transistor_537_out), .gate(rst));
  Transistor #(.gate("br")) transistor_538 (.in(1'b0), .out(transistor_537_out), .gate(transistor_501_out));
  Transistor #(.\type ("n")) transistor_539 (
    .in(transistor_477_out), .out(transistor_537_out), .gate(transistor_501_out));
  Transistor #(.gate("br")) transistor_540 (.in(transistor_477_out), .out(transistor_537_out), .gate(rst));
  Transistor transistor_541 (.in(1'b1), .out(transistor_541_out), .gate(mar));
  Transistor #(.\type ("n")) transistor_542 (.in(1'b0), .out(transistor_541_out), .gate(mar));
  Transistor transistor_543 (.in(1'b1), .out(transistor_543_out), .gate(r3_r));
  Transistor #(.\type ("n")) transistor_544 (.in(1'b0), .out(transistor_543_out), .gate(r3_r));
  Transistor #(.gate("br")) transistor_545 (
    .in(transistor_509_out), .out(transistor_111_out), .gate(transistor_543_out));
  Transistor #(.\type ("n")) transistor_546 (.in(transistor_509_out), .out(transistor_111_out), .gate(r3_r));
  Transistor transistor_547 (.in(1'b1), .out(transistor_547_out), .gate(r3_r));
  Transistor #(.\type ("n")) transistor_548 (.in(1'b0), .out(transistor_547_out), .gate(r3_r));
  Transistor #(.gate("br")) transistor_549 (
    .in(transistor_513_out), .out(transistor_115_out), .gate(transistor_547_out));
  Transistor #(.\type ("n")) transistor_550 (.in(transistor_513_out), .out(transistor_115_out), .gate(r3_r));
  Transistor transistor_551 (.in(1'b1), .out(transistor_551_out), .gate(r3_r));
  Transistor #(.\type ("n")) transistor_552 (.in(1'b0), .out(transistor_551_out), .gate(r3_r));
  Transistor #(.gate("br")) transistor_553 (
    .in(transistor_517_out), .out(transistor_119_out), .gate(transistor_551_out));
  Transistor #(.\type ("n")) transistor_554 (.in(transistor_517_out), .out(transistor_119_out), .gate(r3_r));
  Transistor transistor_555 (.in(1'b1), .out(transistor_555_out), .gate(r3_r));
  Transistor #(.\type ("n")) transistor_556 (.in(1'b0), .out(transistor_555_out), .gate(r3_r));
  Transistor #(.gate("br")) transistor_557 (
    .in(transistor_521_out), .out(transistor_123_out), .gate(transistor_555_out));
  Transistor #(.\type ("n")) transistor_558 (.in(transistor_521_out), .out(transistor_123_out), .gate(r3_r));
  Transistor transistor_559 (.in(1'b1), .out(transistor_559_out), .gate(r3_r));
  Transistor #(.\type ("n")) transistor_560 (.in(1'b0), .out(transistor_559_out), .gate(r3_r));
  Transistor #(.gate("br")) transistor_561 (
    .in(transistor_525_out), .out(transistor_127_out), .gate(transistor_559_out));
  Transistor #(.\type ("n")) transistor_562 (.in(transistor_525_out), .out(transistor_127_out), .gate(r3_r));
  Transistor transistor_563 (.in(1'b1), .out(transistor_563_out), .gate(r3_r));
  Transistor #(.\type ("n")) transistor_564 (.in(1'b0), .out(transistor_563_out), .gate(r3_r));
  Transistor #(.\type ("n")) transistor_565 (.in(transistor_529_out), .out(transistor_131_out), .gate(r3_r));
  Transistor #(.gate("br")) transistor_566 (
    .in(transistor_529_out), .out(transistor_131_out), .gate(transistor_563_out));
  Transistor transistor_567 (.in(1'b1), .out(transistor_567_out), .gate(r3_r));
  Transistor #(.\type ("n")) transistor_568 (.in(1'b0), .out(transistor_567_out), .gate(r3_r));
  Transistor #(.gate("br")) transistor_569 (
    .in(transistor_533_out), .out(transistor_135_out), .gate(transistor_567_out));
  Transistor #(.\type ("n")) transistor_570 (.in(transistor_533_out), .out(transistor_135_out), .gate(r3_r));
  Transistor transistor_571 (.in(1'b1), .out(transistor_571_out), .gate(r3_r));
  Transistor #(.\type ("n")) transistor_572 (.in(1'b0), .out(transistor_571_out), .gate(r3_r));
  Transistor #(.\type ("n")) transistor_573 (.in(transistor_537_out), .out(transistor_139_out), .gate(r3_r));
  Transistor #(.gate("br")) transistor_574 (
    .in(transistor_537_out), .out(transistor_139_out), .gate(transistor_571_out));
  Transistor #(.\type ("n")) transistor_575 (.in(transistor_1287_out), .out(transistor_575_out), .gate(mar));
  Transistor #(.gate("br")) transistor_576 (
    .in(transistor_1287_out), .out(transistor_575_out), .gate(transistor_541_out));
  Transistor #(.\type ("n")) transistor_577 (
    .in(transistor_629_out), .out(transistor_575_out), .gate(transistor_541_out));
  Transistor #(.gate("br")) transistor_578 (.in(transistor_629_out), .out(transistor_575_out), .gate(mar));
  Transistor transistor_579 (.in(1'b1), .out(transistor_579_out), .gate(pc_w));
  Transistor #(.\type ("n")) transistor_580 (.in(1'b0), .out(transistor_579_out), .gate(pc_w));
  Transistor transistor_581 (.in(1'b1), .out(transistor_581_out), .gate(pc_w));
  Transistor #(.\type ("n")) transistor_582 (.in(1'b0), .out(transistor_581_out), .gate(pc_w));
  Transistor transistor_583 (.in(1'b1), .out(transistor_583_out), .gate(pc_w));
  Transistor #(.\type ("n")) transistor_584 (.in(1'b0), .out(transistor_583_out), .gate(pc_w));
  Transistor transistor_585 (.in(1'b1), .out(transistor_585_out), .gate(pc_w));
  Transistor #(.\type ("n")) transistor_586 (.in(1'b0), .out(transistor_585_out), .gate(pc_w));
  Transistor transistor_587 (.in(1'b1), .out(transistor_587_out), .gate(pc_w));
  Transistor #(.\type ("n")) transistor_588 (.in(1'b0), .out(transistor_587_out), .gate(pc_w));
  Transistor transistor_589 (.in(1'b1), .out(transistor_589_out), .gate(pc_w));
  Transistor #(.\type ("n")) transistor_590 (.in(1'b0), .out(transistor_589_out), .gate(pc_w));
  Transistor transistor_591 (.in(1'b1), .out(transistor_591_out), .gate(pc_w));
  Transistor #(.\type ("n")) transistor_592 (.in(1'b0), .out(transistor_591_out), .gate(pc_w));
  Transistor transistor_593 (.in(1'b1), .out(transistor_593_out), .gate(pc_w));
  Transistor #(.\type ("n")) transistor_594 (.in(1'b0), .out(transistor_593_out), .gate(pc_w));
  Transistor transistor_595 (.in(1'b1), .out(transistor_595_out), .gate(rst));
  Transistor #(.\type ("n")) transistor_596 (.in(1'b0), .out(transistor_595_out), .gate(rst));
  LED led_6 (.in(transistor_629_out));
  Transistor #(.\type ("n")) transistor_597 (.in(transistor_1367_out), .out(transistor_597_out), .gate(pc_w));
  Transistor #(.gate("br")) transistor_598 (
    .in(transistor_1367_out), .out(transistor_597_out), .gate(transistor_579_out));
  Transistor #(.\type ("n")) transistor_599 (
    .in(transistor_655_out), .out(transistor_597_out), .gate(transistor_579_out));
  Transistor #(.gate("br")) transistor_600 (.in(transistor_655_out), .out(transistor_597_out), .gate(pc_w));
  Transistor #(.\type ("n")) transistor_601 (.in(transistor_1355_out), .out(transistor_601_out), .gate(pc_w));
  Transistor #(.gate("br")) transistor_602 (
    .in(transistor_1355_out), .out(transistor_601_out), .gate(transistor_581_out));
  Transistor #(.\type ("n")) transistor_603 (
    .in(transistor_659_out), .out(transistor_601_out), .gate(transistor_581_out));
  Transistor #(.gate("br")) transistor_604 (.in(transistor_659_out), .out(transistor_601_out), .gate(pc_w));
  Transistor #(.\type ("n")) transistor_605 (.in(transistor_1287_out), .out(transistor_605_out), .gate(pc_w));
  Transistor #(.gate("br")) transistor_606 (
    .in(transistor_1287_out), .out(transistor_605_out), .gate(transistor_583_out));
  Transistor #(.\type ("n")) transistor_607 (
    .in(transistor_663_out), .out(transistor_605_out), .gate(transistor_583_out));
  Transistor #(.gate("br")) transistor_608 (.in(transistor_663_out), .out(transistor_605_out), .gate(pc_w));
  Transistor #(.\type ("n")) transistor_609 (.in(transistor_1251_out), .out(transistor_609_out), .gate(pc_w));
  Transistor #(.gate("br")) transistor_610 (
    .in(transistor_1251_out), .out(transistor_609_out), .gate(transistor_585_out));
  Transistor #(.\type ("n")) transistor_611 (
    .in(transistor_667_out), .out(transistor_609_out), .gate(transistor_585_out));
  Transistor #(.gate("br")) transistor_612 (.in(transistor_667_out), .out(transistor_609_out), .gate(pc_w));
  Transistor #(.\type ("n")) transistor_613 (.in(transistor_1215_out), .out(transistor_613_out), .gate(pc_w));
  Transistor #(.gate("br")) transistor_614 (
    .in(transistor_1215_out), .out(transistor_613_out), .gate(transistor_587_out));
  Transistor #(.\type ("n")) transistor_615 (
    .in(transistor_671_out), .out(transistor_613_out), .gate(transistor_587_out));
  Transistor #(.gate("br")) transistor_616 (.in(transistor_671_out), .out(transistor_613_out), .gate(pc_w));
  Transistor #(.\type ("n")) transistor_617 (.in(transistor_1179_out), .out(transistor_617_out), .gate(pc_w));
  Transistor #(.gate("br")) transistor_618 (
    .in(transistor_1179_out), .out(transistor_617_out), .gate(transistor_589_out));
  Transistor #(.\type ("n")) transistor_619 (
    .in(transistor_675_out), .out(transistor_617_out), .gate(transistor_589_out));
  Transistor #(.gate("br")) transistor_620 (.in(transistor_675_out), .out(transistor_617_out), .gate(pc_w));
  Transistor #(.\type ("n")) transistor_621 (.in(transistor_1143_out), .out(transistor_621_out), .gate(pc_w));
  Transistor #(.gate("br")) transistor_622 (
    .in(transistor_1143_out), .out(transistor_621_out), .gate(transistor_591_out));
  Transistor #(.\type ("n")) transistor_623 (
    .in(transistor_679_out), .out(transistor_621_out), .gate(transistor_591_out));
  Transistor #(.gate("br")) transistor_624 (.in(transistor_679_out), .out(transistor_621_out), .gate(pc_w));
  Transistor #(.\type ("n")) transistor_625 (.in(transistor_1083_out), .out(transistor_625_out), .gate(pc_w));
  Transistor #(.gate("br")) transistor_626 (
    .in(transistor_1083_out), .out(transistor_625_out), .gate(transistor_593_out));
  Transistor #(.\type ("n")) transistor_627 (
    .in(transistor_683_out), .out(transistor_625_out), .gate(transistor_593_out));
  Transistor #(.gate("br")) transistor_628 (.in(transistor_683_out), .out(transistor_625_out), .gate(pc_w));
  Transistor #(.\type ("n")) transistor_629 (.in(1'b0), .out(transistor_629_out), .gate(rst));
  Transistor #(.gate("br")) transistor_630 (.in(1'b0), .out(transistor_629_out), .gate(transistor_595_out));
  Transistor #(.\type ("n")) transistor_631 (
    .in(transistor_575_out), .out(transistor_629_out), .gate(transistor_595_out));
  Transistor #(.gate("br")) transistor_632 (.in(transistor_575_out), .out(transistor_629_out), .gate(rst));
  Transistor transistor_633 (.in(1'b1), .out(transistor_633_out), .gate(rst));
  Transistor #(.\type ("n")) transistor_634 (.in(1'b0), .out(transistor_633_out), .gate(rst));
  Transistor transistor_635 (.in(1'b1), .out(transistor_635_out), .gate(rst));
  Transistor #(.\type ("n")) transistor_636 (.in(1'b0), .out(transistor_635_out), .gate(rst));
  Transistor transistor_637 (.in(1'b1), .out(transistor_637_out), .gate(rst));
  Transistor #(.\type ("n")) transistor_638 (.in(1'b0), .out(transistor_637_out), .gate(rst));
  Transistor transistor_639 (.in(1'b1), .out(transistor_639_out), .gate(rst));
  Transistor #(.\type ("n")) transistor_640 (.in(1'b0), .out(transistor_639_out), .gate(rst));
  Transistor transistor_641 (.in(1'b1), .out(transistor_641_out), .gate(rst));
  Transistor #(.\type ("n")) transistor_642 (.in(1'b0), .out(transistor_641_out), .gate(rst));
  Transistor transistor_643 (.in(1'b1), .out(transistor_643_out), .gate(rst));
  Transistor #(.\type ("n")) transistor_644 (.in(1'b0), .out(transistor_643_out), .gate(rst));
  Transistor transistor_645 (.in(1'b1), .out(transistor_645_out), .gate(rst));
  Transistor #(.\type ("n")) transistor_646 (.in(1'b0), .out(transistor_645_out), .gate(rst));
  Transistor transistor_647 (.in(1'b1), .out(transistor_647_out), .gate(rst));
  Transistor #(.\type ("n")) transistor_648 (.in(1'b0), .out(transistor_647_out), .gate(rst));
  Transistor #(.\type ("n")) transistor_649 (.in(transistor_1355_out), .out(transistor_649_out), .gate(mar));
  Transistor #(.gate("br")) transistor_650 (
    .in(transistor_1355_out), .out(transistor_649_out), .gate(transistor_651_out));
  Transistor transistor_651 (.in(1'b1), .out(transistor_651_out), .gate(mar));
  Transistor #(.\type ("n")) transistor_652 (.in(1'b0), .out(transistor_651_out), .gate(mar));
  Transistor #(.\type ("n")) transistor_653 (
    .in(transistor_721_out), .out(transistor_649_out), .gate(transistor_651_out));
  Transistor #(.gate("br")) transistor_654 (.in(transistor_721_out), .out(transistor_649_out), .gate(mar));
  Transistor #(.\type ("n")) transistor_655 (.in(1'b0), .out(transistor_655_out), .gate(rst));
  Transistor #(.gate("br")) transistor_656 (.in(1'b0), .out(transistor_655_out), .gate(transistor_633_out));
  Transistor #(.\type ("n")) transistor_657 (
    .in(transistor_597_out), .out(transistor_655_out), .gate(transistor_633_out));
  Transistor #(.gate("br")) transistor_658 (.in(transistor_597_out), .out(transistor_655_out), .gate(rst));
  Transistor #(.\type ("n")) transistor_659 (.in(1'b0), .out(transistor_659_out), .gate(rst));
  Transistor #(.gate("br")) transistor_660 (.in(1'b0), .out(transistor_659_out), .gate(transistor_635_out));
  Transistor #(.\type ("n")) transistor_661 (
    .in(transistor_601_out), .out(transistor_659_out), .gate(transistor_635_out));
  Transistor #(.gate("br")) transistor_662 (.in(transistor_601_out), .out(transistor_659_out), .gate(rst));
  Transistor #(.\type ("n")) transistor_663 (.in(1'b0), .out(transistor_663_out), .gate(rst));
  Transistor #(.gate("br")) transistor_664 (.in(1'b0), .out(transistor_663_out), .gate(transistor_637_out));
  Transistor #(.\type ("n")) transistor_665 (
    .in(transistor_605_out), .out(transistor_663_out), .gate(transistor_637_out));
  Transistor #(.gate("br")) transistor_666 (.in(transistor_605_out), .out(transistor_663_out), .gate(rst));
  Transistor #(.\type ("n")) transistor_667 (.in(1'b0), .out(transistor_667_out), .gate(rst));
  Transistor #(.gate("br")) transistor_668 (.in(1'b0), .out(transistor_667_out), .gate(transistor_639_out));
  Transistor #(.\type ("n")) transistor_669 (
    .in(transistor_609_out), .out(transistor_667_out), .gate(transistor_639_out));
  Transistor #(.gate("br")) transistor_670 (.in(transistor_609_out), .out(transistor_667_out), .gate(rst));
  Transistor #(.\type ("n")) transistor_671 (.in(1'b0), .out(transistor_671_out), .gate(rst));
  Transistor #(.gate("br")) transistor_672 (.in(1'b0), .out(transistor_671_out), .gate(transistor_641_out));
  Transistor #(.\type ("n")) transistor_673 (
    .in(transistor_613_out), .out(transistor_671_out), .gate(transistor_641_out));
  Transistor #(.gate("br")) transistor_674 (.in(transistor_613_out), .out(transistor_671_out), .gate(rst));
  Transistor #(.\type ("n")) transistor_675 (.in(1'b0), .out(transistor_675_out), .gate(rst));
  Transistor #(.gate("br")) transistor_676 (.in(1'b0), .out(transistor_675_out), .gate(transistor_643_out));
  Transistor #(.\type ("n")) transistor_677 (
    .in(transistor_617_out), .out(transistor_675_out), .gate(transistor_643_out));
  Transistor #(.gate("br")) transistor_678 (.in(transistor_617_out), .out(transistor_675_out), .gate(rst));
  Transistor #(.\type ("n")) transistor_679 (.in(1'b0), .out(transistor_679_out), .gate(rst));
  Transistor #(.gate("br")) transistor_680 (.in(1'b0), .out(transistor_679_out), .gate(transistor_645_out));
  Transistor #(.\type ("n")) transistor_681 (
    .in(transistor_621_out), .out(transistor_679_out), .gate(transistor_645_out));
  Transistor #(.gate("br")) transistor_682 (.in(transistor_621_out), .out(transistor_679_out), .gate(rst));
  Transistor #(.\type ("n")) transistor_683 (.in(1'b0), .out(transistor_683_out), .gate(rst));
  Transistor #(.gate("br")) transistor_684 (.in(1'b0), .out(transistor_683_out), .gate(transistor_647_out));
  Transistor #(.\type ("n")) transistor_685 (
    .in(transistor_625_out), .out(transistor_683_out), .gate(transistor_647_out));
  Transistor #(.gate("br")) transistor_686 (.in(transistor_625_out), .out(transistor_683_out), .gate(rst));
  Transistor transistor_687 (.in(1'b1), .out(transistor_687_out), .gate(rst));
  Transistor #(.\type ("n")) transistor_688 (.in(1'b0), .out(transistor_687_out), .gate(rst));
  LED led_7 (.in(transistor_721_out));
  Transistor transistor_689 (.in(1'b1), .out(transistor_689_out), .gate(pc_r));
  Transistor #(.\type ("n")) transistor_690 (.in(1'b0), .out(transistor_689_out), .gate(pc_r));
  Transistor #(.gate("br")) transistor_691 (
    .in(transistor_655_out), .out(transistor_111_out), .gate(transistor_689_out));
  Transistor #(.\type ("n")) transistor_692 (.in(transistor_655_out), .out(transistor_111_out), .gate(pc_r));
  Transistor transistor_693 (.in(1'b1), .out(transistor_693_out), .gate(pc_r));
  Transistor #(.\type ("n")) transistor_694 (.in(1'b0), .out(transistor_693_out), .gate(pc_r));
  Transistor #(.gate("br")) transistor_695 (
    .in(transistor_659_out), .out(transistor_115_out), .gate(transistor_693_out));
  Transistor #(.\type ("n")) transistor_696 (.in(transistor_659_out), .out(transistor_115_out), .gate(pc_r));
  Transistor transistor_697 (.in(1'b1), .out(transistor_697_out), .gate(pc_r));
  Transistor #(.\type ("n")) transistor_698 (.in(1'b0), .out(transistor_697_out), .gate(pc_r));
  Transistor #(.\type ("n")) transistor_699 (.in(transistor_663_out), .out(transistor_119_out), .gate(pc_r));
  Transistor #(.gate("br")) transistor_700 (
    .in(transistor_663_out), .out(transistor_119_out), .gate(transistor_697_out));
  Transistor transistor_701 (.in(1'b1), .out(transistor_701_out), .gate(pc_r));
  Transistor #(.\type ("n")) transistor_702 (.in(1'b0), .out(transistor_701_out), .gate(pc_r));
  Transistor #(.gate("br")) transistor_703 (
    .in(transistor_667_out), .out(transistor_123_out), .gate(transistor_701_out));
  Transistor #(.\type ("n")) transistor_704 (.in(transistor_667_out), .out(transistor_123_out), .gate(pc_r));
  Transistor transistor_705 (.in(1'b1), .out(transistor_705_out), .gate(pc_r));
  Transistor #(.\type ("n")) transistor_706 (.in(1'b0), .out(transistor_705_out), .gate(pc_r));
  Transistor #(.\type ("n")) transistor_707 (.in(transistor_671_out), .out(transistor_127_out), .gate(pc_r));
  Transistor #(.gate("br")) transistor_708 (
    .in(transistor_671_out), .out(transistor_127_out), .gate(transistor_705_out));
  Transistor transistor_709 (.in(1'b1), .out(transistor_709_out), .gate(pc_r));
  Transistor #(.\type ("n")) transistor_710 (.in(1'b0), .out(transistor_709_out), .gate(pc_r));
  Transistor #(.gate("br")) transistor_711 (
    .in(transistor_675_out), .out(transistor_131_out), .gate(transistor_709_out));
  Transistor #(.\type ("n")) transistor_712 (.in(transistor_675_out), .out(transistor_131_out), .gate(pc_r));
  Transistor transistor_713 (.in(1'b1), .out(transistor_713_out), .gate(pc_r));
  Transistor #(.\type ("n")) transistor_714 (.in(1'b0), .out(transistor_713_out), .gate(pc_r));
  Transistor #(.\type ("n")) transistor_715 (.in(transistor_679_out), .out(transistor_135_out), .gate(pc_r));
  Transistor #(.gate("br")) transistor_716 (
    .in(transistor_679_out), .out(transistor_135_out), .gate(transistor_713_out));
  Transistor transistor_717 (.in(1'b1), .out(transistor_717_out), .gate(pc_r));
  Transistor #(.\type ("n")) transistor_718 (.in(1'b0), .out(transistor_717_out), .gate(pc_r));
  Transistor #(.\type ("n")) transistor_719 (.in(transistor_683_out), .out(transistor_139_out), .gate(pc_r));
  Transistor #(.gate("br")) transistor_720 (
    .in(transistor_683_out), .out(transistor_139_out), .gate(transistor_717_out));
  Transistor #(.\type ("n")) transistor_721 (.in(1'b0), .out(transistor_721_out), .gate(rst));
  Transistor #(.gate("br")) transistor_722 (.in(1'b0), .out(transistor_721_out), .gate(transistor_687_out));
  Transistor #(.\type ("n")) transistor_723 (
    .in(transistor_649_out), .out(transistor_721_out), .gate(transistor_687_out));
  Transistor #(.gate("br")) transistor_724 (.in(transistor_649_out), .out(transistor_721_out), .gate(rst));
  Transistor transistor_725 (.in(1'b1), .out(transistor_725_out), .gate(bus0));
  Transistor #(.\type ("n")) transistor_726 (.in(1'b0), .out(transistor_725_out), .gate(bus0));
  Transistor transistor_727 (.in(1'b1), .out(transistor_727_out), .gate(bus0));
  Transistor #(.\type ("n")) transistor_728 (.in(1'b0), .out(transistor_727_out), .gate(bus0));
  Transistor transistor_729 (.in(1'b1), .out(transistor_729_out), .gate(bus0));
  Transistor #(.\type ("n")) transistor_730 (.in(1'b0), .out(transistor_729_out), .gate(bus0));
  Transistor transistor_731 (.in(1'b1), .out(transistor_731_out), .gate(bus0));
  Transistor #(.\type ("n")) transistor_732 (.in(1'b0), .out(transistor_731_out), .gate(bus0));
  Transistor transistor_733 (.in(1'b1), .out(transistor_733_out), .gate(bus0));
  Transistor #(.\type ("n")) transistor_734 (.in(1'b0), .out(transistor_733_out), .gate(bus0));
  Transistor transistor_735 (.in(1'b1), .out(transistor_735_out), .gate(bus0));
  Transistor #(.\type ("n")) transistor_736 (.in(1'b0), .out(transistor_735_out), .gate(bus0));
  Transistor transistor_737 (.in(1'b1), .out(transistor_737_out), .gate(bus0));
  Transistor #(.\type ("n")) transistor_738 (.in(1'b0), .out(transistor_737_out), .gate(bus0));
  Transistor transistor_739 (.in(1'b1), .out(transistor_739_out), .gate(bus0));
  Transistor #(.\type ("n")) transistor_740 (.in(1'b0), .out(transistor_739_out), .gate(bus0));
  Transistor transistor_741 (.in(1'b1), .out(transistor_741_out), .gate(mar));
  Transistor #(.\type ("n")) transistor_742 (.in(1'b0), .out(transistor_741_out), .gate(mar));
  Transistor transistor_743 (.in(1'b0), .out(transistor_743_out), .gate(bus0));
  Transistor #(.\type ("n"), .gate("br")) transistor_744 (
    .in(1'b0), .out(transistor_743_out), .gate(transistor_725_out));
  Transistor transistor_745 (.in(transistor_111_out), .out(transistor_743_out), .gate(transistor_725_out));
  Transistor #(.\type ("n"), .gate("br")) transistor_746 (
    .in(transistor_111_out), .out(transistor_743_out), .gate(bus0));
  Pull_Resistor pull_resistor_1 (.node(transistor_743_out));
  Transistor transistor_747 (.in(1'b0), .out(transistor_747_out), .gate(bus0));
  Transistor #(.\type ("n"), .gate("br")) transistor_748 (
    .in(1'b0), .out(transistor_747_out), .gate(transistor_727_out));
  Transistor transistor_749 (.in(transistor_115_out), .out(transistor_747_out), .gate(transistor_727_out));
  Transistor #(.\type ("n"), .gate("br")) transistor_750 (
    .in(transistor_115_out), .out(transistor_747_out), .gate(bus0));
  Pull_Resistor pull_resistor_2 (.node(transistor_747_out));
  Transistor transistor_751 (.in(1'b0), .out(transistor_751_out), .gate(bus0));
  Transistor #(.\type ("n"), .gate("br")) transistor_752 (
    .in(1'b0), .out(transistor_751_out), .gate(transistor_729_out));
  Transistor transistor_753 (.in(transistor_119_out), .out(transistor_751_out), .gate(transistor_729_out));
  Transistor #(.\type ("n"), .gate("br")) transistor_754 (
    .in(transistor_119_out), .out(transistor_751_out), .gate(bus0));
  Pull_Resistor pull_resistor_3 (.node(transistor_751_out));
  Transistor transistor_755 (.in(1'b0), .out(transistor_755_out), .gate(bus0));
  Transistor #(.\type ("n"), .gate("br")) transistor_756 (
    .in(1'b0), .out(transistor_755_out), .gate(transistor_731_out));
  Transistor transistor_757 (.in(transistor_123_out), .out(transistor_755_out), .gate(transistor_731_out));
  Pull_Resistor pull_resistor_4 (.node(transistor_755_out));
  Transistor #(.\type ("n"), .gate("br")) transistor_758 (
    .in(transistor_123_out), .out(transistor_755_out), .gate(bus0));
  Transistor transistor_759 (.in(1'b0), .out(transistor_759_out), .gate(bus0));
  Transistor #(.\type ("n"), .gate("br")) transistor_760 (
    .in(1'b0), .out(transistor_759_out), .gate(transistor_733_out));
  Transistor transistor_761 (.in(transistor_127_out), .out(transistor_759_out), .gate(transistor_733_out));
  Transistor #(.\type ("n"), .gate("br")) transistor_762 (
    .in(transistor_127_out), .out(transistor_759_out), .gate(bus0));
  Pull_Resistor pull_resistor_5 (.node(transistor_759_out));
  Transistor transistor_763 (.in(1'b0), .out(transistor_763_out), .gate(bus0));
  Transistor #(.\type ("n"), .gate("br")) transistor_764 (
    .in(1'b0), .out(transistor_763_out), .gate(transistor_735_out));
  Transistor transistor_765 (.in(transistor_131_out), .out(transistor_763_out), .gate(transistor_735_out));
  Pull_Resistor pull_resistor_6 (.node(transistor_763_out));
  Transistor #(.\type ("n"), .gate("br")) transistor_766 (
    .in(transistor_131_out), .out(transistor_763_out), .gate(bus0));
  Transistor transistor_767 (.in(1'b0), .out(transistor_767_out), .gate(bus0));
  Transistor #(.\type ("n"), .gate("br")) transistor_768 (
    .in(1'b0), .out(transistor_767_out), .gate(transistor_737_out));
  Transistor transistor_769 (.in(transistor_135_out), .out(transistor_767_out), .gate(transistor_737_out));
  Pull_Resistor pull_resistor_7 (.node(transistor_767_out));
  Transistor #(.\type ("n"), .gate("br")) transistor_770 (
    .in(transistor_135_out), .out(transistor_767_out), .gate(bus0));
  Transistor transistor_771 (.in(1'b0), .out(transistor_771_out), .gate(bus0));
  Transistor #(.\type ("n"), .gate("br")) transistor_772 (
    .in(1'b0), .out(transistor_771_out), .gate(transistor_739_out));
  Transistor transistor_773 (.in(transistor_139_out), .out(transistor_771_out), .gate(transistor_739_out));
  Transistor #(.\type ("n"), .gate("br")) transistor_774 (
    .in(transistor_139_out), .out(transistor_771_out), .gate(bus0));
  Pull_Resistor pull_resistor_8 (.node(transistor_771_out));
  Transistor #(.\type ("n")) transistor_775 (.in(transistor_1367_out), .out(transistor_775_out), .gate(mar));
  Transistor #(.gate("br")) transistor_776 (
    .in(transistor_1367_out), .out(transistor_775_out), .gate(transistor_741_out));
  Transistor #(.\type ("n")) transistor_777 (
    .in(transistor_795_out), .out(transistor_775_out), .gate(transistor_741_out));
  Transistor #(.gate("br")) transistor_778 (.in(transistor_795_out), .out(transistor_775_out), .gate(mar));
  LED led_8 (.in(transistor_795_out));
  Transistor transistor_779 (.in(1'b1), .out(transistor_779_out), .gate(ra_w));
  Transistor #(.\type ("n")) transistor_780 (.in(1'b0), .out(transistor_779_out), .gate(ra_w));
  Transistor transistor_781 (.in(1'b1), .out(transistor_781_out), .gate(ra_w));
  Transistor #(.\type ("n")) transistor_782 (.in(1'b0), .out(transistor_781_out), .gate(ra_w));
  Transistor transistor_783 (.in(1'b1), .out(transistor_783_out), .gate(ra_w));
  Transistor #(.\type ("n")) transistor_784 (.in(1'b0), .out(transistor_783_out), .gate(ra_w));
  Transistor transistor_785 (.in(1'b1), .out(transistor_785_out), .gate(ra_w));
  Transistor #(.\type ("n")) transistor_786 (.in(1'b0), .out(transistor_785_out), .gate(ra_w));
  Transistor transistor_787 (.in(1'b1), .out(transistor_787_out), .gate(ra_w));
  Transistor #(.\type ("n")) transistor_788 (.in(1'b0), .out(transistor_787_out), .gate(ra_w));
  Transistor transistor_789 (.in(1'b1), .out(transistor_789_out), .gate(ra_w));
  Transistor #(.\type ("n")) transistor_790 (.in(1'b0), .out(transistor_789_out), .gate(ra_w));
  Transistor transistor_791 (.in(1'b1), .out(transistor_791_out), .gate(ra_w));
  Transistor #(.\type ("n")) transistor_792 (.in(1'b0), .out(transistor_791_out), .gate(ra_w));
  Transistor transistor_793 (.in(1'b1), .out(transistor_793_out), .gate(ra_w));
  Transistor #(.\type ("n")) transistor_794 (.in(1'b0), .out(transistor_793_out), .gate(ra_w));
  Transistor #(.\type ("n")) transistor_795 (.in(1'b0), .out(transistor_795_out), .gate(rst));
  Transistor #(.gate("br")) transistor_796 (.in(1'b0), .out(transistor_795_out), .gate(transistor_797_out));
  Transistor transistor_797 (.in(1'b1), .out(transistor_797_out), .gate(rst));
  Transistor #(.\type ("n")) transistor_798 (.in(1'b0), .out(transistor_797_out), .gate(rst));
  Transistor #(.\type ("n")) transistor_799 (
    .in(transistor_775_out), .out(transistor_795_out), .gate(transistor_797_out));
  Transistor #(.gate("br")) transistor_800 (.in(transistor_775_out), .out(transistor_795_out), .gate(rst));
  Transistor #(.\type ("n")) transistor_801 (.in(transistor_743_out), .out(transistor_801_out), .gate(ra_w));
  Transistor #(.gate("br")) transistor_802 (
    .in(transistor_743_out), .out(transistor_801_out), .gate(transistor_779_out));
  Transistor #(.\type ("n")) transistor_803 (
    .in(transistor_833_out), .out(transistor_801_out), .gate(transistor_779_out));
  Transistor #(.gate("br")) transistor_804 (.in(transistor_833_out), .out(transistor_801_out), .gate(ra_w));
  Transistor #(.\type ("n")) transistor_805 (.in(transistor_747_out), .out(transistor_805_out), .gate(ra_w));
  Transistor #(.gate("br")) transistor_806 (
    .in(transistor_747_out), .out(transistor_805_out), .gate(transistor_781_out));
  Transistor #(.\type ("n")) transistor_807 (
    .in(transistor_839_out), .out(transistor_805_out), .gate(transistor_781_out));
  Transistor #(.gate("br")) transistor_808 (.in(transistor_839_out), .out(transistor_805_out), .gate(ra_w));
  Transistor #(.\type ("n")) transistor_809 (.in(transistor_751_out), .out(transistor_809_out), .gate(ra_w));
  Transistor #(.gate("br")) transistor_810 (
    .in(transistor_751_out), .out(transistor_809_out), .gate(transistor_783_out));
  Transistor #(.\type ("n")) transistor_811 (
    .in(transistor_845_out), .out(transistor_809_out), .gate(transistor_783_out));
  Transistor #(.gate("br")) transistor_812 (.in(transistor_845_out), .out(transistor_809_out), .gate(ra_w));
  Transistor #(.\type ("n")) transistor_813 (.in(transistor_755_out), .out(transistor_813_out), .gate(ra_w));
  Transistor #(.gate("br")) transistor_814 (
    .in(transistor_755_out), .out(transistor_813_out), .gate(transistor_785_out));
  Transistor #(.\type ("n")) transistor_815 (
    .in(transistor_851_out), .out(transistor_813_out), .gate(transistor_785_out));
  Transistor #(.gate("br")) transistor_816 (.in(transistor_851_out), .out(transistor_813_out), .gate(ra_w));
  Transistor #(.\type ("n")) transistor_817 (.in(transistor_759_out), .out(transistor_817_out), .gate(ra_w));
  Transistor #(.gate("br")) transistor_818 (
    .in(transistor_759_out), .out(transistor_817_out), .gate(transistor_787_out));
  Transistor #(.\type ("n")) transistor_819 (
    .in(transistor_857_out), .out(transistor_817_out), .gate(transistor_787_out));
  Transistor #(.gate("br")) transistor_820 (.in(transistor_857_out), .out(transistor_817_out), .gate(ra_w));
  Transistor #(.\type ("n")) transistor_821 (.in(transistor_763_out), .out(transistor_821_out), .gate(ra_w));
  Transistor #(.gate("br")) transistor_822 (
    .in(transistor_763_out), .out(transistor_821_out), .gate(transistor_789_out));
  Transistor #(.\type ("n")) transistor_823 (
    .in(transistor_863_out), .out(transistor_821_out), .gate(transistor_789_out));
  Transistor #(.gate("br")) transistor_824 (.in(transistor_863_out), .out(transistor_821_out), .gate(ra_w));
  Transistor #(.\type ("n")) transistor_825 (.in(transistor_767_out), .out(transistor_825_out), .gate(ra_w));
  Transistor #(.gate("br")) transistor_826 (
    .in(transistor_767_out), .out(transistor_825_out), .gate(transistor_791_out));
  Transistor #(.\type ("n")) transistor_827 (
    .in(transistor_869_out), .out(transistor_825_out), .gate(transistor_791_out));
  Transistor #(.gate("br")) transistor_828 (.in(transistor_869_out), .out(transistor_825_out), .gate(ra_w));
  Transistor #(.\type ("n")) transistor_829 (.in(transistor_771_out), .out(transistor_829_out), .gate(ra_w));
  Transistor #(.gate("br")) transistor_830 (
    .in(transistor_771_out), .out(transistor_829_out), .gate(transistor_793_out));
  Transistor #(.\type ("n")) transistor_831 (
    .in(transistor_875_out), .out(transistor_829_out), .gate(transistor_793_out));
  Transistor #(.gate("br")) transistor_832 (.in(transistor_875_out), .out(transistor_829_out), .gate(ra_w));
  Transistor #(.\type ("n")) transistor_833 (.in(1'b0), .out(transistor_833_out), .gate(rst));
  Transistor #(.gate("br")) transistor_834 (.in(1'b0), .out(transistor_833_out), .gate(transistor_835_out));
  Transistor transistor_835 (.in(1'b1), .out(transistor_835_out), .gate(rst));
  Transistor #(.\type ("n")) transistor_836 (.in(1'b0), .out(transistor_835_out), .gate(rst));
  Transistor #(.\type ("n")) transistor_837 (
    .in(transistor_801_out), .out(transistor_833_out), .gate(transistor_835_out));
  Transistor #(.gate("br")) transistor_838 (.in(transistor_801_out), .out(transistor_833_out), .gate(rst));
  Transistor #(.\type ("n")) transistor_839 (.in(1'b0), .out(transistor_839_out), .gate(rst));
  Transistor #(.gate("br")) transistor_840 (.in(1'b0), .out(transistor_839_out), .gate(transistor_841_out));
  Transistor transistor_841 (.in(1'b1), .out(transistor_841_out), .gate(rst));
  Transistor #(.\type ("n")) transistor_842 (.in(1'b0), .out(transistor_841_out), .gate(rst));
  Transistor #(.\type ("n")) transistor_843 (
    .in(transistor_805_out), .out(transistor_839_out), .gate(transistor_841_out));
  Transistor #(.gate("br")) transistor_844 (.in(transistor_805_out), .out(transistor_839_out), .gate(rst));
  Transistor #(.\type ("n")) transistor_845 (.in(1'b0), .out(transistor_845_out), .gate(rst));
  Transistor #(.gate("br")) transistor_846 (.in(1'b0), .out(transistor_845_out), .gate(transistor_847_out));
  Transistor transistor_847 (.in(1'b1), .out(transistor_847_out), .gate(rst));
  Transistor #(.\type ("n")) transistor_848 (.in(1'b0), .out(transistor_847_out), .gate(rst));
  Transistor #(.\type ("n")) transistor_849 (
    .in(transistor_809_out), .out(transistor_845_out), .gate(transistor_847_out));
  Transistor #(.gate("br")) transistor_850 (.in(transistor_809_out), .out(transistor_845_out), .gate(rst));
  Transistor #(.\type ("n")) transistor_851 (.in(1'b0), .out(transistor_851_out), .gate(rst));
  Transistor #(.gate("br")) transistor_852 (.in(1'b0), .out(transistor_851_out), .gate(transistor_853_out));
  Transistor transistor_853 (.in(1'b1), .out(transistor_853_out), .gate(rst));
  Transistor #(.\type ("n")) transistor_854 (.in(1'b0), .out(transistor_853_out), .gate(rst));
  Transistor #(.\type ("n")) transistor_855 (
    .in(transistor_813_out), .out(transistor_851_out), .gate(transistor_853_out));
  Transistor #(.gate("br")) transistor_856 (.in(transistor_813_out), .out(transistor_851_out), .gate(rst));
  Transistor #(.\type ("n")) transistor_857 (.in(1'b0), .out(transistor_857_out), .gate(rst));
  Transistor #(.gate("br")) transistor_858 (.in(1'b0), .out(transistor_857_out), .gate(transistor_859_out));
  Transistor transistor_859 (.in(1'b1), .out(transistor_859_out), .gate(rst));
  Transistor #(.\type ("n")) transistor_860 (.in(1'b0), .out(transistor_859_out), .gate(rst));
  Transistor #(.\type ("n")) transistor_861 (
    .in(transistor_817_out), .out(transistor_857_out), .gate(transistor_859_out));
  Transistor #(.gate("br")) transistor_862 (.in(transistor_817_out), .out(transistor_857_out), .gate(rst));
  Transistor #(.\type ("n")) transistor_863 (.in(1'b0), .out(transistor_863_out), .gate(rst));
  Transistor #(.gate("br")) transistor_864 (.in(1'b0), .out(transistor_863_out), .gate(transistor_865_out));
  Transistor transistor_865 (.in(1'b1), .out(transistor_865_out), .gate(rst));
  Transistor #(.\type ("n")) transistor_866 (.in(1'b0), .out(transistor_865_out), .gate(rst));
  Transistor #(.\type ("n")) transistor_867 (
    .in(transistor_821_out), .out(transistor_863_out), .gate(transistor_865_out));
  Transistor #(.gate("br")) transistor_868 (.in(transistor_821_out), .out(transistor_863_out), .gate(rst));
  Transistor #(.\type ("n")) transistor_869 (.in(1'b0), .out(transistor_869_out), .gate(rst));
  Transistor #(.gate("br")) transistor_870 (.in(1'b0), .out(transistor_869_out), .gate(transistor_871_out));
  Transistor transistor_871 (.in(1'b1), .out(transistor_871_out), .gate(rst));
  Transistor #(.\type ("n")) transistor_872 (.in(1'b0), .out(transistor_871_out), .gate(rst));
  Transistor #(.\type ("n")) transistor_873 (
    .in(transistor_825_out), .out(transistor_869_out), .gate(transistor_871_out));
  Transistor #(.gate("br")) transistor_874 (.in(transistor_825_out), .out(transistor_869_out), .gate(rst));
  Transistor #(.\type ("n")) transistor_875 (.in(1'b0), .out(transistor_875_out), .gate(rst));
  Transistor #(.gate("br")) transistor_876 (.in(1'b0), .out(transistor_875_out), .gate(transistor_877_out));
  Transistor transistor_877 (.in(1'b1), .out(transistor_877_out), .gate(rst));
  Transistor #(.\type ("n")) transistor_878 (.in(1'b0), .out(transistor_877_out), .gate(rst));
  Transistor #(.\type ("n")) transistor_879 (
    .in(transistor_829_out), .out(transistor_875_out), .gate(transistor_877_out));
  Transistor #(.gate("br")) transistor_880 (.in(transistor_829_out), .out(transistor_875_out), .gate(rst));
  Transistor #(.\type ("n")) transistor_881 (.in(transistor_743_out), .out(transistor_881_out), .gate(rb_w));
  Transistor #(.gate("br")) transistor_882 (
    .in(transistor_743_out), .out(transistor_881_out), .gate(transistor_883_out));
  Transistor transistor_883 (.in(1'b1), .out(transistor_883_out), .gate(rb_w));
  Transistor #(.\type ("n")) transistor_884 (.in(1'b0), .out(transistor_883_out), .gate(rb_w));
  Transistor #(.\type ("n")) transistor_885 (
    .in(transistor_945_out), .out(transistor_881_out), .gate(transistor_883_out));
  Transistor #(.gate("br")) transistor_886 (.in(transistor_945_out), .out(transistor_881_out), .gate(rb_w));
  Transistor #(.\type ("n")) transistor_887 (.in(transistor_747_out), .out(transistor_887_out), .gate(rb_w));
  Transistor #(.gate("br")) transistor_888 (
    .in(transistor_747_out), .out(transistor_887_out), .gate(transistor_889_out));
  Transistor transistor_889 (.in(1'b1), .out(transistor_889_out), .gate(rb_w));
  Transistor #(.\type ("n")) transistor_890 (.in(1'b0), .out(transistor_889_out), .gate(rb_w));
  Transistor #(.\type ("n")) transistor_891 (
    .in(transistor_949_out), .out(transistor_887_out), .gate(transistor_889_out));
  Transistor #(.gate("br")) transistor_892 (.in(transistor_949_out), .out(transistor_887_out), .gate(rb_w));
  Transistor #(.\type ("n")) transistor_893 (.in(transistor_751_out), .out(transistor_893_out), .gate(rb_w));
  Transistor #(.gate("br")) transistor_894 (
    .in(transistor_751_out), .out(transistor_893_out), .gate(transistor_895_out));
  Transistor transistor_895 (.in(1'b1), .out(transistor_895_out), .gate(rb_w));
  Transistor #(.\type ("n")) transistor_896 (.in(1'b0), .out(transistor_895_out), .gate(rb_w));
  Transistor #(.\type ("n")) transistor_897 (
    .in(transistor_953_out), .out(transistor_893_out), .gate(transistor_895_out));
  Transistor #(.gate("br")) transistor_898 (.in(transistor_953_out), .out(transistor_893_out), .gate(rb_w));
  Transistor #(.\type ("n")) transistor_899 (.in(transistor_755_out), .out(transistor_899_out), .gate(rb_w));
  Transistor #(.gate("br")) transistor_900 (
    .in(transistor_755_out), .out(transistor_899_out), .gate(transistor_901_out));
  Transistor transistor_901 (.in(1'b1), .out(transistor_901_out), .gate(rb_w));
  Transistor #(.\type ("n")) transistor_902 (.in(1'b0), .out(transistor_901_out), .gate(rb_w));
  Transistor #(.\type ("n")) transistor_903 (
    .in(transistor_957_out), .out(transistor_899_out), .gate(transistor_901_out));
  Transistor #(.gate("br")) transistor_904 (.in(transistor_957_out), .out(transistor_899_out), .gate(rb_w));
  Transistor #(.\type ("n")) transistor_905 (.in(transistor_759_out), .out(transistor_905_out), .gate(rb_w));
  Transistor #(.gate("br")) transistor_906 (
    .in(transistor_759_out), .out(transistor_905_out), .gate(transistor_907_out));
  Transistor transistor_907 (.in(1'b1), .out(transistor_907_out), .gate(rb_w));
  Transistor #(.\type ("n")) transistor_908 (.in(1'b0), .out(transistor_907_out), .gate(rb_w));
  Transistor #(.\type ("n")) transistor_909 (
    .in(transistor_961_out), .out(transistor_905_out), .gate(transistor_907_out));
  Transistor #(.gate("br")) transistor_910 (.in(transistor_961_out), .out(transistor_905_out), .gate(rb_w));
  Transistor #(.\type ("n")) transistor_911 (.in(transistor_763_out), .out(transistor_911_out), .gate(rb_w));
  Transistor #(.gate("br")) transistor_912 (
    .in(transistor_763_out), .out(transistor_911_out), .gate(transistor_913_out));
  Transistor transistor_913 (.in(1'b1), .out(transistor_913_out), .gate(rb_w));
  Transistor #(.\type ("n")) transistor_914 (.in(1'b0), .out(transistor_913_out), .gate(rb_w));
  Transistor #(.\type ("n")) transistor_915 (
    .in(transistor_965_out), .out(transistor_911_out), .gate(transistor_913_out));
  Transistor #(.gate("br")) transistor_916 (.in(transistor_965_out), .out(transistor_911_out), .gate(rb_w));
  Transistor #(.\type ("n")) transistor_917 (.in(transistor_767_out), .out(transistor_917_out), .gate(rb_w));
  Transistor #(.gate("br")) transistor_918 (
    .in(transistor_767_out), .out(transistor_917_out), .gate(transistor_919_out));
  Transistor transistor_919 (.in(1'b1), .out(transistor_919_out), .gate(rb_w));
  Transistor #(.\type ("n")) transistor_920 (.in(1'b0), .out(transistor_919_out), .gate(rb_w));
  Transistor #(.\type ("n")) transistor_921 (
    .in(transistor_969_out), .out(transistor_917_out), .gate(transistor_919_out));
  Transistor #(.gate("br")) transistor_922 (.in(transistor_969_out), .out(transistor_917_out), .gate(rb_w));
  Transistor #(.\type ("n")) transistor_923 (.in(transistor_771_out), .out(transistor_923_out), .gate(rb_w));
  Transistor #(.gate("br")) transistor_924 (
    .in(transistor_771_out), .out(transistor_923_out), .gate(transistor_925_out));
  Transistor transistor_925 (.in(1'b1), .out(transistor_925_out), .gate(rb_w));
  Transistor #(.\type ("n")) transistor_926 (.in(1'b0), .out(transistor_925_out), .gate(rb_w));
  Transistor #(.\type ("n")) transistor_927 (
    .in(transistor_973_out), .out(transistor_923_out), .gate(transistor_925_out));
  Transistor #(.gate("br")) transistor_928 (.in(transistor_973_out), .out(transistor_923_out), .gate(rb_w));
  Transistor transistor_929 (.in(1'b1), .out(transistor_929_out), .gate(rst));
  Transistor #(.\type ("n")) transistor_930 (.in(1'b0), .out(transistor_929_out), .gate(rst));
  Transistor transistor_931 (.in(1'b1), .out(transistor_931_out), .gate(rst));
  Transistor #(.\type ("n")) transistor_932 (.in(1'b0), .out(transistor_931_out), .gate(rst));
  Transistor transistor_933 (.in(1'b1), .out(transistor_933_out), .gate(rst));
  Transistor #(.\type ("n")) transistor_934 (.in(1'b0), .out(transistor_933_out), .gate(rst));
  Transistor transistor_935 (.in(1'b1), .out(transistor_935_out), .gate(rst));
  Transistor #(.\type ("n")) transistor_936 (.in(1'b0), .out(transistor_935_out), .gate(rst));
  Transistor transistor_937 (.in(1'b1), .out(transistor_937_out), .gate(rst));
  Transistor #(.\type ("n")) transistor_938 (.in(1'b0), .out(transistor_937_out), .gate(rst));
  Transistor transistor_939 (.in(1'b1), .out(transistor_939_out), .gate(rst));
  Transistor #(.\type ("n")) transistor_940 (.in(1'b0), .out(transistor_939_out), .gate(rst));
  Transistor transistor_941 (.in(1'b1), .out(transistor_941_out), .gate(rst));
  Transistor #(.\type ("n")) transistor_942 (.in(1'b0), .out(transistor_941_out), .gate(rst));
  Transistor transistor_943 (.in(1'b1), .out(transistor_943_out), .gate(rst));
  Transistor #(.\type ("n")) transistor_944 (.in(1'b0), .out(transistor_943_out), .gate(rst));
  Transistor #(.\type ("n")) transistor_945 (.in(1'b0), .out(transistor_945_out), .gate(rst));
  Transistor #(.gate("br")) transistor_946 (.in(1'b0), .out(transistor_945_out), .gate(transistor_929_out));
  Transistor #(.\type ("n")) transistor_947 (
    .in(transistor_881_out), .out(transistor_945_out), .gate(transistor_929_out));
  Transistor #(.gate("br")) transistor_948 (.in(transistor_881_out), .out(transistor_945_out), .gate(rst));
  Transistor #(.\type ("n")) transistor_949 (.in(1'b0), .out(transistor_949_out), .gate(rst));
  Transistor #(.gate("br")) transistor_950 (.in(1'b0), .out(transistor_949_out), .gate(transistor_931_out));
  Transistor #(.\type ("n")) transistor_951 (
    .in(transistor_887_out), .out(transistor_949_out), .gate(transistor_931_out));
  Transistor #(.gate("br")) transistor_952 (.in(transistor_887_out), .out(transistor_949_out), .gate(rst));
  Transistor #(.\type ("n")) transistor_953 (.in(1'b0), .out(transistor_953_out), .gate(rst));
  Transistor #(.gate("br")) transistor_954 (.in(1'b0), .out(transistor_953_out), .gate(transistor_933_out));
  Transistor #(.\type ("n")) transistor_955 (
    .in(transistor_893_out), .out(transistor_953_out), .gate(transistor_933_out));
  Transistor #(.gate("br")) transistor_956 (.in(transistor_893_out), .out(transistor_953_out), .gate(rst));
  Transistor #(.\type ("n")) transistor_957 (.in(1'b0), .out(transistor_957_out), .gate(rst));
  Transistor #(.gate("br")) transistor_958 (.in(1'b0), .out(transistor_957_out), .gate(transistor_935_out));
  Transistor #(.\type ("n")) transistor_959 (
    .in(transistor_899_out), .out(transistor_957_out), .gate(transistor_935_out));
  Transistor #(.gate("br")) transistor_960 (.in(transistor_899_out), .out(transistor_957_out), .gate(rst));
  Transistor #(.\type ("n")) transistor_961 (.in(1'b0), .out(transistor_961_out), .gate(rst));
  Transistor #(.gate("br")) transistor_962 (.in(1'b0), .out(transistor_961_out), .gate(transistor_937_out));
  Transistor #(.\type ("n")) transistor_963 (
    .in(transistor_905_out), .out(transistor_961_out), .gate(transistor_937_out));
  Transistor #(.gate("br")) transistor_964 (.in(transistor_905_out), .out(transistor_961_out), .gate(rst));
  Transistor #(.\type ("n")) transistor_965 (.in(1'b0), .out(transistor_965_out), .gate(rst));
  Transistor #(.gate("br")) transistor_966 (.in(1'b0), .out(transistor_965_out), .gate(transistor_939_out));
  Transistor #(.\type ("n")) transistor_967 (
    .in(transistor_911_out), .out(transistor_965_out), .gate(transistor_939_out));
  Transistor #(.gate("br")) transistor_968 (.in(transistor_911_out), .out(transistor_965_out), .gate(rst));
  Transistor #(.\type ("n")) transistor_969 (.in(1'b0), .out(transistor_969_out), .gate(rst));
  Transistor #(.gate("br")) transistor_970 (.in(1'b0), .out(transistor_969_out), .gate(transistor_941_out));
  Transistor #(.\type ("n")) transistor_971 (
    .in(transistor_917_out), .out(transistor_969_out), .gate(transistor_941_out));
  Transistor #(.gate("br")) transistor_972 (.in(transistor_917_out), .out(transistor_969_out), .gate(rst));
  Transistor #(.\type ("n")) transistor_973 (.in(1'b0), .out(transistor_973_out), .gate(rst));
  Transistor #(.gate("br")) transistor_974 (.in(1'b0), .out(transistor_973_out), .gate(transistor_943_out));
  Transistor #(.\type ("n")) transistor_975 (
    .in(transistor_923_out), .out(transistor_973_out), .gate(transistor_943_out));
  Transistor #(.gate("br")) transistor_976 (.in(transistor_923_out), .out(transistor_973_out), .gate(rst));
  Transistor transistor_977 (.in(1'b1), .out(transistor_977_out), .gate(transistor_833_out));
  Transistor transistor_978 (.in(1'b1), .out(transistor_978_out), .gate(transistor_839_out));
  Transistor transistor_979 (.in(1'b1), .out(transistor_979_out), .gate(transistor_845_out));
  Transistor transistor_980 (.in(1'b1), .out(transistor_980_out), .gate(transistor_851_out));
  Transistor transistor_981 (.in(1'b1), .out(transistor_981_out), .gate(transistor_857_out));
  Transistor transistor_982 (.in(1'b1), .out(transistor_982_out), .gate(transistor_863_out));
  Transistor transistor_983 (.in(1'b1), .out(transistor_983_out), .gate(transistor_869_out));
  Transistor transistor_984 (.in(1'b1), .out(transistor_984_out), .gate(transistor_875_out));
  Transistor transistor_985 (.in(1'b1), .out(transistor_977_out), .gate(transistor_945_out));
  Transistor #(.\type ("n")) transistor_986 (
    .in(transistor_987_out), .out(transistor_977_out), .gate(transistor_945_out));
  Transistor #(.\type ("n")) transistor_987 (.in(1'b0), .out(transistor_987_out), .gate(transistor_833_out));
  Transistor transistor_988 (.in(1'b1), .out(transistor_978_out), .gate(transistor_949_out));
  Transistor #(.\type ("n")) transistor_989 (
    .in(transistor_990_out), .out(transistor_978_out), .gate(transistor_949_out));
  Transistor #(.\type ("n")) transistor_990 (.in(1'b0), .out(transistor_990_out), .gate(transistor_839_out));
  Transistor transistor_991 (.in(1'b1), .out(transistor_979_out), .gate(transistor_953_out));
  Transistor #(.\type ("n")) transistor_992 (
    .in(transistor_993_out), .out(transistor_979_out), .gate(transistor_953_out));
  Transistor #(.\type ("n")) transistor_993 (.in(1'b0), .out(transistor_993_out), .gate(transistor_845_out));
  Transistor transistor_994 (.in(1'b1), .out(transistor_980_out), .gate(transistor_957_out));
  Transistor #(.\type ("n")) transistor_995 (
    .in(transistor_996_out), .out(transistor_980_out), .gate(transistor_957_out));
  Transistor #(.\type ("n")) transistor_996 (.in(1'b0), .out(transistor_996_out), .gate(transistor_851_out));
  Transistor transistor_997 (.in(1'b1), .out(transistor_981_out), .gate(transistor_961_out));
  Transistor #(.\type ("n")) transistor_998 (
    .in(transistor_999_out), .out(transistor_981_out), .gate(transistor_961_out));
  Transistor #(.\type ("n")) transistor_999 (.in(1'b0), .out(transistor_999_out), .gate(transistor_857_out));
  Transistor transistor_1000 (.in(1'b1), .out(transistor_982_out), .gate(transistor_965_out));
  Transistor #(.\type ("n")) transistor_1001 (
    .in(transistor_1002_out), .out(transistor_982_out), .gate(transistor_965_out));
  Transistor #(.\type ("n")) transistor_1002 (.in(1'b0), .out(transistor_1002_out), .gate(transistor_863_out));
  Transistor transistor_1003 (.in(1'b1), .out(transistor_983_out), .gate(transistor_969_out));
  Transistor #(.\type ("n")) transistor_1004 (
    .in(transistor_1005_out), .out(transistor_983_out), .gate(transistor_969_out));
  Transistor #(.\type ("n")) transistor_1005 (.in(1'b0), .out(transistor_1005_out), .gate(transistor_869_out));
  Transistor transistor_1006 (.in(1'b1), .out(transistor_984_out), .gate(transistor_973_out));
  Transistor #(.\type ("n")) transistor_1007 (
    .in(transistor_1008_out), .out(transistor_984_out), .gate(transistor_973_out));
  Transistor #(.\type ("n")) transistor_1008 (.in(1'b0), .out(transistor_1008_out), .gate(transistor_875_out));
  Transistor transistor_1009 (.in(1'b1), .out(transistor_1009_out), .gate(transistor_977_out));
  Transistor #(.\type ("n")) transistor_1010 (.in(1'b0), .out(transistor_1009_out), .gate(transistor_977_out));
  Transistor transistor_1011 (.in(1'b1), .out(transistor_1011_out), .gate(transistor_978_out));
  Transistor #(.\type ("n")) transistor_1012 (.in(1'b0), .out(transistor_1011_out), .gate(transistor_978_out));
  Transistor transistor_1013 (.in(1'b1), .out(transistor_1013_out), .gate(transistor_979_out));
  Transistor #(.\type ("n")) transistor_1014 (.in(1'b0), .out(transistor_1013_out), .gate(transistor_979_out));
  Transistor transistor_1015 (.in(1'b1), .out(transistor_1015_out), .gate(transistor_980_out));
  Transistor #(.\type ("n")) transistor_1016 (.in(1'b0), .out(transistor_1015_out), .gate(transistor_980_out));
  Transistor transistor_1017 (.in(1'b1), .out(transistor_1017_out), .gate(transistor_981_out));
  Transistor #(.\type ("n")) transistor_1018 (.in(1'b0), .out(transistor_1017_out), .gate(transistor_981_out));
  Transistor transistor_1019 (.in(1'b1), .out(transistor_1019_out), .gate(transistor_982_out));
  Transistor #(.\type ("n")) transistor_1020 (.in(1'b0), .out(transistor_1019_out), .gate(transistor_982_out));
  Transistor transistor_1021 (.in(1'b1), .out(transistor_1021_out), .gate(transistor_983_out));
  Transistor #(.\type ("n")) transistor_1022 (.in(1'b0), .out(transistor_1021_out), .gate(transistor_983_out));
  Transistor transistor_1023 (.in(1'b1), .out(transistor_1023_out), .gate(transistor_984_out));
  Transistor #(.\type ("n")) transistor_1024 (.in(1'b0), .out(transistor_1023_out), .gate(transistor_984_out));
  Transistor transistor_1025 (.in(1'b1), .out(transistor_1025_out), .gate(transistor_833_out));
  Transistor transistor_1026 (.in(transistor_1025_out), .out(transistor_1026_out), .gate(transistor_945_out));
  Transistor #(.\type ("n")) transistor_1027 (.in(1'b0), .out(transistor_1026_out), .gate(transistor_945_out));
  Transistor #(.\type ("n")) transistor_1028 (.in(1'b0), .out(transistor_1026_out), .gate(transistor_833_out));
  Transistor transistor_1029 (.in(1'b1), .out(transistor_1029_out), .gate(transistor_839_out));
  Transistor transistor_1030 (.in(transistor_1029_out), .out(transistor_1030_out), .gate(transistor_949_out));
  Transistor #(.\type ("n")) transistor_1031 (.in(1'b0), .out(transistor_1030_out), .gate(transistor_839_out));
  Transistor #(.\type ("n")) transistor_1032 (.in(1'b0), .out(transistor_1030_out), .gate(transistor_949_out));
  Transistor transistor_1033 (.in(1'b1), .out(transistor_1033_out), .gate(transistor_845_out));
  Transistor transistor_1034 (.in(transistor_1033_out), .out(transistor_1034_out), .gate(transistor_953_out));
  Transistor #(.\type ("n")) transistor_1035 (.in(1'b0), .out(transistor_1034_out), .gate(transistor_845_out));
  Transistor #(.\type ("n")) transistor_1036 (.in(1'b0), .out(transistor_1034_out), .gate(transistor_953_out));
  Transistor transistor_1037 (.in(1'b1), .out(transistor_1037_out), .gate(transistor_851_out));
  Transistor transistor_1038 (.in(transistor_1037_out), .out(transistor_1038_out), .gate(transistor_957_out));
  Transistor #(.\type ("n")) transistor_1039 (.in(1'b0), .out(transistor_1038_out), .gate(transistor_851_out));
  Transistor #(.\type ("n")) transistor_1040 (.in(1'b0), .out(transistor_1038_out), .gate(transistor_957_out));
  Transistor transistor_1041 (.in(1'b1), .out(transistor_1041_out), .gate(transistor_857_out));
  Transistor transistor_1042 (.in(transistor_1041_out), .out(transistor_1042_out), .gate(transistor_961_out));
  Transistor #(.\type ("n")) transistor_1043 (.in(1'b0), .out(transistor_1042_out), .gate(transistor_857_out));
  Transistor #(.\type ("n")) transistor_1044 (.in(1'b0), .out(transistor_1042_out), .gate(transistor_961_out));
  Transistor transistor_1045 (.in(1'b1), .out(transistor_1045_out), .gate(transistor_863_out));
  Transistor transistor_1046 (.in(transistor_1045_out), .out(transistor_1046_out), .gate(transistor_965_out));
  Transistor #(.\type ("n")) transistor_1047 (.in(1'b0), .out(transistor_1046_out), .gate(transistor_965_out));
  Transistor #(.\type ("n")) transistor_1048 (.in(1'b0), .out(transistor_1046_out), .gate(transistor_863_out));
  Transistor transistor_1049 (.in(1'b1), .out(transistor_1049_out), .gate(transistor_869_out));
  Transistor transistor_1050 (.in(transistor_1049_out), .out(transistor_1050_out), .gate(transistor_969_out));
  Transistor #(.\type ("n")) transistor_1051 (.in(1'b0), .out(transistor_1050_out), .gate(transistor_969_out));
  Transistor #(.\type ("n")) transistor_1052 (.in(1'b0), .out(transistor_1050_out), .gate(transistor_869_out));
  Transistor transistor_1053 (.in(1'b1), .out(transistor_1053_out), .gate(transistor_875_out));
  Transistor transistor_1054 (.in(transistor_1053_out), .out(transistor_1054_out), .gate(transistor_973_out));
  Transistor #(.\type ("n")) transistor_1055 (.in(1'b0), .out(transistor_1054_out), .gate(transistor_875_out));
  Transistor #(.\type ("n")) transistor_1056 (.in(1'b0), .out(transistor_1054_out), .gate(transistor_973_out));
  Transistor transistor_1057 (.in(1'b1), .out(transistor_1057_out), .gate(transistor_1026_out));
  Transistor #(.\type ("n")) transistor_1058 (.in(1'b0), .out(transistor_1057_out), .gate(transistor_1026_out));
  Transistor transistor_1059 (.in(1'b1), .out(transistor_1059_out), .gate(transistor_1030_out));
  Transistor #(.\type ("n")) transistor_1060 (.in(1'b0), .out(transistor_1059_out), .gate(transistor_1030_out));
  Transistor transistor_1061 (.in(1'b1), .out(transistor_1061_out), .gate(transistor_1034_out));
  Transistor #(.\type ("n")) transistor_1062 (.in(1'b0), .out(transistor_1061_out), .gate(transistor_1034_out));
  Transistor transistor_1063 (.in(1'b1), .out(transistor_1063_out), .gate(transistor_1038_out));
  Transistor #(.\type ("n")) transistor_1064 (.in(1'b0), .out(transistor_1063_out), .gate(transistor_1038_out));
  Transistor transistor_1065 (.in(1'b1), .out(transistor_1065_out), .gate(transistor_1042_out));
  Transistor #(.\type ("n")) transistor_1066 (.in(1'b0), .out(transistor_1065_out), .gate(transistor_1042_out));
  Transistor transistor_1067 (.in(1'b1), .out(transistor_1067_out), .gate(transistor_1046_out));
  Transistor #(.\type ("n")) transistor_1068 (.in(1'b0), .out(transistor_1067_out), .gate(transistor_1046_out));
  Transistor transistor_1069 (.in(1'b1), .out(transistor_1069_out), .gate(transistor_1050_out));
  Transistor #(.\type ("n")) transistor_1070 (.in(1'b0), .out(transistor_1069_out), .gate(transistor_1050_out));
  Transistor transistor_1071 (.in(1'b1), .out(transistor_1071_out), .gate(transistor_1054_out));
  Transistor #(.\type ("n")) transistor_1072 (.in(1'b0), .out(transistor_1071_out), .gate(transistor_1054_out));
  Transistor transistor_1073 (.in(1'b1), .out(transistor_1073_out), .gate(transistor_833_out));
  Transistor transistor_1074 (.in(1'b1), .out(transistor_1074_out), .gate(transistor_839_out));
  Transistor transistor_1075 (.in(1'b1), .out(transistor_1075_out), .gate(transistor_845_out));
  Transistor transistor_1076 (.in(1'b1), .out(transistor_1076_out), .gate(transistor_851_out));
  Transistor transistor_1077 (.in(1'b1), .out(transistor_1077_out), .gate(transistor_857_out));
  Transistor transistor_1078 (.in(1'b1), .out(transistor_1078_out), .gate(transistor_863_out));
  Transistor transistor_1079 (.in(1'b1), .out(transistor_1079_out), .gate(transistor_869_out));
  Transistor transistor_1080 (.in(1'b1), .out(transistor_1080_out), .gate(transistor_875_out));
  Transistor transistor_1081 (.in(1'b1), .out(transistor_1081_out), .gate(r));
  Transistor #(.\type ("n")) transistor_1082 (.in(1'b0), .out(transistor_1081_out), .gate(r));
  Transistor #(.\type ("n")) transistor_1083 (.in(undriven), .out(transistor_1083_out), .gate(r));
  Transistor #(.gate("br")) transistor_1084 (.in(undriven), .out(transistor_1083_out), .gate(transistor_1081_out));
  LED led_9 (.in(undriven));
  Transistor transistor_1085 (.in(1'b1), .out(transistor_1073_out), .gate(transistor_945_out));
  Transistor transistor_1086 (.in(1'b1), .out(transistor_1086_out), .gate(transistor_1073_out));
  Transistor #(.\type ("n")) transistor_1087 (
    .in(transistor_1088_out), .out(transistor_1073_out), .gate(transistor_833_out));
  Transistor #(.\type ("n")) transistor_1088 (.in(1'b0), .out(transistor_1088_out), .gate(transistor_945_out));
  Transistor transistor_1089 (.in(1'b1), .out(transistor_1074_out), .gate(transistor_949_out));
  Transistor transistor_1090 (.in(1'b1), .out(transistor_1090_out), .gate(transistor_1074_out));
  Transistor #(.\type ("n")) transistor_1091 (
    .in(transistor_1092_out), .out(transistor_1074_out), .gate(transistor_839_out));
  Transistor #(.\type ("n")) transistor_1092 (.in(1'b0), .out(transistor_1092_out), .gate(transistor_949_out));
  Transistor transistor_1093 (.in(1'b1), .out(transistor_1075_out), .gate(transistor_953_out));
  Transistor transistor_1094 (.in(1'b1), .out(transistor_1094_out), .gate(transistor_1075_out));
  Transistor #(.\type ("n")) transistor_1095 (
    .in(transistor_1096_out), .out(transistor_1075_out), .gate(transistor_845_out));
  Transistor #(.\type ("n")) transistor_1096 (.in(1'b0), .out(transistor_1096_out), .gate(transistor_953_out));
  Transistor transistor_1097 (.in(1'b1), .out(transistor_1097_out), .gate(transistor_1076_out));
  Transistor transistor_1098 (.in(1'b1), .out(transistor_1076_out), .gate(transistor_957_out));
  Transistor #(.\type ("n")) transistor_1099 (
    .in(transistor_1100_out), .out(transistor_1076_out), .gate(transistor_851_out));
  Transistor #(.\type ("n")) transistor_1100 (.in(1'b0), .out(transistor_1100_out), .gate(transistor_957_out));
  Transistor transistor_1101 (.in(1'b1), .out(transistor_1077_out), .gate(transistor_961_out));
  Transistor transistor_1102 (.in(1'b1), .out(transistor_1102_out), .gate(transistor_1077_out));
  Transistor #(.\type ("n")) transistor_1103 (
    .in(transistor_1104_out), .out(transistor_1077_out), .gate(transistor_857_out));
  Transistor #(.\type ("n")) transistor_1104 (.in(1'b0), .out(transistor_1104_out), .gate(transistor_961_out));
  Transistor transistor_1105 (.in(1'b1), .out(transistor_1078_out), .gate(transistor_965_out));
  Transistor transistor_1106 (.in(1'b1), .out(transistor_1106_out), .gate(transistor_1078_out));
  Transistor #(.\type ("n")) transistor_1107 (
    .in(transistor_1108_out), .out(transistor_1078_out), .gate(transistor_863_out));
  Transistor #(.\type ("n")) transistor_1108 (.in(1'b0), .out(transistor_1108_out), .gate(transistor_965_out));
  Transistor transistor_1109 (.in(1'b1), .out(transistor_1109_out), .gate(transistor_1079_out));
  Transistor transistor_1110 (.in(1'b1), .out(transistor_1079_out), .gate(transistor_969_out));
  Transistor #(.\type ("n")) transistor_1111 (
    .in(transistor_1112_out), .out(transistor_1079_out), .gate(transistor_869_out));
  Transistor #(.\type ("n")) transistor_1112 (.in(1'b0), .out(transistor_1112_out), .gate(transistor_969_out));
  Transistor transistor_1113 (.in(1'b1), .out(transistor_1080_out), .gate(transistor_973_out));
  Transistor transistor_1114 (.in(1'b1), .out(transistor_1114_out), .gate(transistor_1080_out));
  Transistor #(.\type ("n")) transistor_1115 (
    .in(transistor_1116_out), .out(transistor_1080_out), .gate(transistor_875_out));
  Transistor #(.\type ("n")) transistor_1116 (.in(1'b0), .out(transistor_1116_out), .gate(transistor_973_out));
  Transistor transistor_1117 (.in(1'b1), .out(transistor_1117_out), .gate(r));
  Transistor #(.\type ("n")) transistor_1118 (.in(1'b0), .out(transistor_1117_out), .gate(r));
  Transistor transistor_1119 (.in(1'b1), .out(transistor_1086_out), .gate(transistor_945_out));
  Transistor #(.\type ("n")) transistor_1120 (
    .in(transistor_1121_out), .out(transistor_1086_out), .gate(transistor_1073_out));
  Transistor #(.\type ("n")) transistor_1121 (.in(1'b0), .out(transistor_1121_out), .gate(transistor_945_out));
  Transistor transistor_1122 (.in(1'b1), .out(transistor_1090_out), .gate(transistor_949_out));
  Transistor #(.\type ("n")) transistor_1123 (
    .in(transistor_1124_out), .out(transistor_1090_out), .gate(transistor_1074_out));
  Transistor #(.\type ("n")) transistor_1124 (.in(1'b0), .out(transistor_1124_out), .gate(transistor_949_out));
  Transistor transistor_1125 (.in(1'b1), .out(transistor_1094_out), .gate(transistor_953_out));
  Transistor #(.\type ("n")) transistor_1126 (
    .in(transistor_1127_out), .out(transistor_1094_out), .gate(transistor_1075_out));
  Transistor #(.\type ("n")) transistor_1127 (.in(1'b0), .out(transistor_1127_out), .gate(transistor_953_out));
  Transistor transistor_1128 (.in(1'b1), .out(transistor_1097_out), .gate(transistor_957_out));
  Transistor #(.\type ("n")) transistor_1129 (
    .in(transistor_1130_out), .out(transistor_1097_out), .gate(transistor_1076_out));
  Transistor #(.\type ("n")) transistor_1130 (.in(1'b0), .out(transistor_1130_out), .gate(transistor_957_out));
  Transistor transistor_1131 (.in(1'b1), .out(transistor_1102_out), .gate(transistor_961_out));
  Transistor #(.\type ("n")) transistor_1132 (
    .in(transistor_1133_out), .out(transistor_1102_out), .gate(transistor_1077_out));
  Transistor #(.\type ("n")) transistor_1133 (.in(1'b0), .out(transistor_1133_out), .gate(transistor_961_out));
  Transistor transistor_1134 (.in(1'b1), .out(transistor_1106_out), .gate(transistor_965_out));
  Transistor #(.\type ("n")) transistor_1135 (
    .in(transistor_1136_out), .out(transistor_1106_out), .gate(transistor_1078_out));
  Transistor #(.\type ("n")) transistor_1136 (.in(1'b0), .out(transistor_1136_out), .gate(transistor_965_out));
  Transistor transistor_1137 (.in(1'b1), .out(transistor_1109_out), .gate(transistor_969_out));
  Transistor #(.\type ("n")) transistor_1138 (
    .in(transistor_1139_out), .out(transistor_1109_out), .gate(transistor_1079_out));
  Transistor #(.\type ("n")) transistor_1139 (.in(1'b0), .out(transistor_1139_out), .gate(transistor_969_out));
  Transistor transistor_1140 (.in(1'b1), .out(transistor_1114_out), .gate(transistor_973_out));
  Transistor #(.\type ("n")) transistor_1141 (
    .in(transistor_1142_out), .out(transistor_1114_out), .gate(transistor_1080_out));
  Transistor #(.\type ("n")) transistor_1142 (.in(1'b0), .out(transistor_1142_out), .gate(transistor_973_out));
  Transistor #(.gate("br")) transistor_1143 (.in(undriven_2), .out(transistor_1143_out), .gate(transistor_1117_out));
  Transistor #(.\type ("n")) transistor_1144 (.in(undriven_2), .out(transistor_1143_out), .gate(r));
  LED led_10 (.in(undriven_2));
  Transistor transistor_1145 (.in(1'b1), .out(transistor_1145_out), .gate(transistor_833_out));
  Transistor transistor_1146 (.in(1'b1), .out(transistor_1145_out), .gate(transistor_1073_out));
  Transistor #(.\type ("n")) transistor_1147 (
    .in(transistor_1148_out), .out(transistor_1145_out), .gate(transistor_1073_out));
  Transistor #(.\type ("n")) transistor_1148 (.in(1'b0), .out(transistor_1148_out), .gate(transistor_833_out));
  Transistor transistor_1149 (.in(1'b1), .out(transistor_1149_out), .gate(transistor_1074_out));
  Transistor transistor_1150 (.in(1'b1), .out(transistor_1149_out), .gate(transistor_839_out));
  Transistor #(.\type ("n")) transistor_1151 (
    .in(transistor_1152_out), .out(transistor_1149_out), .gate(transistor_1074_out));
  Transistor #(.\type ("n")) transistor_1152 (.in(1'b0), .out(transistor_1152_out), .gate(transistor_839_out));
  Transistor transistor_1153 (.in(1'b1), .out(transistor_1153_out), .gate(transistor_845_out));
  Transistor transistor_1154 (.in(1'b1), .out(transistor_1153_out), .gate(transistor_1075_out));
  Transistor #(.\type ("n")) transistor_1155 (
    .in(transistor_1156_out), .out(transistor_1153_out), .gate(transistor_1075_out));
  Transistor #(.\type ("n")) transistor_1156 (.in(1'b0), .out(transistor_1156_out), .gate(transistor_845_out));
  Transistor transistor_1157 (.in(1'b1), .out(transistor_1157_out), .gate(transistor_851_out));
  Transistor transistor_1158 (.in(1'b1), .out(transistor_1157_out), .gate(transistor_1076_out));
  Transistor #(.\type ("n")) transistor_1159 (
    .in(transistor_1160_out), .out(transistor_1157_out), .gate(transistor_1076_out));
  Transistor #(.\type ("n")) transistor_1160 (.in(1'b0), .out(transistor_1160_out), .gate(transistor_851_out));
  Transistor transistor_1161 (.in(1'b1), .out(transistor_1161_out), .gate(transistor_857_out));
  Transistor transistor_1162 (.in(1'b1), .out(transistor_1161_out), .gate(transistor_1077_out));
  Transistor #(.\type ("n")) transistor_1163 (
    .in(transistor_1164_out), .out(transistor_1161_out), .gate(transistor_1077_out));
  Transistor #(.\type ("n")) transistor_1164 (.in(1'b0), .out(transistor_1164_out), .gate(transistor_857_out));
  Transistor transistor_1165 (.in(1'b1), .out(transistor_1165_out), .gate(transistor_863_out));
  Transistor transistor_1166 (.in(1'b1), .out(transistor_1165_out), .gate(transistor_1078_out));
  Transistor #(.\type ("n")) transistor_1167 (
    .in(transistor_1168_out), .out(transistor_1165_out), .gate(transistor_1078_out));
  Transistor #(.\type ("n")) transistor_1168 (.in(1'b0), .out(transistor_1168_out), .gate(transistor_863_out));
  Transistor transistor_1169 (.in(1'b1), .out(transistor_1169_out), .gate(transistor_869_out));
  Transistor transistor_1170 (.in(1'b1), .out(transistor_1169_out), .gate(transistor_1079_out));
  Transistor #(.\type ("n")) transistor_1171 (
    .in(transistor_1172_out), .out(transistor_1169_out), .gate(transistor_1079_out));
  Transistor #(.\type ("n")) transistor_1172 (.in(1'b0), .out(transistor_1172_out), .gate(transistor_869_out));
  Transistor transistor_1173 (.in(1'b1), .out(transistor_1173_out), .gate(transistor_875_out));
  Transistor transistor_1174 (.in(1'b1), .out(transistor_1173_out), .gate(transistor_1080_out));
  Transistor #(.\type ("n")) transistor_1175 (
    .in(transistor_1176_out), .out(transistor_1173_out), .gate(transistor_1080_out));
  Transistor #(.\type ("n")) transistor_1176 (.in(1'b0), .out(transistor_1176_out), .gate(transistor_875_out));
  Transistor transistor_1177 (.in(1'b1), .out(transistor_1177_out), .gate(r));
  Transistor #(.\type ("n")) transistor_1178 (.in(1'b0), .out(transistor_1177_out), .gate(r));
  Transistor #(.gate("br")) transistor_1179 (.in(undriven_3), .out(transistor_1179_out), .gate(transistor_1177_out));
  Transistor #(.\type ("n")) transistor_1180 (.in(undriven_3), .out(transistor_1179_out), .gate(r));
  LED led_11 (.in(undriven_3));
  Transistor transistor_1181 (.in(1'b1), .out(transistor_1181_out), .gate(transistor_1145_out));
  Transistor transistor_1182 (.in(1'b1), .out(transistor_1182_out), .gate(transistor_1149_out));
  Transistor transistor_1183 (.in(1'b1), .out(transistor_1183_out), .gate(transistor_1153_out));
  Transistor transistor_1184 (.in(1'b1), .out(transistor_1184_out), .gate(transistor_1157_out));
  Transistor transistor_1185 (.in(1'b1), .out(transistor_1185_out), .gate(transistor_1161_out));
  Transistor transistor_1186 (.in(1'b1), .out(transistor_1186_out), .gate(transistor_1165_out));
  Transistor transistor_1187 (.in(1'b1), .out(transistor_1187_out), .gate(transistor_1169_out));
  Transistor transistor_1188 (.in(1'b1), .out(transistor_1188_out), .gate(transistor_1173_out));
  Transistor transistor_1189 (.in(1'b1), .out(transistor_1181_out), .gate(transistor_1086_out));
  Transistor #(.\type ("n")) transistor_1190 (
    .in(transistor_1191_out), .out(transistor_1181_out), .gate(transistor_1145_out));
  Transistor #(.\type ("n")) transistor_1191 (.in(1'b0), .out(transistor_1191_out), .gate(transistor_1086_out));
  Transistor transistor_1192 (.in(1'b1), .out(transistor_1182_out), .gate(transistor_1090_out));
  Transistor #(.\type ("n")) transistor_1193 (
    .in(transistor_1194_out), .out(transistor_1182_out), .gate(transistor_1149_out));
  Transistor #(.\type ("n")) transistor_1194 (.in(1'b0), .out(transistor_1194_out), .gate(transistor_1090_out));
  Transistor transistor_1195 (.in(1'b1), .out(transistor_1183_out), .gate(transistor_1094_out));
  Transistor #(.\type ("n")) transistor_1196 (
    .in(transistor_1197_out), .out(transistor_1183_out), .gate(transistor_1153_out));
  Transistor #(.\type ("n")) transistor_1197 (.in(1'b0), .out(transistor_1197_out), .gate(transistor_1094_out));
  Transistor transistor_1198 (.in(1'b1), .out(transistor_1184_out), .gate(transistor_1097_out));
  Transistor #(.\type ("n")) transistor_1199 (
    .in(transistor_1200_out), .out(transistor_1184_out), .gate(transistor_1157_out));
  Transistor #(.\type ("n")) transistor_1200 (.in(1'b0), .out(transistor_1200_out), .gate(transistor_1097_out));
  Transistor transistor_1201 (.in(1'b1), .out(transistor_1185_out), .gate(transistor_1102_out));
  Transistor #(.\type ("n")) transistor_1202 (
    .in(transistor_1203_out), .out(transistor_1185_out), .gate(transistor_1161_out));
  Transistor #(.\type ("n")) transistor_1203 (.in(1'b0), .out(transistor_1203_out), .gate(transistor_1102_out));
  Transistor transistor_1204 (.in(1'b1), .out(transistor_1186_out), .gate(transistor_1106_out));
  Transistor #(.\type ("n")) transistor_1205 (
    .in(transistor_1206_out), .out(transistor_1186_out), .gate(transistor_1165_out));
  Transistor #(.\type ("n")) transistor_1206 (.in(1'b0), .out(transistor_1206_out), .gate(transistor_1106_out));
  Transistor transistor_1207 (.in(1'b1), .out(transistor_1187_out), .gate(transistor_1109_out));
  Transistor #(.\type ("n")) transistor_1208 (
    .in(transistor_1209_out), .out(transistor_1187_out), .gate(transistor_1169_out));
  Transistor #(.\type ("n")) transistor_1209 (.in(1'b0), .out(transistor_1209_out), .gate(transistor_1109_out));
  Transistor transistor_1210 (.in(1'b1), .out(transistor_1188_out), .gate(transistor_1114_out));
  Transistor #(.\type ("n")) transistor_1211 (
    .in(transistor_1212_out), .out(transistor_1188_out), .gate(transistor_1173_out));
  Transistor #(.\type ("n")) transistor_1212 (.in(1'b0), .out(transistor_1212_out), .gate(transistor_1114_out));
  Transistor transistor_1213 (.in(1'b1), .out(transistor_1213_out), .gate(r));
  Transistor #(.\type ("n")) transistor_1214 (.in(1'b0), .out(transistor_1213_out), .gate(r));
  Transistor #(.\type ("n")) transistor_1215 (.in(undriven_4), .out(transistor_1215_out), .gate(r));
  Transistor #(.gate("br")) transistor_1216 (.in(undriven_4), .out(transistor_1215_out), .gate(transistor_1213_out));
  LED led_12 (.in(undriven_4));
  Transistor transistor_1217 (.in(1'b1), .out(transistor_1217_out), .gate(transistor_945_out));
  Transistor transistor_1218 (.in(1'b1), .out(transistor_1217_out), .gate(op0));
  Transistor #(.\type ("n")) transistor_1219 (.in(transistor_1220_out), .out(transistor_1217_out), .gate(op0));
  Transistor #(.\type ("n")) transistor_1220 (.in(1'b0), .out(transistor_1220_out), .gate(transistor_945_out));
  Transistor transistor_1221 (.in(1'b1), .out(transistor_1221_out), .gate(op0));
  Transistor transistor_1222 (.in(1'b1), .out(transistor_1221_out), .gate(transistor_949_out));
  Transistor #(.\type ("n")) transistor_1223 (.in(transistor_1224_out), .out(transistor_1221_out), .gate(op0));
  Transistor #(.\type ("n")) transistor_1224 (.in(1'b0), .out(transistor_1224_out), .gate(transistor_949_out));
  Transistor transistor_1225 (.in(1'b1), .out(transistor_1225_out), .gate(transistor_953_out));
  Transistor transistor_1226 (.in(1'b1), .out(transistor_1225_out), .gate(op0));
  Transistor #(.\type ("n")) transistor_1227 (.in(transistor_1228_out), .out(transistor_1225_out), .gate(op0));
  Transistor #(.\type ("n")) transistor_1228 (.in(1'b0), .out(transistor_1228_out), .gate(transistor_953_out));
  Transistor transistor_1229 (.in(1'b1), .out(transistor_1229_out), .gate(transistor_957_out));
  Transistor transistor_1230 (.in(1'b1), .out(transistor_1229_out), .gate(op0));
  Transistor #(.\type ("n")) transistor_1231 (.in(transistor_1232_out), .out(transistor_1229_out), .gate(op0));
  Transistor #(.\type ("n")) transistor_1232 (.in(1'b0), .out(transistor_1232_out), .gate(transistor_957_out));
  Transistor transistor_1233 (.in(1'b1), .out(transistor_1233_out), .gate(transistor_961_out));
  Transistor transistor_1234 (.in(1'b1), .out(transistor_1233_out), .gate(op0));
  Transistor #(.\type ("n")) transistor_1235 (.in(transistor_1236_out), .out(transistor_1233_out), .gate(op0));
  Transistor #(.\type ("n")) transistor_1236 (.in(1'b0), .out(transistor_1236_out), .gate(transistor_961_out));
  Transistor transistor_1237 (.in(1'b1), .out(transistor_1237_out), .gate(op0));
  Transistor transistor_1238 (.in(1'b1), .out(transistor_1237_out), .gate(transistor_965_out));
  Transistor #(.\type ("n")) transistor_1239 (.in(transistor_1240_out), .out(transistor_1237_out), .gate(op0));
  Transistor #(.\type ("n")) transistor_1240 (.in(1'b0), .out(transistor_1240_out), .gate(transistor_965_out));
  Transistor transistor_1241 (.in(1'b1), .out(transistor_1241_out), .gate(transistor_969_out));
  Transistor transistor_1242 (.in(1'b1), .out(transistor_1241_out), .gate(op0));
  Transistor #(.\type ("n")) transistor_1243 (.in(transistor_1244_out), .out(transistor_1241_out), .gate(op0));
  Transistor #(.\type ("n")) transistor_1244 (.in(1'b0), .out(transistor_1244_out), .gate(transistor_969_out));
  Transistor transistor_1245 (.in(1'b1), .out(transistor_1245_out), .gate(transistor_973_out));
  Transistor transistor_1246 (.in(1'b1), .out(transistor_1245_out), .gate(op0));
  Transistor #(.\type ("n")) transistor_1247 (.in(transistor_1248_out), .out(transistor_1245_out), .gate(op0));
  Transistor #(.\type ("n")) transistor_1248 (.in(1'b0), .out(transistor_1248_out), .gate(transistor_973_out));
  Transistor transistor_1249 (.in(1'b1), .out(transistor_1249_out), .gate(r));
  Transistor #(.\type ("n")) transistor_1250 (.in(1'b0), .out(transistor_1249_out), .gate(r));
  Transistor #(.\type ("n")) transistor_1251 (.in(undriven_5), .out(transistor_1251_out), .gate(r));
  Transistor transistor_1252 (.in(1'b1), .out(transistor_1252_out), .gate(transistor_1217_out));
  Transistor transistor_1253 (.in(1'b1), .out(transistor_1253_out), .gate(transistor_1221_out));
  Transistor transistor_1254 (.in(1'b1), .out(transistor_1254_out), .gate(transistor_1225_out));
  Transistor transistor_1255 (.in(1'b1), .out(transistor_1255_out), .gate(transistor_1229_out));
  Transistor transistor_1256 (.in(1'b1), .out(transistor_1256_out), .gate(transistor_1233_out));
  Transistor transistor_1257 (.in(1'b1), .out(transistor_1257_out), .gate(transistor_1237_out));
  Transistor transistor_1258 (.in(1'b1), .out(transistor_1258_out), .gate(transistor_1241_out));
  Transistor transistor_1259 (.in(1'b1), .out(transistor_1259_out), .gate(transistor_1245_out));
  Transistor #(.gate("br")) transistor_1260 (.in(undriven_5), .out(transistor_1251_out), .gate(transistor_1249_out));
  LED led_13 (.in(undriven_5));
  Transistor transistor_1261 (.in(1'b1), .out(transistor_1252_out), .gate(transistor_945_out));
  Transistor #(.\type ("n")) transistor_1262 (
    .in(transistor_1263_out), .out(transistor_1252_out), .gate(transistor_1217_out));
  Transistor #(.\type ("n")) transistor_1263 (.in(1'b0), .out(transistor_1263_out), .gate(transistor_945_out));
  Transistor transistor_1264 (.in(1'b1), .out(transistor_1253_out), .gate(transistor_949_out));
  Transistor #(.\type ("n")) transistor_1265 (
    .in(transistor_1266_out), .out(transistor_1253_out), .gate(transistor_1221_out));
  Transistor #(.\type ("n")) transistor_1266 (.in(1'b0), .out(transistor_1266_out), .gate(transistor_949_out));
  Transistor transistor_1267 (.in(1'b1), .out(transistor_1254_out), .gate(transistor_953_out));
  Transistor #(.\type ("n")) transistor_1268 (
    .in(transistor_1269_out), .out(transistor_1254_out), .gate(transistor_1225_out));
  Transistor #(.\type ("n")) transistor_1269 (.in(1'b0), .out(transistor_1269_out), .gate(transistor_953_out));
  Transistor transistor_1270 (.in(1'b1), .out(transistor_1255_out), .gate(transistor_957_out));
  Transistor #(.\type ("n")) transistor_1271 (
    .in(transistor_1272_out), .out(transistor_1255_out), .gate(transistor_1229_out));
  Transistor #(.\type ("n")) transistor_1272 (.in(1'b0), .out(transistor_1272_out), .gate(transistor_957_out));
  Transistor transistor_1273 (.in(1'b1), .out(transistor_1256_out), .gate(transistor_961_out));
  Transistor #(.\type ("n")) transistor_1274 (
    .in(transistor_1275_out), .out(transistor_1256_out), .gate(transistor_1233_out));
  Transistor #(.\type ("n")) transistor_1275 (.in(1'b0), .out(transistor_1275_out), .gate(transistor_961_out));
  Transistor transistor_1276 (.in(1'b1), .out(transistor_1257_out), .gate(transistor_965_out));
  Transistor #(.\type ("n")) transistor_1277 (
    .in(transistor_1278_out), .out(transistor_1257_out), .gate(transistor_1237_out));
  Transistor #(.\type ("n")) transistor_1278 (.in(1'b0), .out(transistor_1278_out), .gate(transistor_965_out));
  Transistor transistor_1279 (.in(1'b1), .out(transistor_1258_out), .gate(transistor_969_out));
  Transistor #(.\type ("n")) transistor_1280 (
    .in(transistor_1281_out), .out(transistor_1258_out), .gate(transistor_1241_out));
  Transistor #(.\type ("n")) transistor_1281 (.in(1'b0), .out(transistor_1281_out), .gate(transistor_969_out));
  Transistor transistor_1282 (.in(1'b1), .out(transistor_1259_out), .gate(transistor_973_out));
  Transistor #(.\type ("n")) transistor_1283 (
    .in(transistor_1284_out), .out(transistor_1259_out), .gate(transistor_1245_out));
  Transistor #(.\type ("n")) transistor_1284 (.in(1'b0), .out(transistor_1284_out), .gate(transistor_973_out));
  Transistor transistor_1285 (.in(1'b1), .out(transistor_1285_out), .gate(r));
  Transistor #(.\type ("n")) transistor_1286 (.in(1'b0), .out(transistor_1285_out), .gate(r));
  Transistor #(.gate("br")) transistor_1287 (.in(undriven_6), .out(transistor_1287_out), .gate(transistor_1285_out));
  Transistor #(.\type ("n")) transistor_1288 (.in(undriven_6), .out(transistor_1287_out), .gate(r));
  LED led_14 (.in(undriven_6));
  Transistor transistor_1289 (.in(1'b1), .out(transistor_1289_out), .gate(op0));
  Transistor transistor_1290 (.in(1'b1), .out(transistor_1289_out), .gate(transistor_1217_out));
  Transistor #(.\type ("n")) transistor_1291 (
    .in(transistor_1292_out), .out(transistor_1289_out), .gate(transistor_1217_out));
  Transistor #(.\type ("n")) transistor_1292 (.in(1'b0), .out(transistor_1292_out), .gate(op0));
  Transistor transistor_1293 (.in(1'b1), .out(transistor_1293_out), .gate(transistor_1221_out));
  Transistor transistor_1294 (.in(1'b1), .out(transistor_1293_out), .gate(op0));
  Transistor #(.\type ("n")) transistor_1295 (
    .in(transistor_1296_out), .out(transistor_1293_out), .gate(transistor_1221_out));
  Transistor #(.\type ("n")) transistor_1296 (.in(1'b0), .out(transistor_1296_out), .gate(op0));
  Transistor transistor_1297 (.in(1'b1), .out(transistor_1297_out), .gate(transistor_1225_out));
  Transistor transistor_1298 (.in(1'b1), .out(transistor_1297_out), .gate(op0));
  Transistor #(.\type ("n")) transistor_1299 (
    .in(transistor_1300_out), .out(transistor_1297_out), .gate(transistor_1225_out));
  Transistor #(.\type ("n")) transistor_1300 (.in(1'b0), .out(transistor_1300_out), .gate(op0));
  Transistor transistor_1301 (.in(1'b1), .out(transistor_1301_out), .gate(transistor_1229_out));
  Transistor transistor_1302 (.in(1'b1), .out(transistor_1301_out), .gate(op0));
  Transistor #(.\type ("n")) transistor_1303 (
    .in(transistor_1304_out), .out(transistor_1301_out), .gate(transistor_1229_out));
  Transistor #(.\type ("n")) transistor_1304 (.in(1'b0), .out(transistor_1304_out), .gate(op0));
  Transistor transistor_1305 (.in(1'b1), .out(transistor_1305_out), .gate(op0));
  Transistor transistor_1306 (.in(1'b1), .out(transistor_1305_out), .gate(transistor_1233_out));
  Transistor #(.\type ("n")) transistor_1307 (
    .in(transistor_1308_out), .out(transistor_1305_out), .gate(transistor_1233_out));
  Transistor #(.\type ("n")) transistor_1308 (.in(1'b0), .out(transistor_1308_out), .gate(op0));
  Transistor transistor_1309 (.in(1'b1), .out(transistor_1309_out), .gate(op0));
  Transistor transistor_1310 (.in(1'b1), .out(transistor_1309_out), .gate(transistor_1237_out));
  Transistor #(.\type ("n")) transistor_1311 (
    .in(transistor_1312_out), .out(transistor_1309_out), .gate(transistor_1237_out));
  Transistor #(.\type ("n")) transistor_1312 (.in(1'b0), .out(transistor_1312_out), .gate(op0));
  Transistor transistor_1313 (.in(1'b1), .out(transistor_1313_out), .gate(transistor_1241_out));
  Transistor transistor_1314 (.in(1'b1), .out(transistor_1313_out), .gate(op0));
  Transistor #(.\type ("n")) transistor_1315 (
    .in(transistor_1316_out), .out(transistor_1313_out), .gate(transistor_1241_out));
  Transistor #(.\type ("n")) transistor_1316 (.in(1'b0), .out(transistor_1316_out), .gate(op0));
  Transistor transistor_1317 (.in(1'b1), .out(transistor_1317_out), .gate(transistor_1245_out));
  Transistor transistor_1318 (.in(1'b1), .out(transistor_1317_out), .gate(op0));
  Transistor #(.\type ("n")) transistor_1319 (
    .in(transistor_1320_out), .out(transistor_1317_out), .gate(transistor_1245_out));
  Transistor #(.\type ("n")) transistor_1320 (.in(1'b0), .out(transistor_1320_out), .gate(op0));
  Transistor transistor_1321 (.in(1'b1), .out(transistor_1321_out), .gate(transistor_1289_out));
  Transistor transistor_1322 (.in(1'b1), .out(transistor_1321_out), .gate(transistor_1252_out));
  Transistor #(.\type ("n")) transistor_1323 (
    .in(transistor_1324_out), .out(transistor_1321_out), .gate(transistor_1289_out));
  Transistor #(.\type ("n")) transistor_1324 (.in(1'b0), .out(transistor_1324_out), .gate(transistor_1252_out));
  Transistor transistor_1325 (.in(1'b1), .out(transistor_1325_out), .gate(transistor_1253_out));
  Transistor transistor_1326 (.in(1'b1), .out(transistor_1325_out), .gate(transistor_1293_out));
  Transistor #(.\type ("n")) transistor_1327 (
    .in(transistor_1328_out), .out(transistor_1325_out), .gate(transistor_1293_out));
  Transistor #(.\type ("n")) transistor_1328 (.in(1'b0), .out(transistor_1328_out), .gate(transistor_1253_out));
  Transistor transistor_1329 (.in(1'b1), .out(transistor_1329_out), .gate(transistor_1297_out));
  Transistor transistor_1330 (.in(1'b1), .out(transistor_1329_out), .gate(transistor_1254_out));
  Transistor #(.\type ("n")) transistor_1331 (
    .in(transistor_1332_out), .out(transistor_1329_out), .gate(transistor_1297_out));
  Transistor #(.\type ("n")) transistor_1332 (.in(1'b0), .out(transistor_1332_out), .gate(transistor_1254_out));
  Transistor transistor_1333 (.in(1'b1), .out(transistor_1333_out), .gate(transistor_1255_out));
  Transistor transistor_1334 (.in(1'b1), .out(transistor_1333_out), .gate(transistor_1301_out));
  Transistor #(.\type ("n")) transistor_1335 (
    .in(transistor_1336_out), .out(transistor_1333_out), .gate(transistor_1301_out));
  Transistor #(.\type ("n")) transistor_1336 (.in(1'b0), .out(transistor_1336_out), .gate(transistor_1255_out));
  Transistor transistor_1337 (.in(1'b1), .out(transistor_1337_out), .gate(transistor_1305_out));
  Transistor transistor_1338 (.in(1'b1), .out(transistor_1337_out), .gate(transistor_1256_out));
  Transistor #(.\type ("n")) transistor_1339 (
    .in(transistor_1340_out), .out(transistor_1337_out), .gate(transistor_1305_out));
  Transistor #(.\type ("n")) transistor_1340 (.in(1'b0), .out(transistor_1340_out), .gate(transistor_1256_out));
  Transistor transistor_1341 (.in(1'b1), .out(transistor_1341_out), .gate(transistor_1309_out));
  Transistor transistor_1342 (.in(1'b1), .out(transistor_1341_out), .gate(transistor_1257_out));
  Transistor #(.\type ("n")) transistor_1343 (
    .in(transistor_1344_out), .out(transistor_1341_out), .gate(transistor_1309_out));
  Transistor #(.\type ("n")) transistor_1344 (.in(1'b0), .out(transistor_1344_out), .gate(transistor_1257_out));
  Transistor transistor_1345 (.in(1'b1), .out(transistor_1345_out), .gate(transistor_1258_out));
  Transistor transistor_1346 (.in(1'b1), .out(transistor_1345_out), .gate(transistor_1313_out));
  Transistor #(.\type ("n")) transistor_1347 (
    .in(transistor_1348_out), .out(transistor_1345_out), .gate(transistor_1313_out));
  Transistor #(.\type ("n")) transistor_1348 (.in(1'b0), .out(transistor_1348_out), .gate(transistor_1258_out));
  Transistor transistor_1349 (.in(1'b1), .out(transistor_1349_out), .gate(transistor_1317_out));
  Transistor transistor_1350 (.in(1'b1), .out(transistor_1349_out), .gate(transistor_1259_out));
  Transistor #(.\type ("n")) transistor_1351 (
    .in(transistor_1352_out), .out(transistor_1349_out), .gate(transistor_1317_out));
  Transistor #(.\type ("n")) transistor_1352 (.in(1'b0), .out(transistor_1352_out), .gate(transistor_1259_out));
  Transistor transistor_1353 (.in(1'b1), .out(transistor_1353_out), .gate(r));
  Transistor #(.\type ("n")) transistor_1354 (.in(1'b0), .out(transistor_1353_out), .gate(r));
  Transistor #(.gate("br")) transistor_1355 (.in(undriven_7), .out(transistor_1355_out), .gate(transistor_1353_out));
  Transistor #(.\type ("n")) transistor_1356 (.in(undriven_7), .out(transistor_1355_out), .gate(r));
  LED led_15 (.in(undriven_7));
  Transistor transistor_1357 (.in(1'b1), .out(transistor_1357_out), .gate(transistor_833_out));
  Transistor transistor_1358 (.in(1'b1), .out(transistor_1358_out), .gate(transistor_839_out));
  Transistor transistor_1359 (.in(1'b1), .out(transistor_1359_out), .gate(transistor_845_out));
  Transistor transistor_1360 (.in(1'b1), .out(transistor_1360_out), .gate(transistor_851_out));
  Transistor transistor_1361 (.in(1'b1), .out(transistor_1361_out), .gate(transistor_857_out));
  Transistor transistor_1362 (.in(1'b1), .out(transistor_1362_out), .gate(transistor_863_out));
  Transistor transistor_1363 (.in(1'b1), .out(transistor_1363_out), .gate(transistor_869_out));
  Transistor transistor_1364 (.in(1'b1), .out(transistor_1364_out), .gate(transistor_875_out));
  Transistor transistor_1365 (.in(1'b1), .out(transistor_1365_out), .gate(r));
  Transistor #(.\type ("n")) transistor_1366 (.in(1'b0), .out(transistor_1365_out), .gate(r));
  Transistor #(.\type ("n")) transistor_1367 (.in(undriven_8), .out(transistor_1367_out), .gate(r));
  LED led_16 (.in(undriven_8));
  Transistor transistor_1368 (.in(1'b1), .out(transistor_1357_out), .gate(transistor_1321_out));
  Transistor #(.\type ("n")) transistor_1369 (
    .in(transistor_1370_out), .out(transistor_1357_out), .gate(transistor_833_out));
  Transistor #(.\type ("n")) transistor_1370 (.in(1'b0), .out(transistor_1370_out), .gate(transistor_1321_out));
  Transistor transistor_1371 (.in(1'b1), .out(transistor_1358_out), .gate(transistor_1325_out));
  Transistor #(.\type ("n")) transistor_1372 (
    .in(transistor_1373_out), .out(transistor_1358_out), .gate(transistor_839_out));
  Transistor #(.\type ("n")) transistor_1373 (.in(1'b0), .out(transistor_1373_out), .gate(transistor_1325_out));
  Transistor transistor_1374 (.in(1'b1), .out(transistor_1359_out), .gate(transistor_1329_out));
  Transistor #(.\type ("n")) transistor_1375 (
    .in(transistor_1376_out), .out(transistor_1359_out), .gate(transistor_845_out));
  Transistor #(.\type ("n")) transistor_1376 (.in(1'b0), .out(transistor_1376_out), .gate(transistor_1329_out));
  Transistor transistor_1377 (.in(1'b1), .out(transistor_1360_out), .gate(transistor_1333_out));
  Transistor #(.\type ("n")) transistor_1378 (
    .in(transistor_1379_out), .out(transistor_1360_out), .gate(transistor_851_out));
  Transistor #(.\type ("n")) transistor_1379 (.in(1'b0), .out(transistor_1379_out), .gate(transistor_1333_out));
  Transistor transistor_1380 (.in(1'b1), .out(transistor_1361_out), .gate(transistor_1337_out));
  Transistor #(.\type ("n")) transistor_1381 (
    .in(transistor_1382_out), .out(transistor_1361_out), .gate(transistor_857_out));
  Transistor #(.\type ("n")) transistor_1382 (.in(1'b0), .out(transistor_1382_out), .gate(transistor_1337_out));
  Transistor transistor_1383 (.in(1'b1), .out(transistor_1362_out), .gate(transistor_1341_out));
  Transistor #(.\type ("n")) transistor_1384 (
    .in(transistor_1385_out), .out(transistor_1362_out), .gate(transistor_863_out));
  Transistor #(.\type ("n")) transistor_1385 (.in(1'b0), .out(transistor_1385_out), .gate(transistor_1341_out));
  Transistor transistor_1386 (.in(1'b1), .out(transistor_1363_out), .gate(transistor_1345_out));
  Transistor #(.\type ("n")) transistor_1387 (
    .in(transistor_1388_out), .out(transistor_1363_out), .gate(transistor_869_out));
  Transistor #(.\type ("n")) transistor_1388 (.in(1'b0), .out(transistor_1388_out), .gate(transistor_1345_out));
  Transistor transistor_1389 (.in(1'b1), .out(transistor_1364_out), .gate(transistor_1349_out));
  Transistor #(.\type ("n")) transistor_1390 (
    .in(transistor_1391_out), .out(transistor_1364_out), .gate(transistor_875_out));
  Transistor #(.\type ("n")) transistor_1391 (.in(1'b0), .out(transistor_1391_out), .gate(transistor_1349_out));
  Transistor #(.gate("br")) transistor_1392 (.in(undriven_8), .out(transistor_1367_out), .gate(transistor_1365_out));
  Transistor transistor_1393 (.in(1'b1), .out(transistor_1393_out), .gate(transistor_1357_out));
  Transistor #(.\type ("n")) transistor_1394 (.in(1'b0), .out(transistor_1393_out), .gate(transistor_1357_out));
  Transistor transistor_1395 (.in(1'b1), .out(transistor_1395_out), .gate(transistor_1358_out));
  Transistor #(.\type ("n")) transistor_1396 (.in(1'b0), .out(transistor_1395_out), .gate(transistor_1358_out));
  Transistor transistor_1397 (.in(1'b1), .out(transistor_1397_out), .gate(transistor_1359_out));
  Transistor #(.\type ("n")) transistor_1398 (.in(1'b0), .out(transistor_1397_out), .gate(transistor_1359_out));
  Transistor transistor_1399 (.in(1'b1), .out(transistor_1399_out), .gate(transistor_1360_out));
  Transistor #(.\type ("n")) transistor_1400 (.in(1'b0), .out(transistor_1399_out), .gate(transistor_1360_out));
  Transistor transistor_1401 (.in(1'b1), .out(transistor_1401_out), .gate(transistor_1361_out));
  Transistor #(.\type ("n")) transistor_1402 (.in(1'b0), .out(transistor_1401_out), .gate(transistor_1361_out));
  Transistor transistor_1403 (.in(1'b1), .out(transistor_1403_out), .gate(transistor_1362_out));
  Transistor #(.\type ("n")) transistor_1404 (.in(1'b0), .out(transistor_1403_out), .gate(transistor_1362_out));
  Transistor transistor_1405 (.in(1'b1), .out(transistor_1405_out), .gate(transistor_1363_out));
  Transistor #(.\type ("n")) transistor_1406 (.in(1'b0), .out(transistor_1405_out), .gate(transistor_1363_out));
  Transistor transistor_1407 (.in(1'b1), .out(transistor_1407_out), .gate(transistor_1364_out));
  Transistor #(.\type ("n")) transistor_1408 (.in(1'b0), .out(transistor_1407_out), .gate(transistor_1364_out));
  Transistor transistor_1409 (.in(1'b1), .out(transistor_1409_out), .gate(transistor_1628_out));
  Transistor transistor_1410 (.in(1'b1), .out(transistor_1410_out), .gate(transistor_1321_out));
  Transistor transistor_1411 (.in(1'b1), .out(transistor_1410_out), .gate(transistor_833_out));
  Transistor #(.\type ("n")) transistor_1412 (
    .in(transistor_1413_out), .out(transistor_1410_out), .gate(transistor_833_out));
  Transistor #(.\type ("n")) transistor_1413 (.in(1'b0), .out(transistor_1413_out), .gate(transistor_1321_out));
  Transistor transistor_1414 (.in(1'b1), .out(transistor_1414_out), .gate(transistor_839_out));
  Transistor transistor_1415 (.in(1'b1), .out(transistor_1414_out), .gate(transistor_1325_out));
  Transistor #(.\type ("n")) transistor_1416 (
    .in(transistor_1417_out), .out(transistor_1414_out), .gate(transistor_839_out));
  Transistor #(.\type ("n")) transistor_1417 (.in(1'b0), .out(transistor_1417_out), .gate(transistor_1325_out));
  Transistor transistor_1418 (.in(1'b1), .out(transistor_1418_out), .gate(transistor_845_out));
  Transistor transistor_1419 (.in(1'b1), .out(transistor_1418_out), .gate(transistor_1329_out));
  Transistor #(.\type ("n")) transistor_1420 (
    .in(transistor_1421_out), .out(transistor_1418_out), .gate(transistor_845_out));
  Transistor #(.\type ("n")) transistor_1421 (.in(1'b0), .out(transistor_1421_out), .gate(transistor_1329_out));
  Transistor transistor_1422 (.in(1'b1), .out(transistor_1422_out), .gate(transistor_851_out));
  Transistor transistor_1423 (.in(1'b1), .out(transistor_1422_out), .gate(transistor_1333_out));
  Transistor #(.\type ("n")) transistor_1424 (
    .in(transistor_1425_out), .out(transistor_1422_out), .gate(transistor_851_out));
  Transistor #(.\type ("n")) transistor_1425 (.in(1'b0), .out(transistor_1425_out), .gate(transistor_1333_out));
  Transistor transistor_1426 (.in(1'b1), .out(transistor_1426_out), .gate(transistor_1337_out));
  Transistor transistor_1427 (.in(1'b1), .out(transistor_1426_out), .gate(transistor_857_out));
  Transistor #(.\type ("n")) transistor_1428 (
    .in(transistor_1429_out), .out(transistor_1426_out), .gate(transistor_857_out));
  Transistor #(.\type ("n")) transistor_1429 (.in(1'b0), .out(transistor_1429_out), .gate(transistor_1337_out));
  Transistor transistor_1430 (.in(1'b1), .out(transistor_1430_out), .gate(transistor_1341_out));
  Transistor transistor_1431 (.in(1'b1), .out(transistor_1430_out), .gate(transistor_863_out));
  Transistor #(.\type ("n")) transistor_1432 (
    .in(transistor_1433_out), .out(transistor_1430_out), .gate(transistor_863_out));
  Transistor #(.\type ("n")) transistor_1433 (.in(1'b0), .out(transistor_1433_out), .gate(transistor_1341_out));
  Transistor transistor_1434 (.in(1'b1), .out(transistor_1434_out), .gate(transistor_869_out));
  Transistor transistor_1435 (.in(1'b1), .out(transistor_1434_out), .gate(transistor_1345_out));
  Transistor #(.\type ("n")) transistor_1436 (
    .in(transistor_1437_out), .out(transistor_1434_out), .gate(transistor_869_out));
  Transistor #(.\type ("n")) transistor_1437 (.in(1'b0), .out(transistor_1437_out), .gate(transistor_1345_out));
  Transistor transistor_1438 (.in(1'b1), .out(transistor_1438_out), .gate(transistor_1349_out));
  Transistor transistor_1439 (.in(1'b1), .out(transistor_1438_out), .gate(transistor_875_out));
  Transistor #(.\type ("n")) transistor_1440 (
    .in(transistor_1441_out), .out(transistor_1438_out), .gate(transistor_875_out));
  Transistor #(.\type ("n")) transistor_1441 (.in(1'b0), .out(transistor_1441_out), .gate(transistor_1349_out));
  Transistor transistor_1442 (.in(1'b1), .out(transistor_1442_out), .gate(transistor_1409_out));
  Transistor transistor_1443 (.in(1'b1), .out(transistor_1409_out), .gate(transistor_1631_out));
  Transistor #(.\type ("n")) transistor_1444 (
    .in(transistor_1445_out), .out(transistor_1409_out), .gate(transistor_1628_out));
  Transistor #(.\type ("n")) transistor_1445 (.in(1'b0), .out(transistor_1445_out), .gate(transistor_1631_out));
  Transistor transistor_1446 (.in(1'b1), .out(transistor_1446_out), .gate(transistor_1410_out));
  Transistor transistor_1447 (.in(1'b1), .out(transistor_1447_out), .gate(transistor_1414_out));
  Transistor transistor_1448 (.in(1'b1), .out(transistor_1448_out), .gate(transistor_1418_out));
  Transistor transistor_1449 (.in(1'b1), .out(transistor_1449_out), .gate(transistor_1422_out));
  Transistor transistor_1450 (.in(1'b1), .out(transistor_1450_out), .gate(transistor_1426_out));
  Transistor transistor_1451 (.in(1'b1), .out(transistor_1451_out), .gate(transistor_1430_out));
  Transistor transistor_1452 (.in(1'b1), .out(transistor_1452_out), .gate(transistor_1434_out));
  Transistor transistor_1453 (.in(1'b1), .out(transistor_1453_out), .gate(transistor_1438_out));
  Transistor transistor_1454 (.in(1'b1), .out(transistor_1442_out), .gate(transistor_1631_out));
  Transistor #(.\type ("n")) transistor_1455 (
    .in(transistor_1456_out), .out(transistor_1442_out), .gate(transistor_1409_out));
  Transistor #(.\type ("n")) transistor_1456 (.in(1'b0), .out(transistor_1456_out), .gate(transistor_1631_out));
  Transistor transistor_1457 (.in(1'b1), .out(transistor_1446_out), .gate(transistor_1321_out));
  Transistor transistor_1458 (.in(1'b1), .out(transistor_1458_out), .gate(transistor_833_out));
  Transistor #(.\type ("n")) transistor_1459 (
    .in(transistor_1460_out), .out(transistor_1446_out), .gate(transistor_1410_out));
  Transistor #(.\type ("n")) transistor_1460 (.in(1'b0), .out(transistor_1460_out), .gate(transistor_1321_out));
  Transistor transistor_1461 (.in(1'b1), .out(transistor_1447_out), .gate(transistor_1325_out));
  Transistor transistor_1462 (.in(1'b1), .out(transistor_1462_out), .gate(transistor_839_out));
  Transistor #(.\type ("n")) transistor_1463 (
    .in(transistor_1464_out), .out(transistor_1447_out), .gate(transistor_1414_out));
  Transistor #(.\type ("n")) transistor_1464 (.in(1'b0), .out(transistor_1464_out), .gate(transistor_1325_out));
  Transistor transistor_1465 (.in(1'b1), .out(transistor_1448_out), .gate(transistor_1329_out));
  Transistor transistor_1466 (.in(1'b1), .out(transistor_1466_out), .gate(transistor_845_out));
  Transistor #(.\type ("n")) transistor_1467 (
    .in(transistor_1468_out), .out(transistor_1448_out), .gate(transistor_1418_out));
  Transistor #(.\type ("n")) transistor_1468 (.in(1'b0), .out(transistor_1468_out), .gate(transistor_1329_out));
  Transistor transistor_1469 (.in(1'b1), .out(transistor_1449_out), .gate(transistor_1333_out));
  Transistor transistor_1470 (.in(1'b1), .out(transistor_1470_out), .gate(transistor_851_out));
  Transistor #(.\type ("n")) transistor_1471 (
    .in(transistor_1472_out), .out(transistor_1449_out), .gate(transistor_1422_out));
  Transistor #(.\type ("n")) transistor_1472 (.in(1'b0), .out(transistor_1472_out), .gate(transistor_1333_out));
  Transistor transistor_1473 (.in(1'b1), .out(transistor_1450_out), .gate(transistor_1337_out));
  Transistor transistor_1474 (.in(1'b1), .out(transistor_1474_out), .gate(transistor_857_out));
  Transistor #(.\type ("n")) transistor_1475 (
    .in(transistor_1476_out), .out(transistor_1450_out), .gate(transistor_1426_out));
  Transistor #(.\type ("n")) transistor_1476 (.in(1'b0), .out(transistor_1476_out), .gate(transistor_1337_out));
  Transistor transistor_1477 (.in(1'b1), .out(transistor_1451_out), .gate(transistor_1341_out));
  Transistor transistor_1478 (.in(1'b1), .out(transistor_1478_out), .gate(transistor_863_out));
  Transistor #(.\type ("n")) transistor_1479 (
    .in(transistor_1480_out), .out(transistor_1451_out), .gate(transistor_1430_out));
  Transistor #(.\type ("n")) transistor_1480 (.in(1'b0), .out(transistor_1480_out), .gate(transistor_1341_out));
  Transistor transistor_1481 (.in(1'b1), .out(transistor_1481_out), .gate(transistor_869_out));
  Transistor transistor_1482 (.in(1'b1), .out(transistor_1452_out), .gate(transistor_1345_out));
  Transistor #(.\type ("n")) transistor_1483 (
    .in(transistor_1484_out), .out(transistor_1452_out), .gate(transistor_1434_out));
  Transistor #(.\type ("n")) transistor_1484 (.in(1'b0), .out(transistor_1484_out), .gate(transistor_1345_out));
  Transistor transistor_1485 (.in(1'b1), .out(transistor_1453_out), .gate(transistor_1349_out));
  Transistor transistor_1486 (.in(1'b1), .out(transistor_1486_out), .gate(transistor_875_out));
  Transistor #(.\type ("n")) transistor_1487 (
    .in(transistor_1488_out), .out(transistor_1453_out), .gate(transistor_1438_out));
  Transistor #(.\type ("n")) transistor_1488 (.in(1'b0), .out(transistor_1488_out), .gate(transistor_1349_out));
  Transistor transistor_1489 (.in(1'b1), .out(transistor_1489_out), .gate(transistor_1628_out));
  Transistor transistor_1490 (.in(1'b1), .out(transistor_1490_out), .gate(w));
  Transistor #(.\type ("n")) transistor_1491 (.in(1'b0), .out(transistor_1490_out), .gate(w));
  Transistor transistor_1492 (.in(1'b1), .out(transistor_1458_out), .gate(transistor_1410_out));
  Transistor #(.\type ("n")) transistor_1493 (
    .in(transistor_1494_out), .out(transistor_1458_out), .gate(transistor_1410_out));
  Transistor #(.\type ("n")) transistor_1494 (.in(1'b0), .out(transistor_1494_out), .gate(transistor_833_out));
  Transistor transistor_1495 (.in(1'b1), .out(transistor_1462_out), .gate(transistor_1414_out));
  Transistor #(.\type ("n")) transistor_1496 (
    .in(transistor_1497_out), .out(transistor_1462_out), .gate(transistor_1414_out));
  Transistor #(.\type ("n")) transistor_1497 (.in(1'b0), .out(transistor_1497_out), .gate(transistor_839_out));
  Transistor transistor_1498 (.in(1'b1), .out(transistor_1466_out), .gate(transistor_1418_out));
  Transistor #(.\type ("n")) transistor_1499 (
    .in(transistor_1500_out), .out(transistor_1466_out), .gate(transistor_1418_out));
  Transistor #(.\type ("n")) transistor_1500 (.in(1'b0), .out(transistor_1500_out), .gate(transistor_845_out));
  Transistor transistor_1501 (.in(1'b1), .out(transistor_1470_out), .gate(transistor_1422_out));
  Transistor #(.\type ("n")) transistor_1502 (
    .in(transistor_1503_out), .out(transistor_1470_out), .gate(transistor_1422_out));
  Transistor #(.\type ("n")) transistor_1503 (.in(1'b0), .out(transistor_1503_out), .gate(transistor_851_out));
  Transistor transistor_1504 (.in(1'b1), .out(transistor_1474_out), .gate(transistor_1426_out));
  Transistor #(.\type ("n")) transistor_1505 (
    .in(transistor_1506_out), .out(transistor_1474_out), .gate(transistor_1426_out));
  Transistor #(.\type ("n")) transistor_1506 (.in(1'b0), .out(transistor_1506_out), .gate(transistor_857_out));
  Transistor transistor_1507 (.in(1'b1), .out(transistor_1478_out), .gate(transistor_1430_out));
  Transistor #(.\type ("n")) transistor_1508 (
    .in(transistor_1509_out), .out(transistor_1478_out), .gate(transistor_1430_out));
  Transistor #(.\type ("n")) transistor_1509 (.in(1'b0), .out(transistor_1509_out), .gate(transistor_863_out));
  Transistor transistor_1510 (.in(1'b1), .out(transistor_1481_out), .gate(transistor_1434_out));
  Transistor #(.\type ("n")) transistor_1511 (
    .in(transistor_1512_out), .out(transistor_1481_out), .gate(transistor_1434_out));
  Transistor #(.\type ("n")) transistor_1512 (.in(1'b0), .out(transistor_1512_out), .gate(transistor_869_out));
  Transistor transistor_1513 (.in(1'b1), .out(transistor_1486_out), .gate(transistor_1438_out));
  Transistor #(.\type ("n")) transistor_1514 (
    .in(transistor_1515_out), .out(transistor_1486_out), .gate(transistor_1438_out));
  Transistor #(.\type ("n")) transistor_1515 (.in(1'b0), .out(transistor_1515_out), .gate(transistor_875_out));
  Transistor transistor_1516 (.in(1'b1), .out(transistor_1516_out), .gate(transistor_1489_out));
  Transistor transistor_1517 (.in(1'b1), .out(transistor_1489_out), .gate(transistor_1409_out));
  Transistor #(.\type ("n")) transistor_1518 (
    .in(transistor_1519_out), .out(transistor_1489_out), .gate(transistor_1409_out));
  Transistor #(.\type ("n")) transistor_1519 (.in(1'b0), .out(transistor_1519_out), .gate(transistor_1628_out));
  Transistor #(.\type ("n")) transistor_1520 (.in(transistor_1083_out), .out(transistor_1520_out), .gate(w));
  Transistor #(.gate("br")) transistor_1521 (
    .in(transistor_1083_out), .out(transistor_1520_out), .gate(transistor_1490_out));
  Transistor #(.\type ("n")) transistor_1522 (
    .in(transistor_1559_out), .out(transistor_1520_out), .gate(transistor_1490_out));
  Transistor #(.gate("br")) transistor_1523 (.in(transistor_1559_out), .out(transistor_1520_out), .gate(w));
  LED led_17 (.in(transistor_1559_out));
  Transistor transistor_1524 (.in(1'b1), .out(transistor_1524_out), .gate(transistor_1458_out));
  Transistor transistor_1525 (.in(1'b1), .out(transistor_1524_out), .gate(transistor_1446_out));
  Transistor #(.\type ("n")) transistor_1526 (
    .in(transistor_1527_out), .out(transistor_1524_out), .gate(transistor_1458_out));
  Transistor #(.\type ("n")) transistor_1527 (.in(1'b0), .out(transistor_1527_out), .gate(transistor_1446_out));
  Transistor transistor_1528 (.in(1'b1), .out(transistor_1528_out), .gate(transistor_1447_out));
  Transistor transistor_1529 (.in(1'b1), .out(transistor_1528_out), .gate(transistor_1462_out));
  Transistor #(.\type ("n")) transistor_1530 (
    .in(transistor_1531_out), .out(transistor_1528_out), .gate(transistor_1462_out));
  Transistor #(.\type ("n")) transistor_1531 (.in(1'b0), .out(transistor_1531_out), .gate(transistor_1447_out));
  Transistor transistor_1532 (.in(1'b1), .out(transistor_1532_out), .gate(transistor_1466_out));
  Transistor transistor_1533 (.in(1'b1), .out(transistor_1532_out), .gate(transistor_1448_out));
  Transistor #(.\type ("n")) transistor_1534 (
    .in(transistor_1535_out), .out(transistor_1532_out), .gate(transistor_1466_out));
  Transistor #(.\type ("n")) transistor_1535 (.in(1'b0), .out(transistor_1535_out), .gate(transistor_1448_out));
  Transistor transistor_1536 (.in(1'b1), .out(transistor_1536_out), .gate(transistor_1449_out));
  Transistor transistor_1537 (.in(1'b1), .out(transistor_1536_out), .gate(transistor_1470_out));
  Transistor #(.\type ("n")) transistor_1538 (
    .in(transistor_1539_out), .out(transistor_1536_out), .gate(transistor_1470_out));
  Transistor #(.\type ("n")) transistor_1539 (.in(1'b0), .out(transistor_1539_out), .gate(transistor_1449_out));
  Transistor transistor_1540 (.in(1'b1), .out(transistor_1540_out), .gate(transistor_1450_out));
  Transistor transistor_1541 (.in(1'b1), .out(transistor_1540_out), .gate(transistor_1474_out));
  Transistor #(.\type ("n")) transistor_1542 (
    .in(transistor_1543_out), .out(transistor_1540_out), .gate(transistor_1474_out));
  Transistor #(.\type ("n")) transistor_1543 (.in(1'b0), .out(transistor_1543_out), .gate(transistor_1450_out));
  Transistor transistor_1544 (.in(1'b1), .out(transistor_1544_out), .gate(transistor_1478_out));
  Transistor transistor_1545 (.in(1'b1), .out(transistor_1544_out), .gate(transistor_1451_out));
  Transistor #(.\type ("n")) transistor_1546 (
    .in(transistor_1547_out), .out(transistor_1544_out), .gate(transistor_1478_out));
  Transistor #(.\type ("n")) transistor_1547 (.in(1'b0), .out(transistor_1547_out), .gate(transistor_1451_out));
  Transistor transistor_1548 (.in(1'b1), .out(transistor_1548_out), .gate(transistor_1481_out));
  Transistor transistor_1549 (.in(1'b1), .out(transistor_1548_out), .gate(transistor_1452_out));
  Transistor #(.\type ("n")) transistor_1550 (
    .in(transistor_1551_out), .out(transistor_1548_out), .gate(transistor_1481_out));
  Transistor #(.\type ("n")) transistor_1551 (.in(1'b0), .out(transistor_1551_out), .gate(transistor_1452_out));
  Transistor transistor_1552 (.in(1'b1), .out(transistor_1552_out), .gate(transistor_1486_out));
  Transistor transistor_1553 (.in(1'b1), .out(transistor_1552_out), .gate(transistor_1453_out));
  Transistor #(.\type ("n")) transistor_1554 (
    .in(transistor_1555_out), .out(transistor_1552_out), .gate(transistor_1486_out));
  Transistor #(.\type ("n")) transistor_1555 (.in(1'b0), .out(transistor_1555_out), .gate(transistor_1453_out));
  Transistor transistor_1556 (.in(1'b1), .out(transistor_1516_out), .gate(transistor_1442_out));
  Transistor #(.\type ("n")) transistor_1557 (
    .in(transistor_1558_out), .out(transistor_1516_out), .gate(transistor_1489_out));
  Transistor #(.\type ("n")) transistor_1558 (.in(1'b0), .out(transistor_1558_out), .gate(transistor_1442_out));
  Transistor #(.\type ("n")) transistor_1559 (.in(1'b0), .out(transistor_1559_out), .gate(rst));
  Transistor #(.gate("br")) transistor_1560 (.in(1'b0), .out(transistor_1559_out), .gate(transistor_1561_out));
  Transistor transistor_1561 (.in(1'b1), .out(transistor_1561_out), .gate(rst));
  Transistor #(.\type ("n")) transistor_1562 (.in(1'b0), .out(transistor_1561_out), .gate(rst));
  Transistor #(.\type ("n")) transistor_1563 (
    .in(transistor_1520_out), .out(transistor_1559_out), .gate(transistor_1561_out));
  Transistor #(.gate("br")) transistor_1564 (.in(transistor_1520_out), .out(transistor_1559_out), .gate(rst));
  Transistor #(.\type ("n")) transistor_1565 (.in(1'b0), .out(transistor_1565_out), .gate(transistor_1393_out));
  Transistor #(.\type ("n")) transistor_1566 (.in(1'b0), .out(transistor_1566_out), .gate(transistor_1395_out));
  Transistor #(.\type ("n")) transistor_1567 (.in(1'b0), .out(transistor_1567_out), .gate(transistor_1397_out));
  Transistor #(.\type ("n")) transistor_1568 (.in(1'b0), .out(transistor_1568_out), .gate(transistor_1399_out));
  Transistor #(.\type ("n")) transistor_1569 (.in(1'b0), .out(transistor_1569_out), .gate(transistor_1401_out));
  Transistor #(.\type ("n")) transistor_1570 (.in(1'b0), .out(transistor_1570_out), .gate(transistor_1403_out));
  Transistor #(.\type ("n")) transistor_1571 (.in(1'b0), .out(transistor_1571_out), .gate(transistor_1405_out));
  Transistor #(.\type ("n")) transistor_1572 (.in(1'b0), .out(transistor_1572_out), .gate(transistor_1407_out));
  Transistor transistor_1573 (.in(1'b1), .out(transistor_1573_out), .gate(op1));
  Transistor #(.\type ("n")) transistor_1574 (.in(1'b0), .out(transistor_1573_out), .gate(op1));
  Transistor transistor_1575 (.in(1'b1), .out(transistor_1575_out), .gate(w));
  Transistor #(.\type ("n")) transistor_1576 (.in(1'b0), .out(transistor_1575_out), .gate(w));
  Transistor transistor_1577 (.in(1'b1), .out(transistor_1577_out), .gate(transistor_1393_out));
  Transistor transistor_1578 (.in(transistor_1577_out), .out(transistor_1565_out), .gate(transistor_1638_out));
  Transistor #(.\type ("n")) transistor_1579 (.in(1'b0), .out(transistor_1565_out), .gate(transistor_1638_out));
  Transistor transistor_1580 (.in(1'b1), .out(transistor_1580_out), .gate(transistor_1395_out));
  Transistor transistor_1581 (.in(transistor_1580_out), .out(transistor_1566_out), .gate(transistor_1643_out));
  Transistor #(.\type ("n")) transistor_1582 (.in(1'b0), .out(transistor_1566_out), .gate(transistor_1643_out));
  Transistor transistor_1583 (.in(1'b1), .out(transistor_1583_out), .gate(transistor_1397_out));
  Transistor transistor_1584 (.in(transistor_1583_out), .out(transistor_1567_out), .gate(transistor_1648_out));
  Transistor #(.\type ("n")) transistor_1585 (.in(1'b0), .out(transistor_1567_out), .gate(transistor_1648_out));
  Transistor transistor_1586 (.in(1'b1), .out(transistor_1586_out), .gate(transistor_1399_out));
  Transistor transistor_1587 (.in(transistor_1586_out), .out(transistor_1568_out), .gate(transistor_1653_out));
  Transistor #(.\type ("n")) transistor_1588 (.in(1'b0), .out(transistor_1568_out), .gate(transistor_1653_out));
  Transistor transistor_1589 (.in(1'b1), .out(transistor_1589_out), .gate(transistor_1401_out));
  Transistor transistor_1590 (.in(transistor_1589_out), .out(transistor_1569_out), .gate(transistor_1658_out));
  Transistor #(.\type ("n")) transistor_1591 (.in(1'b0), .out(transistor_1569_out), .gate(transistor_1658_out));
  Transistor transistor_1592 (.in(1'b1), .out(transistor_1592_out), .gate(transistor_1403_out));
  Transistor transistor_1593 (.in(transistor_1592_out), .out(transistor_1570_out), .gate(transistor_1662_out));
  Transistor #(.\type ("n")) transistor_1594 (.in(1'b0), .out(transistor_1570_out), .gate(transistor_1662_out));
  Transistor transistor_1595 (.in(1'b1), .out(transistor_1595_out), .gate(transistor_1405_out));
  Transistor transistor_1596 (.in(transistor_1595_out), .out(transistor_1571_out), .gate(transistor_1667_out));
  Transistor #(.\type ("n")) transistor_1597 (.in(1'b0), .out(transistor_1571_out), .gate(transistor_1667_out));
  Transistor transistor_1598 (.in(1'b1), .out(transistor_1598_out), .gate(transistor_1407_out));
  Transistor transistor_1599 (.in(transistor_1598_out), .out(transistor_1572_out), .gate(transistor_1673_out));
  Transistor #(.\type ("n")) transistor_1600 (.in(1'b0), .out(transistor_1572_out), .gate(transistor_1673_out));
  Transistor transistor_1601 (.in(1'b1), .out(transistor_1601_out), .gate(transistor_1573_out));
  Transistor transistor_1602 (.in(1'b1), .out(transistor_1601_out), .gate(op2));
  Transistor #(.\type ("n")) transistor_1603 (
    .in(transistor_1604_out), .out(transistor_1601_out), .gate(transistor_1573_out));
  Transistor #(.\type ("n")) transistor_1604 (.in(1'b0), .out(transistor_1604_out), .gate(op2));
  Transistor #(.\type ("n")) transistor_1605 (.in(transistor_1143_out), .out(transistor_1605_out), .gate(w));
  Transistor #(.gate("br")) transistor_1606 (
    .in(transistor_1143_out), .out(transistor_1605_out), .gate(transistor_1575_out));
  Transistor #(.\type ("n")) transistor_1607 (
    .in(transistor_1681_out), .out(transistor_1605_out), .gate(transistor_1575_out));
  Transistor #(.gate("br")) transistor_1608 (.in(transistor_1681_out), .out(transistor_1605_out), .gate(w));
  Transistor transistor_1609 (.in(1'b1), .out(transistor_1609_out), .gate(transistor_1790_out));
  Transistor transistor_1610 (.in(1'b1), .out(transistor_1610_out), .gate(transistor_1565_out));
  Transistor #(.\type ("n")) transistor_1611 (.in(1'b0), .out(transistor_1610_out), .gate(transistor_1565_out));
  Transistor transistor_1612 (.in(1'b1), .out(transistor_1612_out), .gate(transistor_1610_out));
  Transistor transistor_1613 (.in(1'b1), .out(transistor_1613_out), .gate(transistor_1566_out));
  Transistor #(.\type ("n")) transistor_1614 (.in(1'b0), .out(transistor_1613_out), .gate(transistor_1566_out));
  Transistor transistor_1615 (.in(1'b1), .out(transistor_1615_out), .gate(transistor_1613_out));
  Transistor transistor_1616 (.in(1'b1), .out(transistor_1616_out), .gate(transistor_1567_out));
  Transistor #(.\type ("n")) transistor_1617 (.in(1'b0), .out(transistor_1616_out), .gate(transistor_1567_out));
  Transistor transistor_1618 (.in(1'b1), .out(transistor_1618_out), .gate(transistor_1616_out));
  Transistor transistor_1619 (.in(1'b1), .out(transistor_1619_out), .gate(transistor_1568_out));
  Transistor #(.\type ("n")) transistor_1620 (.in(1'b0), .out(transistor_1619_out), .gate(transistor_1568_out));
  Transistor transistor_1621 (.in(1'b1), .out(transistor_1621_out), .gate(transistor_1619_out));
  Transistor transistor_1622 (.in(1'b1), .out(transistor_1622_out), .gate(transistor_1569_out));
  Transistor #(.\type ("n")) transistor_1623 (.in(1'b0), .out(transistor_1622_out), .gate(transistor_1569_out));
  Transistor transistor_1624 (.in(1'b1), .out(transistor_1624_out), .gate(transistor_1622_out));
  Transistor transistor_1625 (.in(1'b1), .out(transistor_1625_out), .gate(transistor_1570_out));
  Transistor #(.\type ("n")) transistor_1626 (.in(1'b0), .out(transistor_1625_out), .gate(transistor_1570_out));
  Transistor transistor_1627 (.in(1'b1), .out(transistor_1627_out), .gate(transistor_1625_out));
  Transistor transistor_1628 (.in(1'b1), .out(transistor_1628_out), .gate(transistor_1571_out));
  Transistor #(.\type ("n")) transistor_1629 (.in(1'b0), .out(transistor_1628_out), .gate(transistor_1571_out));
  Transistor transistor_1630 (.in(1'b1), .out(transistor_1630_out), .gate(transistor_1628_out));
  Transistor transistor_1631 (.in(1'b1), .out(transistor_1631_out), .gate(transistor_1572_out));
  Transistor #(.\type ("n")) transistor_1632 (.in(1'b0), .out(transistor_1631_out), .gate(transistor_1572_out));
  Transistor transistor_1633 (.in(1'b1), .out(transistor_1633_out), .gate(transistor_1601_out));
  Transistor #(.\type ("n")) transistor_1634 (.in(1'b0), .out(transistor_1633_out), .gate(transistor_1601_out));
  Transistor transistor_1635 (.in(1'b1), .out(transistor_1635_out), .gate(rst));
  Transistor #(.\type ("n")) transistor_1636 (.in(1'b0), .out(transistor_1635_out), .gate(rst));
  LED led_18 (.in(transistor_1681_out));
  Transistor transistor_1637 (.in(1'b1), .out(transistor_1609_out), .gate(transistor_1524_out));
  Transistor transistor_1638 (.in(1'b1), .out(transistor_1638_out), .gate(transistor_1609_out));
  Transistor #(.\type ("n")) transistor_1639 (
    .in(transistor_1641_out), .out(transistor_1609_out), .gate(transistor_1790_out));
  Transistor #(.\type ("n")) transistor_1640 (.in(1'b0), .out(transistor_1638_out), .gate(transistor_1609_out));
  Transistor #(.\type ("n")) transistor_1641 (.in(1'b0), .out(transistor_1641_out), .gate(transistor_1524_out));
  Transistor transistor_1642 (.in(1'b1), .out(transistor_1612_out), .gate(transistor_1528_out));
  Transistor transistor_1643 (.in(1'b1), .out(transistor_1643_out), .gate(transistor_1612_out));
  Transistor #(.\type ("n")) transistor_1644 (.in(1'b0), .out(transistor_1643_out), .gate(transistor_1612_out));
  Transistor #(.\type ("n")) transistor_1645 (
    .in(transistor_1646_out), .out(transistor_1612_out), .gate(transistor_1610_out));
  Transistor #(.\type ("n")) transistor_1646 (.in(1'b0), .out(transistor_1646_out), .gate(transistor_1528_out));
  Transistor transistor_1647 (.in(1'b1), .out(transistor_1615_out), .gate(transistor_1532_out));
  Transistor transistor_1648 (.in(1'b1), .out(transistor_1648_out), .gate(transistor_1615_out));
  Transistor #(.\type ("n")) transistor_1649 (
    .in(transistor_1651_out), .out(transistor_1615_out), .gate(transistor_1613_out));
  Transistor #(.\type ("n")) transistor_1650 (.in(1'b0), .out(transistor_1648_out), .gate(transistor_1615_out));
  Transistor #(.\type ("n")) transistor_1651 (.in(1'b0), .out(transistor_1651_out), .gate(transistor_1532_out));
  Transistor transistor_1652 (.in(1'b1), .out(transistor_1618_out), .gate(transistor_1536_out));
  Transistor transistor_1653 (.in(1'b1), .out(transistor_1653_out), .gate(transistor_1618_out));
  Transistor #(.\type ("n")) transistor_1654 (.in(1'b0), .out(transistor_1653_out), .gate(transistor_1618_out));
  Transistor #(.\type ("n")) transistor_1655 (
    .in(transistor_1656_out), .out(transistor_1618_out), .gate(transistor_1616_out));
  Transistor #(.\type ("n")) transistor_1656 (.in(1'b0), .out(transistor_1656_out), .gate(transistor_1536_out));
  Transistor transistor_1657 (.in(1'b1), .out(transistor_1621_out), .gate(transistor_1540_out));
  Transistor transistor_1658 (.in(1'b1), .out(transistor_1658_out), .gate(transistor_1621_out));
  Transistor #(.\type ("n")) transistor_1659 (
    .in(transistor_1661_out), .out(transistor_1621_out), .gate(transistor_1619_out));
  Transistor #(.\type ("n")) transistor_1660 (.in(1'b0), .out(transistor_1658_out), .gate(transistor_1621_out));
  Transistor #(.\type ("n")) transistor_1661 (.in(1'b0), .out(transistor_1661_out), .gate(transistor_1540_out));
  Transistor transistor_1662 (.in(1'b1), .out(transistor_1662_out), .gate(transistor_1624_out));
  Transistor transistor_1663 (.in(1'b1), .out(transistor_1624_out), .gate(transistor_1544_out));
  Transistor #(.\type ("n")) transistor_1664 (
    .in(transistor_1666_out), .out(transistor_1624_out), .gate(transistor_1622_out));
  Transistor #(.\type ("n")) transistor_1665 (.in(1'b0), .out(transistor_1662_out), .gate(transistor_1624_out));
  Transistor #(.\type ("n")) transistor_1666 (.in(1'b0), .out(transistor_1666_out), .gate(transistor_1544_out));
  Transistor transistor_1667 (.in(1'b1), .out(transistor_1667_out), .gate(transistor_1627_out));
  Transistor transistor_1668 (.in(1'b1), .out(transistor_1627_out), .gate(transistor_1548_out));
  Transistor #(.\type ("n")) transistor_1669 (
    .in(transistor_1671_out), .out(transistor_1627_out), .gate(transistor_1625_out));
  Transistor #(.\type ("n")) transistor_1670 (.in(1'b0), .out(transistor_1667_out), .gate(transistor_1627_out));
  Transistor #(.\type ("n")) transistor_1671 (.in(1'b0), .out(transistor_1671_out), .gate(transistor_1548_out));
  Transistor transistor_1672 (.in(1'b1), .out(transistor_1630_out), .gate(transistor_1552_out));
  Transistor transistor_1673 (.in(1'b1), .out(transistor_1673_out), .gate(transistor_1630_out));
  Transistor #(.\type ("n")) transistor_1674 (.in(1'b0), .out(transistor_1673_out), .gate(transistor_1630_out));
  Transistor #(.\type ("n")) transistor_1675 (
    .in(transistor_1676_out), .out(transistor_1630_out), .gate(transistor_1628_out));
  Transistor #(.\type ("n")) transistor_1676 (.in(1'b0), .out(transistor_1676_out), .gate(transistor_1552_out));
  Transistor transistor_1677 (.in(1'b1), .out(transistor_1677_out), .gate(transistor_1633_out));
  Transistor transistor_1678 (.in(1'b1), .out(transistor_1677_out), .gate(transistor_1516_out));
  Transistor #(.\type ("n")) transistor_1679 (
    .in(transistor_1680_out), .out(transistor_1677_out), .gate(transistor_1633_out));
  Transistor #(.\type ("n")) transistor_1680 (.in(1'b0), .out(transistor_1680_out), .gate(transistor_1516_out));
  Transistor #(.\type ("n")) transistor_1681 (.in(1'b0), .out(transistor_1681_out), .gate(rst));
  Transistor #(.gate("br")) transistor_1682 (.in(1'b0), .out(transistor_1681_out), .gate(transistor_1635_out));
  Transistor #(.\type ("n")) transistor_1683 (
    .in(transistor_1605_out), .out(transistor_1681_out), .gate(transistor_1635_out));
  Transistor #(.gate("br")) transistor_1684 (.in(transistor_1605_out), .out(transistor_1681_out), .gate(rst));
  Transistor transistor_1685 (.in(1'b1), .out(transistor_1685_out), .gate(op0));
  Transistor transistor_1686 (.in(1'b1), .out(transistor_1686_out), .gate(transistor_1524_out));
  Transistor transistor_1687 (.in(1'b1), .out(transistor_1687_out), .gate(transistor_1528_out));
  Transistor transistor_1688 (.in(1'b1), .out(transistor_1688_out), .gate(transistor_1532_out));
  Transistor transistor_1689 (.in(1'b1), .out(transistor_1689_out), .gate(transistor_1536_out));
  Transistor transistor_1690 (.in(1'b1), .out(transistor_1690_out), .gate(transistor_1540_out));
  Transistor transistor_1691 (.in(1'b1), .out(transistor_1691_out), .gate(transistor_1544_out));
  Transistor transistor_1692 (.in(1'b1), .out(transistor_1692_out), .gate(transistor_1548_out));
  Transistor transistor_1693 (.in(1'b1), .out(transistor_1693_out), .gate(transistor_1552_out));
  Transistor transistor_1694 (.in(1'b1), .out(transistor_1694_out), .gate(transistor_1677_out));
  Transistor #(.\type ("n")) transistor_1695 (.in(1'b0), .out(transistor_1694_out), .gate(transistor_1677_out));
  Transistor transistor_1696 (.in(1'b1), .out(transistor_1696_out), .gate(w));
  Transistor #(.\type ("n")) transistor_1697 (.in(1'b0), .out(transistor_1696_out), .gate(w));
  Transistor transistor_1698 (.in(1'b1), .out(transistor_1685_out), .gate(cin));
  Transistor #(.\type ("n")) transistor_1699 (.in(transistor_1700_out), .out(transistor_1685_out), .gate(op0));
  Transistor #(.\type ("n")) transistor_1700 (.in(1'b0), .out(transistor_1700_out), .gate(cin));
  Transistor transistor_1701 (.in(1'b1), .out(transistor_1686_out), .gate(transistor_1790_out));
  Transistor #(.\type ("n")) transistor_1702 (
    .in(transistor_1703_out), .out(transistor_1686_out), .gate(transistor_1524_out));
  Transistor #(.\type ("n")) transistor_1703 (.in(1'b0), .out(transistor_1703_out), .gate(transistor_1790_out));
  Transistor transistor_1704 (.in(1'b1), .out(transistor_1687_out), .gate(transistor_1610_out));
  Transistor #(.\type ("n")) transistor_1705 (
    .in(transistor_1706_out), .out(transistor_1687_out), .gate(transistor_1528_out));
  Transistor #(.\type ("n")) transistor_1706 (.in(1'b0), .out(transistor_1706_out), .gate(transistor_1610_out));
  Transistor transistor_1707 (.in(1'b1), .out(transistor_1688_out), .gate(transistor_1613_out));
  Transistor #(.\type ("n")) transistor_1708 (
    .in(transistor_1709_out), .out(transistor_1688_out), .gate(transistor_1532_out));
  Transistor #(.\type ("n")) transistor_1709 (.in(1'b0), .out(transistor_1709_out), .gate(transistor_1613_out));
  Transistor transistor_1710 (.in(1'b1), .out(transistor_1689_out), .gate(transistor_1616_out));
  Transistor #(.\type ("n")) transistor_1711 (
    .in(transistor_1712_out), .out(transistor_1689_out), .gate(transistor_1536_out));
  Transistor #(.\type ("n")) transistor_1712 (.in(1'b0), .out(transistor_1712_out), .gate(transistor_1616_out));
  Transistor transistor_1713 (.in(1'b1), .out(transistor_1690_out), .gate(transistor_1619_out));
  Transistor #(.\type ("n")) transistor_1714 (
    .in(transistor_1715_out), .out(transistor_1690_out), .gate(transistor_1540_out));
  Transistor #(.\type ("n")) transistor_1715 (.in(1'b0), .out(transistor_1715_out), .gate(transistor_1619_out));
  Transistor transistor_1716 (.in(1'b1), .out(transistor_1691_out), .gate(transistor_1622_out));
  Transistor #(.\type ("n")) transistor_1717 (
    .in(transistor_1718_out), .out(transistor_1691_out), .gate(transistor_1544_out));
  Transistor #(.\type ("n")) transistor_1718 (.in(1'b0), .out(transistor_1718_out), .gate(transistor_1622_out));
  Transistor transistor_1719 (.in(1'b1), .out(transistor_1692_out), .gate(transistor_1625_out));
  Transistor #(.\type ("n")) transistor_1720 (
    .in(transistor_1721_out), .out(transistor_1692_out), .gate(transistor_1548_out));
  Transistor #(.\type ("n")) transistor_1721 (.in(1'b0), .out(transistor_1721_out), .gate(transistor_1625_out));
  Transistor transistor_1722 (.in(1'b1), .out(transistor_1693_out), .gate(transistor_1628_out));
  Transistor #(.\type ("n")) transistor_1723 (
    .in(transistor_1724_out), .out(transistor_1693_out), .gate(transistor_1552_out));
  Transistor #(.\type ("n")) transistor_1724 (.in(1'b0), .out(transistor_1724_out), .gate(transistor_1628_out));
  Transistor transistor_1725 (.in(1'b1), .out(transistor_1725_out), .gate(op0));
  Transistor #(.\type ("n")) transistor_1726 (.in(transistor_1179_out), .out(transistor_1726_out), .gate(w));
  Transistor #(.gate("br")) transistor_1727 (
    .in(transistor_1179_out), .out(transistor_1726_out), .gate(transistor_1696_out));
  Transistor transistor_1728 (.in(1'b1), .out(transistor_1728_out), .gate(rst));
  Transistor #(.\type ("n")) transistor_1729 (.in(1'b0), .out(transistor_1728_out), .gate(rst));
  Transistor #(.\type ("n")) transistor_1730 (
    .in(transistor_1772_out), .out(transistor_1726_out), .gate(transistor_1696_out));
  Transistor #(.gate("br")) transistor_1731 (.in(transistor_1772_out), .out(transistor_1726_out), .gate(w));
  LED led_19 (.in(transistor_1772_out));
  Transistor transistor_1732 (.in(1'b1), .out(transistor_1732_out), .gate(transistor_1685_out));
  Transistor transistor_1733 (.in(1'b1), .out(transistor_1732_out), .gate(cin));
  Transistor #(.\type ("n")) transistor_1734 (
    .in(transistor_1735_out), .out(transistor_1732_out), .gate(transistor_1685_out));
  Transistor #(.\type ("n")) transistor_1735 (.in(1'b0), .out(transistor_1735_out), .gate(cin));
  Transistor transistor_1736 (.in(1'b1), .out(transistor_1736_out), .gate(transistor_1686_out));
  Transistor transistor_1737 (.in(1'b1), .out(transistor_1736_out), .gate(transistor_1790_out));
  Transistor #(.\type ("n")) transistor_1738 (
    .in(transistor_1739_out), .out(transistor_1736_out), .gate(transistor_1686_out));
  Transistor #(.\type ("n")) transistor_1739 (.in(1'b0), .out(transistor_1739_out), .gate(transistor_1790_out));
  Transistor transistor_1740 (.in(1'b1), .out(transistor_1740_out), .gate(transistor_1687_out));
  Transistor transistor_1741 (.in(1'b1), .out(transistor_1740_out), .gate(transistor_1610_out));
  Transistor #(.\type ("n")) transistor_1742 (
    .in(transistor_1743_out), .out(transistor_1740_out), .gate(transistor_1687_out));
  Transistor #(.\type ("n")) transistor_1743 (.in(1'b0), .out(transistor_1743_out), .gate(transistor_1610_out));
  Transistor transistor_1744 (.in(1'b1), .out(transistor_1744_out), .gate(transistor_1613_out));
  Transistor transistor_1745 (.in(1'b1), .out(transistor_1744_out), .gate(transistor_1688_out));
  Transistor #(.\type ("n")) transistor_1746 (
    .in(transistor_1747_out), .out(transistor_1744_out), .gate(transistor_1688_out));
  Transistor #(.\type ("n")) transistor_1747 (.in(1'b0), .out(transistor_1747_out), .gate(transistor_1613_out));
  Transistor transistor_1748 (.in(1'b1), .out(transistor_1748_out), .gate(transistor_1689_out));
  Transistor transistor_1749 (.in(1'b1), .out(transistor_1748_out), .gate(transistor_1616_out));
  Transistor #(.\type ("n")) transistor_1750 (
    .in(transistor_1751_out), .out(transistor_1748_out), .gate(transistor_1689_out));
  Transistor #(.\type ("n")) transistor_1751 (.in(1'b0), .out(transistor_1751_out), .gate(transistor_1616_out));
  Transistor transistor_1752 (.in(1'b1), .out(transistor_1752_out), .gate(transistor_1619_out));
  Transistor transistor_1753 (.in(1'b1), .out(transistor_1752_out), .gate(transistor_1690_out));
  Transistor #(.\type ("n")) transistor_1754 (
    .in(transistor_1755_out), .out(transistor_1752_out), .gate(transistor_1690_out));
  Transistor #(.\type ("n")) transistor_1755 (.in(1'b0), .out(transistor_1755_out), .gate(transistor_1619_out));
  Transistor transistor_1756 (.in(1'b1), .out(transistor_1756_out), .gate(transistor_1622_out));
  Transistor transistor_1757 (.in(1'b1), .out(transistor_1756_out), .gate(transistor_1691_out));
  Transistor #(.\type ("n")) transistor_1758 (
    .in(transistor_1759_out), .out(transistor_1756_out), .gate(transistor_1691_out));
  Transistor #(.\type ("n")) transistor_1759 (.in(1'b0), .out(transistor_1759_out), .gate(transistor_1622_out));
  Transistor transistor_1760 (.in(1'b1), .out(transistor_1760_out), .gate(transistor_1625_out));
  Transistor transistor_1761 (.in(1'b1), .out(transistor_1760_out), .gate(transistor_1692_out));
  Transistor #(.\type ("n")) transistor_1762 (
    .in(transistor_1763_out), .out(transistor_1760_out), .gate(transistor_1692_out));
  Transistor #(.\type ("n")) transistor_1763 (.in(1'b0), .out(transistor_1763_out), .gate(transistor_1625_out));
  Transistor transistor_1764 (.in(1'b1), .out(transistor_1764_out), .gate(transistor_1693_out));
  Transistor transistor_1765 (.in(1'b1), .out(transistor_1764_out), .gate(transistor_1628_out));
  Transistor #(.\type ("n")) transistor_1766 (
    .in(transistor_1767_out), .out(transistor_1764_out), .gate(transistor_1693_out));
  Transistor #(.\type ("n")) transistor_1767 (.in(1'b0), .out(transistor_1767_out), .gate(transistor_1628_out));
  Transistor transistor_1768 (.in(1'b1), .out(transistor_1725_out), .gate(transistor_1631_out));
  Transistor transistor_1769 (.in(1'b1), .out(transistor_1769_out), .gate(transistor_1725_out));
  Transistor #(.\type ("n")) transistor_1770 (.in(transistor_1771_out), .out(transistor_1725_out), .gate(op0));
  Transistor #(.\type ("n")) transistor_1771 (.in(1'b0), .out(transistor_1771_out), .gate(transistor_1631_out));
  Transistor #(.\type ("n")) transistor_1772 (.in(1'b0), .out(transistor_1772_out), .gate(rst));
  Transistor #(.gate("br")) transistor_1773 (.in(1'b0), .out(transistor_1772_out), .gate(transistor_1728_out));
  Transistor #(.\type ("n")) transistor_1774 (
    .in(transistor_1726_out), .out(transistor_1772_out), .gate(transistor_1728_out));
  Transistor #(.gate("br")) transistor_1775 (.in(transistor_1726_out), .out(transistor_1772_out), .gate(rst));
  Transistor transistor_1776 (.in(1'b1), .out(transistor_1776_out), .gate(op0));
  Transistor transistor_1777 (.in(1'b1), .out(transistor_1777_out), .gate(transistor_1524_out));
  Transistor transistor_1778 (.in(1'b1), .out(transistor_1778_out), .gate(transistor_1528_out));
  Transistor transistor_1779 (.in(1'b1), .out(transistor_1779_out), .gate(transistor_1532_out));
  Transistor transistor_1780 (.in(1'b1), .out(transistor_1780_out), .gate(transistor_1536_out));
  Transistor transistor_1781 (.in(1'b1), .out(transistor_1781_out), .gate(transistor_1540_out));
  Transistor transistor_1782 (.in(1'b1), .out(transistor_1782_out), .gate(transistor_1544_out));
  Transistor transistor_1783 (.in(1'b1), .out(transistor_1783_out), .gate(transistor_1548_out));
  Transistor transistor_1784 (.in(1'b1), .out(transistor_1784_out), .gate(transistor_1552_out));
  Transistor transistor_1785 (.in(1'b1), .out(transistor_1769_out), .gate(transistor_1631_out));
  Transistor #(.\type ("n")) transistor_1786 (
    .in(transistor_1787_out), .out(transistor_1769_out), .gate(transistor_1725_out));
  Transistor #(.\type ("n")) transistor_1787 (.in(1'b0), .out(transistor_1787_out), .gate(transistor_1631_out));
  Transistor transistor_1788 (.in(1'b1), .out(transistor_1788_out), .gate(w));
  Transistor #(.\type ("n")) transistor_1789 (.in(1'b0), .out(transistor_1788_out), .gate(w));
  Transistor transistor_1790 (.in(1'b1), .out(transistor_1790_out), .gate(transistor_1776_out));
  Transistor transistor_1791 (.in(1'b1), .out(transistor_1776_out), .gate(transistor_1685_out));
  Transistor #(.\type ("n")) transistor_1792 (
    .in(transistor_1793_out), .out(transistor_1776_out), .gate(transistor_1685_out));
  Transistor #(.\type ("n")) transistor_1793 (.in(1'b0), .out(transistor_1793_out), .gate(op0));
  Transistor transistor_1794 (.in(1'b1), .out(transistor_1794_out), .gate(transistor_1777_out));
  Transistor transistor_1795 (.in(1'b1), .out(transistor_1777_out), .gate(transistor_1686_out));
  Transistor #(.\type ("n")) transistor_1796 (
    .in(transistor_1797_out), .out(transistor_1777_out), .gate(transistor_1686_out));
  Transistor #(.\type ("n")) transistor_1797 (.in(1'b0), .out(transistor_1797_out), .gate(transistor_1524_out));
  Transistor transistor_1798 (.in(1'b1), .out(transistor_1778_out), .gate(transistor_1687_out));
  Transistor transistor_1799 (.in(1'b1), .out(transistor_1799_out), .gate(transistor_1778_out));
  Transistor #(.\type ("n")) transistor_1800 (
    .in(transistor_1801_out), .out(transistor_1778_out), .gate(transistor_1687_out));
  Transistor #(.\type ("n")) transistor_1801 (.in(1'b0), .out(transistor_1801_out), .gate(transistor_1528_out));
  Transistor transistor_1802 (.in(1'b1), .out(transistor_1802_out), .gate(transistor_1779_out));
  Transistor transistor_1803 (.in(1'b1), .out(transistor_1779_out), .gate(transistor_1688_out));
  Transistor #(.\type ("n")) transistor_1804 (
    .in(transistor_1805_out), .out(transistor_1779_out), .gate(transistor_1688_out));
  Transistor #(.\type ("n")) transistor_1805 (.in(1'b0), .out(transistor_1805_out), .gate(transistor_1532_out));
  Transistor transistor_1806 (.in(1'b1), .out(transistor_1780_out), .gate(transistor_1689_out));
  Transistor transistor_1807 (.in(1'b1), .out(transistor_1807_out), .gate(transistor_1780_out));
  Transistor #(.\type ("n")) transistor_1808 (
    .in(transistor_1809_out), .out(transistor_1780_out), .gate(transistor_1689_out));
  Transistor #(.\type ("n")) transistor_1809 (.in(1'b0), .out(transistor_1809_out), .gate(transistor_1536_out));
  Transistor transistor_1810 (.in(1'b1), .out(transistor_1781_out), .gate(transistor_1690_out));
  Transistor transistor_1811 (.in(1'b1), .out(transistor_1811_out), .gate(transistor_1781_out));
  Transistor #(.\type ("n")) transistor_1812 (
    .in(transistor_1813_out), .out(transistor_1781_out), .gate(transistor_1690_out));
  Transistor #(.\type ("n")) transistor_1813 (.in(1'b0), .out(transistor_1813_out), .gate(transistor_1540_out));
  Transistor transistor_1814 (.in(1'b1), .out(transistor_1782_out), .gate(transistor_1691_out));
  Transistor transistor_1815 (.in(1'b1), .out(transistor_1815_out), .gate(transistor_1782_out));
  Transistor #(.\type ("n")) transistor_1816 (
    .in(transistor_1817_out), .out(transistor_1782_out), .gate(transistor_1691_out));
  Transistor #(.\type ("n")) transistor_1817 (.in(1'b0), .out(transistor_1817_out), .gate(transistor_1544_out));
  Transistor transistor_1818 (.in(1'b1), .out(transistor_1783_out), .gate(transistor_1692_out));
  Transistor transistor_1819 (.in(1'b1), .out(transistor_1819_out), .gate(transistor_1783_out));
  Transistor #(.\type ("n")) transistor_1820 (
    .in(transistor_1821_out), .out(transistor_1783_out), .gate(transistor_1692_out));
  Transistor #(.\type ("n")) transistor_1821 (.in(1'b0), .out(transistor_1821_out), .gate(transistor_1548_out));
  Transistor transistor_1822 (.in(1'b1), .out(transistor_1784_out), .gate(transistor_1693_out));
  Transistor transistor_1823 (.in(1'b1), .out(transistor_1823_out), .gate(transistor_1784_out));
  Transistor #(.\type ("n")) transistor_1824 (
    .in(transistor_1825_out), .out(transistor_1784_out), .gate(transistor_1693_out));
  Transistor #(.\type ("n")) transistor_1825 (.in(1'b0), .out(transistor_1825_out), .gate(transistor_1552_out));
  Transistor transistor_1826 (.in(1'b1), .out(transistor_1826_out), .gate(op0));
  Transistor transistor_1827 (.in(1'b1), .out(transistor_1826_out), .gate(transistor_1725_out));
  Transistor #(.\type ("n")) transistor_1828 (
    .in(transistor_1829_out), .out(transistor_1826_out), .gate(transistor_1725_out));
  Transistor #(.\type ("n")) transistor_1829 (.in(1'b0), .out(transistor_1829_out), .gate(op0));
  Transistor #(.\type ("n")) transistor_1830 (.in(transistor_1215_out), .out(transistor_1830_out), .gate(w));
  Transistor #(.gate("br")) transistor_1831 (
    .in(transistor_1215_out), .out(transistor_1830_out), .gate(transistor_1788_out));
  Transistor #(.\type ("n")) transistor_1832 (
    .in(transistor_1867_out), .out(transistor_1830_out), .gate(transistor_1788_out));
  Transistor #(.gate("br")) transistor_1833 (.in(transistor_1867_out), .out(transistor_1830_out), .gate(w));
  LED led_20 (.in(transistor_1867_out));
  Transistor transistor_1834 (.in(1'b1), .out(transistor_1790_out), .gate(transistor_1732_out));
  Transistor #(.\type ("n")) transistor_1835 (
    .in(transistor_1836_out), .out(transistor_1790_out), .gate(transistor_1776_out));
  Transistor #(.\type ("n")) transistor_1836 (.in(1'b0), .out(transistor_1836_out), .gate(transistor_1732_out));
  Transistor transistor_1837 (.in(1'b1), .out(transistor_1794_out), .gate(transistor_1736_out));
  Transistor #(.\type ("n")) transistor_1838 (
    .in(transistor_1839_out), .out(transistor_1794_out), .gate(transistor_1777_out));
  Transistor #(.\type ("n")) transistor_1839 (.in(1'b0), .out(transistor_1839_out), .gate(transistor_1736_out));
  Transistor transistor_1840 (.in(1'b1), .out(transistor_1799_out), .gate(transistor_1740_out));
  Transistor #(.\type ("n")) transistor_1841 (
    .in(transistor_1842_out), .out(transistor_1799_out), .gate(transistor_1778_out));
  Transistor #(.\type ("n")) transistor_1842 (.in(1'b0), .out(transistor_1842_out), .gate(transistor_1740_out));
  Transistor transistor_1843 (.in(1'b1), .out(transistor_1802_out), .gate(transistor_1744_out));
  Transistor #(.\type ("n")) transistor_1844 (
    .in(transistor_1845_out), .out(transistor_1802_out), .gate(transistor_1779_out));
  Transistor #(.\type ("n")) transistor_1845 (.in(1'b0), .out(transistor_1845_out), .gate(transistor_1744_out));
  Transistor transistor_1846 (.in(1'b1), .out(transistor_1807_out), .gate(transistor_1748_out));
  Transistor #(.\type ("n")) transistor_1847 (
    .in(transistor_1848_out), .out(transistor_1807_out), .gate(transistor_1780_out));
  Transistor #(.\type ("n")) transistor_1848 (.in(1'b0), .out(transistor_1848_out), .gate(transistor_1748_out));
  Transistor transistor_1849 (.in(1'b1), .out(transistor_1811_out), .gate(transistor_1752_out));
  Transistor #(.\type ("n")) transistor_1850 (
    .in(transistor_1851_out), .out(transistor_1811_out), .gate(transistor_1781_out));
  Transistor #(.\type ("n")) transistor_1851 (.in(1'b0), .out(transistor_1851_out), .gate(transistor_1752_out));
  Transistor transistor_1852 (.in(1'b1), .out(transistor_1815_out), .gate(transistor_1756_out));
  Transistor #(.\type ("n")) transistor_1853 (
    .in(transistor_1854_out), .out(transistor_1815_out), .gate(transistor_1782_out));
  Transistor #(.\type ("n")) transistor_1854 (.in(1'b0), .out(transistor_1854_out), .gate(transistor_1756_out));
  Transistor transistor_1855 (.in(1'b1), .out(transistor_1819_out), .gate(transistor_1760_out));
  Transistor #(.\type ("n")) transistor_1856 (
    .in(transistor_1857_out), .out(transistor_1819_out), .gate(transistor_1783_out));
  Transistor #(.\type ("n")) transistor_1857 (.in(1'b0), .out(transistor_1857_out), .gate(transistor_1760_out));
  Transistor transistor_1858 (.in(1'b1), .out(transistor_1823_out), .gate(transistor_1764_out));
  Transistor #(.\type ("n")) transistor_1859 (
    .in(transistor_1860_out), .out(transistor_1823_out), .gate(transistor_1784_out));
  Transistor #(.\type ("n")) transistor_1860 (.in(1'b0), .out(transistor_1860_out), .gate(transistor_1764_out));
  Transistor transistor_1861 (.in(1'b1), .out(transistor_1861_out), .gate(transistor_1826_out));
  Transistor transistor_1862 (.in(1'b1), .out(transistor_1862_out), .gate(rst));
  Transistor #(.\type ("n")) transistor_1863 (.in(1'b0), .out(transistor_1862_out), .gate(rst));
  Transistor transistor_1864 (.in(1'b1), .out(transistor_1861_out), .gate(transistor_1769_out));
  Transistor #(.\type ("n")) transistor_1865 (
    .in(transistor_1866_out), .out(transistor_1861_out), .gate(transistor_1826_out));
  Transistor #(.\type ("n")) transistor_1866 (.in(1'b0), .out(transistor_1866_out), .gate(transistor_1769_out));
  Transistor #(.\type ("n")) transistor_1867 (.in(1'b0), .out(transistor_1867_out), .gate(rst));
  Transistor #(.gate("br")) transistor_1868 (.in(1'b0), .out(transistor_1867_out), .gate(transistor_1862_out));
  Transistor #(.\type ("n")) transistor_1869 (
    .in(transistor_1830_out), .out(transistor_1867_out), .gate(transistor_1862_out));
  Transistor #(.gate("br")) transistor_1870 (.in(transistor_1830_out), .out(transistor_1867_out), .gate(rst));
  Transistor #(.\type ("n")) transistor_1871 (.in(transistor_833_out), .out(transistor_1871_out), .gate(op0));
  Transistor #(.gate("br")) transistor_1872 (
    .in(transistor_833_out), .out(transistor_1871_out), .gate(transistor_1879_out));
  Transistor #(.\type ("n")) transistor_1873 (.in(transistor_1251_out), .out(transistor_1873_out), .gate(w));
  Transistor #(.gate("br")) transistor_1874 (
    .in(transistor_1251_out), .out(transistor_1873_out), .gate(transistor_1875_out));
  Transistor transistor_1875 (.in(1'b1), .out(transistor_1875_out), .gate(w));
  Transistor #(.\type ("n")) transistor_1876 (.in(1'b0), .out(transistor_1875_out), .gate(w));
  Transistor #(.\type ("n")) transistor_1877 (
    .in(transistor_1917_out), .out(transistor_1873_out), .gate(transistor_1875_out));
  Transistor #(.gate("br")) transistor_1878 (.in(transistor_1917_out), .out(transistor_1873_out), .gate(w));
  Transistor #(.\type ("n")) transistor_1879 (.in(1'b0), .out(transistor_1879_out), .gate(op0));
  Transistor transistor_1880 (.in(1'b1), .out(transistor_1879_out), .gate(op0));
  Transistor #(.\type ("n")) transistor_1881 (
    .in(transistor_875_out), .out(transistor_1871_out), .gate(transistor_1879_out));
  Transistor #(.gate("br")) transistor_1882 (.in(transistor_875_out), .out(transistor_1871_out), .gate(op0));
  Transistor transistor_1883 (.in(1'b1), .out(transistor_1883_out), .gate(rst));
  Transistor #(.\type ("n")) transistor_1884 (.in(1'b0), .out(transistor_1883_out), .gate(rst));
  LED led_21 (.in(transistor_1917_out));
  Transistor transistor_1885 (.in(1'b1), .out(transistor_1885_out), .gate(op0));
  Transistor #(.\type ("n")) transistor_1886 (.in(1'b0), .out(transistor_1885_out), .gate(op0));
  Transistor #(.gate("br")) transistor_1887 (
    .in(transistor_839_out), .out(transistor_1887_out), .gate(transistor_1885_out));
  Transistor #(.\type ("n")) transistor_1888 (.in(transistor_839_out), .out(transistor_1887_out), .gate(op0));
  Transistor transistor_1889 (.in(1'b1), .out(transistor_1889_out), .gate(op0));
  Transistor #(.\type ("n")) transistor_1890 (.in(1'b0), .out(transistor_1889_out), .gate(op0));
  Transistor #(.gate("br")) transistor_1891 (
    .in(transistor_845_out), .out(transistor_1891_out), .gate(transistor_1889_out));
  Transistor #(.\type ("n")) transistor_1892 (.in(transistor_845_out), .out(transistor_1891_out), .gate(op0));
  Transistor #(.\type ("n")) transistor_1893 (.in(1'b0), .out(transistor_1893_out), .gate(op0));
  Transistor transistor_1894 (.in(1'b1), .out(transistor_1893_out), .gate(op0));
  Transistor #(.\type ("n")) transistor_1895 (.in(transistor_851_out), .out(transistor_1895_out), .gate(op0));
  Transistor #(.gate("br")) transistor_1896 (
    .in(transistor_851_out), .out(transistor_1895_out), .gate(transistor_1893_out));
  Transistor transistor_1897 (.in(1'b1), .out(transistor_1897_out), .gate(op0));
  Transistor #(.\type ("n")) transistor_1898 (.in(1'b0), .out(transistor_1897_out), .gate(op0));
  Transistor #(.\type ("n")) transistor_1899 (.in(transistor_857_out), .out(transistor_1899_out), .gate(op0));
  Transistor #(.gate("br")) transistor_1900 (
    .in(transistor_857_out), .out(transistor_1899_out), .gate(transistor_1897_out));
  Transistor #(.\type ("n")) transistor_1901 (.in(1'b0), .out(transistor_1901_out), .gate(op0));
  Transistor transistor_1902 (.in(1'b1), .out(transistor_1901_out), .gate(op0));
  Transistor #(.\type ("n")) transistor_1903 (.in(transistor_863_out), .out(transistor_1903_out), .gate(op0));
  Transistor #(.gate("br")) transistor_1904 (
    .in(transistor_863_out), .out(transistor_1903_out), .gate(transistor_1901_out));
  Transistor transistor_1905 (.in(1'b1), .out(transistor_1905_out), .gate(op0));
  Transistor #(.\type ("n")) transistor_1906 (.in(1'b0), .out(transistor_1905_out), .gate(op0));
  Transistor #(.gate("br")) transistor_1907 (
    .in(transistor_869_out), .out(transistor_1907_out), .gate(transistor_1905_out));
  Transistor #(.\type ("n")) transistor_1908 (.in(transistor_869_out), .out(transistor_1907_out), .gate(op0));
  Transistor #(.\type ("n")) transistor_1909 (.in(1'b0), .out(transistor_1909_out), .gate(op0));
  Transistor transistor_1910 (.in(1'b1), .out(transistor_1909_out), .gate(op0));
  Transistor #(.gate("br")) transistor_1911 (
    .in(transistor_875_out), .out(transistor_1911_out), .gate(transistor_1909_out));
  Transistor #(.\type ("n")) transistor_1912 (.in(transistor_875_out), .out(transistor_1911_out), .gate(op0));
  Transistor transistor_1913 (.in(1'b1), .out(transistor_1913_out), .gate(op0));
  Transistor #(.\type ("n")) transistor_1914 (.in(1'b0), .out(transistor_1913_out), .gate(op0));
  Transistor #(.\type ("n")) transistor_1915 (.in(cin), .out(transistor_1915_out), .gate(op0));
  Transistor #(.gate("br")) transistor_1916 (.in(cin), .out(transistor_1915_out), .gate(transistor_1913_out));
  Transistor #(.\type ("n")) transistor_1917 (.in(1'b0), .out(transistor_1917_out), .gate(rst));
  Transistor #(.gate("br")) transistor_1918 (.in(1'b0), .out(transistor_1917_out), .gate(transistor_1883_out));
  Transistor #(.\type ("n")) transistor_1919 (
    .in(transistor_1873_out), .out(transistor_1917_out), .gate(transistor_1883_out));
  Transistor #(.gate("br")) transistor_1920 (.in(transistor_1873_out), .out(transistor_1917_out), .gate(rst));
  Transistor #(.\type ("n")) transistor_1921 (.in(cin), .out(transistor_1887_out), .gate(transistor_1885_out));
  Transistor #(.gate("br")) transistor_1922 (.in(cin), .out(transistor_1887_out), .gate(op0));
  Transistor #(.gate("br")) transistor_1923 (.in(transistor_833_out), .out(transistor_1891_out), .gate(op0));
  Transistor #(.\type ("n")) transistor_1924 (
    .in(transistor_833_out), .out(transistor_1891_out), .gate(transistor_1889_out));
  Transistor #(.gate("br")) transistor_1925 (.in(transistor_839_out), .out(transistor_1895_out), .gate(op0));
  Transistor #(.\type ("n")) transistor_1926 (
    .in(transistor_839_out), .out(transistor_1895_out), .gate(transistor_1893_out));
  Transistor #(.\type ("n")) transistor_1927 (
    .in(transistor_845_out), .out(transistor_1899_out), .gate(transistor_1897_out));
  Transistor #(.gate("br")) transistor_1928 (.in(transistor_845_out), .out(transistor_1899_out), .gate(op0));
  Transistor #(.\type ("n")) transistor_1929 (
    .in(transistor_851_out), .out(transistor_1903_out), .gate(transistor_1901_out));
  Transistor #(.gate("br")) transistor_1930 (.in(transistor_851_out), .out(transistor_1903_out), .gate(op0));
  Transistor #(.\type ("n")) transistor_1931 (
    .in(transistor_857_out), .out(transistor_1907_out), .gate(transistor_1905_out));
  Transistor #(.gate("br")) transistor_1932 (.in(transistor_857_out), .out(transistor_1907_out), .gate(op0));
  Transistor #(.gate("br")) transistor_1933 (.in(transistor_863_out), .out(transistor_1911_out), .gate(op0));
  Transistor #(.\type ("n")) transistor_1934 (
    .in(transistor_863_out), .out(transistor_1911_out), .gate(transistor_1909_out));
  Transistor #(.\type ("n")) transistor_1935 (
    .in(transistor_869_out), .out(transistor_1915_out), .gate(transistor_1913_out));
  Transistor #(.gate("br")) transistor_1936 (.in(transistor_869_out), .out(transistor_1915_out), .gate(op0));
  Transistor transistor_1937 (.in(1'b1), .out(transistor_1937_out), .gate(op1));
  Transistor #(.gate("br")) transistor_1938 (
    .in(transistor_1871_out), .out(transistor_1938_out), .gate(transistor_1937_out));
  Transistor #(.\type ("n")) transistor_1939 (.in(transistor_1871_out), .out(transistor_1938_out), .gate(op1));
  Transistor transistor_1940 (.in(1'b1), .out(transistor_1940_out), .gate(w));
  Transistor #(.\type ("n")) transistor_1941 (.in(1'b0), .out(transistor_1940_out), .gate(w));
  Transistor #(.\type ("n")) transistor_1942 (.in(transistor_1181_out), .out(transistor_1942_out), .gate(op0));
  Transistor #(.gate("br")) transistor_1943 (
    .in(transistor_1181_out), .out(transistor_1942_out), .gate(transistor_1965_out));
  Transistor #(.gate("br")) transistor_1944 (
    .in(transistor_1182_out), .out(transistor_1944_out), .gate(transistor_1969_out));
  Transistor #(.\type ("n")) transistor_1945 (.in(transistor_1182_out), .out(transistor_1944_out), .gate(op0));
  Transistor #(.\type ("n")) transistor_1946 (.in(transistor_1183_out), .out(transistor_1946_out), .gate(op0));
  Transistor #(.gate("br")) transistor_1947 (
    .in(transistor_1183_out), .out(transistor_1946_out), .gate(transistor_1973_out));
  Transistor #(.\type ("n")) transistor_1948 (.in(transistor_1184_out), .out(transistor_1948_out), .gate(op0));
  Transistor #(.gate("br")) transistor_1949 (
    .in(transistor_1184_out), .out(transistor_1948_out), .gate(transistor_1977_out));
  Transistor #(.\type ("n")) transistor_1950 (.in(transistor_1185_out), .out(transistor_1950_out), .gate(op0));
  Transistor #(.gate("br")) transistor_1951 (
    .in(transistor_1185_out), .out(transistor_1950_out), .gate(transistor_1981_out));
  Transistor #(.\type ("n")) transistor_1952 (.in(transistor_1186_out), .out(transistor_1952_out), .gate(op0));
  Transistor #(.gate("br")) transistor_1953 (
    .in(transistor_1186_out), .out(transistor_1952_out), .gate(transistor_1985_out));
  Transistor #(.gate("br")) transistor_1954 (
    .in(transistor_1187_out), .out(transistor_1954_out), .gate(transistor_1989_out));
  Transistor #(.\type ("n")) transistor_1955 (.in(transistor_1187_out), .out(transistor_1954_out), .gate(op0));
  Transistor #(.gate("br")) transistor_1956 (
    .in(transistor_1188_out), .out(transistor_1956_out), .gate(transistor_1993_out));
  Transistor #(.\type ("n")) transistor_1957 (.in(transistor_1188_out), .out(transistor_1956_out), .gate(op0));
  Transistor #(.\type ("n")) transistor_1958 (.in(1'b0), .out(transistor_1937_out), .gate(op1));
  Transistor #(.\type ("n")) transistor_1959 (
    .in(transistor_1861_out), .out(transistor_1938_out), .gate(transistor_1937_out));
  Transistor #(.gate("br")) transistor_1960 (.in(transistor_1861_out), .out(transistor_1938_out), .gate(op1));
  Transistor #(.\type ("n")) transistor_1961 (.in(transistor_1287_out), .out(transistor_1961_out), .gate(w));
  Transistor #(.gate("br")) transistor_1962 (
    .in(transistor_1287_out), .out(transistor_1961_out), .gate(transistor_1940_out));
  Transistor #(.\type ("n")) transistor_1963 (
    .in(transistor_1998_out), .out(transistor_1961_out), .gate(transistor_1940_out));
  Transistor #(.gate("br")) transistor_1964 (.in(transistor_1998_out), .out(transistor_1961_out), .gate(w));
  LED led_22 (.in(transistor_1998_out));
  Transistor transistor_1965 (.in(1'b1), .out(transistor_1965_out), .gate(op0));
  Transistor #(.\type ("n")) transistor_1966 (.in(1'b0), .out(transistor_1965_out), .gate(op0));
  Transistor #(.gate("br")) transistor_1967 (.in(transistor_1057_out), .out(transistor_1942_out), .gate(op0));
  Transistor #(.\type ("n")) transistor_1968 (
    .in(transistor_1057_out), .out(transistor_1942_out), .gate(transistor_1965_out));
  Transistor transistor_1969 (.in(1'b1), .out(transistor_1969_out), .gate(op0));
  Transistor #(.\type ("n")) transistor_1970 (.in(1'b0), .out(transistor_1969_out), .gate(op0));
  Transistor #(.\type ("n")) transistor_1971 (
    .in(transistor_1059_out), .out(transistor_1944_out), .gate(transistor_1969_out));
  Transistor #(.gate("br")) transistor_1972 (.in(transistor_1059_out), .out(transistor_1944_out), .gate(op0));
  Transistor #(.\type ("n")) transistor_1973 (.in(1'b0), .out(transistor_1973_out), .gate(op0));
  Transistor transistor_1974 (.in(1'b1), .out(transistor_1973_out), .gate(op0));
  Transistor #(.\type ("n")) transistor_1975 (
    .in(transistor_1061_out), .out(transistor_1946_out), .gate(transistor_1973_out));
  Transistor #(.gate("br")) transistor_1976 (.in(transistor_1061_out), .out(transistor_1946_out), .gate(op0));
  Transistor #(.\type ("n")) transistor_1977 (.in(1'b0), .out(transistor_1977_out), .gate(op0));
  Transistor transistor_1978 (.in(1'b1), .out(transistor_1977_out), .gate(op0));
  Transistor #(.gate("br")) transistor_1979 (.in(transistor_1063_out), .out(transistor_1948_out), .gate(op0));
  Transistor #(.\type ("n")) transistor_1980 (
    .in(transistor_1063_out), .out(transistor_1948_out), .gate(transistor_1977_out));
  Transistor #(.\type ("n")) transistor_1981 (.in(1'b0), .out(transistor_1981_out), .gate(op0));
  Transistor transistor_1982 (.in(1'b1), .out(transistor_1981_out), .gate(op0));
  Transistor #(.\type ("n")) transistor_1983 (
    .in(transistor_1065_out), .out(transistor_1950_out), .gate(transistor_1981_out));
  Transistor #(.gate("br")) transistor_1984 (.in(transistor_1065_out), .out(transistor_1950_out), .gate(op0));
  Transistor #(.\type ("n")) transistor_1985 (.in(1'b0), .out(transistor_1985_out), .gate(op0));
  Transistor transistor_1986 (.in(1'b1), .out(transistor_1985_out), .gate(op0));
  Transistor #(.\type ("n")) transistor_1987 (
    .in(transistor_1067_out), .out(transistor_1952_out), .gate(transistor_1985_out));
  Transistor #(.gate("br")) transistor_1988 (.in(transistor_1067_out), .out(transistor_1952_out), .gate(op0));
  Transistor transistor_1989 (.in(1'b1), .out(transistor_1989_out), .gate(op0));
  Transistor #(.\type ("n")) transistor_1990 (.in(1'b0), .out(transistor_1989_out), .gate(op0));
  Transistor #(.gate("br")) transistor_1991 (.in(transistor_1069_out), .out(transistor_1954_out), .gate(op0));
  Transistor #(.\type ("n")) transistor_1992 (
    .in(transistor_1069_out), .out(transistor_1954_out), .gate(transistor_1989_out));
  Transistor #(.\type ("n")) transistor_1993 (.in(1'b0), .out(transistor_1993_out), .gate(op0));
  Transistor transistor_1994 (.in(1'b1), .out(transistor_1993_out), .gate(op0));
  Transistor #(.gate("br")) transistor_1995 (.in(transistor_1071_out), .out(transistor_1956_out), .gate(op0));
  Transistor #(.\type ("n")) transistor_1996 (
    .in(transistor_1071_out), .out(transistor_1956_out), .gate(transistor_1993_out));
  Transistor #(.\type ("n")) transistor_1997 (.in(transistor_1938_out), .out(transistor_1997_out), .gate(op2));
  Transistor #(.\type ("n")) transistor_1998 (.in(1'b0), .out(transistor_1998_out), .gate(rst));
  Transistor #(.gate("br")) transistor_1999 (.in(1'b0), .out(transistor_1998_out), .gate(transistor_2000_out));
  Transistor transistor_2000 (.in(1'b1), .out(transistor_2000_out), .gate(rst));
  Transistor #(.\type ("n")) transistor_2001 (.in(1'b0), .out(transistor_2000_out), .gate(rst));
  Transistor #(.\type ("n")) transistor_2002 (
    .in(transistor_1961_out), .out(transistor_1998_out), .gate(transistor_2000_out));
  Transistor #(.gate("br")) transistor_2003 (.in(transistor_1961_out), .out(transistor_1998_out), .gate(rst));
  Transistor transistor_2004 (.in(1'b1), .out(transistor_2004_out), .gate(op2));
  Transistor #(.\type ("n")) transistor_2005 (.in(1'b0), .out(transistor_2004_out), .gate(op2));
  Transistor #(.gate("br")) transistor_2006 (
    .in(transistor_1938_out), .out(transistor_1997_out), .gate(transistor_2004_out));
  Transistor #(.\type ("n")) transistor_2007 (.in(1'b0), .out(transistor_1997_out), .gate(transistor_2004_out));
  Transistor transistor_2008 (.in(1'b1), .out(transistor_2008_out), .gate(w));
  Transistor #(.\type ("n")) transistor_2009 (.in(1'b0), .out(transistor_2008_out), .gate(w));
  Transistor transistor_2010 (.in(1'b1), .out(transistor_2010_out), .gate(op0));
  Transistor #(.\type ("n")) transistor_2011 (.in(1'b0), .out(transistor_2010_out), .gate(op0));
  Transistor #(.gate("br")) transistor_2012 (
    .in(transistor_1009_out), .out(transistor_2012_out), .gate(transistor_2010_out));
  Transistor #(.\type ("n")) transistor_2013 (.in(transistor_1009_out), .out(transistor_2012_out), .gate(op0));
  Transistor #(.\type ("n")) transistor_2014 (.in(1'b0), .out(transistor_2014_out), .gate(op0));
  Transistor transistor_2015 (.in(1'b1), .out(transistor_2014_out), .gate(op0));
  Transistor #(.\type ("n")) transistor_2016 (.in(transistor_1011_out), .out(transistor_2016_out), .gate(op0));
  Transistor #(.gate("br")) transistor_2017 (
    .in(transistor_1011_out), .out(transistor_2016_out), .gate(transistor_2014_out));
  Transistor transistor_2018 (.in(1'b1), .out(transistor_2018_out), .gate(op0));
  Transistor #(.\type ("n")) transistor_2019 (.in(1'b0), .out(transistor_2018_out), .gate(op0));
  Transistor #(.\type ("n")) transistor_2020 (.in(transistor_1013_out), .out(transistor_2020_out), .gate(op0));
  Transistor #(.gate("br")) transistor_2021 (
    .in(transistor_1013_out), .out(transistor_2020_out), .gate(transistor_2018_out));
  Transistor #(.\type ("n")) transistor_2022 (.in(1'b0), .out(transistor_2022_out), .gate(op0));
  Transistor transistor_2023 (.in(1'b1), .out(transistor_2022_out), .gate(op0));
  Transistor #(.gate("br")) transistor_2024 (
    .in(transistor_1015_out), .out(transistor_2024_out), .gate(transistor_2022_out));
  Transistor #(.\type ("n")) transistor_2025 (.in(transistor_1015_out), .out(transistor_2024_out), .gate(op0));
  Transistor transistor_2026 (.in(1'b1), .out(transistor_2026_out), .gate(op0));
  Transistor #(.\type ("n")) transistor_2027 (.in(1'b0), .out(transistor_2026_out), .gate(op0));
  Transistor #(.\type ("n")) transistor_2028 (.in(transistor_1017_out), .out(transistor_2028_out), .gate(op0));
  Transistor #(.gate("br")) transistor_2029 (
    .in(transistor_1017_out), .out(transistor_2028_out), .gate(transistor_2026_out));
  Transistor #(.\type ("n")) transistor_2030 (.in(1'b0), .out(transistor_2030_out), .gate(op0));
  Transistor transistor_2031 (.in(1'b1), .out(transistor_2030_out), .gate(op0));
  Transistor #(.\type ("n")) transistor_2032 (.in(transistor_1019_out), .out(transistor_2032_out), .gate(op0));
  Transistor #(.gate("br")) transistor_2033 (
    .in(transistor_1019_out), .out(transistor_2032_out), .gate(transistor_2030_out));
  Transistor transistor_2034 (.in(1'b1), .out(transistor_2034_out), .gate(op0));
  Transistor #(.\type ("n")) transistor_2035 (.in(1'b0), .out(transistor_2034_out), .gate(op0));
  Transistor #(.\type ("n")) transistor_2036 (.in(transistor_1021_out), .out(transistor_2036_out), .gate(op0));
  Transistor #(.gate("br")) transistor_2037 (
    .in(transistor_1021_out), .out(transistor_2036_out), .gate(transistor_2034_out));
  Transistor transistor_2038 (.in(1'b1), .out(transistor_2038_out), .gate(op0));
  Transistor #(.\type ("n")) transistor_2039 (.in(1'b0), .out(transistor_2038_out), .gate(op0));
  Transistor #(.\type ("n")) transistor_2040 (.in(transistor_1023_out), .out(transistor_2040_out), .gate(op0));
  Transistor #(.gate("br")) transistor_2041 (
    .in(transistor_1023_out), .out(transistor_2040_out), .gate(transistor_2038_out));
  Transistor #(.gate("br")) transistor_2042 (.in(1'b0), .out(transistor_1997_out), .gate(op2));
  Transistor #(.\type ("n")) transistor_2043 (.in(transistor_1355_out), .out(transistor_2043_out), .gate(w));
  Transistor #(.gate("br")) transistor_2044 (
    .in(transistor_1355_out), .out(transistor_2043_out), .gate(transistor_2008_out));
  Transistor #(.\type ("n")) transistor_2045 (
    .in(transistor_2087_out), .out(transistor_2043_out), .gate(transistor_2008_out));
  Transistor #(.gate("br")) transistor_2046 (.in(transistor_2087_out), .out(transistor_2043_out), .gate(w));
  Transistor #(.\type ("n")) transistor_2047 (
    .in(transistor_833_out), .out(transistor_2012_out), .gate(transistor_2010_out));
  Transistor #(.gate("br")) transistor_2048 (.in(transistor_833_out), .out(transistor_2012_out), .gate(op0));
  Transistor #(.gate("br")) transistor_2049 (.in(transistor_839_out), .out(transistor_2016_out), .gate(op0));
  Transistor #(.\type ("n")) transistor_2050 (
    .in(transistor_839_out), .out(transistor_2016_out), .gate(transistor_2014_out));
  Transistor #(.gate("br")) transistor_2051 (.in(transistor_845_out), .out(transistor_2020_out), .gate(op0));
  Transistor #(.\type ("n")) transistor_2052 (
    .in(transistor_845_out), .out(transistor_2020_out), .gate(transistor_2018_out));
  Transistor #(.\type ("n")) transistor_2053 (
    .in(transistor_851_out), .out(transistor_2024_out), .gate(transistor_2022_out));
  Transistor #(.gate("br")) transistor_2054 (.in(transistor_851_out), .out(transistor_2024_out), .gate(op0));
  Transistor #(.gate("br")) transistor_2055 (.in(transistor_857_out), .out(transistor_2028_out), .gate(op0));
  Transistor #(.\type ("n")) transistor_2056 (
    .in(transistor_857_out), .out(transistor_2028_out), .gate(transistor_2026_out));
  Transistor #(.gate("br")) transistor_2057 (.in(transistor_863_out), .out(transistor_2032_out), .gate(op0));
  Transistor #(.\type ("n")) transistor_2058 (
    .in(transistor_863_out), .out(transistor_2032_out), .gate(transistor_2030_out));
  Transistor #(.\type ("n")) transistor_2059 (
    .in(transistor_869_out), .out(transistor_2036_out), .gate(transistor_2034_out));
  Transistor #(.gate("br")) transistor_2060 (.in(transistor_869_out), .out(transistor_2036_out), .gate(op0));
  Transistor #(.\type ("n")) transistor_2061 (
    .in(transistor_875_out), .out(transistor_2040_out), .gate(transistor_2038_out));
  Transistor #(.gate("br")) transistor_2062 (.in(transistor_875_out), .out(transistor_2040_out), .gate(op0));
  Transistor transistor_2063 (.in(1'b1), .out(transistor_2063_out), .gate(fr_w));
  Transistor #(.\type ("n")) transistor_2064 (.in(1'b0), .out(transistor_2063_out), .gate(fr_w));
  Transistor transistor_2065 (.in(1'b1), .out(transistor_2065_out), .gate(rst));
  Transistor #(.\type ("n")) transistor_2066 (.in(1'b0), .out(transistor_2065_out), .gate(rst));
  LED led_23 (.in(transistor_2087_out));
  Transistor #(.\type ("n")) transistor_2067 (.in(transistor_1887_out), .out(transistor_2067_out), .gate(op1));
  Transistor #(.gate("br")) transistor_2068 (
    .in(transistor_1887_out), .out(transistor_2067_out), .gate(transistor_2091_out));
  Transistor #(.gate("br")) transistor_2069 (
    .in(transistor_1891_out), .out(transistor_2069_out), .gate(transistor_2095_out));
  Transistor #(.\type ("n")) transistor_2070 (.in(transistor_1891_out), .out(transistor_2069_out), .gate(op1));
  Transistor #(.gate("br")) transistor_2071 (
    .in(transistor_1895_out), .out(transistor_2071_out), .gate(transistor_2099_out));
  Transistor #(.\type ("n")) transistor_2072 (.in(transistor_1895_out), .out(transistor_2071_out), .gate(op1));
  Transistor #(.gate("br")) transistor_2073 (
    .in(transistor_1899_out), .out(transistor_2073_out), .gate(transistor_2103_out));
  Transistor #(.\type ("n")) transistor_2074 (.in(transistor_1899_out), .out(transistor_2073_out), .gate(op1));
  Transistor #(.gate("br")) transistor_2075 (
    .in(transistor_1903_out), .out(transistor_2075_out), .gate(transistor_2107_out));
  Transistor #(.\type ("n")) transistor_2076 (.in(transistor_1903_out), .out(transistor_2075_out), .gate(op1));
  Transistor #(.gate("br")) transistor_2077 (
    .in(transistor_1907_out), .out(transistor_2077_out), .gate(transistor_2111_out));
  Transistor #(.\type ("n")) transistor_2078 (.in(transistor_1907_out), .out(transistor_2077_out), .gate(op1));
  Transistor #(.gate("br")) transistor_2079 (
    .in(transistor_1911_out), .out(transistor_2079_out), .gate(transistor_2115_out));
  Transistor #(.\type ("n")) transistor_2080 (.in(transistor_1911_out), .out(transistor_2079_out), .gate(op1));
  Transistor #(.\type ("n")) transistor_2081 (.in(transistor_1915_out), .out(transistor_2081_out), .gate(op1));
  Transistor #(.gate("br")) transistor_2082 (
    .in(transistor_1915_out), .out(transistor_2081_out), .gate(transistor_2119_out));
  Transistor #(.\type ("n")) transistor_2083 (.in(transistor_1694_out), .out(transistor_2083_out), .gate(fr_w));
  Transistor #(.gate("br")) transistor_2084 (
    .in(transistor_1694_out), .out(transistor_2083_out), .gate(transistor_2063_out));
  Transistor #(.\type ("n")) transistor_2085 (.in(v), .out(transistor_2083_out), .gate(transistor_2063_out));
  Transistor #(.gate("br")) transistor_2086 (.in(v), .out(transistor_2083_out), .gate(fr_w));
  Transistor #(.\type ("n")) transistor_2087 (.in(1'b0), .out(transistor_2087_out), .gate(rst));
  Transistor #(.gate("br")) transistor_2088 (.in(1'b0), .out(transistor_2087_out), .gate(transistor_2065_out));
  Transistor #(.\type ("n")) transistor_2089 (
    .in(transistor_2043_out), .out(transistor_2087_out), .gate(transistor_2065_out));
  Transistor #(.gate("br")) transistor_2090 (.in(transistor_2043_out), .out(transistor_2087_out), .gate(rst));
  Transistor #(.\type ("n")) transistor_2091 (.in(1'b0), .out(transistor_2091_out), .gate(op1));
  Transistor transistor_2092 (.in(1'b1), .out(transistor_2091_out), .gate(op1));
  Transistor #(.\type ("n")) transistor_2093 (
    .in(transistor_1794_out), .out(transistor_2067_out), .gate(transistor_2091_out));
  Transistor #(.gate("br")) transistor_2094 (.in(transistor_1794_out), .out(transistor_2067_out), .gate(op1));
  Transistor transistor_2095 (.in(1'b1), .out(transistor_2095_out), .gate(op1));
  Transistor #(.\type ("n")) transistor_2096 (.in(1'b0), .out(transistor_2095_out), .gate(op1));
  Transistor #(.gate("br")) transistor_2097 (.in(transistor_1799_out), .out(transistor_2069_out), .gate(op1));
  Transistor #(.\type ("n")) transistor_2098 (
    .in(transistor_1799_out), .out(transistor_2069_out), .gate(transistor_2095_out));
  Transistor transistor_2099 (.in(1'b1), .out(transistor_2099_out), .gate(op1));
  Transistor #(.\type ("n")) transistor_2100 (.in(1'b0), .out(transistor_2099_out), .gate(op1));
  Transistor #(.gate("br")) transistor_2101 (.in(transistor_1802_out), .out(transistor_2071_out), .gate(op1));
  Transistor #(.\type ("n")) transistor_2102 (
    .in(transistor_1802_out), .out(transistor_2071_out), .gate(transistor_2099_out));
  Transistor #(.\type ("n")) transistor_2103 (.in(1'b0), .out(transistor_2103_out), .gate(op1));
  Transistor transistor_2104 (.in(1'b1), .out(transistor_2103_out), .gate(op1));
  Transistor #(.gate("br")) transistor_2105 (.in(transistor_1807_out), .out(transistor_2073_out), .gate(op1));
  Transistor #(.\type ("n")) transistor_2106 (
    .in(transistor_1807_out), .out(transistor_2073_out), .gate(transistor_2103_out));
  Transistor transistor_2107 (.in(1'b1), .out(transistor_2107_out), .gate(op1));
  Transistor #(.\type ("n")) transistor_2108 (.in(1'b0), .out(transistor_2107_out), .gate(op1));
  Transistor #(.\type ("n")) transistor_2109 (
    .in(transistor_1811_out), .out(transistor_2075_out), .gate(transistor_2107_out));
  Transistor #(.gate("br")) transistor_2110 (.in(transistor_1811_out), .out(transistor_2075_out), .gate(op1));
  Transistor transistor_2111 (.in(1'b1), .out(transistor_2111_out), .gate(op1));
  Transistor #(.\type ("n")) transistor_2112 (.in(1'b0), .out(transistor_2111_out), .gate(op1));
  Transistor #(.gate("br")) transistor_2113 (.in(transistor_1815_out), .out(transistor_2077_out), .gate(op1));
  Transistor #(.\type ("n")) transistor_2114 (
    .in(transistor_1815_out), .out(transistor_2077_out), .gate(transistor_2111_out));
  Transistor transistor_2115 (.in(1'b1), .out(transistor_2115_out), .gate(op1));
  Transistor #(.\type ("n")) transistor_2116 (.in(1'b0), .out(transistor_2115_out), .gate(op1));
  Transistor #(.\type ("n")) transistor_2117 (
    .in(transistor_1819_out), .out(transistor_2079_out), .gate(transistor_2115_out));
  Transistor #(.gate("br")) transistor_2118 (.in(transistor_1819_out), .out(transistor_2079_out), .gate(op1));
  Transistor transistor_2119 (.in(1'b1), .out(transistor_2119_out), .gate(op1));
  Transistor #(.\type ("n")) transistor_2120 (.in(1'b0), .out(transistor_2119_out), .gate(op1));
  Transistor #(.gate("br")) transistor_2121 (.in(transistor_1823_out), .out(transistor_2081_out), .gate(op1));
  Transistor #(.\type ("n")) transistor_2122 (
    .in(transistor_1823_out), .out(transistor_2081_out), .gate(transistor_2119_out));
  Transistor transistor_2123 (.in(1'b1), .out(transistor_2123_out), .gate(rst));
  Transistor #(.\type ("n")) transistor_2124 (.in(1'b0), .out(transistor_2123_out), .gate(rst));
  Transistor #(.\type ("n")) transistor_2125 (.in(transistor_1367_out), .out(transistor_2125_out), .gate(w));
  Transistor #(.gate("br")) transistor_2126 (
    .in(transistor_1367_out), .out(transistor_2125_out), .gate(transistor_2127_out));
  Transistor transistor_2127 (.in(1'b1), .out(transistor_2127_out), .gate(w));
  Transistor #(.\type ("n")) transistor_2128 (.in(1'b0), .out(transistor_2127_out), .gate(w));
  Transistor #(.\type ("n")) transistor_2129 (
    .in(transistor_2171_out), .out(transistor_2125_out), .gate(transistor_2127_out));
  Transistor #(.gate("br")) transistor_2130 (.in(transistor_2171_out), .out(transistor_2125_out), .gate(w));
  Transistor #(.\type ("n")) transistor_2131 (.in(1'b0), .out(v), .gate(rst));
  Transistor #(.gate("br")) transistor_2132 (.in(1'b0), .out(v), .gate(transistor_2123_out));
  Pull_Resistor pull_resistor_9 (.node(v));
  Transistor #(.\type ("n")) transistor_2133 (.in(transistor_2083_out), .out(v), .gate(transistor_2123_out));
  Transistor #(.gate("br")) transistor_2134 (.in(transistor_2083_out), .out(v), .gate(rst));
  Transistor transistor_2135 (.in(1'b1), .out(transistor_2135_out), .gate(rst));
  Transistor #(.\type ("n")) transistor_2136 (.in(1'b0), .out(transistor_2135_out), .gate(rst));
  LED led_24 (.in(transistor_2171_out));
  Transistor transistor_2137 (.in(1'b1), .out(transistor_2137_out), .gate(op1));
  Transistor #(.\type ("n")) transistor_2138 (.in(1'b0), .out(transistor_2137_out), .gate(op1));
  Transistor #(.\type ("n")) transistor_2139 (.in(transistor_1942_out), .out(transistor_2139_out), .gate(op1));
  Transistor #(.gate("br")) transistor_2140 (
    .in(transistor_1942_out), .out(transistor_2139_out), .gate(transistor_2137_out));
  Transistor #(.\type ("n")) transistor_2141 (.in(1'b0), .out(transistor_2141_out), .gate(op1));
  Transistor transistor_2142 (.in(1'b1), .out(transistor_2141_out), .gate(op1));
  Transistor #(.\type ("n")) transistor_2143 (.in(transistor_1944_out), .out(transistor_2143_out), .gate(op1));
  Transistor #(.gate("br")) transistor_2144 (
    .in(transistor_1944_out), .out(transistor_2143_out), .gate(transistor_2141_out));
  Transistor transistor_2145 (.in(1'b1), .out(transistor_2145_out), .gate(op1));
  Transistor #(.\type ("n")) transistor_2146 (.in(1'b0), .out(transistor_2145_out), .gate(op1));
  Transistor #(.gate("br")) transistor_2147 (
    .in(transistor_1946_out), .out(transistor_2147_out), .gate(transistor_2145_out));
  Transistor #(.\type ("n")) transistor_2148 (.in(transistor_1946_out), .out(transistor_2147_out), .gate(op1));
  Transistor transistor_2149 (.in(1'b1), .out(transistor_2149_out), .gate(op1));
  Transistor #(.\type ("n")) transistor_2150 (.in(1'b0), .out(transistor_2149_out), .gate(op1));
  Transistor #(.gate("br")) transistor_2151 (
    .in(transistor_1948_out), .out(transistor_2151_out), .gate(transistor_2149_out));
  Transistor #(.\type ("n")) transistor_2152 (.in(transistor_1948_out), .out(transistor_2151_out), .gate(op1));
  Transistor #(.\type ("n")) transistor_2153 (.in(1'b0), .out(transistor_2153_out), .gate(op1));
  Transistor transistor_2154 (.in(1'b1), .out(transistor_2153_out), .gate(op1));
  Transistor #(.\type ("n")) transistor_2155 (.in(transistor_1950_out), .out(transistor_2155_out), .gate(op1));
  Transistor #(.gate("br")) transistor_2156 (
    .in(transistor_1950_out), .out(transistor_2155_out), .gate(transistor_2153_out));
  Transistor transistor_2157 (.in(1'b1), .out(transistor_2157_out), .gate(op1));
  Transistor #(.\type ("n")) transistor_2158 (.in(1'b0), .out(transistor_2157_out), .gate(op1));
  Transistor #(.gate("br")) transistor_2159 (
    .in(transistor_1952_out), .out(transistor_2159_out), .gate(transistor_2157_out));
  Transistor #(.\type ("n")) transistor_2160 (.in(transistor_1952_out), .out(transistor_2159_out), .gate(op1));
  Transistor transistor_2161 (.in(1'b1), .out(transistor_2161_out), .gate(op1));
  Transistor #(.\type ("n")) transistor_2162 (.in(1'b0), .out(transistor_2161_out), .gate(op1));
  Transistor #(.\type ("n")) transistor_2163 (.in(transistor_1954_out), .out(transistor_2163_out), .gate(op1));
  Transistor #(.gate("br")) transistor_2164 (
    .in(transistor_1954_out), .out(transistor_2163_out), .gate(transistor_2161_out));
  Transistor transistor_2165 (.in(1'b1), .out(transistor_2165_out), .gate(op1));
  Transistor #(.\type ("n")) transistor_2166 (.in(1'b0), .out(transistor_2165_out), .gate(op1));
  Transistor #(.gate("br")) transistor_2167 (
    .in(transistor_1956_out), .out(transistor_2167_out), .gate(transistor_2165_out));
  Transistor #(.\type ("n")) transistor_2168 (.in(transistor_1956_out), .out(transistor_2167_out), .gate(op1));
  Transistor transistor_2169 (.in(1'b1), .out(transistor_2169_out), .gate(fr_w));
  Transistor #(.\type ("n")) transistor_2170 (.in(1'b0), .out(transistor_2169_out), .gate(fr_w));
  Transistor #(.\type ("n")) transistor_2171 (.in(1'b0), .out(transistor_2171_out), .gate(rst));
  Transistor #(.gate("br")) transistor_2172 (.in(1'b0), .out(transistor_2171_out), .gate(transistor_2135_out));
  Transistor #(.\type ("n")) transistor_2173 (
    .in(transistor_2125_out), .out(transistor_2171_out), .gate(transistor_2135_out));
  Transistor #(.gate("br")) transistor_2174 (.in(transistor_2125_out), .out(transistor_2171_out), .gate(rst));
  Transistor #(.\type ("n")) transistor_2175 (
    .in(transistor_2012_out), .out(transistor_2139_out), .gate(transistor_2137_out));
  Transistor #(.gate("br")) transistor_2176 (.in(transistor_2012_out), .out(transistor_2139_out), .gate(op1));
  Transistor #(.\type ("n")) transistor_2177 (
    .in(transistor_2016_out), .out(transistor_2143_out), .gate(transistor_2141_out));
  Transistor #(.gate("br")) transistor_2178 (.in(transistor_2016_out), .out(transistor_2143_out), .gate(op1));
  Transistor #(.gate("br")) transistor_2179 (.in(transistor_2020_out), .out(transistor_2147_out), .gate(op1));
  Transistor #(.\type ("n")) transistor_2180 (
    .in(transistor_2020_out), .out(transistor_2147_out), .gate(transistor_2145_out));
  Transistor #(.gate("br")) transistor_2181 (.in(transistor_2024_out), .out(transistor_2151_out), .gate(op1));
  Transistor #(.\type ("n")) transistor_2182 (
    .in(transistor_2024_out), .out(transistor_2151_out), .gate(transistor_2149_out));
  Transistor #(.\type ("n")) transistor_2183 (
    .in(transistor_2028_out), .out(transistor_2155_out), .gate(transistor_2153_out));
  Transistor #(.gate("br")) transistor_2184 (.in(transistor_2028_out), .out(transistor_2155_out), .gate(op1));
  Transistor #(.gate("br")) transistor_2185 (.in(transistor_2032_out), .out(transistor_2159_out), .gate(op1));
  Transistor #(.\type ("n")) transistor_2186 (
    .in(transistor_2032_out), .out(transistor_2159_out), .gate(transistor_2157_out));
  Transistor #(.\type ("n")) transistor_2187 (
    .in(transistor_2036_out), .out(transistor_2163_out), .gate(transistor_2161_out));
  Transistor #(.gate("br")) transistor_2188 (.in(transistor_2036_out), .out(transistor_2163_out), .gate(op1));
  Transistor #(.\type ("n")) transistor_2189 (
    .in(transistor_2040_out), .out(transistor_2167_out), .gate(transistor_2165_out));
  Transistor #(.gate("br")) transistor_2190 (.in(transistor_2040_out), .out(transistor_2167_out), .gate(op1));
  Transistor #(.\type ("n")) transistor_2191 (.in(transistor_1997_out), .out(transistor_2191_out), .gate(fr_w));
  Transistor #(.gate("br")) transistor_2192 (
    .in(transistor_1997_out), .out(transistor_2191_out), .gate(transistor_2169_out));
  Transistor #(.\type ("n")) transistor_2193 (.in(c), .out(transistor_2191_out), .gate(transistor_2169_out));
  Transistor #(.gate("br")) transistor_2194 (.in(c), .out(transistor_2191_out), .gate(fr_w));
  Transistor #(.gate("br")) transistor_2195 (
    .in(transistor_2067_out), .out(transistor_2195_out), .gate(transistor_2213_out));
  Transistor #(.\type ("n")) transistor_2196 (.in(transistor_2067_out), .out(transistor_2195_out), .gate(op2));
  Transistor #(.gate("br")) transistor_2197 (
    .in(transistor_2069_out), .out(transistor_2197_out), .gate(transistor_2217_out));
  Transistor #(.\type ("n")) transistor_2198 (.in(transistor_2069_out), .out(transistor_2197_out), .gate(op2));
  Transistor #(.gate("br")) transistor_2199 (
    .in(transistor_2071_out), .out(transistor_2199_out), .gate(transistor_2221_out));
  Transistor #(.\type ("n")) transistor_2200 (.in(transistor_2071_out), .out(transistor_2199_out), .gate(op2));
  Transistor #(.gate("br")) transistor_2201 (
    .in(transistor_2073_out), .out(transistor_2201_out), .gate(transistor_2225_out));
  Transistor #(.\type ("n")) transistor_2202 (.in(transistor_2073_out), .out(transistor_2201_out), .gate(op2));
  Transistor #(.\type ("n")) transistor_2203 (.in(transistor_2075_out), .out(transistor_2203_out), .gate(op2));
  Transistor #(.gate("br")) transistor_2204 (
    .in(transistor_2075_out), .out(transistor_2203_out), .gate(transistor_2229_out));
  Transistor #(.\type ("n")) transistor_2205 (.in(transistor_2077_out), .out(transistor_2205_out), .gate(op2));
  Transistor #(.gate("br")) transistor_2206 (
    .in(transistor_2077_out), .out(transistor_2205_out), .gate(transistor_2233_out));
  Transistor #(.\type ("n")) transistor_2207 (.in(transistor_2079_out), .out(transistor_2207_out), .gate(op2));
  Transistor #(.gate("br")) transistor_2208 (
    .in(transistor_2079_out), .out(transistor_2207_out), .gate(transistor_2237_out));
  Transistor #(.gate("br")) transistor_2209 (
    .in(transistor_2081_out), .out(transistor_2209_out), .gate(transistor_2241_out));
  Transistor #(.\type ("n")) transistor_2210 (.in(transistor_2081_out), .out(transistor_2209_out), .gate(op2));
  Transistor transistor_2211 (.in(1'b1), .out(transistor_2211_out), .gate(rst));
  Transistor #(.\type ("n")) transistor_2212 (.in(1'b0), .out(transistor_2211_out), .gate(rst));
  Transistor #(.\type ("n")) transistor_2213 (.in(1'b0), .out(transistor_2213_out), .gate(op2));
  Transistor transistor_2214 (.in(1'b1), .out(transistor_2213_out), .gate(op2));
  Transistor #(.gate("br")) transistor_2215 (.in(transistor_2139_out), .out(transistor_2195_out), .gate(op2));
  Transistor #(.\type ("n")) transistor_2216 (
    .in(transistor_2139_out), .out(transistor_2195_out), .gate(transistor_2213_out));
  Transistor transistor_2217 (.in(1'b1), .out(transistor_2217_out), .gate(op2));
  Transistor #(.\type ("n")) transistor_2218 (.in(1'b0), .out(transistor_2217_out), .gate(op2));
  Transistor #(.\type ("n")) transistor_2219 (
    .in(transistor_2143_out), .out(transistor_2197_out), .gate(transistor_2217_out));
  Transistor #(.gate("br")) transistor_2220 (.in(transistor_2143_out), .out(transistor_2197_out), .gate(op2));
  Transistor transistor_2221 (.in(1'b1), .out(transistor_2221_out), .gate(op2));
  Transistor #(.\type ("n")) transistor_2222 (.in(1'b0), .out(transistor_2221_out), .gate(op2));
  Transistor #(.gate("br")) transistor_2223 (.in(transistor_2147_out), .out(transistor_2199_out), .gate(op2));
  Transistor #(.\type ("n")) transistor_2224 (
    .in(transistor_2147_out), .out(transistor_2199_out), .gate(transistor_2221_out));
  Transistor transistor_2225 (.in(1'b1), .out(transistor_2225_out), .gate(op2));
  Transistor #(.\type ("n")) transistor_2226 (.in(1'b0), .out(transistor_2225_out), .gate(op2));
  Transistor #(.gate("br")) transistor_2227 (.in(transistor_2151_out), .out(transistor_2201_out), .gate(op2));
  Transistor #(.\type ("n")) transistor_2228 (
    .in(transistor_2151_out), .out(transistor_2201_out), .gate(transistor_2225_out));
  Transistor transistor_2229 (.in(1'b1), .out(transistor_2229_out), .gate(op2));
  Transistor #(.\type ("n")) transistor_2230 (.in(1'b0), .out(transistor_2229_out), .gate(op2));
  Transistor #(.\type ("n")) transistor_2231 (
    .in(transistor_2155_out), .out(transistor_2203_out), .gate(transistor_2229_out));
  Transistor #(.gate("br")) transistor_2232 (.in(transistor_2155_out), .out(transistor_2203_out), .gate(op2));
  Transistor transistor_2233 (.in(1'b1), .out(transistor_2233_out), .gate(op2));
  Transistor #(.\type ("n")) transistor_2234 (.in(1'b0), .out(transistor_2233_out), .gate(op2));
  Transistor #(.gate("br")) transistor_2235 (.in(transistor_2159_out), .out(transistor_2205_out), .gate(op2));
  Transistor #(.\type ("n")) transistor_2236 (
    .in(transistor_2159_out), .out(transistor_2205_out), .gate(transistor_2233_out));
  Transistor transistor_2237 (.in(1'b1), .out(transistor_2237_out), .gate(op2));
  Transistor #(.\type ("n")) transistor_2238 (.in(1'b0), .out(transistor_2237_out), .gate(op2));
  Transistor #(.\type ("n")) transistor_2239 (
    .in(transistor_2163_out), .out(transistor_2207_out), .gate(transistor_2237_out));
  Transistor #(.gate("br")) transistor_2240 (.in(transistor_2163_out), .out(transistor_2207_out), .gate(op2));
  Transistor #(.\type ("n")) transistor_2241 (.in(1'b0), .out(transistor_2241_out), .gate(op2));
  Transistor transistor_2242 (.in(1'b1), .out(transistor_2241_out), .gate(op2));
  Transistor #(.\type ("n")) transistor_2243 (
    .in(transistor_2167_out), .out(transistor_2209_out), .gate(transistor_2241_out));
  Transistor #(.gate("br")) transistor_2244 (.in(transistor_2167_out), .out(transistor_2209_out), .gate(op2));
  Transistor #(.\type ("n")) transistor_2245 (.in(1'b0), .out(c), .gate(rst));
  Transistor #(.gate("br")) transistor_2246 (.in(1'b0), .out(c), .gate(transistor_2211_out));
  Pull_Resistor pull_resistor_10 (.node(c));
  Transistor #(.\type ("n")) transistor_2247 (.in(transistor_2191_out), .out(c), .gate(transistor_2211_out));
  Transistor #(.gate("br")) transistor_2248 (.in(transistor_2191_out), .out(c), .gate(rst));
  Pull_Resistor pull_resistor_11 (.node(transistor_2195_out));
  Pull_Resistor pull_resistor_12 (.node(transistor_2197_out));
  Pull_Resistor pull_resistor_13 (.node(transistor_2199_out));
  Pull_Resistor pull_resistor_14 (.node(transistor_2201_out));
  Pull_Resistor pull_resistor_15 (.node(transistor_2203_out));
  Pull_Resistor pull_resistor_16 (.node(transistor_2205_out));
  Pull_Resistor pull_resistor_17 (.node(transistor_2207_out));
  Pull_Resistor pull_resistor_18 (.node(transistor_2209_out));
  Transistor transistor_2249 (.in(1'b1), .out(transistor_2249_out), .gate(fr_w));
  Transistor #(.\type ("n")) transistor_2250 (.in(1'b0), .out(transistor_2249_out), .gate(fr_w));
  Transistor transistor_2251 (.in(1'b1), .out(transistor_2251_out), .gate(1'b1));
  Transistor #(.\type ("n")) transistor_2252 (.in(1'b0), .out(transistor_2251_out), .gate(1'b1));
  Transistor transistor_2253 (.in(1'b1), .out(transistor_2253_out), .gate(1'b1));
  Transistor #(.\type ("n")) transistor_2254 (.in(1'b0), .out(transistor_2253_out), .gate(1'b1));
  Transistor transistor_2255 (.in(1'b1), .out(transistor_2255_out), .gate(1'b1));
  Transistor #(.\type ("n")) transistor_2256 (.in(1'b0), .out(transistor_2255_out), .gate(1'b1));
  Transistor transistor_2257 (.in(1'b1), .out(transistor_2257_out), .gate(1'b1));
  Transistor #(.\type ("n")) transistor_2258 (.in(1'b0), .out(transistor_2257_out), .gate(1'b1));
  Transistor transistor_2259 (.in(1'b1), .out(transistor_2259_out), .gate(1'b1));
  Transistor #(.\type ("n")) transistor_2260 (.in(1'b0), .out(transistor_2259_out), .gate(1'b1));
  Transistor transistor_2261 (.in(1'b1), .out(transistor_2261_out), .gate(1'b1));
  Transistor #(.\type ("n")) transistor_2262 (.in(1'b0), .out(transistor_2261_out), .gate(1'b1));
  Transistor transistor_2263 (.in(1'b1), .out(transistor_2263_out), .gate(1'b1));
  Transistor #(.\type ("n")) transistor_2264 (.in(1'b0), .out(transistor_2263_out), .gate(1'b1));
  Transistor transistor_2265 (.in(1'b1), .out(transistor_2265_out), .gate(1'b1));
  Transistor #(.\type ("n")) transistor_2266 (.in(1'b0), .out(transistor_2265_out), .gate(1'b1));
  Transistor #(.\type ("n")) transistor_2267 (.in(transistor_2351_out), .out(transistor_2267_out), .gate(fr_w));
  Transistor #(.gate("br")) transistor_2268 (
    .in(transistor_2351_out), .out(transistor_2267_out), .gate(transistor_2249_out));
  Transistor #(.\type ("n")) transistor_2269 (.in(s), .out(transistor_2267_out), .gate(transistor_2249_out));
  Transistor #(.gate("br")) transistor_2270 (.in(s), .out(transistor_2267_out), .gate(fr_w));
  Transistor #(.\type ("n")) transistor_2271 (.in(transistor_2195_out), .out(transistor_2271_out), .gate(1'b1));
  Transistor #(.gate("br")) transistor_2272 (
    .in(transistor_2195_out), .out(transistor_2271_out), .gate(transistor_2251_out));
  Transistor #(.\type ("n")) transistor_2273 (
    .in(transistor_2309_out), .out(transistor_2271_out), .gate(transistor_2251_out));
  Transistor #(.gate("br")) transistor_2274 (.in(transistor_2309_out), .out(transistor_2271_out), .gate(1'b1));
  Transistor #(.\type ("n")) transistor_2275 (.in(transistor_2197_out), .out(transistor_2275_out), .gate(1'b1));
  Transistor #(.gate("br")) transistor_2276 (
    .in(transistor_2197_out), .out(transistor_2275_out), .gate(transistor_2253_out));
  Transistor #(.\type ("n")) transistor_2277 (
    .in(transistor_2315_out), .out(transistor_2275_out), .gate(transistor_2253_out));
  Transistor #(.gate("br")) transistor_2278 (.in(transistor_2315_out), .out(transistor_2275_out), .gate(1'b1));
  Transistor #(.\type ("n")) transistor_2279 (.in(transistor_2199_out), .out(transistor_2279_out), .gate(1'b1));
  Transistor #(.gate("br")) transistor_2280 (
    .in(transistor_2199_out), .out(transistor_2279_out), .gate(transistor_2255_out));
  Transistor #(.\type ("n")) transistor_2281 (
    .in(transistor_2321_out), .out(transistor_2279_out), .gate(transistor_2255_out));
  Transistor #(.gate("br")) transistor_2282 (.in(transistor_2321_out), .out(transistor_2279_out), .gate(1'b1));
  Transistor #(.\type ("n")) transistor_2283 (.in(transistor_2201_out), .out(transistor_2283_out), .gate(1'b1));
  Transistor #(.gate("br")) transistor_2284 (
    .in(transistor_2201_out), .out(transistor_2283_out), .gate(transistor_2257_out));
  Transistor #(.\type ("n")) transistor_2285 (
    .in(transistor_2327_out), .out(transistor_2283_out), .gate(transistor_2257_out));
  Transistor #(.gate("br")) transistor_2286 (.in(transistor_2327_out), .out(transistor_2283_out), .gate(1'b1));
  Transistor #(.\type ("n")) transistor_2287 (.in(transistor_2203_out), .out(transistor_2287_out), .gate(1'b1));
  Transistor #(.gate("br")) transistor_2288 (
    .in(transistor_2203_out), .out(transistor_2287_out), .gate(transistor_2259_out));
  Transistor #(.\type ("n")) transistor_2289 (
    .in(transistor_2333_out), .out(transistor_2287_out), .gate(transistor_2259_out));
  Transistor #(.gate("br")) transistor_2290 (.in(transistor_2333_out), .out(transistor_2287_out), .gate(1'b1));
  Transistor #(.\type ("n")) transistor_2291 (.in(transistor_2205_out), .out(transistor_2291_out), .gate(1'b1));
  Transistor #(.gate("br")) transistor_2292 (
    .in(transistor_2205_out), .out(transistor_2291_out), .gate(transistor_2261_out));
  Transistor #(.\type ("n")) transistor_2293 (
    .in(transistor_2339_out), .out(transistor_2291_out), .gate(transistor_2261_out));
  Transistor #(.gate("br")) transistor_2294 (.in(transistor_2339_out), .out(transistor_2291_out), .gate(1'b1));
  Transistor #(.\type ("n")) transistor_2295 (.in(transistor_2207_out), .out(transistor_2295_out), .gate(1'b1));
  Transistor #(.gate("br")) transistor_2296 (
    .in(transistor_2207_out), .out(transistor_2295_out), .gate(transistor_2263_out));
  Transistor #(.\type ("n")) transistor_2297 (
    .in(transistor_2345_out), .out(transistor_2295_out), .gate(transistor_2263_out));
  Transistor #(.gate("br")) transistor_2298 (.in(transistor_2345_out), .out(transistor_2295_out), .gate(1'b1));
  Transistor #(.\type ("n")) transistor_2299 (.in(transistor_2209_out), .out(transistor_2299_out), .gate(1'b1));
  Transistor #(.gate("br")) transistor_2300 (
    .in(transistor_2209_out), .out(transistor_2299_out), .gate(transistor_2265_out));
  Transistor #(.\type ("n")) transistor_2301 (
    .in(transistor_2351_out), .out(transistor_2299_out), .gate(transistor_2265_out));
  Transistor #(.gate("br")) transistor_2302 (.in(transistor_2351_out), .out(transistor_2299_out), .gate(1'b1));
  Transistor #(.\type ("n")) transistor_2303 (.in(1'b0), .out(s), .gate(rst));
  Transistor #(.gate("br")) transistor_2304 (.in(1'b0), .out(s), .gate(transistor_2305_out));
  Transistor transistor_2305 (.in(1'b1), .out(transistor_2305_out), .gate(rst));
  Transistor #(.\type ("n")) transistor_2306 (.in(1'b0), .out(transistor_2305_out), .gate(rst));
  Transistor #(.\type ("n")) transistor_2307 (.in(transistor_2267_out), .out(s), .gate(transistor_2305_out));
  Transistor #(.gate("br")) transistor_2308 (.in(transistor_2267_out), .out(s), .gate(rst));
  Transistor #(.\type ("n")) transistor_2309 (.in(1'b0), .out(transistor_2309_out), .gate(rst));
  Transistor #(.gate("br")) transistor_2310 (.in(1'b0), .out(transistor_2309_out), .gate(transistor_2311_out));
  Transistor transistor_2311 (.in(1'b1), .out(transistor_2311_out), .gate(rst));
  Transistor #(.\type ("n")) transistor_2312 (.in(1'b0), .out(transistor_2311_out), .gate(rst));
  Transistor #(.\type ("n")) transistor_2313 (
    .in(transistor_2271_out), .out(transistor_2309_out), .gate(transistor_2311_out));
  Transistor #(.gate("br")) transistor_2314 (.in(transistor_2271_out), .out(transistor_2309_out), .gate(rst));
  Transistor #(.\type ("n")) transistor_2315 (.in(1'b0), .out(transistor_2315_out), .gate(rst));
  Transistor #(.gate("br")) transistor_2316 (.in(1'b0), .out(transistor_2315_out), .gate(transistor_2317_out));
  Transistor transistor_2317 (.in(1'b1), .out(transistor_2317_out), .gate(rst));
  Transistor #(.\type ("n")) transistor_2318 (.in(1'b0), .out(transistor_2317_out), .gate(rst));
  Transistor #(.\type ("n")) transistor_2319 (
    .in(transistor_2275_out), .out(transistor_2315_out), .gate(transistor_2317_out));
  Transistor #(.gate("br")) transistor_2320 (.in(transistor_2275_out), .out(transistor_2315_out), .gate(rst));
  Transistor #(.\type ("n")) transistor_2321 (.in(1'b0), .out(transistor_2321_out), .gate(rst));
  Transistor #(.gate("br")) transistor_2322 (.in(1'b0), .out(transistor_2321_out), .gate(transistor_2323_out));
  Transistor transistor_2323 (.in(1'b1), .out(transistor_2323_out), .gate(rst));
  Transistor #(.\type ("n")) transistor_2324 (.in(1'b0), .out(transistor_2323_out), .gate(rst));
  Transistor #(.\type ("n")) transistor_2325 (
    .in(transistor_2279_out), .out(transistor_2321_out), .gate(transistor_2323_out));
  Transistor #(.gate("br")) transistor_2326 (.in(transistor_2279_out), .out(transistor_2321_out), .gate(rst));
  Transistor #(.\type ("n")) transistor_2327 (.in(1'b0), .out(transistor_2327_out), .gate(rst));
  Transistor #(.gate("br")) transistor_2328 (.in(1'b0), .out(transistor_2327_out), .gate(transistor_2329_out));
  Transistor transistor_2329 (.in(1'b1), .out(transistor_2329_out), .gate(rst));
  Transistor #(.\type ("n")) transistor_2330 (.in(1'b0), .out(transistor_2329_out), .gate(rst));
  Transistor #(.\type ("n")) transistor_2331 (
    .in(transistor_2283_out), .out(transistor_2327_out), .gate(transistor_2329_out));
  Transistor #(.gate("br")) transistor_2332 (.in(transistor_2283_out), .out(transistor_2327_out), .gate(rst));
  Transistor #(.\type ("n")) transistor_2333 (.in(1'b0), .out(transistor_2333_out), .gate(rst));
  Transistor #(.gate("br")) transistor_2334 (.in(1'b0), .out(transistor_2333_out), .gate(transistor_2335_out));
  Transistor transistor_2335 (.in(1'b1), .out(transistor_2335_out), .gate(rst));
  Transistor #(.\type ("n")) transistor_2336 (.in(1'b0), .out(transistor_2335_out), .gate(rst));
  Transistor #(.\type ("n")) transistor_2337 (
    .in(transistor_2287_out), .out(transistor_2333_out), .gate(transistor_2335_out));
  Transistor #(.gate("br")) transistor_2338 (.in(transistor_2287_out), .out(transistor_2333_out), .gate(rst));
  Transistor #(.\type ("n")) transistor_2339 (.in(1'b0), .out(transistor_2339_out), .gate(rst));
  Transistor #(.gate("br")) transistor_2340 (.in(1'b0), .out(transistor_2339_out), .gate(transistor_2341_out));
  Transistor transistor_2341 (.in(1'b1), .out(transistor_2341_out), .gate(rst));
  Transistor #(.\type ("n")) transistor_2342 (.in(1'b0), .out(transistor_2341_out), .gate(rst));
  Transistor #(.\type ("n")) transistor_2343 (
    .in(transistor_2291_out), .out(transistor_2339_out), .gate(transistor_2341_out));
  Transistor #(.gate("br")) transistor_2344 (.in(transistor_2291_out), .out(transistor_2339_out), .gate(rst));
  Transistor #(.\type ("n")) transistor_2345 (.in(1'b0), .out(transistor_2345_out), .gate(rst));
  Transistor #(.gate("br")) transistor_2346 (.in(1'b0), .out(transistor_2345_out), .gate(transistor_2347_out));
  Transistor transistor_2347 (.in(1'b1), .out(transistor_2347_out), .gate(rst));
  Transistor #(.\type ("n")) transistor_2348 (.in(1'b0), .out(transistor_2347_out), .gate(rst));
  Transistor #(.\type ("n")) transistor_2349 (
    .in(transistor_2295_out), .out(transistor_2345_out), .gate(transistor_2347_out));
  Transistor #(.gate("br")) transistor_2350 (.in(transistor_2295_out), .out(transistor_2345_out), .gate(rst));
  Transistor #(.\type ("n")) transistor_2351 (.in(1'b0), .out(transistor_2351_out), .gate(rst));
  Transistor #(.gate("br")) transistor_2352 (.in(1'b0), .out(transistor_2351_out), .gate(transistor_2353_out));
  Transistor transistor_2353 (.in(1'b1), .out(transistor_2353_out), .gate(rst));
  Transistor #(.\type ("n")) transistor_2354 (.in(1'b0), .out(transistor_2353_out), .gate(rst));
  Transistor #(.\type ("n")) transistor_2355 (
    .in(transistor_2299_out), .out(transistor_2351_out), .gate(transistor_2353_out));
  Transistor #(.gate("br")) transistor_2356 (.in(transistor_2299_out), .out(transistor_2351_out), .gate(rst));
  Pull_Resistor pull_resistor_19 (.node(s));
  Transistor #(.\type ("n")) transistor_2357 (.in(1'b0), .out(transistor_2357_out), .gate(transistor_2315_out));
  Transistor #(.\type ("n")) transistor_2358 (.in(1'b0), .out(transistor_2358_out), .gate(transistor_2321_out));
  Transistor #(.\type ("n")) transistor_2359 (.in(1'b0), .out(transistor_2359_out), .gate(transistor_2327_out));
  Transistor #(.\type ("n")) transistor_2360 (.in(1'b0), .out(transistor_2360_out), .gate(transistor_2333_out));
  Transistor #(.\type ("n")) transistor_2361 (.in(1'b0), .out(transistor_2361_out), .gate(transistor_2339_out));
  Transistor #(.\type ("n")) transistor_2362 (.in(1'b0), .out(transistor_2362_out), .gate(transistor_2345_out));
  Transistor #(.\type ("n")) transistor_2363 (.in(1'b0), .out(transistor_2363_out), .gate(transistor_2351_out));
  Transistor #(.\type ("n")) transistor_2364 (.in(transistor_2363_out), .out(transistor_2364_out), .gate(fr_w));
  Transistor #(.gate("br")) transistor_2365 (
    .in(transistor_2363_out), .out(transistor_2364_out), .gate(transistor_2366_out));
  Transistor transistor_2366 (.in(1'b1), .out(transistor_2366_out), .gate(fr_w));
  Transistor #(.\type ("n")) transistor_2367 (.in(1'b0), .out(transistor_2366_out), .gate(fr_w));
  Transistor #(.\type ("n")) transistor_2368 (.in(z), .out(transistor_2364_out), .gate(transistor_2366_out));
  Transistor #(.gate("br")) transistor_2369 (.in(z), .out(transistor_2364_out), .gate(fr_w));
  Transistor transistor_2370 (.in(1'b1), .out(transistor_2370_out), .gate(transistor_2315_out));
  Transistor transistor_2371 (.in(transistor_2370_out), .out(transistor_2357_out), .gate(transistor_2309_out));
  Transistor #(.\type ("n")) transistor_2372 (.in(1'b0), .out(transistor_2357_out), .gate(transistor_2309_out));
  Transistor transistor_2373 (.in(1'b1), .out(transistor_2373_out), .gate(transistor_2321_out));
  Transistor transistor_2374 (.in(transistor_2373_out), .out(transistor_2358_out), .gate(transistor_2393_out));
  Transistor #(.\type ("n")) transistor_2375 (.in(1'b0), .out(transistor_2358_out), .gate(transistor_2393_out));
  Transistor transistor_2376 (.in(1'b1), .out(transistor_2376_out), .gate(transistor_2327_out));
  Transistor transistor_2377 (.in(transistor_2376_out), .out(transistor_2359_out), .gate(transistor_2395_out));
  Transistor #(.\type ("n")) transistor_2378 (.in(1'b0), .out(transistor_2359_out), .gate(transistor_2395_out));
  Transistor transistor_2379 (.in(1'b1), .out(transistor_2379_out), .gate(transistor_2333_out));
  Transistor transistor_2380 (.in(transistor_2379_out), .out(transistor_2360_out), .gate(transistor_2397_out));
  Transistor #(.\type ("n")) transistor_2381 (.in(1'b0), .out(transistor_2360_out), .gate(transistor_2397_out));
  Transistor transistor_2382 (.in(1'b1), .out(transistor_2382_out), .gate(transistor_2339_out));
  Transistor transistor_2383 (.in(transistor_2382_out), .out(transistor_2361_out), .gate(transistor_2399_out));
  Transistor #(.\type ("n")) transistor_2384 (.in(1'b0), .out(transistor_2361_out), .gate(transistor_2399_out));
  Transistor transistor_2385 (.in(1'b1), .out(transistor_2385_out), .gate(transistor_2345_out));
  Transistor transistor_2386 (.in(transistor_2385_out), .out(transistor_2362_out), .gate(transistor_2401_out));
  Transistor #(.\type ("n")) transistor_2387 (.in(1'b0), .out(transistor_2362_out), .gate(transistor_2401_out));
  Transistor transistor_2388 (.in(1'b1), .out(transistor_2388_out), .gate(transistor_2351_out));
  Transistor transistor_2389 (.in(transistor_2388_out), .out(transistor_2363_out), .gate(transistor_2403_out));
  Transistor #(.\type ("n")) transistor_2390 (.in(1'b0), .out(transistor_2363_out), .gate(transistor_2403_out));
  Transistor transistor_2391 (.in(1'b1), .out(transistor_2391_out), .gate(rst));
  Transistor #(.\type ("n")) transistor_2392 (.in(1'b0), .out(transistor_2391_out), .gate(rst));
  Transistor transistor_2393 (.in(1'b1), .out(transistor_2393_out), .gate(transistor_2357_out));
  Transistor #(.\type ("n")) transistor_2394 (.in(1'b0), .out(transistor_2393_out), .gate(transistor_2357_out));
  Transistor transistor_2395 (.in(1'b1), .out(transistor_2395_out), .gate(transistor_2358_out));
  Transistor #(.\type ("n")) transistor_2396 (.in(1'b0), .out(transistor_2395_out), .gate(transistor_2358_out));
  Transistor transistor_2397 (.in(1'b1), .out(transistor_2397_out), .gate(transistor_2359_out));
  Transistor #(.\type ("n")) transistor_2398 (.in(1'b0), .out(transistor_2397_out), .gate(transistor_2359_out));
  Transistor transistor_2399 (.in(1'b1), .out(transistor_2399_out), .gate(transistor_2360_out));
  Transistor #(.\type ("n")) transistor_2400 (.in(1'b0), .out(transistor_2399_out), .gate(transistor_2360_out));
  Transistor transistor_2401 (.in(1'b1), .out(transistor_2401_out), .gate(transistor_2361_out));
  Transistor #(.\type ("n")) transistor_2402 (.in(1'b0), .out(transistor_2401_out), .gate(transistor_2361_out));
  Transistor transistor_2403 (.in(1'b1), .out(transistor_2403_out), .gate(transistor_2362_out));
  Transistor #(.\type ("n")) transistor_2404 (.in(1'b0), .out(transistor_2403_out), .gate(transistor_2362_out));
  Transistor #(.\type ("n")) transistor_2405 (.in(1'b0), .out(z), .gate(rst));
  Transistor #(.gate("br")) transistor_2406 (.in(1'b0), .out(z), .gate(transistor_2391_out));
  Pull_Resistor pull_resistor_20 (.node(z));
  Transistor #(.\type ("n")) transistor_2407 (.in(transistor_2364_out), .out(z), .gate(transistor_2391_out));
  Transistor #(.gate("br")) transistor_2408 (.in(transistor_2364_out), .out(z), .gate(rst));
  Transistor transistor_2409 (.in(1'b1), .out(transistor_2409_out), .gate(rd_r));
  Transistor #(.\type ("n")) transistor_2410 (.in(1'b0), .out(transistor_2409_out), .gate(rd_r));
  Transistor #(.\type ("n")) transistor_2411 (.in(transistor_2309_out), .out(transistor_1367_out), .gate(rd_r));
  Transistor transistor_2412 (.in(1'b1), .out(transistor_2412_out), .gate(rd_r));
  Transistor #(.\type ("n")) transistor_2413 (.in(1'b0), .out(transistor_2412_out), .gate(rd_r));
  Transistor #(.\type ("n")) transistor_2414 (.in(transistor_2315_out), .out(transistor_1355_out), .gate(rd_r));
  Transistor transistor_2415 (.in(1'b1), .out(transistor_2415_out), .gate(rd_r));
  Transistor #(.\type ("n")) transistor_2416 (.in(1'b0), .out(transistor_2415_out), .gate(rd_r));
  Transistor #(.\type ("n")) transistor_2417 (.in(transistor_2321_out), .out(transistor_1287_out), .gate(rd_r));
  Transistor transistor_2418 (.in(1'b1), .out(transistor_2418_out), .gate(rd_r));
  Transistor #(.\type ("n")) transistor_2419 (.in(1'b0), .out(transistor_2418_out), .gate(rd_r));
  Transistor #(.\type ("n")) transistor_2420 (.in(transistor_2327_out), .out(transistor_1251_out), .gate(rd_r));
  Transistor transistor_2421 (.in(1'b1), .out(transistor_2421_out), .gate(rd_r));
  Transistor #(.\type ("n")) transistor_2422 (.in(1'b0), .out(transistor_2421_out), .gate(rd_r));
  Transistor #(.\type ("n")) transistor_2423 (.in(transistor_2333_out), .out(transistor_1215_out), .gate(rd_r));
  Transistor transistor_2424 (.in(1'b1), .out(transistor_2424_out), .gate(rd_r));
  Transistor #(.\type ("n")) transistor_2425 (.in(1'b0), .out(transistor_2424_out), .gate(rd_r));
  Transistor #(.\type ("n")) transistor_2426 (.in(transistor_2339_out), .out(transistor_1179_out), .gate(rd_r));
  Transistor transistor_2427 (.in(1'b1), .out(transistor_2427_out), .gate(rd_r));
  Transistor #(.\type ("n")) transistor_2428 (.in(1'b0), .out(transistor_2427_out), .gate(rd_r));
  Transistor #(.\type ("n")) transistor_2429 (.in(transistor_2345_out), .out(transistor_1143_out), .gate(rd_r));
  Transistor transistor_2430 (.in(1'b1), .out(transistor_2430_out), .gate(rd_r));
  Transistor #(.\type ("n")) transistor_2431 (.in(1'b0), .out(transistor_2430_out), .gate(rd_r));
  Transistor #(.\type ("n")) transistor_2432 (.in(transistor_2351_out), .out(transistor_1083_out), .gate(rd_r));
  Transistor #(.gate("br")) transistor_2433 (
    .in(transistor_2309_out), .out(transistor_1367_out), .gate(transistor_2409_out));
  Transistor #(.gate("br")) transistor_2434 (
    .in(transistor_2315_out), .out(transistor_1355_out), .gate(transistor_2412_out));
  Transistor #(.gate("br")) transistor_2435 (
    .in(transistor_2321_out), .out(transistor_1287_out), .gate(transistor_2415_out));
  Transistor #(.gate("br")) transistor_2436 (
    .in(transistor_2327_out), .out(transistor_1251_out), .gate(transistor_2418_out));
  Transistor #(.gate("br")) transistor_2437 (
    .in(transistor_2333_out), .out(transistor_1215_out), .gate(transistor_2421_out));
  Transistor #(.gate("br")) transistor_2438 (
    .in(transistor_2339_out), .out(transistor_1179_out), .gate(transistor_2424_out));
  Transistor #(.gate("br")) transistor_2439 (
    .in(transistor_2345_out), .out(transistor_1143_out), .gate(transistor_2427_out));
  Transistor #(.gate("br")) transistor_2440 (
    .in(transistor_2351_out), .out(transistor_1083_out), .gate(transistor_2430_out));
  Pull_Resistor pull_resistor_21 (.node(transistor_1215_out));
  Pull_Resistor pull_resistor_22 (.node(transistor_1179_out));
  Pull_Resistor pull_resistor_23 (.node(transistor_1143_out));
  Pull_Resistor pull_resistor_24 (.node(transistor_1083_out));
  Pull_Resistor pull_resistor_25 (.node(transistor_1367_out));
  Pull_Resistor pull_resistor_26 (.node(transistor_1355_out));
  Pull_Resistor pull_resistor_27 (.node(transistor_1287_out));
  Pull_Resistor pull_resistor_28 (.node(transistor_1251_out));
endmodule

module NAND2x1x1 (
  input  a,
  input  b,
  output out
);

  wire transistor_4_out;

  Transistor transistor_1 (.in(1'b1), .out(out), .gate(a));
  Transistor transistor_2 (.in(1'b1), .out(out), .gate(b));
  Transistor #(.\type ("n")) transistor_3 (.in(transistor_4_out), .out(out), .gate(a));
  Transistor #(.\type ("n")) transistor_4 (.in(1'b0), .out(transistor_4_out), .gate(b));
endmodule

module NAND3x1x1 (
  input  a,
  input  b,
  input  c,
  output out
);

  wire transistor_5_out, transistor_6_out;

  Transistor transistor_1 (.in(1'b1), .out(out), .gate(a));
  Transistor transistor_2 (.in(1'b1), .out(out), .gate(c));
  Transistor transistor_3 (.in(1'b1), .out(out), .gate(b));
  Transistor #(.\type ("n")) transistor_4 (.in(transistor_5_out), .out(out), .gate(a));
  Transistor #(.\type ("n")) transistor_5 (.in(transistor_6_out), .out(transistor_5_out), .gate(b));
  Transistor #(.\type ("n")) transistor_6 (.in(1'b0), .out(transistor_6_out), .gate(c));
endmodule

module NOR2x1x1 (
  input  a,
  input  b,
  output out
);

  wire transistor_1_out;

  Transistor transistor_1 (.in(1'b1), .out(transistor_1_out), .gate(a));
  Transistor transistor_2 (.in(transistor_1_out), .out(out), .gate(b));
  Transistor #(.\type ("n")) transistor_3 (.in(1'b0), .out(out), .gate(a));
  Transistor #(.\type ("n")) transistor_4 (.in(1'b0), .out(out), .gate(b));
endmodule

module NOR3x1x1 (
  input  a,
  input  b,
  input  c,
  output out
);

  wire transistor_3_out, transistor_4_out;

  Transistor #(.\type ("n")) transistor_1 (.in(1'b0), .out(out), .gate(b));
  Transistor #(.\type ("n")) transistor_2 (.in(1'b0), .out(out), .gate(a));
  Transistor transistor_3 (.in(1'b1), .out(transistor_3_out), .gate(a));
  Transistor transistor_4 (.in(transistor_3_out), .out(transistor_4_out), .gate(b));
  Transistor transistor_5 (.in(transistor_4_out), .out(out), .gate(c));
  Transistor #(.\type ("n")) transistor_6 (.in(1'b0), .out(out), .gate(c));
endmodule

module XOR2x1x1 (
  input  a,
  input  b,
  output out
);

  wire transistor_1_out, transistor_4_out, transistor_5_out, transistor_6_out, transistor_9_out,
       transistor_13_out, transistor_16_out;

  Transistor transistor_1 (.in(1'b1), .out(transistor_1_out), .gate(b));
  Transistor transistor_2 (.in(1'b1), .out(transistor_1_out), .gate(a));
  Transistor #(.\type ("n")) transistor_3 (.in(transistor_4_out), .out(transistor_1_out), .gate(a));
  Transistor #(.\type ("n")) transistor_4 (.in(1'b0), .out(transistor_4_out), .gate(b));
  Transistor transistor_5 (.in(1'b1), .out(transistor_5_out), .gate(a));
  Transistor transistor_6 (.in(1'b1), .out(transistor_6_out), .gate(transistor_1_out));
  Transistor transistor_7 (.in(1'b1), .out(transistor_5_out), .gate(transistor_1_out));
  Transistor #(.\type ("n")) transistor_8 (.in(transistor_9_out), .out(transistor_5_out), .gate(a));
  Transistor #(.\type ("n")) transistor_9 (.in(1'b0), .out(transistor_9_out), .gate(transistor_1_out));
  Transistor transistor_10 (.in(1'b1), .out(out), .gate(transistor_5_out));
  Transistor transistor_11 (.in(1'b1), .out(transistor_6_out), .gate(b));
  Transistor #(.\type ("n")) transistor_12 (.in(transistor_13_out), .out(transistor_6_out), .gate(transistor_1_out));
  Transistor #(.\type ("n")) transistor_13 (.in(1'b0), .out(transistor_13_out), .gate(b));
  Transistor transistor_14 (.in(1'b1), .out(out), .gate(transistor_6_out));
  Transistor #(.\type ("n")) transistor_15 (.in(transistor_16_out), .out(out), .gate(transistor_5_out));
  Transistor #(.\type ("n")) transistor_16 (.in(1'b0), .out(transistor_16_out), .gate(transistor_6_out));
endmodule

module NOT1x1x1 (
  input  in,
  output out
);

  Transistor transistor_1 (.in(1'b1), .out(out), .gate(in));
  Transistor #(.\type ("n")) transistor_2 (.in(1'b0), .out(out), .gate(in));
endmodule

module EN1x1x1 (
  input  in,
  input  en,
  output out
);

  wire transistor_1_out;

  Transistor #(.gate("br")) transistor_1 (.in(1'b1), .out(transistor_1_out), .gate(en));
  Transistor #(.\type ("n")) transistor_2 (.in(in), .out(out), .gate(en));
  Transistor #(.gate("br")) transistor_3 (.in(in), .out(out), .gate(transistor_1_out));
  Transistor #(.\type ("n"), .gate("br")) transistor_4 (.in(1'b0), .out(transistor_1_out), .gate(en));
endmodule

module MUX2x1x1 (
  input  a,
  input  sel,
  input  b,
  output out
);

  wire transistor_1_out;

  Transistor transistor_1 (.in(1'b1), .out(transistor_1_out), .gate(sel));
  Transistor #(.\type ("n")) transistor_2 (.in(1'b0), .out(transistor_1_out), .gate(sel));
  Transistor transistor_3 (.in(a), .out(out), .gate(sel));
  Transistor #(.\type ("n"), .gate("br")) transistor_4 (.in(a), .out(out), .gate(transistor_1_out));
  Transistor transistor_5 (.in(b), .out(out), .gate(transistor_1_out));
  Transistor #(.\type ("n"), .gate("br")) transistor_6 (.in(b), .out(out), .gate(sel));
endmodule

module MUX4x1x1 (
  input  a,
  input  b,
  input  c,
  input  d,
  input  sel0,
  input  sel1,
  output out
);

  wire transistor_1_out, transistor_3_out, transistor_5_out, transistor_9_out, transistor_15_out;

  Transistor transistor_1 (.in(1'b1), .out(transistor_1_out), .gate(sel0));
  Transistor #(.\type ("n")) transistor_2 (.in(1'b0), .out(transistor_1_out), .gate(sel0));
  Transistor transistor_3 (.in(1'b1), .out(transistor_3_out), .gate(sel0));
  Transistor #(.\type ("n")) transistor_4 (.in(1'b0), .out(transistor_3_out), .gate(sel0));
  Transistor transistor_5 (.in(a), .out(transistor_5_out), .gate(sel0));
  Transistor #(.\type ("n"), .gate("br")) transistor_6 (.in(a), .out(transistor_5_out), .gate(transistor_1_out));
  Transistor transistor_7 (.in(b), .out(transistor_5_out), .gate(transistor_1_out));
  Transistor #(.\type ("n"), .gate("br")) transistor_8 (.in(b), .out(transistor_5_out), .gate(sel0));
  Transistor transistor_9 (.in(c), .out(transistor_9_out), .gate(sel0));
  Transistor #(.\type ("n"), .gate("br")) transistor_10 (.in(c), .out(transistor_9_out), .gate(transistor_3_out));
  Transistor transistor_11 (.in(d), .out(transistor_9_out), .gate(transistor_3_out));
  Transistor #(.\type ("n"), .gate("br")) transistor_12 (.in(d), .out(transistor_9_out), .gate(sel0));
  Transistor transistor_13 (.in(transistor_5_out), .out(out), .gate(sel1));
  Transistor #(.\type ("n"), .gate("br")) transistor_14 (.in(transistor_5_out), .out(out), .gate(transistor_15_out));
  Transistor transistor_15 (.in(1'b1), .out(transistor_15_out), .gate(sel1));
  Transistor #(.\type ("n")) transistor_16 (.in(1'b0), .out(transistor_15_out), .gate(sel1));
  Transistor transistor_17 (.in(transistor_9_out), .out(out), .gate(transistor_15_out));
  Transistor #(.\type ("n"), .gate("br")) transistor_18 (.in(transistor_9_out), .out(out), .gate(sel1));
endmodule

module MUX8x1x1 (
  input  a,
  input  b,
  input  c,
  input  d,
  input  e,
  input  f,
  input  g,
  input  h,
  input  sel0,
  input  sel1,
  input  sel2,
  output out
);

  wire transistor_1_out, transistor_3_out, transistor_5_out, transistor_7_out, transistor_9_out,
       transistor_13_out, transistor_17_out, transistor_21_out, transistor_25_out, transistor_27_out,
       transistor_31_out, transistor_33_out, transistor_37_out;

  Transistor transistor_1 (.in(1'b1), .out(transistor_1_out), .gate(sel0));
  Transistor #(.\type ("n")) transistor_2 (.in(1'b0), .out(transistor_1_out), .gate(sel0));
  Transistor transistor_3 (.in(1'b1), .out(transistor_3_out), .gate(sel0));
  Transistor #(.\type ("n")) transistor_4 (.in(1'b0), .out(transistor_3_out), .gate(sel0));
  Transistor transistor_5 (.in(1'b1), .out(transistor_5_out), .gate(sel0));
  Transistor #(.\type ("n")) transistor_6 (.in(1'b0), .out(transistor_5_out), .gate(sel0));
  Transistor transistor_7 (.in(1'b1), .out(transistor_7_out), .gate(sel0));
  Transistor #(.\type ("n")) transistor_8 (.in(1'b0), .out(transistor_7_out), .gate(sel0));
  Transistor transistor_9 (.in(a), .out(transistor_9_out), .gate(sel0));
  Transistor #(.\type ("n"), .gate("br")) transistor_10 (.in(a), .out(transistor_9_out), .gate(transistor_1_out));
  Transistor transistor_11 (.in(b), .out(transistor_9_out), .gate(transistor_1_out));
  Transistor #(.\type ("n"), .gate("br")) transistor_12 (.in(b), .out(transistor_9_out), .gate(sel0));
  Transistor transistor_13 (.in(c), .out(transistor_13_out), .gate(sel0));
  Transistor #(.\type ("n"), .gate("br")) transistor_14 (.in(c), .out(transistor_13_out), .gate(transistor_3_out));
  Transistor transistor_15 (.in(d), .out(transistor_13_out), .gate(transistor_3_out));
  Transistor #(.\type ("n"), .gate("br")) transistor_16 (.in(d), .out(transistor_13_out), .gate(sel0));
  Transistor transistor_17 (.in(e), .out(transistor_17_out), .gate(sel0));
  Transistor #(.\type ("n"), .gate("br")) transistor_18 (.in(e), .out(transistor_17_out), .gate(transistor_5_out));
  Transistor transistor_19 (.in(f), .out(transistor_17_out), .gate(transistor_5_out));
  Transistor #(.\type ("n"), .gate("br")) transistor_20 (.in(f), .out(transistor_17_out), .gate(sel0));
  Transistor transistor_21 (.in(g), .out(transistor_21_out), .gate(sel0));
  Transistor #(.\type ("n"), .gate("br")) transistor_22 (.in(g), .out(transistor_21_out), .gate(transistor_7_out));
  Transistor transistor_23 (.in(h), .out(transistor_21_out), .gate(transistor_7_out));
  Transistor #(.\type ("n"), .gate("br")) transistor_24 (.in(h), .out(transistor_21_out), .gate(sel0));
  Transistor transistor_25 (.in(transistor_9_out), .out(transistor_25_out), .gate(sel1));
  Transistor #(.\type ("n"), .gate("br")) transistor_26 (
    .in(transistor_9_out), .out(transistor_25_out), .gate(transistor_27_out));
  Transistor transistor_27 (.in(1'b1), .out(transistor_27_out), .gate(sel1));
  Transistor #(.\type ("n")) transistor_28 (.in(1'b0), .out(transistor_27_out), .gate(sel1));
  Transistor transistor_29 (.in(transistor_13_out), .out(transistor_25_out), .gate(transistor_27_out));
  Transistor #(.\type ("n"), .gate("br")) transistor_30 (.in(transistor_13_out), .out(transistor_25_out), .gate(sel1));
  Transistor transistor_31 (.in(transistor_17_out), .out(transistor_31_out), .gate(sel1));
  Transistor #(.\type ("n"), .gate("br")) transistor_32 (
    .in(transistor_17_out), .out(transistor_31_out), .gate(transistor_33_out));
  Transistor transistor_33 (.in(1'b1), .out(transistor_33_out), .gate(sel1));
  Transistor #(.\type ("n")) transistor_34 (.in(1'b0), .out(transistor_33_out), .gate(sel1));
  Transistor transistor_35 (.in(transistor_21_out), .out(transistor_31_out), .gate(transistor_33_out));
  Transistor #(.\type ("n"), .gate("br")) transistor_36 (.in(transistor_21_out), .out(transistor_31_out), .gate(sel1));
  Transistor transistor_37 (.in(1'b1), .out(transistor_37_out), .gate(sel2));
  Transistor #(.\type ("n")) transistor_38 (.in(1'b0), .out(transistor_37_out), .gate(sel2));
  Transistor transistor_39 (.in(transistor_25_out), .out(out), .gate(sel2));
  Transistor #(.\type ("n"), .gate("br")) transistor_40 (.in(transistor_25_out), .out(out), .gate(transistor_37_out));
  Transistor transistor_41 (.in(transistor_31_out), .out(out), .gate(transistor_37_out));
  Transistor #(.\type ("n"), .gate("br")) transistor_42 (.in(transistor_31_out), .out(out), .gate(sel2));
endmodule
module DEC1x2x4 (
  input  in1,
  input  in0,
  output _00,
  output _01,
  output _10,
  output _11
);

  wire transistor_1_out, transistor_3_out, transistor_5_out, transistor_7_out, transistor_9_out,
       transistor_12_out, transistor_13_out, transistor_16_out, transistor_17_out, transistor_20_out,
       transistor_21_out, transistor_24_out;

  Transistor #(.\type ("n")) transistor_1 (.in(1'b0), .out(transistor_1_out), .gate(in0));
  Transistor transistor_2 (.in(1'b1), .out(transistor_1_out), .gate(in0));
  Transistor transistor_3 (.in(1'b1), .out(transistor_3_out), .gate(in1));
  Transistor #(.\type ("n")) transistor_4 (.in(1'b0), .out(transistor_3_out), .gate(in1));
  Transistor #(.\type ("n")) transistor_5 (.in(1'b0), .out(transistor_5_out), .gate(in1));
  Transistor transistor_6 (.in(1'b1), .out(transistor_5_out), .gate(in1));
  Transistor transistor_7 (.in(1'b1), .out(transistor_7_out), .gate(in0));
  Transistor #(.\type ("n")) transistor_8 (.in(1'b0), .out(transistor_7_out), .gate(in0));
  Transistor transistor_9 (.in(1'b1), .out(transistor_9_out), .gate(transistor_3_out));
  Transistor transistor_10 (.in(1'b1), .out(transistor_9_out), .gate(transistor_1_out));
  Transistor #(.\type ("n")) transistor_11 (.in(transistor_12_out), .out(transistor_9_out), .gate(transistor_1_out));
  Transistor #(.\type ("n")) transistor_12 (.in(1'b0), .out(transistor_12_out), .gate(transistor_3_out));
  Transistor transistor_13 (.in(1'b1), .out(transistor_13_out), .gate(in0));
  Transistor transistor_14 (.in(1'b1), .out(transistor_13_out), .gate(transistor_5_out));
  Transistor #(.\type ("n")) transistor_15 (.in(transistor_16_out), .out(transistor_13_out), .gate(in0));
  Transistor #(.\type ("n")) transistor_16 (.in(1'b0), .out(transistor_16_out), .gate(transistor_5_out));
  Transistor transistor_17 (.in(1'b1), .out(transistor_17_out), .gate(transistor_7_out));
  Transistor transistor_18 (.in(1'b1), .out(transistor_17_out), .gate(in1));
  Transistor #(.\type ("n")) transistor_19 (.in(transistor_20_out), .out(transistor_17_out), .gate(transistor_7_out));
  Transistor #(.\type ("n")) transistor_20 (.in(1'b0), .out(transistor_20_out), .gate(in1));
  Transistor transistor_21 (.in(1'b1), .out(transistor_21_out), .gate(in1));
  Transistor transistor_22 (.in(1'b1), .out(transistor_21_out), .gate(in0));
  Transistor #(.\type ("n")) transistor_23 (.in(transistor_24_out), .out(transistor_21_out), .gate(in0));
  Transistor #(.\type ("n")) transistor_24 (.in(1'b0), .out(transistor_24_out), .gate(in1));
  Transistor transistor_25 (.in(1'b1), .out(_00), .gate(transistor_9_out));
  Transistor #(.\type ("n")) transistor_26 (.in(1'b0), .out(_00), .gate(transistor_9_out));
  Transistor transistor_27 (.in(1'b1), .out(_01), .gate(transistor_13_out));
  Transistor #(.\type ("n")) transistor_28 (.in(1'b0), .out(_01), .gate(transistor_13_out));
  Transistor transistor_29 (.in(1'b1), .out(_10), .gate(transistor_17_out));
  Transistor #(.\type ("n")) transistor_30 (.in(1'b0), .out(_10), .gate(transistor_17_out));
  Transistor transistor_31 (.in(1'b1), .out(_11), .gate(transistor_21_out));
  Transistor #(.\type ("n")) transistor_32 (.in(1'b0), .out(_11), .gate(transistor_21_out));
endmodule

module DEC1x3x8 (
  input  in2,
  input  in1,
  input  in0,
  output _000,
  output _001,
  output _010,
  output _011,
  output _100,
  output _101,
  output _110,
  output _111
);

  wire transistor_1_out, transistor_2_out, transistor_3_out, transistor_4_out, transistor_5_out,
       transistor_6_out, transistor_7_out, transistor_8_out, transistor_9_out, transistor_10_out,
       transistor_11_out, transistor_12_out, transistor_25_out, transistor_27_out, transistor_29_out,
       transistor_31_out, transistor_33_out, transistor_35_out, transistor_37_out, transistor_39_out,
       transistor_43_out, transistor_44_out, transistor_47_out, transistor_48_out, transistor_51_out,
       transistor_52_out, transistor_55_out, transistor_56_out, transistor_59_out, transistor_60_out,
       transistor_63_out, transistor_64_out, transistor_67_out, transistor_68_out, transistor_71_out,
       transistor_72_out;

  Transistor transistor_1 (.in(1'b1), .out(transistor_1_out), .gate(in0));
  Transistor transistor_2 (.in(1'b1), .out(transistor_2_out), .gate(in1));
  Transistor transistor_3 (.in(1'b1), .out(transistor_3_out), .gate(in2));
  Transistor transistor_4 (.in(1'b1), .out(transistor_4_out), .gate(in1));
  Transistor transistor_5 (.in(1'b1), .out(transistor_5_out), .gate(in2));
  Transistor transistor_6 (.in(1'b1), .out(transistor_6_out), .gate(in0));
  Transistor transistor_7 (.in(1'b1), .out(transistor_7_out), .gate(in2));
  Transistor transistor_8 (.in(1'b1), .out(transistor_8_out), .gate(in2));
  Transistor transistor_9 (.in(1'b1), .out(transistor_9_out), .gate(in0));
  Transistor transistor_10 (.in(1'b1), .out(transistor_10_out), .gate(in1));
  Transistor transistor_11 (.in(1'b1), .out(transistor_11_out), .gate(in1));
  Transistor transistor_12 (.in(1'b1), .out(transistor_12_out), .gate(in0));
  Transistor #(.\type ("n")) transistor_13 (.in(1'b0), .out(transistor_1_out), .gate(in0));
  Transistor #(.\type ("n")) transistor_14 (.in(1'b0), .out(transistor_2_out), .gate(in1));
  Transistor #(.\type ("n")) transistor_15 (.in(1'b0), .out(transistor_3_out), .gate(in2));
  Transistor #(.\type ("n")) transistor_16 (.in(1'b0), .out(transistor_4_out), .gate(in1));
  Transistor #(.\type ("n")) transistor_17 (.in(1'b0), .out(transistor_5_out), .gate(in2));
  Transistor #(.\type ("n")) transistor_18 (.in(1'b0), .out(transistor_6_out), .gate(in0));
  Transistor #(.\type ("n")) transistor_19 (.in(1'b0), .out(transistor_7_out), .gate(in2));
  Transistor #(.\type ("n")) transistor_20 (.in(1'b0), .out(transistor_8_out), .gate(in2));
  Transistor #(.\type ("n")) transistor_21 (.in(1'b0), .out(transistor_9_out), .gate(in0));
  Transistor #(.\type ("n")) transistor_22 (.in(1'b0), .out(transistor_10_out), .gate(in1));
  Transistor #(.\type ("n")) transistor_23 (.in(1'b0), .out(transistor_11_out), .gate(in1));
  Transistor #(.\type ("n")) transistor_24 (.in(1'b0), .out(transistor_12_out), .gate(in0));
  Transistor transistor_25 (.in(1'b1), .out(transistor_25_out), .gate(transistor_2_out));
  Transistor transistor_26 (.in(1'b1), .out(transistor_25_out), .gate(transistor_1_out));
  Transistor transistor_27 (.in(1'b1), .out(transistor_27_out), .gate(transistor_4_out));
  Transistor transistor_28 (.in(1'b1), .out(transistor_27_out), .gate(in0));
  Transistor transistor_29 (.in(1'b1), .out(transistor_29_out), .gate(transistor_6_out));
  Transistor transistor_30 (.in(1'b1), .out(transistor_29_out), .gate(in1));
  Transistor transistor_31 (.in(1'b1), .out(transistor_31_out), .gate(in1));
  Transistor transistor_32 (.in(1'b1), .out(transistor_31_out), .gate(in0));
  Transistor transistor_33 (.in(1'b1), .out(transistor_33_out), .gate(transistor_10_out));
  Transistor transistor_34 (.in(1'b1), .out(transistor_33_out), .gate(transistor_9_out));
  Transistor transistor_35 (.in(1'b1), .out(transistor_35_out), .gate(transistor_11_out));
  Transistor transistor_36 (.in(1'b1), .out(transistor_35_out), .gate(in0));
  Transistor transistor_37 (.in(1'b1), .out(transistor_37_out), .gate(in1));
  Transistor transistor_38 (.in(1'b1), .out(transistor_37_out), .gate(transistor_12_out));
  Transistor transistor_39 (.in(1'b1), .out(transistor_39_out), .gate(in1));
  Transistor transistor_40 (.in(1'b1), .out(transistor_39_out), .gate(in0));
  Transistor transistor_41 (.in(1'b1), .out(transistor_25_out), .gate(transistor_3_out));
  Transistor #(.\type ("n")) transistor_42 (.in(transistor_43_out), .out(transistor_25_out), .gate(transistor_1_out));
  Transistor #(.\type ("n")) transistor_43 (.in(transistor_44_out), .out(transistor_43_out), .gate(transistor_2_out));
  Transistor #(.\type ("n")) transistor_44 (.in(1'b0), .out(transistor_44_out), .gate(transistor_3_out));
  Transistor transistor_45 (.in(1'b1), .out(transistor_27_out), .gate(transistor_5_out));
  Transistor #(.\type ("n")) transistor_46 (.in(transistor_47_out), .out(transistor_27_out), .gate(in0));
  Transistor #(.\type ("n")) transistor_47 (.in(transistor_48_out), .out(transistor_47_out), .gate(transistor_4_out));
  Transistor #(.\type ("n")) transistor_48 (.in(1'b0), .out(transistor_48_out), .gate(transistor_5_out));
  Transistor transistor_49 (.in(1'b1), .out(transistor_29_out), .gate(transistor_7_out));
  Transistor #(.\type ("n")) transistor_50 (.in(transistor_51_out), .out(transistor_29_out), .gate(transistor_6_out));
  Transistor #(.\type ("n")) transistor_51 (.in(transistor_52_out), .out(transistor_51_out), .gate(in1));
  Transistor #(.\type ("n")) transistor_52 (.in(1'b0), .out(transistor_52_out), .gate(transistor_7_out));
  Transistor transistor_53 (.in(1'b1), .out(transistor_31_out), .gate(transistor_8_out));
  Transistor #(.\type ("n")) transistor_54 (.in(transistor_55_out), .out(transistor_31_out), .gate(in0));
  Transistor #(.\type ("n")) transistor_55 (.in(transistor_56_out), .out(transistor_55_out), .gate(in1));
  Transistor #(.\type ("n")) transistor_56 (.in(1'b0), .out(transistor_56_out), .gate(transistor_8_out));
  Transistor transistor_57 (.in(1'b1), .out(transistor_33_out), .gate(in2));
  Transistor #(.\type ("n")) transistor_58 (.in(transistor_59_out), .out(transistor_33_out), .gate(transistor_9_out));
  Transistor #(.\type ("n")) transistor_59 (.in(transistor_60_out), .out(transistor_59_out), .gate(transistor_10_out));
  Transistor #(.\type ("n")) transistor_60 (.in(1'b0), .out(transistor_60_out), .gate(in2));
  Transistor transistor_61 (.in(1'b1), .out(transistor_35_out), .gate(in2));
  Transistor #(.\type ("n")) transistor_62 (.in(transistor_63_out), .out(transistor_35_out), .gate(in0));
  Transistor #(.\type ("n")) transistor_63 (.in(transistor_64_out), .out(transistor_63_out), .gate(transistor_11_out));
  Transistor #(.\type ("n")) transistor_64 (.in(1'b0), .out(transistor_64_out), .gate(in2));
  Transistor transistor_65 (.in(1'b1), .out(transistor_37_out), .gate(in2));
  Transistor #(.\type ("n")) transistor_66 (.in(transistor_67_out), .out(transistor_37_out), .gate(transistor_12_out));
  Transistor #(.\type ("n")) transistor_67 (.in(transistor_68_out), .out(transistor_67_out), .gate(in1));
  Transistor #(.\type ("n")) transistor_68 (.in(1'b0), .out(transistor_68_out), .gate(in2));
  Transistor transistor_69 (.in(1'b1), .out(transistor_39_out), .gate(in2));
  Transistor #(.\type ("n")) transistor_70 (.in(transistor_71_out), .out(transistor_39_out), .gate(in0));
  Transistor #(.\type ("n")) transistor_71 (.in(transistor_72_out), .out(transistor_71_out), .gate(in1));
  Transistor #(.\type ("n")) transistor_72 (.in(1'b0), .out(transistor_72_out), .gate(in2));
  Transistor transistor_73 (.in(1'b1), .out(_000), .gate(transistor_25_out));
  Transistor #(.\type ("n")) transistor_74 (.in(1'b0), .out(_000), .gate(transistor_25_out));
  Transistor transistor_75 (.in(1'b1), .out(_001), .gate(transistor_27_out));
  Transistor #(.\type ("n")) transistor_76 (.in(1'b0), .out(_001), .gate(transistor_27_out));
  Transistor transistor_77 (.in(1'b1), .out(_010), .gate(transistor_29_out));
  Transistor #(.\type ("n")) transistor_78 (.in(1'b0), .out(_010), .gate(transistor_29_out));
  Transistor transistor_79 (.in(1'b1), .out(_011), .gate(transistor_31_out));
  Transistor #(.\type ("n")) transistor_80 (.in(1'b0), .out(_011), .gate(transistor_31_out));
  Transistor transistor_81 (.in(1'b1), .out(_100), .gate(transistor_33_out));
  Transistor #(.\type ("n")) transistor_82 (.in(1'b0), .out(_100), .gate(transistor_33_out));
  Transistor transistor_83 (.in(1'b1), .out(_101), .gate(transistor_35_out));
  Transistor #(.\type ("n")) transistor_84 (.in(1'b0), .out(_101), .gate(transistor_35_out));
  Transistor transistor_85 (.in(1'b1), .out(_110), .gate(transistor_37_out));
  Transistor #(.\type ("n")) transistor_86 (.in(1'b0), .out(_110), .gate(transistor_37_out));
  Transistor transistor_87 (.in(1'b1), .out(_111), .gate(transistor_39_out));
  Transistor #(.\type ("n")) transistor_88 (.in(1'b0), .out(_111), .gate(transistor_39_out));
endmodule

module DLATCH (
  input  in,
  input  w,
  input  rst,
  input  r,
  input  in_2,
  input  w_2,
  input  rst_2,
  output out,
  output out_2
);

  wire transistor_1_out, transistor_3_out, transistor_9_out, transistor_13_out, transistor_15_out,
       transistor_19_out, transistor_21_out, transistor_25_out;

  Transistor transistor_1 (.in(1'b1), .out(transistor_1_out), .gate(w_2));
  Transistor #(.\type ("n")) transistor_2 (.in(1'b0), .out(transistor_1_out), .gate(w_2));
  Transistor #(.\type ("n")) transistor_3 (.in(in), .out(transistor_3_out), .gate(w_2));
  Transistor #(.gate("br")) transistor_4 (.in(in), .out(transistor_3_out), .gate(transistor_1_out));
  Transistor #(.\type ("n")) transistor_5 (.in(out), .out(transistor_3_out), .gate(transistor_1_out));
  Transistor #(.gate("br")) transistor_6 (.in(out), .out(transistor_3_out), .gate(w_2));
  Transistor #(.\type ("n")) transistor_7 (.in(1'b0), .out(out), .gate(rst_2));
  Transistor #(.gate("br")) transistor_8 (.in(1'b0), .out(out), .gate(transistor_9_out));
  Transistor transistor_9 (.in(1'b1), .out(transistor_9_out), .gate(rst_2));
  Transistor #(.\type ("n")) transistor_10 (.in(1'b0), .out(transistor_9_out), .gate(rst_2));
  Transistor #(.\type ("n")) transistor_11 (.in(transistor_3_out), .out(out), .gate(transistor_9_out));
  Transistor #(.gate("br")) transistor_12 (.in(transistor_3_out), .out(out), .gate(rst_2));
  Transistor transistor_13 (.in(1'b1), .out(transistor_13_out), .gate(w));
  Transistor #(.\type ("n")) transistor_14 (.in(1'b0), .out(transistor_13_out), .gate(w));
  Transistor #(.\type ("n")) transistor_15 (.in(in_2), .out(transistor_15_out), .gate(w));
  Transistor #(.gate("br")) transistor_16 (.in(in_2), .out(transistor_15_out), .gate(transistor_13_out));
  Transistor #(.\type ("n")) transistor_17 (.in(transistor_21_out), .out(transistor_15_out), .gate(transistor_13_out));
  Transistor #(.gate("br")) transistor_18 (.in(transistor_21_out), .out(transistor_15_out), .gate(w));
  Transistor transistor_19 (.in(1'b1), .out(transistor_19_out), .gate(rst));
  Transistor #(.\type ("n")) transistor_20 (.in(1'b0), .out(transistor_19_out), .gate(rst));
  Transistor #(.\type ("n")) transistor_21 (.in(1'b0), .out(transistor_21_out), .gate(rst));
  Transistor #(.gate("br")) transistor_22 (.in(1'b0), .out(transistor_21_out), .gate(transistor_19_out));
  Transistor #(.\type ("n")) transistor_23 (.in(transistor_15_out), .out(transistor_21_out), .gate(transistor_19_out));
  Transistor #(.gate("br")) transistor_24 (.in(transistor_15_out), .out(transistor_21_out), .gate(rst));
  Transistor transistor_25 (.in(1'b1), .out(transistor_25_out), .gate(r));
  Transistor #(.\type ("n")) transistor_26 (.in(1'b0), .out(transistor_25_out), .gate(r));
  Transistor transistor_27 (.in(transistor_21_out), .out(out_2), .gate(transistor_25_out));
  Transistor #(.\type ("n"), .gate("br")) transistor_28 (.in(transistor_21_out), .out(out_2), .gate(r));
endmodule

module FLIPFLOP (
  input  rst,
  input  w,
  input  r,
  input  in,
  output out
);

  wire transistor_1_out, transistor_3_out, transistor_5_out, transistor_9_out, transistor_11_out,
       transistor_15_out, transistor_19_out, transistor_23_out, transistor_25_out, transistor_29_out;

  Transistor transistor_1 (.in(1'b1), .out(transistor_1_out), .gate(transistor_3_out));
  Transistor #(.\type ("n")) transistor_2 (.in(1'b0), .out(transistor_1_out), .gate(transistor_3_out));
  Transistor transistor_3 (.in(1'b1), .out(transistor_3_out), .gate(w));
  Transistor #(.\type ("n")) transistor_4 (.in(1'b0), .out(transistor_3_out), .gate(w));
  Transistor #(.\type ("n")) transistor_5 (.in(in), .out(transistor_5_out), .gate(transistor_3_out));
  Transistor #(.gate("br")) transistor_6 (.in(in), .out(transistor_5_out), .gate(transistor_1_out));
  Transistor #(.\type ("n")) transistor_7 (.in(transistor_11_out), .out(transistor_5_out), .gate(transistor_1_out));
  Transistor #(.gate("br")) transistor_8 (.in(transistor_11_out), .out(transistor_5_out), .gate(transistor_3_out));
  Transistor transistor_9 (.in(1'b1), .out(transistor_9_out), .gate(rst));
  Transistor #(.\type ("n")) transistor_10 (.in(1'b0), .out(transistor_9_out), .gate(rst));
  Transistor #(.\type ("n")) transistor_11 (.in(1'b0), .out(transistor_11_out), .gate(rst));
  Transistor #(.gate("br")) transistor_12 (.in(1'b0), .out(transistor_11_out), .gate(transistor_9_out));
  Transistor #(.\type ("n")) transistor_13 (.in(transistor_5_out), .out(transistor_11_out), .gate(transistor_9_out));
  Transistor #(.gate("br")) transistor_14 (.in(transistor_5_out), .out(transistor_11_out), .gate(rst));
  Transistor transistor_15 (.in(1'b1), .out(transistor_15_out), .gate(rst));
  Transistor #(.\type ("n")) transistor_16 (.in(1'b0), .out(transistor_15_out), .gate(rst));
  Transistor transistor_17 (.in(1'b1), .out(rst), .gate(transistor_3_out));
  Transistor #(.\type ("n")) transistor_18 (.in(1'b0), .out(rst), .gate(transistor_3_out));
  Transistor #(.\type ("n")) transistor_19 (.in(transistor_11_out), .out(transistor_19_out), .gate(rst));
  Transistor #(.gate("br")) transistor_20 (.in(transistor_11_out), .out(transistor_19_out), .gate(transistor_15_out));
  Transistor #(.\type ("n")) transistor_21 (.in(transistor_25_out), .out(transistor_19_out), .gate(transistor_15_out));
  Transistor #(.gate("br")) transistor_22 (.in(transistor_25_out), .out(transistor_19_out), .gate(rst));
  Transistor transistor_23 (.in(1'b1), .out(transistor_23_out), .gate(rst));
  Transistor #(.\type ("n")) transistor_24 (.in(1'b0), .out(transistor_23_out), .gate(rst));
  Transistor #(.\type ("n")) transistor_25 (.in(1'b0), .out(transistor_25_out), .gate(rst));
  Transistor #(.gate("br")) transistor_26 (.in(1'b0), .out(transistor_25_out), .gate(transistor_23_out));
  Transistor #(.\type ("n")) transistor_27 (.in(transistor_19_out), .out(transistor_25_out), .gate(transistor_23_out));
  Transistor #(.gate("br")) transistor_28 (.in(transistor_19_out), .out(transistor_25_out), .gate(rst));
  Transistor transistor_29 (.in(1'b1), .out(transistor_29_out), .gate(r));
  Transistor #(.\type ("n")) transistor_30 (.in(1'b0), .out(transistor_29_out), .gate(r));
  Transistor transistor_31 (.in(transistor_25_out), .out(out), .gate(transistor_29_out));
  Transistor #(.\type ("n"), .gate("br")) transistor_32 (.in(transistor_25_out), .out(out), .gate(r));
endmodule

module DLatch (
  input  data,
  input  write,
  input  reset,
  output out
);

  wire nand_1_out, nand_2_out, nand_3_out, nand_4_out, nand_6_out;

  nand nand_1 (nand_1_out, data, data);
  nand nand_2 (nand_2_out, data, write);
  nand nand_3 (nand_3_out, write, nand_1_out);
  nand nand_4 (nand_4_out, reset, reset);
  nand nand_5 (out, nand_2_out, nand_6_out);
  nand nand_6 (nand_6_out, out, nand_3_out, nand_4_out);
endmodule

module Reg4 (
  input  in0,
  input  in1,
  input  in2,
  input  in3,
  input  read,
  input  write,
  input  reset,
  output out0,
  output out1,
  output out2,
  output out3
);

  wire dlatch_1_out, dlatch_2_out, dlatch_3_out, dlatch_4_out;

  DLatch dlatch_1 (.data(in0), .write(write), .out(dlatch_1_out), .reset(reset));
  DLatch dlatch_2 (.data(in1), .write(write), .out(dlatch_2_out), .reset(reset));
  DLatch dlatch_3 (.data(in2), .write(write), .out(dlatch_3_out), .reset(reset));
  DLatch dlatch_4 (.data(in3), .write(write), .out(dlatch_4_out), .reset(reset));
  assign out0 = read ? dlatch_1_out : 1'bz;  // Controlled_Buffer controlled_buffer_1
  assign out1 = read ? dlatch_2_out : 1'bz;  // Controlled_Buffer controlled_buffer_2
  assign out2 = read ? dlatch_3_out : 1'bz;  // Controlled_Buffer controlled_buffer_3
  assign out3 = read ? dlatch_4_out : 1'bz;  // Controlled_Buffer controlled_buffer_4
endmodule

module Reg8 (
  input  read,
  input  write,
  input  reset,
  input  in0,
  input  in1,
  input  in2,
  input  in3,
  input  in4,
  input  in5,
  input  in6,
  input  in7,
  output out0,
  output out1,
  output out2,
  output out3,
  output out4,
  output out5,
  output out6,
  output out7
);

  Reg4 reg4_1 (
    .in0(in0), .in1(in1), .in2(in2), .in3(in3), .read(read), .write(write), .out0(out0), .out1(out1),
    .out2(out2), .out3(out3), .reset(reset));
  Reg4 reg4_2 (
    .in0(in4), .in1(in5), .in2(in6), .in3(in7), .read(read), .write(write), .out0(out4), .out1(out5),
    .out2(out6), .out3(out7), .reset(reset));
endmodule

module Ram256 (
  input  addr0,
  input  addr1,
  input  addr2,
  input  addr3,
  input  addr4,
  input  addr5,
  input  addr6,
  input  addr7,
  input  marw,
  input  read,
  input  write,
  input  clk,
  input  reset,
  input  in0,
  input  in1,
  input  in2,
  input  in3,
  input  in4,
  input  in5,
  input  in6,
  input  in7,
  output out0,
  output out1,
  output out2,
  output out3,
  output out4,
  output out5,
  output out6,
  output out7
);

  wire delayer_1_out, or_1_out;
  wire [7:0] MAR_out0;

  Reg8 MAR (
    .in0(addr0), .in1(addr1), .in2(addr2), .in3(addr3), .in4(addr4), .in5(addr5), .in6(addr6), .in7(addr7),
    .read(1'b1), .write(marw), .reset(reset), .out0(MAR_out0[0]), .out1(MAR_out0[1]), .out2(MAR_out0[2]),
    .out3(MAR_out0[3]), .out4(MAR_out0[4]), .out5(MAR_out0[5]), .out6(MAR_out0[6]), .out7(MAR_out0[7]));
  Delayer delayer_1 (.in(clk), .out(delayer_1_out));
  or or_1 (or_1_out, read, write);
  RAM #(.bus("separate")) ram_1 (
    .addr(MAR_out0), .din({in7, in6, in5, in4, in3, in2, in1, in0}),
    .data({out7, out6, out5, out4, out3, out2, out1, out0}), .str(write), .sel(or_1_out),
    .clk(delayer_1_out), .ld(read), .clr(reset));
endmodule

module LeftShifter8 (
  input  cin,
  input  in0,
  input  in1,
  input  in2,
  input  in3,
  input  in4,
  input  in5,
  input  in6,
  input  in7,
  output out0,
  output out1,
  output out2,
  output out3,
  output out4,
  output out6,
  output out6_2,
  output out7,
  output cout
);


  assign cout = in7;
  assign out0 = cin;
  assign out1 = in0;
  assign out2 = in1;
  assign out3 = in2;
  assign out4 = in3;
  assign out6 = in4;
  assign out6_2 = in5;
  assign out7 = in6;
endmodule

module RightShifter8 (
  input  in0,
  input  in1,
  input  in2,
  input  in3,
  input  in4,
  input  in5,
  input  in6,
  input  in7,
  input  cin,
  output cout,
  output out0,
  output out1,
  output out2,
  output out3,
  output out4,
  output out6,
  output out6_2,
  output out7
);


  assign cout = in0;
  assign out0 = in1;
  assign out1 = in2;
  assign out2 = in3;
  assign out3 = in4;
  assign out4 = in5;
  assign out6 = in6;
  assign out6_2 = in7;
  assign out7 = cin;
endmodule

module Ander8 (
  input  a0,
  input  b0,
  input  a1,
  input  b1,
  input  a2,
  input  b2,
  input  a3,
  input  b3,
  input  a4,
  input  b4,
  input  a5,
  input  b5,
  input  a6,
  input  b6,
  input  a7,
  input  b7,
  output out0,
  output out1,
  output out2,
  output out3,
  output out4,
  output out5,
  output out6,
  output out7
);

  and and_1 (out0, a0, b0);
  and and_2 (out1, a1, b1);
  and and_3 (out2, a2, b2);
  and and_4 (out3, a3, b3);
  and and_5 (out4, a4, b4);
  and and_6 (out5, a5, b5);
  and and_7 (out6, a6, b6);
  and and_8 (out7, a7, b7);
endmodule

module Orer8 (
  input  a0,
  input  b0,
  input  a1,
  input  b1,
  input  a2,
  input  b2,
  input  a3,
  input  b3,
  input  a4,
  input  b4,
  input  a5,
  input  b5,
  input  a6,
  input  b6,
  input  a7,
  input  b7,
  output out0,
  output out1,
  output out2,
  output out3,
  output out4,
  output out5,
  output out6,
  output out7
);

  or or_1 (out0, a0, b0);
  or or_2 (out1, a1, b1);
  or or_3 (out2, a2, b2);
  or or_4 (out3, a3, b3);
  or or_5 (out4, a4, b4);
  or or_6 (out5, a5, b5);
  or or_7 (out6, a6, b6);
  or or_8 (out7, a7, b7);
endmodule

module Xorer8 (
  input  a0,
  input  b0,
  input  a1,
  input  b1,
  input  a2,
  input  b2,
  input  a3,
  input  b3,
  input  a4,
  input  b4,
  input  a5,
  input  b5,
  input  a6,
  input  b6,
  input  a7,
  input  b7,
  output out0,
  output out1,
  output out2,
  output out3,
  output out4,
  output out5,
  output out6,
  output out7
);

  xor xor_1 (out0, a0, b0);
  xor xor_2 (out1, a1, b1);
  xor xor_3 (out2, a2, b2);
  xor xor_4 (out3, a3, b3);
  xor xor_5 (out4, a4, b4);
  xor xor_6 (out5, a5, b5);
  xor xor_7 (out6, a6, b6);
  xor xor_8 (out7, a7, b7);
endmodule

module FullAdder (
  input  a,
  input  b,
  input  cin,
  output sum,
  output cout
);

  wire and_1_out, and_2_out, xor_1_out;

  xor xor_1 (xor_1_out, a, b);
  xor xor_2 (sum, xor_1_out, cin);
  and and_1 (and_1_out, xor_1_out, cin);
  and and_2 (and_2_out, a, b);
  or or_1 (cout, and_1_out, and_2_out);
endmodule

module Adder8 (
  input  cin,
  input  a0,
  input  b0,
  input  a1,
  input  b1,
  input  a2,
  input  b2,
  input  a3,
  input  b3,
  input  a4,
  input  b4,
  input  a5,
  input  b5,
  input  a6,
  input  b6,
  input  a7,
  input  b7,
  output out0,
  output out1,
  output out2,
  output out3,
  output out4,
  output out5,
  output out6,
  output out7,
  output ovcarry,
  output cout
);

  wire fulladder_1_cout, fulladder_2_cout, fulladder_3_cout, fulladder_4_cout, fulladder_5_cout,
       fulladder_6_cout;

  FullAdder fulladder_1 (.a(a0), .b(b0), .cin(cin), .sum(out0), .cout(fulladder_1_cout));
  FullAdder fulladder_2 (.a(a1), .b(b1), .cin(fulladder_1_cout), .sum(out1), .cout(fulladder_2_cout));
  FullAdder fulladder_3 (.a(a2), .b(b2), .cin(fulladder_2_cout), .sum(out2), .cout(fulladder_3_cout));
  FullAdder fulladder_4 (.a(a3), .b(b3), .cin(fulladder_3_cout), .sum(out3), .cout(fulladder_4_cout));
  FullAdder fulladder_5 (.a(a4), .b(b4), .cin(fulladder_4_cout), .sum(out4), .cout(fulladder_5_cout));
  FullAdder fulladder_6 (.a(a5), .b(b5), .cin(fulladder_5_cout), .sum(out5), .cout(fulladder_6_cout));
  FullAdder fulladder_7 (.a(a6), .b(b6), .cin(fulladder_6_cout), .sum(out6), .cout(ovcarry));
  FullAdder fulladder_8 (.a(a7), .b(b7), .cin(ovcarry), .sum(out7), .cout(cout));
endmodule

module AddSub8 (
  input  sub,
  input  a0,
  input  b0,
  input  a1,
  input  b1,
  input  a2,
  input  b2,
  input  a3,
  input  b3,
  input  a4,
  input  b4,
  input  a5,
  input  b5,
  input  a6,
  input  b6,
  input  a7,
  input  b7,
  input  cin,
  output carry,
  output overflow,
  output out7,
  output out6,
  output out5,
  output out4,
  output out3,
  output out2,
  output out1,
  output out0
);

  wire adder8_1_cout, adder8_1_ovcarry, xor_3_out, xor_4_out, xor_5_out, xor_6_out, xor_7_out, xor_8_out,
       xor_9_out, xor_10_out, xor_11_out;

  xor xor_1 (carry, sub, adder8_1_cout);
  xor xor_2 (overflow, adder8_1_ovcarry, adder8_1_cout);
  xor xor_3 (xor_3_out, sub, b0);
  xor xor_4 (xor_4_out, sub, b1);
  xor xor_5 (xor_5_out, sub, b2);
  xor xor_6 (xor_6_out, sub, b3);
  xor xor_7 (xor_7_out, sub, b4);
  xor xor_8 (xor_8_out, sub, b5);
  xor xor_9 (xor_9_out, sub, b6);
  xor xor_10 (xor_10_out, sub, b7);
  Adder8 adder8_1 (
    .cin(xor_11_out), .a0(a0), .b0(xor_3_out), .a1(a1), .b1(xor_4_out), .a2(a2), .b2(xor_5_out), .a3(a3),
    .b3(xor_6_out), .a4(a4), .b4(xor_7_out), .a5(a5), .b5(xor_8_out), .a6(a6), .b6(xor_9_out), .a7(a7),
    .b7(xor_10_out), .out0(out0), .out1(out1), .out2(out2), .out3(out3), .out4(out4), .out5(out5),
    .out6(out6), .out7(out7), .ovcarry(adder8_1_ovcarry), .cout(adder8_1_cout));
  xor xor_11 (xor_11_out, sub, cin);
endmodule

module Bus0Gate (
  input  in7,
  input  in6,
  input  in5,
  input  in4,
  input  in3,
  input  in2,
  input  in1,
  input  in0,
  input  _0_bus,
  output out7,
  output out6,
  output out5,
  output out4,
  output out3,
  output out2,
  output out1,
  output out0
);

  and and_1 (out6, in6, _0_bus);
  and and_2 (out7, in7, _0_bus);
  and and_3 (out4, in4, _0_bus);
  and and_4 (out5, in5, _0_bus);
  and and_5 (out2, in2, _0_bus);
  and and_6 (out3, in3, _0_bus);
  and and_7 (out1, in1, _0_bus);
  and and_8 (out0, in0, _0_bus);
endmodule

module Enable8 (
  input  in0,
  input  in1,
  input  in2,
  input  in3,
  input  in4,
  input  in5,
  input  in6,
  input  in7,
  input  en,
  output out0,
  output out1,
  output out2,
  output out3,
  output out4,
  output out6,
  output out6_2,
  output out7
);

  wire transistor_1_out, transistor_2_out, transistor_3_out, transistor_4_out, transistor_5_out,
       transistor_6_out, transistor_7_out, transistor_8_out;

  Transistor #(.gate("br")) transistor_1 (.in(1'b1), .out(transistor_1_out), .gate(en));
  Transistor #(.gate("br")) transistor_2 (.in(1'b1), .out(transistor_2_out), .gate(en));
  Transistor #(.gate("br")) transistor_3 (.in(1'b1), .out(transistor_3_out), .gate(en));
  Transistor #(.gate("br")) transistor_4 (.in(1'b1), .out(transistor_4_out), .gate(en));
  Transistor #(.gate("br")) transistor_5 (.in(1'b1), .out(transistor_5_out), .gate(en));
  Transistor #(.gate("br")) transistor_6 (.in(1'b1), .out(transistor_6_out), .gate(en));
  Transistor #(.gate("br")) transistor_7 (.in(1'b1), .out(transistor_7_out), .gate(en));
  Transistor #(.gate("br")) transistor_8 (.in(1'b1), .out(transistor_8_out), .gate(en));
  Transistor #(.\type ("n")) transistor_9 (.in(in0), .out(out0), .gate(en));
  Transistor #(.gate("br")) transistor_10 (.in(in0), .out(out0), .gate(transistor_1_out));
  Transistor #(.\type ("n"), .gate("br")) transistor_11 (.in(1'b0), .out(transistor_1_out), .gate(en));
  Transistor #(.\type ("n")) transistor_12 (.in(in1), .out(out1), .gate(en));
  Transistor #(.gate("br")) transistor_13 (.in(in1), .out(out1), .gate(transistor_2_out));
  Transistor #(.\type ("n"), .gate("br")) transistor_14 (.in(1'b0), .out(transistor_2_out), .gate(en));
  Transistor #(.\type ("n")) transistor_15 (.in(in2), .out(out2), .gate(en));
  Transistor #(.gate("br")) transistor_16 (.in(in2), .out(out2), .gate(transistor_3_out));
  Transistor #(.\type ("n"), .gate("br")) transistor_17 (.in(1'b0), .out(transistor_3_out), .gate(en));
  Transistor #(.\type ("n")) transistor_18 (.in(in3), .out(out3), .gate(en));
  Transistor #(.gate("br")) transistor_19 (.in(in3), .out(out3), .gate(transistor_4_out));
  Transistor #(.\type ("n"), .gate("br")) transistor_20 (.in(1'b0), .out(transistor_4_out), .gate(en));
  Transistor #(.\type ("n")) transistor_21 (.in(in4), .out(out4), .gate(en));
  Transistor #(.gate("br")) transistor_22 (.in(in4), .out(out4), .gate(transistor_5_out));
  Transistor #(.\type ("n"), .gate("br")) transistor_23 (.in(1'b0), .out(transistor_5_out), .gate(en));
  Transistor #(.\type ("n")) transistor_24 (.in(in5), .out(out6), .gate(en));
  Transistor #(.gate("br")) transistor_25 (.in(in5), .out(out6), .gate(transistor_6_out));
  Transistor #(.\type ("n"), .gate("br")) transistor_26 (.in(1'b0), .out(transistor_6_out), .gate(en));
  Transistor #(.\type ("n")) transistor_27 (.in(in6), .out(out6_2), .gate(en));
  Transistor #(.gate("br")) transistor_28 (.in(in6), .out(out6_2), .gate(transistor_7_out));
  Transistor #(.\type ("n"), .gate("br")) transistor_29 (.in(1'b0), .out(transistor_7_out), .gate(en));
  Transistor #(.\type ("n")) transistor_30 (.in(in7), .out(out7), .gate(en));
  Transistor #(.gate("br")) transistor_31 (.in(in7), .out(out7), .gate(transistor_8_out));
  Transistor #(.\type ("n"), .gate("br")) transistor_32 (.in(1'b0), .out(transistor_8_out), .gate(en));
endmodule

module ALU (
  input  a7,
  input  a6,
  input  a5,
  input  a4,
  input  a3,
  input  a2,
  input  a1,
  input  a0,
  input  b7,
  input  b6,
  input  b5,
  input  b4,
  input  b3,
  input  b2,
  input  b1,
  input  b0,
  input  op2,
  input  op1,
  input  op0,
  input  cin,
  output out0,
  output out1,
  output out2,
  output out3,
  output out4,
  output out5,
  output out6,
  output out7,
  output overflow,
  output carry,
  output sign,
  output zero
);

  wire addsub8_1_carry, addsub8_1_out0, addsub8_1_out1, addsub8_1_out2, addsub8_1_out3, addsub8_1_out4,
       addsub8_1_out5, addsub8_1_out6, addsub8_1_out7, addsub8_1_overflow, ander8_1_out0, ander8_1_out1,
       ander8_1_out2, ander8_1_out3, ander8_1_out4, ander8_1_out5, ander8_1_out6, ander8_1_out7,
       leftshifter8_1_cout, leftshifter8_1_out0, leftshifter8_1_out1, leftshifter8_1_out2,
       leftshifter8_1_out3, leftshifter8_1_out4, leftshifter8_1_out6, leftshifter8_1_out6_2,
       leftshifter8_1_out7, nor_2_out, or_1_out, orer8_1_out0, orer8_1_out1, orer8_1_out2, orer8_1_out3,
       orer8_1_out4, orer8_1_out5, orer8_1_out6, orer8_1_out7, rightshifter8_1_cout, rightshifter8_1_out0,
       rightshifter8_1_out1, rightshifter8_1_out2, rightshifter8_1_out3, rightshifter8_1_out4,
       rightshifter8_1_out6, rightshifter8_1_out6_2, rightshifter8_1_out7, xorer8_1_out0, xorer8_1_out1,
       xorer8_1_out2, xorer8_1_out3, xorer8_1_out4, xorer8_1_out5, xorer8_1_out6, xorer8_1_out7;
  wire [7:0] decoder_1_out0;

  Ander8 ander8_1 (
    .a0(a0), .b0(b0), .a1(a1), .b1(b1), .a2(a2), .b2(b2), .a3(a3), .b3(b3), .a4(a4), .b4(b4), .a5(a5),
    .b5(b5), .a6(a6), .b6(b6), .a7(a7), .b7(b7), .out0(ander8_1_out0), .out1(ander8_1_out1),
    .out2(ander8_1_out2), .out3(ander8_1_out3), .out4(ander8_1_out4), .out5(ander8_1_out5),
    .out6(ander8_1_out6), .out7(ander8_1_out7));
  Orer8 orer8_1 (
    .a0(a0), .b0(b0), .a1(a1), .b1(b1), .a2(a2), .b2(b2), .a3(a3), .b3(b3), .a4(a4), .b4(b4), .a5(a5),
    .b5(b5), .a6(a6), .b6(b6), .a7(a7), .b7(b7), .out0(orer8_1_out0), .out1(orer8_1_out1),
    .out2(orer8_1_out2), .out3(orer8_1_out3), .out4(orer8_1_out4), .out5(orer8_1_out5), .out6(orer8_1_out6),
    .out7(orer8_1_out7));
  Xorer8 xorer8_1 (
    .a0(a0), .b0(b0), .a1(a1), .b1(b1), .a2(a2), .b2(b2), .a3(a3), .b3(b3), .a4(a4), .b4(b4), .a5(a5),
    .b5(b5), .a6(a6), .b6(b6), .a7(a7), .b7(b7), .out0(xorer8_1_out0), .out1(xorer8_1_out1),
    .out2(xorer8_1_out2), .out3(xorer8_1_out3), .out4(xorer8_1_out4), .out5(xorer8_1_out5),
    .out6(xorer8_1_out6), .out7(xorer8_1_out7));
  AddSub8 addsub8_1 (
    .cin(cin), .a0(a0), .b0(b0), .a1(a1), .b1(b1), .a2(a2), .b2(b2), .a3(a3), .b3(b3), .a4(a4), .b4(b4),
    .a5(a5), .b5(b5), .a6(a6), .b6(b6), .a7(a7), .b7(b7), .out0(addsub8_1_out0), .out1(addsub8_1_out1),
    .out2(addsub8_1_out2), .out3(addsub8_1_out3), .out4(addsub8_1_out4), .out5(addsub8_1_out5),
    .out6(addsub8_1_out6), .out7(addsub8_1_out7), .carry(addsub8_1_carry), .sub(decoder_1_out0[5]),
    .overflow(addsub8_1_overflow));
  LeftShifter8 leftshifter8_1 (
    .cin(cin), .in0(a0), .in1(a1), .in2(a2), .in3(a3), .in4(a4), .in5(a5), .in6(a6), .in7(a7),
    .out0(leftshifter8_1_out0), .out1(leftshifter8_1_out1), .out2(leftshifter8_1_out2),
    .out3(leftshifter8_1_out3), .out4(leftshifter8_1_out4), .out6(leftshifter8_1_out6),
    .out6_2(leftshifter8_1_out6_2), .out7(leftshifter8_1_out7), .cout(leftshifter8_1_cout));
  RightShifter8 rightshifter8_1 (
    .in0(a0), .in1(a1), .in2(a2), .in3(a3), .in4(a4), .in5(a5), .in6(a6), .in7(a7), .cin(cin),
    .cout(rightshifter8_1_cout), .out0(rightshifter8_1_out0), .out1(rightshifter8_1_out1),
    .out2(rightshifter8_1_out2), .out3(rightshifter8_1_out3), .out4(rightshifter8_1_out4),
    .out6(rightshifter8_1_out6), .out6_2(rightshifter8_1_out6_2), .out7(rightshifter8_1_out7));
  Decoder #(.select(3), .enable("false")) decoder_1 (
    .out0(decoder_1_out0[0]), .out1(decoder_1_out0[1]), .out2(decoder_1_out0[2]), .out3(decoder_1_out0[3]),
    .out4(decoder_1_out0[4]), .out5(decoder_1_out0[5]), .out6(decoder_1_out0[6]), .out7(decoder_1_out0[7]),
    .sel({op2, op1, op0}));
  Enable8 enable8_1 (
    .in0(a0), .in1(a1), .in2(a2), .in3(a3), .in4(a4), .in5(a5), .in6(a6), .in7(a7), .en(decoder_1_out0[0]),
    .out0(out0), .out1(out1), .out2(out2), .out3(out3), .out4(out4), .out6(out5), .out6_2(out6), .out7(out7));
  Enable8 enable8_2 (
    .in0(ander8_1_out0), .in1(ander8_1_out1), .in2(ander8_1_out2), .in3(ander8_1_out3), .in4(ander8_1_out4),
    .in5(ander8_1_out5), .in6(ander8_1_out6), .in7(ander8_1_out7), .en(decoder_1_out0[1]), .out0(out0),
    .out1(out1), .out2(out2), .out3(out3), .out4(out4), .out6(out5), .out6_2(out6), .out7(out7));
  Enable8 enable8_3 (
    .in0(orer8_1_out0), .in1(orer8_1_out1), .in2(orer8_1_out2), .in3(orer8_1_out3), .in4(orer8_1_out4),
    .in5(orer8_1_out5), .in6(orer8_1_out6), .in7(orer8_1_out7), .en(decoder_1_out0[2]), .out0(out0),
    .out1(out1), .out2(out2), .out3(out3), .out4(out4), .out6(out5), .out6_2(out6), .out7(out7));
  Enable8 enable8_4 (
    .in0(xorer8_1_out0), .in1(xorer8_1_out1), .in2(xorer8_1_out2), .in3(xorer8_1_out3), .in4(xorer8_1_out4),
    .in5(xorer8_1_out5), .in6(xorer8_1_out6), .in7(xorer8_1_out7), .en(decoder_1_out0[3]), .out0(out0),
    .out1(out1), .out2(out2), .out3(out3), .out4(out4), .out6(out5), .out6_2(out6), .out7(out7));
  or or_1 (or_1_out, decoder_1_out0[4], decoder_1_out0[5]);
  Enable8 enable8_5 (
    .in0(addsub8_1_out0), .in1(addsub8_1_out1), .in2(addsub8_1_out2), .in3(addsub8_1_out3),
    .in4(addsub8_1_out4), .in5(addsub8_1_out5), .in6(addsub8_1_out6), .in7(addsub8_1_out7), .en(or_1_out),
    .out0(out0), .out1(out1), .out2(out2), .out3(out3), .out4(out4), .out6(out5), .out6_2(out6), .out7(out7));
  Enable8 enable8_6 (
    .in0(leftshifter8_1_out0), .in1(leftshifter8_1_out1), .in2(leftshifter8_1_out2),
    .in3(leftshifter8_1_out3), .in4(leftshifter8_1_out4), .in5(leftshifter8_1_out6),
    .in6(leftshifter8_1_out6_2), .in7(leftshifter8_1_out7), .en(decoder_1_out0[6]), .out0(out0), .out1(out1),
    .out2(out2), .out3(out3), .out4(out4), .out6(out5), .out6_2(out6), .out7(out7));
  Enable8 enable8_7 (
    .in0(rightshifter8_1_out0), .in1(rightshifter8_1_out1), .in2(rightshifter8_1_out2),
    .in3(rightshifter8_1_out3), .in4(rightshifter8_1_out4), .in5(rightshifter8_1_out6),
    .in6(rightshifter8_1_out6_2), .in7(rightshifter8_1_out7), .en(decoder_1_out0[7]), .out0(out0),
    .out1(out1), .out2(out2), .out3(out3), .out4(out4), .out6(out5), .out6_2(out6), .out7(out7));
  nor nor_1 (zero, out7, out6, out5, out4, out3, out2, out1, out0);
  Multiplexer #(.enable("false")) multiplexer_1 (.in0(1'b0), .in1(addsub8_1_overflow), .out(overflow), .sel(or_1_out));
  nor nor_2 (nor_2_out, or_1_out, decoder_1_out0[6], decoder_1_out0[7]);
  assign carry = nor_2_out ? 1'b0 : 1'bz;  // Controlled_Buffer controlled_buffer_1
  assign carry = or_1_out ? addsub8_1_carry : 1'bz;  // Controlled_Buffer controlled_buffer_2
  assign carry = decoder_1_out0[6] ? leftshifter8_1_cout : 1'bz;  // Controlled_Buffer controlled_buffer_3
  assign carry = decoder_1_out0[7] ? rightshifter8_1_cout : 1'bz;  // Controlled_Buffer controlled_buffer_4

  assign sign = out7;
endmodule

module Clock (
  input  clk,
  input  rst,
  output clk_r,
  output clk_w
);

  wire j_k_ff_1_q, j_k_ff_1_qn, nand_1_out, nand_2_out, not_1_out;

  not not_1 (not_1_out, clk);
  nand nand_1 (nand_1_out, clk, j_k_ff_1_q);
  J_K_Flip_Flop j_k_ff_1 (
    .J(1'b1), .clk(not_1_out), .K(1'b1), .Q(j_k_ff_1_q), .Qn(j_k_ff_1_qn), .preset(rst), .en(1'b1),
    .reset(1'b0));
  nand nand_2 (nand_2_out, j_k_ff_1_qn, clk);
  buf buffer_1 (clk_r, nand_1_out);
  not not_2 (clk_w, nand_2_out);
endmodule

module Delayer (
  input  in,
  output out
);

  wire not_1_out, not_2_out, not_3_out, not_4_out, not_5_out, not_6_out, not_7_out;

  not not_1 (not_1_out, not_2_out);
  not not_2 (not_2_out, in);
  not not_3 (not_3_out, not_5_out);
  not not_4 (not_4_out, not_3_out);
  not not_5 (not_5_out, not_1_out);
  not not_6 (not_6_out, not_4_out);
  not not_7 (not_7_out, not_6_out);
  not not_8 (out, not_7_out);
endmodule

module BranchChecker (
  input  zero,
  input  sign,
  input  carry,
  input  overflow,
  input  op2,
  input  op1,
  input  op0,
  output result
);

  wire and_1_out, and_2_out, and_3_out, and_4_out, and_5_out, and_6_out, and_7_out, decoder_1_out0,
       decoder_1_out1, decoder_1_out2, decoder_1_out3, decoder_1_out4, decoder_1_out5, decoder_1_out6,
       decoder_1_out7, or_1_out, or_2_out, xor_1_out;

  Decoder #(.select(3), .enable("false")) decoder_1 (
    .out0(decoder_1_out0), .out1(decoder_1_out1), .out2(decoder_1_out2), .out3(decoder_1_out3),
    .out4(decoder_1_out4), .out5(decoder_1_out5), .out6(decoder_1_out6), .out7(decoder_1_out7),
    .sel({op2, op1, op0}));
  or or_1 (or_1_out, zero, xor_1_out);
  or or_2 (or_2_out, carry, zero);
  xor xor_1 (xor_1_out, overflow, sign);
  and and_1 (and_1_out, decoder_1_out1, zero);
  and and_2 (and_2_out, decoder_1_out2, sign);
  and and_3 (and_3_out, decoder_1_out3, overflow);
  and and_4 (and_4_out, decoder_1_out4, carry);
  and and_5 (and_5_out, decoder_1_out5, or_2_out);
  and and_6 (and_6_out, decoder_1_out6, xor_1_out);
  and and_7 (and_7_out, decoder_1_out7, or_1_out);
  or or_3 (result, and_7_out, and_6_out, and_5_out, and_4_out, and_3_out, and_2_out, and_1_out, decoder_1_out0);
endmodule

module ControlUnit (
  input  rst,
  input  zero,
  input  sign,
  input  carry,
  input  overflow,
  input  clk,
  input  ir7,
  input  ir6,
  input  ir5,
  input  ir4,
  input  ir3,
  input  ir2,
  input  ir1,
  input  ir0,
  output rd_r,
  output ra_w,
  output rb_w,
  output bus_0,
  output io,
  output io_in_out,
  output io_data_addr,
  output rx_r,
  output rx_w,
  output fr_w,
  output rx1,
  output pc_w,
  output rx0,
  output pc_r,
  output ir_w,
  output cin,
  output mar_w,
  output op2,
  output ram_w,
  output op1,
  output op0,
  output ram_r,
  output halt,
  output new_cycle,
  output new_instr
);

  wire and_10_out, and_13_out, and_14_out, and_15_out, branchchecker_1_result, clock_1_clk_r, clock_1_clk_w,
       delayer_1_out, instr_state_qn, or_1_out, or_2_out, or_3_out;
  wire [1:0] multiplexer_2_out, multiplexer_3_out;
  wire [6:0] adder_1_out, mPC_q, multiplexer_1_out, rom_1_data;
  wire [6:6] instr_state_q;
  wire [31:4] rom_1_data_2;

  and and_1 (fr_w, rom_1_data_2[12], clock_1_clk_w);
  and and_2 (pc_w, rom_1_data_2[13], clock_1_clk_w);
  and and_3 (pc_r, rom_1_data_2[14], clock_1_clk_r);
  and and_4 (ir_w, rom_1_data_2[15], clock_1_clk_w);
  and and_5 (mar_w, rom_1_data_2[16], clock_1_clk_w);
  and and_6 (ram_w, rom_1_data_2[17], clock_1_clk_w);
  and and_7 (ram_r, rom_1_data_2[18], clock_1_clk_r);
  Clock clock_1 (.clk_r(clock_1_clk_r), .clk(clk), .clk_w(clock_1_clk_w), .rst(or_1_out));
  nor nor_1 (new_cycle, clock_1_clk_r, clock_1_clk_w);
  or or_1 (or_1_out, rst, halt);
  and and_8 (ra_w, clock_1_clk_w, rom_1_data_2[10]);
  and and_9 (rd_r, clock_1_clk_r, rom_1_data_2[11]);
  Register #(.width(7)) mPC (.D(multiplexer_1_out), .en(1'b1), .Q(mPC_q), .clk(new_cycle), .clr(or_1_out));
  Multiplexer #(.select(2), .width(7), .enable("false")) multiplexer_1 (
    .in0(adder_1_out), .in1(adder_1_out), .in2(rom_1_data),
    .in3({instr_state_q[6], ir7, ir6, ir5, ir4, 2'b00}), .out(multiplexer_1_out), .sel(multiplexer_2_out));
  and and_10 (and_10_out, clock_1_clk_w, rom_1_data_2[31]);
  and and_11 (rb_w, clock_1_clk_w, rom_1_data_2[9]);
  Delayer delayer_1 (.in(new_cycle), .out(delayer_1_out));
  and and_12 (new_instr, delayer_1_out, and_13_out);
  and and_13 (and_13_out, ~mPC_q[6], ~mPC_q[5], ~mPC_q[4], ~mPC_q[3], ~mPC_q[2], ~mPC_q[1], mPC_q[0]);  // AND_Gate
  Adder #(.width(7)) adder_1 (.a(mPC_q), .b({7{1'b0}}), .out(adder_1_out), .cin(1'b1));  // open: cout
  D_Flip_Flop instr_state (
    .clk(and_10_out), .D(instr_state_qn), .Q(instr_state_q[6]), .Qn(instr_state_qn), .en(1'b1),
    .reset(or_1_out));  // open: preset
  ROM #(.addrWidth(7), .dataWidth(32)) rom_1 (
    .addr(mPC_q),
    .data({rom_1_data_2[31:27], rom_1_data, halt, rom_1_data_2[18:9], bus_0, io, rom_1_data_2[6:4], cin, op2, op1, op0}),
    .sel(1'b1));
  Multiplexer #(.select(2), .width(2), .enable("false")) multiplexer_2 (
    .in0(2'b00), .in1(multiplexer_3_out), .in2(2'b10), .in3(2'b11), .out(multiplexer_2_out),
    .sel(rom_1_data_2[29:28]));
  and and_14 (and_14_out, ir3, io);
  and and_15 (and_15_out, io, ~ir3);  // AND_Gate
  BranchChecker branchchecker_1 (
    .zero(zero), .sign(sign), .carry(carry), .overflow(overflow), .op0(ir0), .op1(ir1), .op2(ir2),
    .result(branchchecker_1_result));
  Multiplexer #(.width(2), .enable("false")) multiplexer_3 (
    .in0(2'b00), .in1(2'b10), .out(multiplexer_3_out), .sel(branchchecker_1_result));
  or or_2 (or_2_out, rom_1_data_2[6], and_15_out);
  or or_3 (or_3_out, rom_1_data_2[5], and_14_out);
  Multiplexer #(.width(2), .enable("false")) multiplexer_4 (
    .in0({ir3, ir2}), .in1({ir1, ir0}), .out({rx1, rx0}), .sel(rom_1_data_2[4]));
  and and_16 (rx_r, clock_1_clk_r, or_2_out);
  and and_17 (rx_w, clock_1_clk_w, or_3_out);

  assign io_data_addr = ir2;
  assign io_in_out = ir3;

  // Notes on the sheet:
  //   Map instructions to 1xxxx00 with xxxx=OPCODE
  //   to avoid collision with IFETCH.
  //   Instructions must complete in 4 steps.
  //   0x00 has no instruction since after reset it won't be executed.
  //   00xy -> jump to addr mPC+1
  //   01xy -> branch to either addr mPC+1 or ROM[mPC]
  //   10xy -> jump to addr ROM[mPC]
  //   11xy -> jump to instr in IR
  //   contents of rom_1 (hex, n*v repeats v):
  //   0 14700 280c b0048000 60*0 450 a0100820 0 0 14700 280c a0140030 0 10050 a0140020 0 0 10050 a0120040
  //   0 0 4400 2050 a0100830 0 15614400 a0102b0c 40200 a0102804 a0080000 0 0 0 a0100000 0 0 0 440 250
  //   a0101824 0 440 250 a0101825 0 450 a0101826 0 0 450 a0101827 0 0 440 250 a0101821 0 440 250 a0101822
  //   0 440 250 a0101823 0 440 a0101255
endmodule

module CPU (
  input  in_1,
  input  in_2,
  input  in_3,
  input  in_4,
  input  in_5,
  input  in_6,
  input  in_7,
  input  in_8,
  input  MANUAL,
  input  in_10,
  input  in_11,
  input  in_12,
  input  in_13,
  input  in_14,
  input  in_15,
  input  in_16,
  input  in_17,
  output out_18,
  output out_19,
  output out_20,
  output out_21,
  output out_22,
  output out_23,
  output out_24,
  output out_25
);

  wire ADDR_out, alu_1_carry, alu_1_out0, alu_1_out1, alu_1_out2, alu_1_out3, alu_1_out4, alu_1_out5,
       alu_1_out6, alu_1_out7, alu_1_overflow, alu_1_sign, alu_1_zero, and_1_out, and_2_out, and_3_out,
       and_4_out, and_5_out, and_6_out, and_7_out, and_8_out, and_9_out, and_10_out, and_11_out, and_12_out,
       bus0gate_1_out0, bus0gate_1_out1, bus0gate_1_out2, bus0gate_1_out3, bus0gate_1_out4, bus0gate_1_out5,
       bus0gate_1_out6, bus0gate_1_out7, CLOCK_out, controlled_buffer_1_out, controlled_buffer_2_out,
       controlunit_1_bus_0, controlunit_1_cin, controlunit_1_fr_w, controlunit_1_halt, controlunit_1_ir_w,
       controlunit_1_mar_w, controlunit_1_new_cycle, controlunit_1_new_instr, controlunit_1_op0,
       controlunit_1_op1, controlunit_1_op2, controlunit_1_pc_r, controlunit_1_pc_w, controlunit_1_ra_w,
       controlunit_1_ram_r, controlunit_1_ram_w, controlunit_1_rb_w, controlunit_1_rd_r, controlunit_1_rx_r,
       controlunit_1_rx_w, decoder_1_out0, decoder_1_out1, decoder_1_out2, decoder_1_out3, FR_out0, FR_out1,
       FR_out2, FR_out3, HALT_2_q, HALT_2_qn, LDR_out, not_1_out, not_2_out, not_3_out, not_4_out, or_1_out,
       or_2_out, or_3_out, or_4_out, or_5_out, or_6_out, or_7_out, RA_out0, RA_out1, RA_out2, RA_out3,
       RA_out4, RA_out5, RA_out6, RA_out7, RB_out0, RB_out1, RB_out2, RB_out3, RB_out4, RB_out5, RB_out6,
       RB_out7, RESET_3_out, RESET_out, RESUME_out, STEP_out, STR_out;
  wire [1:0] controlunit_1_rx0;
  wire [3:0] CYCLES_q, CYCLES_q_2;
  wire [7:0] INSTR_q, IR_out0;

  ALU alu_1 (
    .a7(RA_out7), .a6(RA_out6), .a5(RA_out5), .a4(RA_out4), .a3(RA_out3), .a2(RA_out2), .a1(RA_out1),
    .a0(RA_out0), .b7(RB_out7), .b6(RB_out6), .b5(RB_out5), .b4(RB_out4), .b3(RB_out3), .b2(RB_out2),
    .b1(RB_out1), .b0(RB_out0), .cin(controlunit_1_cin), .op2(controlunit_1_op2), .op1(controlunit_1_op1),
    .op0(controlunit_1_op0), .out0(alu_1_out0), .out1(alu_1_out1), .out2(alu_1_out2), .out3(alu_1_out3),
    .out4(alu_1_out4), .out5(alu_1_out5), .out6(alu_1_out6), .out7(alu_1_out7), .overflow(alu_1_overflow),
    .sign(alu_1_sign), .zero(alu_1_zero), .carry(alu_1_carry));
  Button RESET (.out(RESET_out));
  LED Reset_2 (.in(RESET_out));
  Button RESUME (.out(RESUME_out));
  not not_1 (not_1_out, MANUAL);
  assign controlled_buffer_1_out = MANUAL ? STEP_out : 1'bz;  // Controlled_Buffer controlled_buffer_1
  Button STEP (.out(STEP_out));
  Clock_part CLOCK (.out(CLOCK_out));
  Pull_Resistor pull_resistor_1 (.node(controlled_buffer_1_out));
  Reg8 RA (
    .in0(out_25), .in1(out_24), .in2(out_23), .in3(out_22), .in4(out_21), .in5(out_20), .in6(out_19),
    .in7(out_18), .read(1'b1), .write(controlunit_1_ra_w), .reset(RESET_out), .out0(RA_out0), .out1(RA_out1),
    .out2(RA_out2), .out3(RA_out3), .out4(RA_out4), .out5(RA_out5), .out6(RA_out6), .out7(RA_out7));
  LED u_Manual (.in(MANUAL));
  LED Auto (.in(not_2_out));
  not not_2 (not_2_out, MANUAL);
  or or_1 (or_1_out, controlled_buffer_1_out, controlled_buffer_2_out);
  assign controlled_buffer_2_out = not_1_out ? CLOCK_out : 1'bz;  // Controlled_Buffer controlled_buffer_2
  Pull_Resistor pull_resistor_2 (.node(controlled_buffer_2_out));
  Reg8 RB (
    .in0(bus0gate_1_out0), .in1(bus0gate_1_out1), .in2(bus0gate_1_out2), .in3(bus0gate_1_out3),
    .in4(bus0gate_1_out4), .in5(bus0gate_1_out5), .in6(bus0gate_1_out6), .in7(bus0gate_1_out7), .read(1'b1),
    .write(controlunit_1_rb_w), .reset(RESET_out), .out0(RB_out0), .out1(RB_out1), .out2(RB_out2),
    .out3(RB_out3), .out4(RB_out4), .out5(RB_out5), .out6(RB_out6), .out7(RB_out7));
  Reg8 RD (
    .in0(alu_1_out0), .in1(alu_1_out1), .in2(alu_1_out2), .in3(alu_1_out3), .in4(alu_1_out4),
    .in5(alu_1_out5), .in6(alu_1_out6), .in7(alu_1_out7), .read(controlunit_1_rd_r), .write(1'b1),
    .reset(RESET_out), .out0(out_25), .out1(out_24), .out2(out_23), .out3(out_22), .out4(out_21),
    .out5(out_20), .out6(out_19), .out7(out_18));
  LED Halt (.in(HALT_2_q));
  LED Clock_2 (.in(or_1_out));
  not not_3 (not_3_out, not_2_out);
  not not_4 (not_4_out, controlunit_1_bus_0);
  Bus0Gate bus0gate_1 (
    .in7(out_18), .in6(out_19), .in5(out_20), .in4(out_21), .in3(out_22), .in2(out_23), .in1(out_24),
    .in0(out_25), ._0_bus(not_4_out), .out7(bus0gate_1_out7), .out6(bus0gate_1_out6), .out5(bus0gate_1_out5),
    .out4(bus0gate_1_out4), .out3(bus0gate_1_out3), .out2(bus0gate_1_out2), .out1(bus0gate_1_out1),
    .out0(bus0gate_1_out0));
  and and_1 (and_1_out, ~HALT_2_q, or_1_out);  // AND_Gate
  Reg4 FR (
    .in0(alu_1_zero), .in1(alu_1_sign), .in2(alu_1_carry), .in3(alu_1_overflow), .read(1'b1),
    .write(controlunit_1_fr_w), .out0(FR_out0), .out1(FR_out1), .out2(FR_out2), .out3(FR_out3),
    .reset(RESET_out));
  ControlUnit controlunit_1 (
    .op0(controlunit_1_op0), .op1(controlunit_1_op1), .op2(controlunit_1_op2), .fr_w(controlunit_1_fr_w),
    .mar_w(controlunit_1_mar_w), .ram_r(controlunit_1_ram_r), .ram_w(controlunit_1_ram_w), .carry(FR_out2),
    .sign(FR_out1), .zero(FR_out0), .ra_w(controlunit_1_ra_w), .rb_w(controlunit_1_rb_w),
    .bus_0(controlunit_1_bus_0), .rx_r(controlunit_1_rx_r), .rx_w(controlunit_1_rx_w), .clk(and_1_out),
    .rst(RESET_out), .rd_r(controlunit_1_rd_r), .ir0(IR_out0[0]), .ir1(IR_out0[1]), .ir2(IR_out0[2]),
    .ir3(IR_out0[3]), .ir4(IR_out0[4]), .ir5(IR_out0[5]), .ir6(IR_out0[6]), .ir7(IR_out0[7]),
    .ir_w(controlunit_1_ir_w), .pc_w(controlunit_1_pc_w), .pc_r(controlunit_1_pc_r), .overflow(FR_out3),
    .halt(controlunit_1_halt), .cin(controlunit_1_cin), .new_instr(controlunit_1_new_instr),
    .new_cycle(controlunit_1_new_cycle), .rx0(controlunit_1_rx0[0]), .rx1(controlunit_1_rx0[1]));  // open: io_in_out, io_data_addr, io
  D_Flip_Flop HALT_2 (
    .clk(controlunit_1_halt), .D(HALT_2_qn), .Q(HALT_2_q), .Qn(HALT_2_qn), .en(1'b1), .reset(or_2_out));  // open: preset
  or or_2 (or_2_out, RESUME_out, RESET_out);
  Reg8 R0 (
    .in0(out_25), .in1(out_24), .in2(out_23), .in3(out_22), .in4(out_21), .in5(out_20), .in6(out_19),
    .in7(out_18), .read(and_2_out), .write(and_3_out), .reset(RESET_out), .out0(out_25), .out1(out_24),
    .out2(out_23), .out3(out_22), .out4(out_21), .out5(out_20), .out6(out_19), .out7(out_18));
  and and_2 (and_2_out, controlunit_1_rx_r, decoder_1_out0);
  Decoder #(.select(2), .enable("false")) decoder_1 (
    .out0(decoder_1_out0), .out1(decoder_1_out1), .out2(decoder_1_out2), .out3(decoder_1_out3),
    .sel(controlunit_1_rx0));
  Counter #(.trigger("falling")) INSTR (
    .load(1'b0), .count(1'b1), .Q(INSTR_q), .clk(controlunit_1_new_instr), .clr(RESET_out));  // open: D, carry
  Hex_Digit_Display hex_digit_display_1 (.value(INSTR_q[7:4]));  // open: dp
  Hex_Digit_Display hex_digit_display_2 (.value(INSTR_q[3:0]));  // open: dp
  and and_3 (and_3_out, decoder_1_out0, controlunit_1_rx_w);
  Counter CYCLES (
    .load(1'b0), .count(1'b1), .Q({CYCLES_q_2, CYCLES_q}), .clk(controlunit_1_new_cycle), .clr(or_3_out));  // open: D, carry
  or or_3 (or_3_out, controlunit_1_new_instr, RESET_out);
  Hex_Digit_Display hex_digit_display_3 (.value(CYCLES_q_2));  // open: dp
  Reg8 IR (
    .in0(out_25), .in1(out_24), .in2(out_23), .in3(out_22), .in4(out_21), .in5(out_20), .in6(out_19),
    .in7(out_18), .read(1'b1), .write(controlunit_1_ir_w), .reset(RESET_out), .out0(IR_out0[0]),
    .out1(IR_out0[1]), .out2(IR_out0[2]), .out3(IR_out0[3]), .out4(IR_out0[4]), .out5(IR_out0[5]),
    .out6(IR_out0[6]), .out7(IR_out0[7]));
  Hex_Digit_Display hex_digit_display_4 (.value(CYCLES_q));  // open: dp
  Reg8 R1 (
    .in0(out_25), .in1(out_24), .in2(out_23), .in3(out_22), .in4(out_21), .in5(out_20), .in6(out_19),
    .in7(out_18), .read(and_4_out), .write(and_5_out), .reset(RESET_out), .out0(out_25), .out1(out_24),
    .out2(out_23), .out3(out_22), .out4(out_21), .out5(out_20), .out6(out_19), .out7(out_18));
  and and_4 (and_4_out, controlunit_1_rx_r, decoder_1_out1);
  and and_5 (and_5_out, decoder_1_out1, controlunit_1_rx_w);
  and and_6 (and_6_out, not_3_out, LDR_out);
  and and_7 (and_7_out, ADDR_out, not_3_out);
  Button LDR (.out(LDR_out));
  Button ADDR (.out(ADDR_out));
  Reg8 R2 (
    .in0(out_25), .in1(out_24), .in2(out_23), .in3(out_22), .in4(out_21), .in5(out_20), .in6(out_19),
    .in7(out_18), .read(and_8_out), .write(and_10_out), .reset(RESET_out), .out0(out_25), .out1(out_24),
    .out2(out_23), .out3(out_22), .out4(out_21), .out5(out_20), .out6(out_19), .out7(out_18));
  and and_8 (and_8_out, controlunit_1_rx_r, decoder_1_out2);
  Reg8 PC (
    .in0(out_25), .in1(out_24), .in2(out_23), .in3(out_22), .in4(out_21), .in5(out_20), .in6(out_19),
    .in7(out_18), .read(controlunit_1_pc_r), .write(controlunit_1_pc_w), .reset(RESET_out), .out0(out_25),
    .out1(out_24), .out2(out_23), .out3(out_22), .out4(out_21), .out5(out_20), .out6(out_19), .out7(out_18));
  and and_9 (and_9_out, not_3_out, STR_out);
  Button STR (.out(STR_out));
  and and_10 (and_10_out, decoder_1_out2, controlunit_1_rx_w);
  assign out_19 = and_7_out ? in_2 : 1'bz;  // Controlled_Buffer controlled_buffer_3
  assign out_21 = and_7_out ? in_4 : 1'bz;  // Controlled_Buffer controlled_buffer_4
  assign out_20 = and_7_out ? in_3 : 1'bz;  // Controlled_Buffer controlled_buffer_5
  assign out_18 = and_7_out ? in_1 : 1'bz;  // Controlled_Buffer controlled_buffer_6
  assign out_21 = and_9_out ? in_13 : 1'bz;  // Controlled_Buffer controlled_buffer_7
  assign out_19 = and_9_out ? in_11 : 1'bz;  // Controlled_Buffer controlled_buffer_8
  assign out_20 = and_9_out ? in_12 : 1'bz;  // Controlled_Buffer controlled_buffer_9
  assign out_18 = and_9_out ? in_10 : 1'bz;  // Controlled_Buffer controlled_buffer_10
  assign out_25 = and_7_out ? in_8 : 1'bz;  // Controlled_Buffer controlled_buffer_11
  assign out_23 = and_7_out ? in_6 : 1'bz;  // Controlled_Buffer controlled_buffer_12
  assign out_22 = and_7_out ? in_5 : 1'bz;  // Controlled_Buffer controlled_buffer_13
  assign out_24 = and_7_out ? in_7 : 1'bz;  // Controlled_Buffer controlled_buffer_14
  assign out_22 = and_9_out ? in_14 : 1'bz;  // Controlled_Buffer controlled_buffer_15
  assign out_24 = and_9_out ? in_16 : 1'bz;  // Controlled_Buffer controlled_buffer_16
  assign out_23 = and_9_out ? in_15 : 1'bz;  // Controlled_Buffer controlled_buffer_17
  assign out_25 = and_9_out ? in_17 : 1'bz;  // Controlled_Buffer controlled_buffer_18
  Reg8 R3 (
    .in0(out_25), .in1(out_24), .in2(out_23), .in3(out_22), .in4(out_21), .in5(out_20), .in6(out_19),
    .in7(out_18), .read(and_12_out), .write(and_11_out), .reset(RESET_out), .out0(out_25), .out1(out_24),
    .out2(out_23), .out3(out_22), .out4(out_21), .out5(out_20), .out6(out_19), .out7(out_18));
  and and_11 (and_11_out, decoder_1_out3, controlunit_1_rx_w);
  and and_12 (and_12_out, controlunit_1_rx_r, decoder_1_out3);
  or or_4 (or_4_out, controlunit_1_mar_w, and_7_out);
  or or_5 (or_5_out, controlunit_1_ram_r, and_6_out);
  or or_6 (or_6_out, controlunit_1_ram_w, and_9_out);
  or or_7 (or_7_out, and_1_out, and_7_out, and_6_out, and_9_out);
  Button RESET_3 (.out(RESET_3_out));
  Ram256 ram256_1 (
    .addr0(out_25), .addr1(out_24), .addr2(out_23), .addr3(out_22), .addr4(out_21), .addr5(out_20),
    .addr6(out_19), .addr7(out_18), .marw(or_4_out), .read(or_5_out), .write(or_6_out), .reset(RESET_3_out),
    .in0(out_25), .in1(out_24), .in2(out_23), .in3(out_22), .in4(out_21), .in5(out_20), .in6(out_19),
    .in7(out_18), .out0(out_25), .out1(out_24), .out2(out_23), .out3(out_22), .out4(out_21), .out5(out_20),
    .out6(out_19), .out7(out_18), .clk(or_7_out));

  // Notes on the sheet:
  //   bits | cond   | flag test  | description
  //   0000 | r      | -----      | branch always
  //   0001 | zs/eq  | z=1        | branch if equal
  //   0010 | ss/neg | s=1        | branch if negative
  //   0011 | ov     | v=1        | branch if overflow
  //   0100 | cs/ltu | c=1        | branch if uint <
  //   0101 | leu    | c=1 or z=1 | branch if uint <=
  //   0110 | lt     | v+s        | branch if int <
  //   0111 | le     | v+s or z=1 | branch if int <=
  //   0000 00 00  ->  mov  ra, rb    ->  ra = rb
  //   0001 00 rb  ->  data rb, imm8  ->  rb = ram[pc++]
  //   0010 ra rb  ->  ldr  ra, [rb]  ->  ra = ram[rb]
  //   0011 ra rb  ->  str  ra, [rb]  ->  ram[rb] = ra
  //   0100 00 rb  ->  jalr rb        ->  pc <-> rb
  //   0101  cond  ->  b<cond> imm8   ->  pc += cond ? ram[pc] : 1
  //   0110 00 00  ->  halt           ->  stop computer
  //   0111 00 rb  ->  in   data, rb  ->  rb = io[active].data
  //   0111 10 rb  ->  out  data, rb  ->  io[active].data = rb
  //   0111 01 rb  ->  in   addr, rb  ->  rb = io[active].addr
  //   0111 11 rb  ->  out  addr, rb  ->  io[rb].active = true
  //   1000 ra rb  ->  add ra, rb  ->  ra = ra + rb       [vcsz]
  //   1001 ra rb  ->  sub ra, rb  ->  ra = ra - rb       [vcsz]
  //   1010 ra rb  ->  shl ra, rb  ->  ra = [rb << 1, 0]  [0csz]
  //   1011 ra rb  ->  shr ra, rb  ->  ra = [0, rb >> 1]  [0csz]
  //   1100 ra rb  ->  and ra, rb  ->  ra = ra & rb       [00sz]
  //   1101 ra rb  ->  orr ra, rb  ->  ra = ra | rb       [00sz]
  //   1110 ra rb  ->  xor ra, rb  ->  ra = ra ^ rb       [00sz]
  //   1111 ra rb  ->  cmp ra, rb  ->  fr = ra - rb       [vcsz]
endmodule
